// Logisim project 74LS42.circ as structural Verilog: 1 circuit, main circuit 74LS42
module _74LS42 (
  input  A0,
  input  A1,
  input  A2,
  input  A3,
  output _0,
  output _1,
  output _2,
  output _3,
  output _4,
  output _5,
  output _6,
  output _7,
  output _8,
  output _9
);

  wire not_1_out, not_2_out, not_3_out, not_4_out, not_5_out, not_6_out, not_7_out, not_8_out;

  nand nand_1 (_1, not_2_out, not_7_out, not_5_out, not_3_out);
  nand nand_2 (_0, not_7_out, not_5_out, not_3_out, not_1_out);
  not not_1 (not_1_out, A0);
  not not_2 (not_2_out, not_1_out);
  nand nand_3 (_2, not_4_out, not_1_out, not_5_out, not_7_out);
  not not_3 (not_3_out, A1);
  not not_4 (not_4_out, not_3_out);
  nand nand_4 (_3, not_2_out, not_5_out, not_4_out, not_7_out);
  nand nand_5 (_4, not_1_out, not_6_out, not_3_out, not_7_out);
  nand nand_6 (_5, not_6_out, not_2_out, not_3_out, not_7_out);
  not not_5 (not_5_out, A2);
  not not_6 (not_6_out, not_5_out);
  nand nand_7 (_6, not_6_out, not_4_out, not_1_out, not_7_out);
  not not_7 (not_7_out, A3);
  not not_8 (not_8_out, not_7_out);
  nand nand_8 (_7, not_7_out, not_6_out, not_4_out, not_2_out);
  nand nand_9 (_8, not_8_out, not_5_out, not_3_out, not_1_out);
  nand nand_10 (_9, not_8_out, not_5_out, not_3_out, not_2_out);

  // Notes on the sheet:
  //   74LS42
endmodule
