// Logisim project 74LS48.circ as structural Verilog: 1 circuit, main circuit 74LS48
module _74LS48 (
  input  INPUT_A,
  input  INPUT_B,
  input  INPUT_C,
  input  INPUT_D,
  input  nBI,
  input  nLT,
  input  nRBI_INPUT,
  output a,
  output b,
  output c,
  output d,
  output e,
  output nRBO_OUTPUT,
  output f,
  output g
);

  wire and_1_out, and_2_out, and_3_out, and_4_out, and_5_out, and_6_out, and_7_out, and_8_out, and_9_out,
       and_10_out, and_11_out, and_12_out, and_13_out, and_14_out, and_15_out, and_16_out, and_17_out,
       and_18_out, buffer_1_out, nand_1_out, nand_2_out, nand_3_out, nand_5_out, nand_6_out, nand_7_out,
       nand_8_out, not_1_out, not_2_out, not_3_out, not_4_out, not_5_out, not_6_out;

  Pull_Resistor #(.pull(1)) pull_resistor_1 (.node(nBI));
  and and_1 (and_1_out, nBI, nRBO_OUTPUT);
  nand nand_1 (nand_1_out, INPUT_A, not_4_out);
  nand nand_2 (nand_2_out, INPUT_B, not_4_out);
  nand nand_3 (nand_3_out, INPUT_C, not_4_out);
  not not_1 (not_1_out, INPUT_D);
  not not_2 (not_2_out, not_3_out);
  not not_3 (not_3_out, and_1_out);
  nand nand_4 (nRBO_OUTPUT, not_4_out, not_6_out, not_1_out, nand_3_out, nand_2_out, nand_1_out);
  not not_4 (not_4_out, not_5_out);
  not not_5 (not_5_out, nLT);
  not not_6 (not_6_out, nRBI_INPUT);
  nand nand_5 (nand_5_out, nand_1_out, not_2_out);
  nand nand_6 (nand_6_out, nand_2_out, not_2_out);
  nand nand_7 (nand_7_out, nand_3_out, not_2_out);
  nand nand_8 (nand_8_out, not_1_out, not_2_out);
  and and_2 (and_2_out, nand_6_out, nand_8_out);
  and and_3 (and_3_out, nand_1_out, nand_7_out);
  and and_4 (and_4_out, nand_5_out, nand_2_out, nand_3_out, not_1_out);
  and and_5 (and_5_out, nand_6_out, nand_8_out);
  and and_6 (and_6_out, nand_5_out, nand_2_out, nand_7_out);
  and and_7 (and_7_out, nand_1_out, nand_6_out, nand_7_out);
  and and_8 (and_8_out, nand_7_out, nand_8_out);
  and and_9 (and_9_out, nand_1_out, nand_6_out, nand_3_out);
  and and_10 (and_10_out, nand_5_out, nand_2_out, nand_3_out);
  and and_11 (and_11_out, nand_1_out, nand_2_out, nand_7_out);
  and and_12 (and_12_out, nand_5_out, nand_6_out, nand_7_out);
  buf buffer_1 (buffer_1_out, nand_5_out);
  and and_13 (and_13_out, nand_2_out, nand_7_out);
  and and_14 (and_14_out, nand_5_out, nand_6_out);
  and and_15 (and_15_out, nand_6_out, nand_3_out);
  and and_16 (and_16_out, nand_5_out, nand_3_out, not_1_out);
  and and_17 (and_17_out, nand_5_out, nand_6_out, nand_7_out);
  and and_18 (and_18_out, nand_2_out, nand_3_out, not_1_out, not_4_out);
  and and_19 (a, ~and_2_out, ~and_3_out, ~and_4_out);  // AND_Gate
  and and_20 (b, ~and_5_out, ~and_6_out, ~and_7_out);  // AND_Gate
  and and_21 (c, ~and_8_out, ~and_9_out);  // AND_Gate
  and and_22 (d, ~and_10_out, ~and_11_out, ~and_12_out);  // AND_Gate
  and and_23 (e, ~buffer_1_out, ~and_13_out);  // AND_Gate
  and and_24 (f, ~and_14_out, ~and_15_out, ~and_16_out);  // AND_Gate
  and and_25 (g, ~and_17_out, ~and_18_out);  // AND_Gate
  _7_Segment_Display u_7_segment_display_1 (.g(g), .f(f), .a(a), .b(b), .e(e), .d(d), .c(c));  // open: dp

  // Notes on the sheet:
  //   74LS48
endmodule
