// Logisim project 74LS82.circ as structural Verilog: 1 circuit, main circuit 74LS82
module _74LS82 (
  input  C0,
  input  A1,
  input  B1,
  input  B2,
  input  A2,
  output \Σ1 ,
  output \Σ2 ,
  output C2
);

  wire and_1_out, and_2_out, and_3_out, and_4_out, and_5_out, and_6_out, and_7_out, and_8_out, and_9_out,
       and_10_out, and_11_out, and_12_out, and_13_out, and_14_out, nor_1_out, nor_2_out, not_1_out, not_2_out;

  not not_1 (not_1_out, B2);
  not not_2 (not_2_out, A2);
  and and_1 (and_1_out, C0, nor_2_out);
  and and_2 (and_2_out, A1, nor_2_out);
  and and_3 (and_3_out, B1, nor_2_out);
  and and_4 (and_4_out, C0, A1, B1);
  and and_5 (and_5_out, C0, A1);
  and and_6 (and_6_out, C0, B1);
  and and_7 (and_7_out, B1, A1);
  and and_8 (and_8_out, nor_2_out, C2);
  and and_9 (and_9_out, not_2_out, C2);
  and and_10 (and_10_out, not_1_out, C2);
  and and_11 (and_11_out, nor_2_out, not_2_out, not_1_out);
  and and_12 (and_12_out, nor_2_out, not_2_out);
  and and_13 (and_13_out, nor_2_out, not_1_out);
  and and_14 (and_14_out, not_2_out, not_1_out);
  nor nor_1 (nor_1_out, and_1_out, and_2_out, and_3_out, and_4_out);
  not not_3 (\Σ1 , nor_1_out);
  nor nor_2 (nor_2_out, and_5_out, and_6_out, and_7_out);
  nor nor_3 (\Σ2 , and_8_out, and_9_out, and_10_out, and_11_out);
  nor nor_4 (C2, and_12_out, and_13_out, and_14_out);

  // Notes on the sheet:
  //   74LS82
endmodule
