// Logisim project BUF_OC.circ as structural Verilog: 1 circuit, main circuit INV_OC
module INV_OC (
  input  in_1,
  output out_2
);

  buf buffer_1 (out_2, in_1);

  // Notes on the sheet:
  //   buffer_1 drives only 0 and floats otherwise
endmodule
