// Logisim project INV_OC.circ as structural Verilog: 1 circuit, main circuit INV_OC
module INV_OC (
  input  in_1,
  output out_2
);

  not not_1 (out_2, in_1);

  // Notes on the sheet:
  //   not_1 drives only 0 and floats otherwise
endmodule
