// Logisim project NAND2_OC.circ as structural Verilog: 1 circuit, main circuit NAND2_OC
module NAND2_OC (
  input  in_1,
  input  in_2,
  output out_3
);

  nand nand_1 (out_3, in_1, in_2);

  // Notes on the sheet:
  //   nand_1 drives only 0 and floats otherwise
endmodule
