// Logisim project 74F455.circ as structural Verilog: 1 circuit, main circuit 74F455
module _74F455 (
  input  PI,
  input  I0,
  input  I1,
  input  I2,
  input  I3,
  input  I4,
  input  I5,
  input  I6,
  input  I7,
  input  nOE1,
  input  nOE2,
  output \ΣE ,
  output \ΣO ,
  output nY0,
  output nY1,
  output nY2,
  output nY3,
  output nY4,
  output nY5,
  output nY6,
  output nY7
);

  wire and_1_out, and_2_out, and_3_out, and_4_out, and_5_out, and_6_out, and_7_out, and_8_out, and_9_out,
       and_10_out, and_11_out, and_12_out, and_13_out, and_14_out, and_15_out, and_16_out, nor_1_out,
       nor_2_out, nor_3_out, nor_4_out, not_1_out, not_2_out, not_3_out, not_4_out, not_5_out, not_6_out,
       not_7_out, not_8_out, not_9_out, not_10_out, not_11_out, not_12_out, not_13_out, not_14_out,
       not_15_out, not_16_out, not_17_out, not_18_out, not_19_out, not_20_out, not_21_out, or_1_out;

  nor nor_1 (nor_1_out, nOE1, nOE2);
  not not_1 (not_1_out, PI);
  not not_2 (not_2_out, I0);
  not not_3 (not_3_out, I1);
  not not_4 (not_4_out, I2);
  not not_5 (not_5_out, I3);
  not not_6 (not_6_out, I4);
  not not_7 (not_7_out, I5);
  not not_8 (not_8_out, I6);
  not not_9 (not_9_out, I7);
  and and_1 (and_1_out, not_3_out, not_2_out, not_10_out);
  not not_10 (not_10_out, not_1_out);
  and and_2 (and_2_out, not_3_out, not_1_out, not_11_out);
  not not_11 (not_11_out, not_2_out);
  and and_3 (and_3_out, not_2_out, not_1_out, not_12_out);
  not not_12 (not_12_out, not_3_out);
  and and_4 (and_4_out, not_10_out, not_11_out, not_12_out);
  and and_5 (and_5_out, not_6_out, not_5_out, not_13_out);
  not not_13 (not_13_out, not_4_out);
  and and_6 (and_6_out, not_6_out, not_4_out, not_14_out);
  not not_14 (not_14_out, not_5_out);
  and and_7 (and_7_out, not_5_out, not_4_out, not_15_out);
  not not_15 (not_15_out, not_6_out);
  and and_8 (and_8_out, not_13_out, not_14_out, not_15_out);
  and and_9 (and_9_out, not_9_out, not_8_out, not_16_out);
  not not_16 (not_16_out, not_7_out);
  and and_10 (and_10_out, not_9_out, not_7_out, not_17_out);
  not not_17 (not_17_out, not_8_out);
  and and_11 (and_11_out, not_8_out, not_7_out, not_18_out);
  not not_18 (not_18_out, not_9_out);
  and and_12 (and_12_out, not_16_out, not_17_out, not_18_out);
  nor nor_2 (nor_2_out, and_1_out, and_2_out, and_3_out, and_4_out);
  nor nor_3 (nor_3_out, and_5_out, and_6_out, and_7_out, and_8_out);
  nor nor_4 (nor_4_out, and_9_out, and_10_out, and_11_out, and_12_out);
  not not_19 (not_19_out, nor_2_out);
  not not_20 (not_20_out, nor_3_out);
  not not_21 (not_21_out, nor_4_out);
  and and_13 (and_13_out, nor_4_out, nor_3_out, not_19_out);
  and and_14 (and_14_out, nor_4_out, nor_2_out, not_20_out);
  and and_15 (and_15_out, nor_3_out, nor_2_out, not_21_out);
  and and_16 (and_16_out, not_19_out, not_20_out, not_21_out);
  or or_1 (or_1_out, and_13_out, and_14_out, and_15_out, and_16_out);
  assign \ΣE  = nor_1_out ? ~or_1_out : 1'bz;  // Controlled_Inverter controlled_inverter_1
  assign \ΣO  = nor_1_out ? or_1_out : 1'bz;  // Controlled_Buffer controlled_buffer_1
  assign nY0 = nor_1_out ? ~I0 : 1'bz;  // Controlled_Inverter controlled_inverter_2
  assign nY1 = nor_1_out ? ~I1 : 1'bz;  // Controlled_Inverter controlled_inverter_3
  assign nY2 = nor_1_out ? ~I2 : 1'bz;  // Controlled_Inverter controlled_inverter_4
  assign nY3 = nor_1_out ? ~I3 : 1'bz;  // Controlled_Inverter controlled_inverter_5
  assign nY4 = nor_1_out ? ~I4 : 1'bz;  // Controlled_Inverter controlled_inverter_6
  assign nY5 = nor_1_out ? ~I5 : 1'bz;  // Controlled_Inverter controlled_inverter_7
  assign nY6 = nor_1_out ? ~I6 : 1'bz;  // Controlled_Inverter controlled_inverter_8
  assign nY7 = nor_1_out ? ~I7 : 1'bz;  // Controlled_Inverter controlled_inverter_9

  // Notes on the sheet:
  //   74F455
endmodule
