// Logisim project 74L116.circ as structural Verilog: 1 circuit, main circuit 74L116
module _74L116 (
  input  _1_CLR,
  input  _2_CLR,
  input  _1_C1,
  input  _2_C1,
  input  _1_C2,
  input  _2_C2,
  input  _1D1,
  input  _2D1,
  input  _1D2,
  input  _2D2,
  input  _1D3,
  input  _2D3,
  input  _1D4,
  input  _2D4,
  output _1Q1,
  output _2Q1,
  output _1Q2,
  output _2Q2,
  output _1Q3,
  output _2Q3,
  output _1Q4,
  output _2Q4
);

  wire and_1_out, and_2_out, not_1_out, not_2_out;

  not not_1 (not_1_out, _1_CLR);
  and and_1 (and_1_out, ~_1_C1, ~_1_C2);  // AND_Gate
  D_Flip_Flop #(.trigger("high")) High_Level (
    .clk(and_1_out), .D(_1D1), .Q(_1Q1), .reset(not_1_out));  // open: Qn, preset, en
  D_Flip_Flop #(.trigger("high")) High_Level_2 (
    .clk(and_1_out), .D(_1D2), .Q(_1Q2), .reset(not_1_out));  // open: Qn, preset, en
  D_Flip_Flop #(.trigger("high")) High_Level_3 (
    .clk(and_1_out), .D(_1D3), .Q(_1Q3), .reset(not_1_out));  // open: Qn, preset, en
  D_Flip_Flop #(.trigger("high")) High_Level_4 (
    .clk(and_1_out), .D(_1D4), .Q(_1Q4), .reset(not_1_out));  // open: Qn, preset, en
  not not_2 (not_2_out, _2_CLR);
  and and_2 (and_2_out, ~_2_C1, ~_2_C2);  // AND_Gate
  D_Flip_Flop #(.trigger("high")) High_Level_5 (
    .clk(and_2_out), .D(_2D1), .Q(_2Q1), .reset(not_2_out));  // open: Qn, preset, en
  D_Flip_Flop #(.trigger("high")) High_Level_6 (
    .clk(and_2_out), .D(_2D2), .Q(_2Q2), .reset(not_2_out));  // open: Qn, preset, en
  D_Flip_Flop #(.trigger("high")) High_Level_7 (
    .clk(and_2_out), .D(_2D3), .Q(_2Q3), .reset(not_2_out));  // open: Qn, preset, en
  D_Flip_Flop #(.trigger("high")) High_Level_8 (
    .clk(and_2_out), .D(_2D4), .Q(_2Q4), .reset(not_2_out));  // open: Qn, preset, en

  // Notes on the sheet:
  //   74L116
endmodule
