// Logisim project 74LS100.circ as structural Verilog: 1 circuit, main circuit 74LS100
module _74LS100 (
  input  _1C,
  input  _2C,
  input  _1D1,
  input  _2D1,
  input  _1D2,
  input  _2D2,
  input  _1D3,
  input  _2D3,
  input  _1D4,
  input  _2D4,
  output _1Q1,
  output _2Q1,
  output _1Q2,
  output _2Q2,
  output _1Q3,
  output _2Q3,
  output _1Q4,
  output _2Q4
);

  D_Flip_Flop #(.trigger("high")) High_Level_Latch (.clk(_1C), .D(_1D1), .Q(_1Q1));  // open: Qn, preset, en, reset
  D_Flip_Flop #(.trigger("high")) High_Level_Latch_2 (.clk(_1C), .D(_1D2), .Q(_1Q2));  // open: Qn, preset, en, reset
  D_Flip_Flop #(.trigger("high")) High_Level_Latch_3 (.clk(_1C), .D(_1D3), .Q(_1Q3));  // open: Qn, preset, en, reset
  D_Flip_Flop #(.trigger("high")) High_Level_Latch_4 (.clk(_1C), .D(_1D4), .Q(_1Q4));  // open: Qn, preset, en, reset
  D_Flip_Flop #(.trigger("high")) High_Level_Latch_5 (.clk(_2C), .D(_2D1), .Q(_2Q1));  // open: Qn, preset, en, reset
  D_Flip_Flop #(.trigger("high")) High_Level_Latch_6 (.clk(_2C), .D(_2D2), .Q(_2Q2));  // open: Qn, preset, en, reset
  D_Flip_Flop #(.trigger("high")) High_Level_Latch_7 (.clk(_2C), .D(_2D3), .Q(_2Q3));  // open: Qn, preset, en, reset
  D_Flip_Flop #(.trigger("high")) High_Level_Latch_8 (.clk(_2C), .D(_2D4), .Q(_2Q4));  // open: Qn, preset, en, reset

  // Notes on the sheet:
  //   74LS100
endmodule
