// Logisim project 74LS101.circ as structural Verilog: 1 circuit, main circuit 74LS101
module _74LS101 (
  input  J1A,
  input  J1B,
  input  J2A,
  input  J2B,
  input  nCLK,
  input  K1A,
  input  K1B,
  input  K2A,
  input  K2B,
  input  nPRE,
  output Q,
  output nQ
);

  wire and_1_out, and_2_out, and_3_out, and_4_out, not_1_out, or_1_out, or_2_out;

  and and_1 (and_1_out, J1A, J1B);
  and and_2 (and_2_out, J2A, J2B);
  and and_3 (and_3_out, K1A, K1B);
  and and_4 (and_4_out, K2A, K2B);
  not not_1 (not_1_out, nPRE);
  or or_1 (or_1_out, and_1_out, and_2_out);
  or or_2 (or_2_out, and_3_out, and_4_out);
  J_K_Flip_Flop #(.trigger("falling")) Fall (
    .J(or_1_out), .clk(nCLK), .K(or_2_out), .Q(Q), .Qn(nQ), .preset(not_1_out));  // open: en, reset

  // Notes on the sheet:
  //   74LS101
endmodule
