// Logisim project 74LS102.circ as structural Verilog: 1 circuit, main circuit 74LS102
module _74LS102 (
  input  J1,
  input  J2,
  input  J3,
  input  nCLK,
  input  K1,
  input  K2,
  input  K3,
  input  nPRE,
  input  nCLR,
  output Q,
  output nQ
);

  wire and_1_out, and_2_out, and_3_out, Fall_q, Fall_qn, not_1_out, not_2_out;

  and and_1 (and_1_out, J1, J2, J3);
  and and_2 (and_2_out, K1, K2, K3);
  not not_1 (not_1_out, nPRE);
  not not_2 (not_2_out, nCLR);
  J_K_Flip_Flop #(.trigger("falling")) Fall (
    .J(and_1_out), .clk(nCLK), .K(and_2_out), .Q(Fall_q), .Qn(Fall_qn), .preset(not_1_out), .reset(not_2_out));  // open: en
  or or_1 (Q, and_3_out, Fall_q);
  or or_2 (nQ, Fall_qn, and_3_out);
  and and_3 (and_3_out, not_1_out, not_2_out);

  // Notes on the sheet:
  //   74LS102
endmodule
