// Logisim project 74LS105.circ as structural Verilog: 1 circuit, main circuit 74LS105
module _74LS105 (
  input  J3,
  input  nJ2,
  input  J1,
  input  CLK,
  input  JK,
  input  K3,
  input  nK2,
  input  K1,
  input  nPRE,
  input  nCLR,
  output Q,
  output nQ
);

  wire and_1_out, and_2_out, and_3_out, not_1_out, not_2_out, Rise_q, Rise_qn;

  not not_1 (not_1_out, nPRE);
  not not_2 (not_2_out, nCLR);
  and and_1 (and_1_out, J3, ~nJ2, J1, JK);  // AND_Gate
  and and_2 (and_2_out, JK, K3, ~nK2, K1);  // AND_Gate
  J_K_Flip_Flop Rise (
    .J(and_1_out), .clk(CLK), .K(and_2_out), .Q(Rise_q), .Qn(Rise_qn), .preset(not_1_out), .reset(not_2_out));  // open: en
  and and_3 (and_3_out, not_1_out, not_2_out);
  or or_1 (Q, and_3_out, Rise_q);
  or or_2 (nQ, Rise_qn, and_3_out);

  // Notes on the sheet:
  //   74LS105
endmodule
