// Logisim project 74LS107.circ as structural Verilog: 1 circuit, main circuit 74LS107
module _74LS107 (
  input  _1J,
  input  _1_CLK,
  input  _1K,
  input  _1_CLR,
  input  _2J,
  input  _2_CLK,
  input  _2K,
  input  _2_CLR,
  output _1Q,
  output _1_Q,
  output _2Q,
  output _2_Q
);

  wire not_1_out, not_2_out;

  J_K_Flip_Flop #(.trigger("falling")) Fall (
    .J(_1J), .clk(_1_CLK), .K(_1K), .Q(_1Q), .Qn(_1_Q), .reset(not_1_out));  // open: preset, en
  not not_1 (not_1_out, _1_CLR);
  J_K_Flip_Flop #(.trigger("falling")) Fall_2 (
    .J(_2J), .clk(_2_CLK), .K(_2K), .Q(_2Q), .Qn(_2_Q), .reset(not_2_out));  // open: preset, en
  not not_2 (not_2_out, _2_CLR);

  // Notes on the sheet:
  //   74LS107
endmodule
