// Logisim project 74LS108.circ as structural Verilog: 1 circuit, main circuit 74LS108
module _74LS108 (
  input  nCLK,
  input  nCLR,
  input  _1J,
  input  _1K,
  input  _1_PRE,
  input  _2J,
  input  _2K,
  input  _2_PRE,
  output _1Q,
  output _1_Q,
  output _2Q,
  output _2_Q
);

  wire and_1_out, and_2_out, Fall_2_q, Fall_2_qn, Fall_q, Fall_qn, not_1_out, not_2_out, not_3_out;

  not not_1 (not_1_out, nCLR);
  not not_2 (not_2_out, _1_PRE);
  not not_3 (not_3_out, _2_PRE);
  J_K_Flip_Flop #(.trigger("falling")) Fall (
    .J(_1J), .clk(nCLK), .K(_1K), .Q(Fall_q), .Qn(Fall_qn), .preset(not_2_out), .reset(not_1_out));  // open: en
  J_K_Flip_Flop #(.trigger("falling")) Fall_2 (
    .J(_2J), .clk(nCLK), .K(_2K), .Q(Fall_2_q), .Qn(Fall_2_qn), .preset(not_3_out), .reset(not_1_out));  // open: en
  or or_1 (_1Q, and_1_out, Fall_q);
  or or_2 (_1_Q, Fall_qn, and_1_out);
  and and_1 (and_1_out, not_1_out, not_2_out);
  or or_3 (_2Q, and_2_out, Fall_2_q);
  or or_4 (_2_Q, Fall_2_qn, and_2_out);
  and and_2 (and_2_out, not_1_out, not_3_out);

  // Notes on the sheet:
  //   74LS108
endmodule
