// Logisim project 74LS109.circ as structural Verilog: 1 circuit, main circuit 74LS109
module _74LS109 (
  input  _1J,
  input  _1CLK,
  input  _1_K,
  input  _1_PRE,
  input  _1_CLR,
  input  _2J,
  input  _2CLK,
  input  _2_K,
  input  _2_PRE,
  input  _2_CLR,
  output _1Q,
  output _1_Q,
  output _2Q,
  output _2_Q
);

  wire and_1_out, and_2_out, not_1_out, not_2_out, not_3_out, not_4_out, not_5_out, not_6_out, Rise_2_q,
       Rise_2_qn, Rise_q, Rise_qn;

  not not_1 (not_1_out, _1_K);
  not not_2 (not_2_out, _1_PRE);
  not not_3 (not_3_out, _1_CLR);
  not not_4 (not_4_out, _2_K);
  not not_5 (not_5_out, _2_PRE);
  not not_6 (not_6_out, _2_CLR);
  J_K_Flip_Flop Rise (
    .J(_1J), .clk(_1CLK), .K(not_1_out), .Q(Rise_q), .Qn(Rise_qn), .preset(not_2_out), .reset(not_3_out));  // open: en
  J_K_Flip_Flop Rise_2 (
    .J(_2J), .clk(_2CLK), .K(not_4_out), .Q(Rise_2_q), .Qn(Rise_2_qn), .preset(not_5_out), .reset(not_6_out));  // open: en
  or or_1 (_1Q, and_1_out, Rise_q);
  or or_2 (_1_Q, Rise_qn, and_1_out);
  and and_1 (and_1_out, not_2_out, not_3_out);
  or or_3 (_2Q, and_2_out, Rise_2_q);
  or or_4 (_2_Q, Rise_2_qn, and_2_out);
  and and_2 (and_2_out, not_5_out, not_6_out);

  // Notes on the sheet:
  //   74LS109
endmodule
