// Logisim project 74LS110.circ as structural Verilog: 1 circuit, main circuit 74LS110
module _74LS110 (
  input  CLK,
  input  J1,
  input  J2,
  input  J3,
  input  K1,
  input  K2,
  input  K3,
  input  nPRE,
  input  nCLR,
  output Q,
  output _1_Q
);

  wire and_1_out, and_2_out, and_3_out, Fall_q, Fall_qn, not_1_out, not_2_out, Rise_2_q, Rise_q;

  and and_1 (and_1_out, J1, J2, J3);
  and and_2 (and_2_out, K1, K2, K3);
  not not_1 (not_1_out, nPRE);
  not not_2 (not_2_out, nCLR);
  D_Flip_Flop Rise (.clk(CLK), .D(and_1_out), .Q(Rise_q));  // open: Qn, preset, en, reset
  D_Flip_Flop Rise_2 (.clk(CLK), .D(and_2_out), .Q(Rise_2_q));  // open: Qn, preset, en, reset
  J_K_Flip_Flop #(.trigger("falling")) Fall (
    .J(Rise_q), .clk(CLK), .K(Rise_2_q), .Q(Fall_q), .Qn(Fall_qn), .preset(not_1_out), .reset(not_2_out));  // open: en
  and and_3 (and_3_out, not_1_out, not_2_out);
  or or_1 (Q, and_3_out, Fall_q);
  or or_2 (_1_Q, Fall_qn, and_3_out);

  // Notes on the sheet:
  //   74LS110
endmodule
