// Logisim project 74LS111.circ as structural Verilog: 1 circuit, main circuit 74LS111
module _74LS111 (
  input  _1CLK,
  input  _1J,
  input  _1K,
  input  _1_PRE,
  input  _1_CLR,
  input  _2CLK,
  input  _2J,
  input  _2K,
  input  _2_PRE,
  input  _2_CLR,
  output _1Q,
  output _1_Q,
  output _2Q,
  output _2_Q
);

  wire and_1_out, and_2_out, Fall_2_q, Fall_2_qn, Fall_q, Fall_qn, not_1_out, not_2_out, not_3_out,
       not_4_out, Rise_2_q, Rise_3_q, Rise_4_q, Rise_q;

  D_Flip_Flop Rise (.clk(_1CLK), .D(_1J), .Q(Rise_q));  // open: Qn, preset, en, reset
  D_Flip_Flop Rise_2 (.clk(_1CLK), .D(_1K), .Q(Rise_2_q));  // open: Qn, preset, en, reset
  not not_1 (not_1_out, _1_PRE);
  not not_2 (not_2_out, _1_CLR);
  D_Flip_Flop Rise_3 (.clk(_2CLK), .D(_2J), .Q(Rise_3_q));  // open: Qn, preset, en, reset
  D_Flip_Flop Rise_4 (.clk(_2CLK), .D(_2K), .Q(Rise_4_q));  // open: Qn, preset, en, reset
  not not_3 (not_3_out, _2_PRE);
  not not_4 (not_4_out, _2_CLR);
  J_K_Flip_Flop #(.trigger("falling")) Fall (
    .J(Rise_q), .clk(_1CLK), .K(Rise_2_q), .Q(Fall_q), .Qn(Fall_qn), .preset(not_1_out), .reset(not_2_out));  // open: en
  and and_1 (and_1_out, not_1_out, not_2_out);
  J_K_Flip_Flop #(.trigger("falling")) Fall_2 (
    .J(Rise_3_q), .clk(_2CLK), .K(Rise_4_q), .Q(Fall_2_q), .Qn(Fall_2_qn), .preset(not_3_out),
    .reset(not_4_out));  // open: en
  and and_2 (and_2_out, not_3_out, not_4_out);
  or or_1 (_1Q, and_1_out, Fall_q);
  or or_2 (_1_Q, Fall_qn, and_1_out);
  or or_3 (_2Q, and_2_out, Fall_2_q);
  or or_4 (_2_Q, Fall_2_qn, and_2_out);

  // Notes on the sheet:
  //   74LS111
endmodule
