// Logisim project 74LS113.circ as structural Verilog: 1 circuit, main circuit 74LS113
module _74LS113 (
  input  _1J,
  input  _1_CLK,
  input  _1K,
  input  _1_PRE,
  input  _2J,
  input  _2_CLK,
  input  _2K,
  input  _2_PRE,
  output _1Q,
  output _1_Q,
  output _2Q,
  output _2_Q
);

  wire not_1_out, not_2_out;

  not not_1 (not_1_out, _1_PRE);
  not not_2 (not_2_out, _2_PRE);
  J_K_Flip_Flop #(.trigger("falling")) Fall (
    .J(_1J), .clk(_1_CLK), .K(_1K), .Q(_1Q), .Qn(_1_Q), .preset(not_1_out));  // open: en, reset
  J_K_Flip_Flop #(.trigger("falling")) Fall_2 (
    .J(_2J), .clk(_2_CLK), .K(_2K), .Q(_2Q), .Qn(_2_Q), .preset(not_2_out));  // open: en, reset

  // Notes on the sheet:
  //   74LS113
endmodule
