// Logisim project 74LS115.circ as structural Verilog: 1 circuit, main circuit 74LS115
module _74LS115 (
  input  _1CLK,
  input  _1J,
  input  _1K,
  input  _1_CLR,
  input  _2CLK,
  input  _2J,
  input  _2K,
  input  _2_CLR,
  output _1Q,
  output _1_Q,
  output _2Q,
  output _2_Q
);

  wire not_1_out, not_2_out, Rise_2_q, Rise_3_q, Rise_4_q, Rise_q;

  D_Flip_Flop Rise (.clk(_1CLK), .D(_1J), .Q(Rise_q));  // open: Qn, preset, en, reset
  D_Flip_Flop Rise_2 (.clk(_1CLK), .D(_1K), .Q(Rise_2_q));  // open: Qn, preset, en, reset
  not not_1 (not_1_out, _1_CLR);
  D_Flip_Flop Rise_3 (.clk(_2CLK), .D(_2J), .Q(Rise_3_q));  // open: Qn, preset, en, reset
  D_Flip_Flop Rise_4 (.clk(_2CLK), .D(_2K), .Q(Rise_4_q));  // open: Qn, preset, en, reset
  not not_2 (not_2_out, _2_CLR);
  J_K_Flip_Flop #(.trigger("falling")) Fall (
    .J(Rise_q), .clk(_1CLK), .K(Rise_2_q), .Q(_1Q), .Qn(_1_Q), .reset(not_1_out));  // open: preset, en
  J_K_Flip_Flop #(.trigger("falling")) Fall_2 (
    .J(Rise_3_q), .clk(_2CLK), .K(Rise_4_q), .Q(_2Q), .Qn(_2_Q), .reset(not_2_out));  // open: preset, en

  // Notes on the sheet:
  //   74LS115
endmodule
