// Logisim project 74LS118.circ as structural Verilog: 1 circuit, main circuit 74LS118
module _74LS118 (
  input  nS1,
  input  nS2,
  input  nS3,
  input  nS4,
  input  nS5,
  input  nS6,
  input  nRESET,
  output Q1,
  output Q2,
  output Q3,
  output Q4,
  output Q5,
  output Q6
);

  wire nand_2_out, nand_4_out, nand_6_out, nand_8_out, nand_10_out, nand_12_out;

  nand nand_1 (Q1, nS1, nand_2_out);
  nand nand_2 (nand_2_out, Q1, nRESET);
  nand nand_3 (Q2, nS2, nand_4_out);
  nand nand_4 (nand_4_out, Q2, nRESET);
  nand nand_5 (Q3, nS3, nand_6_out);
  nand nand_6 (nand_6_out, Q3, nRESET);
  nand nand_7 (Q4, nS4, nand_8_out);
  nand nand_8 (nand_8_out, Q4, nRESET);
  nand nand_9 (Q5, nS5, nand_10_out);
  nand nand_10 (nand_10_out, Q5, nRESET);
  nand nand_11 (Q6, nS6, nand_12_out);
  nand nand_12 (nand_12_out, Q6, nRESET);

  // Notes on the sheet:
  //   74LS118
endmodule
