// Logisim project 74LS120.circ as structural Verilog: 1 circuit, main circuit 74LS120
module _74LS120 (
  input  _1_R,
  input  _1_S1,
  input  _1_S2,
  input  _1C,
  input  _1M,
  input  _2_R,
  input  _2_S1,
  input  _2_S2,
  input  _2C,
  input  _2M,
  output _1Y,
  output _1_Y,
  output _2Y,
  output _2_Y
);

  wire nand_1_out, nand_2_out, nand_4_out, nand_5_out, nand_6_out, nand_8_out, or_1_out, or_2_out, or_3_out,
       or_4_out, or_5_out, or_6_out, or_7_out, or_8_out;

  or or_1 (or_1_out, ~_1_R, ~or_2_out);  // OR_Gate
  or or_2 (or_2_out, ~or_1_out, ~_1_S1, ~_1_S2);  // OR_Gate
  or or_3 (or_3_out, ~_2_R, ~or_4_out);  // OR_Gate
  or or_4 (or_4_out, ~or_3_out, ~_2_S1, ~_2_S2);  // OR_Gate
  nand nand_1 (nand_1_out, ~_1C, or_2_out, nand_4_out);  // NAND_Gate
  nand nand_2 (nand_2_out, or_2_out, nand_4_out, or_5_out);
  nand nand_3 (_1_Y, or_5_out, _1C);
  nand nand_4 (nand_4_out, or_2_out, _1M, or_6_out);
  nand nand_5 (nand_5_out, ~_2C, or_4_out, nand_8_out);  // NAND_Gate
  nand nand_6 (nand_6_out, or_4_out, nand_8_out, or_7_out);
  nand nand_7 (_2_Y, or_7_out, _2C);
  nand nand_8 (nand_8_out, or_4_out, _2M, or_8_out);
  or or_5 (or_5_out, ~nand_1_out, ~nand_2_out, ~_1_Y);  // OR_Gate
  or or_6 (or_6_out, ~_1_Y, ~nand_4_out);  // OR_Gate
  or or_7 (or_7_out, ~nand_5_out, ~nand_6_out, ~_2_Y);  // OR_Gate
  or or_8 (or_8_out, ~_2_Y, ~nand_8_out);  // OR_Gate
  not not_1 (_1Y, _1_Y);
  not not_2 (_2Y, _2_Y);

  // Notes on the sheet:
  //   74LS120
endmodule
