// Logisim project 74LS125.circ as structural Verilog: 1 circuit, main circuit 74LS125
module _74LS125 (
  input  _1A,
  input  _1_G,
  input  _2A,
  input  _2_G,
  input  _3A,
  input  _3_G,
  input  _4A,
  input  _4_G,
  output _1Y,
  output _2Y,
  output _3Y,
  output _4Y
);

  wire not_1_out, not_2_out, not_3_out, not_4_out;

  assign _1Y = not_1_out ? _1A : 1'bz;  // Controlled_Buffer controlled_buffer_1
  not not_1 (not_1_out, _1_G);
  assign _2Y = not_2_out ? _2A : 1'bz;  // Controlled_Buffer controlled_buffer_2
  not not_2 (not_2_out, _2_G);
  assign _3Y = not_3_out ? _3A : 1'bz;  // Controlled_Buffer controlled_buffer_3
  not not_3 (not_3_out, _3_G);
  assign _4Y = not_4_out ? _4A : 1'bz;  // Controlled_Buffer controlled_buffer_4
  not not_4 (not_4_out, _4_G);

  // Notes on the sheet:
  //   74LS125
endmodule
