// Logisim project 74LS126.circ as structural Verilog: 1 circuit, main circuit 74LS126
module _74LS126 (
  input  _1A,
  input  _1G,
  input  _2A,
  input  _2G,
  input  _3A,
  input  _3G,
  input  _4A,
  input  _4G,
  output _1Y,
  output _2Y,
  output _3Y,
  output _4Y
);

  assign _1Y = _1G ? _1A : 1'bz;  // Controlled_Buffer controlled_buffer_1
  assign _2Y = _2G ? _2A : 1'bz;  // Controlled_Buffer controlled_buffer_2
  assign _3Y = _3G ? _3A : 1'bz;  // Controlled_Buffer controlled_buffer_3
  assign _4Y = _4G ? _4A : 1'bz;  // Controlled_Buffer controlled_buffer_4

  // Notes on the sheet:
  //   74LS126
endmodule
