// Logisim project 74LS131.circ as structural Verilog: 1 circuit, main circuit 74LS131
module _74LS131 (
  input  nG2,
  input  G1,
  input  CLK,
  input  A,
  input  B,
  input  C,
  output out_7,
  output out_8,
  output out_9,
  output out_10,
  output out_11,
  output out_12,
  output out_13,
  output out_14
);

  wire and_1_out, demultiplexer_1_out0, demultiplexer_1_out1, demultiplexer_1_out2, demultiplexer_1_out3,
       demultiplexer_1_out4, demultiplexer_1_out5, demultiplexer_1_out6, demultiplexer_1_out7;
  wire [2:0] Rise_q;

  and and_1 (and_1_out, ~nG2, G1);  // AND_Gate
  D_Flip_Flop Rise (.clk(CLK), .D(A), .Q(Rise_q[0]));  // open: Qn, preset, en, reset
  D_Flip_Flop Rise_2 (.clk(CLK), .D(B), .Q(Rise_q[1]));  // open: Qn, preset, en, reset
  D_Flip_Flop Rise_3 (.clk(CLK), .D(C), .Q(Rise_q[2]));  // open: Qn, preset, en, reset
  Demultiplexer #(.select(3), .enable("false")) demultiplexer_1 (
    .out0(demultiplexer_1_out0), .out1(demultiplexer_1_out1), .out2(demultiplexer_1_out2),
    .out3(demultiplexer_1_out3), .out4(demultiplexer_1_out4), .out5(demultiplexer_1_out5),
    .out6(demultiplexer_1_out6), .out7(demultiplexer_1_out7), .in(1'b1), .sel(Rise_q));
  Pull_Resistor #(.pull(1)) pull_resistor_1 (.node(out_8));
  Pull_Resistor #(.pull(1)) pull_resistor_2 (.node(out_9));
  Pull_Resistor #(.pull(1)) pull_resistor_3 (.node(out_7));
  Pull_Resistor #(.pull(1)) pull_resistor_4 (.node(out_10));
  assign out_7 = and_1_out ? ~demultiplexer_1_out0 : 1'bz;  // Controlled_Inverter controlled_inverter_1
  assign out_8 = and_1_out ? ~demultiplexer_1_out1 : 1'bz;  // Controlled_Inverter controlled_inverter_2
  assign out_9 = and_1_out ? ~demultiplexer_1_out2 : 1'bz;  // Controlled_Inverter controlled_inverter_3
  assign out_10 = and_1_out ? ~demultiplexer_1_out3 : 1'bz;  // Controlled_Inverter controlled_inverter_4
  assign out_11 = and_1_out ? ~demultiplexer_1_out4 : 1'bz;  // Controlled_Inverter controlled_inverter_5
  assign out_12 = and_1_out ? ~demultiplexer_1_out5 : 1'bz;  // Controlled_Inverter controlled_inverter_6
  assign out_13 = and_1_out ? ~demultiplexer_1_out6 : 1'bz;  // Controlled_Inverter controlled_inverter_7
  assign out_14 = and_1_out ? ~demultiplexer_1_out7 : 1'bz;  // Controlled_Inverter controlled_inverter_8
  Pull_Resistor #(.pull(1)) pull_resistor_5 (.node(out_12));
  Pull_Resistor #(.pull(1)) pull_resistor_6 (.node(out_11));
  Pull_Resistor #(.pull(1)) pull_resistor_7 (.node(out_14));
  Pull_Resistor #(.pull(1)) pull_resistor_8 (.node(out_13));

  // Notes on the sheet:
  //   74LS131
endmodule
