// Logisim project 74LS137.circ as structural Verilog: 1 circuit, main circuit 74LS137
module _74LS137 (
  input  nOE1,
  input  OE0,
  input  nLE,
  input  A0,
  input  A1,
  input  A2,
  output nY0,
  output nY1,
  output nY2,
  output nY3,
  output nY4,
  output nY5,
  output nY6,
  output nY7
);

  wire demultiplexer_1_out0, demultiplexer_1_out1, demultiplexer_1_out2, demultiplexer_1_out3,
       demultiplexer_1_out4, demultiplexer_1_out5, demultiplexer_1_out6, demultiplexer_1_out7, nor_1_out,
       not_1_out;
  wire [2:0] Low_Level_q;

  nor nor_1 (nor_1_out, nOE1, not_1_out);
  not not_1 (not_1_out, OE0);
  D_Flip_Flop #(.trigger("low")) Low_Level (.clk(nLE), .D(A0), .Q(Low_Level_q[0]));  // open: Qn, preset, en, reset
  D_Flip_Flop #(.trigger("low")) Low_Level_2 (.clk(nLE), .D(A1), .Q(Low_Level_q[1]));  // open: Qn, preset, en, reset
  D_Flip_Flop #(.trigger("low")) Low_Level_3 (.clk(nLE), .D(A2), .Q(Low_Level_q[2]));  // open: Qn, preset, en, reset
  Demultiplexer #(.select(3), .disabled(0)) demultiplexer_1 (
    .out0(demultiplexer_1_out0), .out1(demultiplexer_1_out1), .out2(demultiplexer_1_out2),
    .out3(demultiplexer_1_out3), .out4(demultiplexer_1_out4), .out5(demultiplexer_1_out5),
    .out6(demultiplexer_1_out6), .out7(demultiplexer_1_out7), .in(1'b1), .sel(Low_Level_q), .en(nor_1_out));
  not not_2 (nY0, demultiplexer_1_out0);
  not not_3 (nY1, demultiplexer_1_out1);
  not not_4 (nY2, demultiplexer_1_out2);
  not not_5 (nY3, demultiplexer_1_out3);
  not not_6 (nY4, demultiplexer_1_out4);
  not not_7 (nY5, demultiplexer_1_out5);
  not not_8 (nY6, demultiplexer_1_out6);
  not not_9 (nY7, demultiplexer_1_out7);

  // Notes on the sheet:
  //   74LS137
endmodule
