// Logisim project 74LS139.circ as structural Verilog: 1 circuit, main circuit 74LS139
module _74LS139 (
  input  _1_G,
  input  _1A,
  input  _1B,
  input  _2_G,
  input  _2A,
  input  _2B,
  output _1Y0,
  output _1Y1,
  output _1Y2,
  output _1Y3,
  output _2Y0,
  output _2Y1,
  output _2Y2,
  output _2Y3
);

  wire demultiplexer_1_out0, demultiplexer_1_out1, demultiplexer_1_out2, demultiplexer_1_out3,
       demultiplexer_2_out0, demultiplexer_2_out1, demultiplexer_2_out2, demultiplexer_2_out3, not_1_out,
       not_2_out;

  not not_1 (not_1_out, _1_G);
  not not_2 (not_2_out, _2_G);
  not not_3 (_1Y0, demultiplexer_1_out0);
  not not_4 (_1Y1, demultiplexer_1_out1);
  Demultiplexer #(.select(2), .disabled(0)) demultiplexer_1 (
    .out0(demultiplexer_1_out0), .out1(demultiplexer_1_out1), .out2(demultiplexer_1_out2),
    .out3(demultiplexer_1_out3), .in(1'b1), .sel({_1B, _1A}), .en(not_1_out));
  not not_5 (_1Y2, demultiplexer_1_out2);
  not not_6 (_1Y3, demultiplexer_1_out3);
  not not_7 (_2Y0, demultiplexer_2_out0);
  not not_8 (_2Y1, demultiplexer_2_out1);
  not not_9 (_2Y2, demultiplexer_2_out2);
  Demultiplexer #(.select(2), .disabled(0)) demultiplexer_2 (
    .out0(demultiplexer_2_out0), .out1(demultiplexer_2_out1), .out2(demultiplexer_2_out2),
    .out3(demultiplexer_2_out3), .in(1'b1), .sel({_2B, _2A}), .en(not_2_out));
  not not_10 (_2Y3, demultiplexer_2_out3);

  // Notes on the sheet:
  //   74LS139
endmodule
