// Logisim project 74LS141.circ as structural Verilog: 1 circuit, main circuit 74LS141
module _74LS141 (
  input  A,
  input  B,
  input  C,
  input  D,
  output _0,
  output _5,
  output _1,
  output _6,
  output _2,
  output _7,
  output _3,
  output _8,
  output _4,
  output _9
);

  wire nA, nB, nC, nD;

  not not_1 (nA, A);
  not not_2 (nB, B);
  not not_3 (nC, C);
  not not_4 (nD, D);
  and u__0 (_0, nA, nB, nC, nD);
  and u__1 (_1, A, nB, nC, nD);
  and u__2 (_2, nA, B, nC, nD);
  and u__3 (_3, A, B, nC, nD);
  and u__4 (_4, nA, nB, C, nD);
  and u__5 (_5, A, nB, C, nD);
  and u__6 (_6, nA, B, C, nD);
  and u__7 (_7, A, B, C, nD);
  and u__8 (_8, nA, nB, nC, D);
  and u__9 (_9, A, nB, nC, D);

  // Notes on the sheet:
  //   74LS141
endmodule
