// Logisim project 74LS142.circ as structural Verilog: 1 circuit, main circuit 74LS142
module _74LS142 (
  input  nSTRB,
  input  CLK,
  input  nCLR,
  output _0,
  output _1,
  output _2,
  output _3,
  output _4,
  output _5,
  output _6,
  output _7,
  output _8,
  output _9,
  output nQD
);

  wire not_1_out;
  wire [3:0] counter_1_q, Low_Level_q;

  Counter #(.width(4), .max('h9)) counter_1 (
    .Q(counter_1_q), .clk(CLK), .clr(not_1_out));  // open: load, D, count, carry
  not not_1 (not_1_out, nCLR);
  Demultiplexer #(.select(4)) demultiplexer_1 (
    .out0(_0), .out1(_1), .out2(_2), .out3(_3), .out4(_4), .out5(_5), .out6(_6), .out7(_7), .out8(_8),
    .out9(_9), .in(1'b1), .sel(Low_Level_q));  // open: out10, out11, out12, out13, out14, out15, en
  Register #(.width(4), .trigger("low")) Low_Level (.D(counter_1_q), .Q(Low_Level_q), .clk(nSTRB));  // open: en, clr
  nor nor_1 (nQD, _8, _9);

  // Notes on the sheet:
  //   74LS142
endmodule
