// Logisim project 74LS143.circ as structural Verilog: 2 circuits, main circuit 74LS143
module _74LS143 (
  input  nSCEI,
  input  nPCEI,
  input  CLOCK,
  input  nCLEAR,
  input  nLATCH,
  input  nRBI,
  input  BI,
  input  DP_INPUT,
  output nMAX_COUNT,
  output QA,
  output QB,
  output QC,
  output QD,
  output a,
  output b,
  output c,
  output d,
  output e,
  output f,
  output g,
  output dp,
  output nRBO
);

  wire and_1_out, and_2_out, and_3_out, and_4_out, and_5_out, and_6_out, and_7_out, buffer_1_out,
       demultiplexer_1_out0, demultiplexer_1_out1, demultiplexer_1_out2, demultiplexer_1_out3,
       demultiplexer_1_out4, demultiplexer_1_out5, demultiplexer_1_out6, demultiplexer_1_out7,
       demultiplexer_1_out9, Fall_2_q, Fall_2_qn, Fall_3_q, Fall_3_qn, Fall_4_q, Fall_4_qn, Fall_q, Fall_qn,
       Low_2_qn, Low_3_qn, Low_4_qn, Low_qn, not_1_out, not_2_out, not_3_out, not_4_out, not_5_out,
       not_6_out, not_7_out, not_8_out, not_9_out, not_10_out, not_11_out, not_12_out, or_1_out;

  not not_1 (not_1_out, CLOCK);
  and and_1 (and_1_out, Fall_3_q, Fall_2_q);
  not not_2 (not_2_out, nSCEI);
  and and_2 (and_2_out, ~nSCEI, ~nPCEI);  // AND_Gate
  or or_1 (or_1_out, and_1_out, Fall_4_q);
  and and_3 (and_3_out, and_2_out, not_1_out);
  and and_4 (and_4_out, Fall_q, and_2_out, Fall_4_qn, not_1_out);
  and and_5 (and_5_out, Fall_2_q, Fall_q, and_2_out, not_1_out);
  and and_6 (and_6_out, Fall_q, and_2_out, or_1_out, not_1_out);
  T_Flip_Flop #(.trigger("falling")) Fall (
    .clk(and_3_out), .T(1'b1), .Q(Fall_q), .Qn(Fall_qn), .reset(not_3_out));  // open: preset, en
  T_Flip_Flop #(.trigger("falling")) Fall_2 (
    .clk(and_4_out), .T(1'b1), .Q(Fall_2_q), .Qn(Fall_2_qn), .reset(not_3_out));  // open: preset, en
  T_Flip_Flop #(.trigger("falling")) Fall_3 (
    .clk(and_5_out), .T(1'b1), .Q(Fall_3_q), .Qn(Fall_3_qn), .reset(not_3_out));  // open: preset, en
  T_Flip_Flop #(.trigger("falling")) Fall_4 (
    .clk(and_6_out), .T(1'b1), .Q(Fall_4_q), .Qn(Fall_4_qn), .reset(not_3_out));  // open: preset, en
  not not_3 (not_3_out, nCLEAR);
  nand nand_1 (nMAX_COUNT, not_2_out, Fall_q, Fall_4_q);
  S_R_Flip_Flop #(.trigger("low")) Low (
    .S(Fall_q), .clk(nLATCH), .R(Fall_qn), .Q(QA), .Qn(Low_qn));  // open: preset, reset, en
  S_R_Flip_Flop #(.trigger("low")) Low_2 (
    .S(Fall_2_q), .clk(nLATCH), .R(Fall_2_qn), .Q(QB), .Qn(Low_2_qn));  // open: preset, reset, en
  S_R_Flip_Flop #(.trigger("low")) Low_3 (
    .S(Fall_3_q), .clk(nLATCH), .R(Fall_3_qn), .Q(QC), .Qn(Low_3_qn));  // open: preset, reset, en
  S_R_Flip_Flop #(.trigger("low")) Low_4 (
    .S(Fall_4_q), .clk(nLATCH), .R(Fall_4_qn), .Q(QD), .Qn(Low_4_qn));  // open: preset, reset, en
  Demultiplexer #(.select(4), .enable("false")) demultiplexer_1 (
    .out0(demultiplexer_1_out0), .out1(demultiplexer_1_out1), .out2(demultiplexer_1_out2),
    .out3(demultiplexer_1_out3), .out4(demultiplexer_1_out4), .out5(demultiplexer_1_out5),
    .out6(demultiplexer_1_out6), .out7(demultiplexer_1_out7), .out9(demultiplexer_1_out9), .in(1'b1),
    .sel({QD, QC, QB, QA}));  // open: out8, out10, out11, out12, out13, out14, out15
  and and_7 (and_7_out, Low_qn, Low_2_qn, Low_3_qn, Low_4_qn, ~nRBI);  // AND_Gate
  nor nor_1 (nRBO, and_7_out, BI);
  not not_4 (not_4_out, demultiplexer_1_out0);
  not not_5 (not_5_out, demultiplexer_1_out1);
  not not_6 (not_6_out, demultiplexer_1_out2);
  not not_7 (not_7_out, demultiplexer_1_out3);
  not not_8 (not_8_out, demultiplexer_1_out4);
  not not_9 (not_9_out, demultiplexer_1_out5);
  not not_10 (not_10_out, demultiplexer_1_out6);
  not not_11 (not_11_out, demultiplexer_1_out7);
  not not_12 (not_12_out, demultiplexer_1_out9);
  buf buffer_1 (buffer_1_out, nRBO);
  nand nand_2 (a, not_5_out, not_8_out, buffer_1_out);
  nand nand_3 (b, not_9_out, not_10_out, buffer_1_out);
  nand nand_4 (c, not_6_out, buffer_1_out);
  nand nand_5 (d, not_5_out, not_8_out, not_11_out, buffer_1_out);
  nand nand_6 (e, not_7_out, not_8_out, not_5_out, not_9_out, not_11_out, not_12_out, buffer_1_out);
  nand nand_7 (f, not_7_out, not_6_out, not_5_out, not_11_out, buffer_1_out);
  nand nand_8 (g, not_5_out, not_4_out, not_11_out, buffer_1_out);
  nand nand_9 (dp, buffer_1_out, DP_INPUT);

  // Notes on the sheet:
  //   SERIAL/PARALLEL
  //   COUNT
  //   ENABLE
  //   INPUTS
  //   74LS143
  //   8x Open Collector!
  //   nand_2 drives only 0 and floats otherwise
  //   nand_3 drives only 0 and floats otherwise
  //   nand_4 drives only 0 and floats otherwise
  //   nand_5 drives only 0 and floats otherwise
  //   nand_6 drives only 0 and floats otherwise
  //   nand_7 drives only 0 and floats otherwise
  //   nand_8 drives only 0 and floats otherwise
  //   nand_9 drives only 0 and floats otherwise
endmodule

module Test (
  input  CK,
  input  nSTROBE,
  input  nRBI,
  input  in_4,
  input  BI,
  input  DP,
  input  nPCEI,
  input  nCLEAR
);

  wire n74ls143_1_nrbo, n74ls143_2_nmax_count, pull_resistor_1_node, pull_resistor_2_node,
       pull_resistor_3_node, pull_resistor_4_node, pull_resistor_5_node, pull_resistor_6_node,
       pull_resistor_7_node, pull_resistor_8_node, pull_resistor_9_node, pull_resistor_10_node,
       pull_resistor_11_node, pull_resistor_12_node, pull_resistor_13_node, pull_resistor_14_node,
       pull_resistor_15_node, pull_resistor_16_node;

  Pull_Resistor #(.pull(1)) pull_resistor_1 (.node(pull_resistor_1_node));
  Pull_Resistor #(.pull(1)) pull_resistor_2 (.node(pull_resistor_2_node));
  Pull_Resistor #(.pull(1)) pull_resistor_3 (.node(pull_resistor_3_node));
  Pull_Resistor #(.pull(1)) pull_resistor_4 (.node(pull_resistor_4_node));
  Pull_Resistor #(.pull(1)) pull_resistor_5 (.node(pull_resistor_5_node));
  Pull_Resistor #(.pull(1)) pull_resistor_6 (.node(pull_resistor_6_node));
  Pull_Resistor #(.pull(1)) pull_resistor_7 (.node(pull_resistor_7_node));
  Pull_Resistor #(.pull(1)) pull_resistor_8 (.node(pull_resistor_8_node));
  _74LS143 u_74ls143_1 (
    .nSCEI(n74ls143_2_nmax_count), .nPCEI(nPCEI), .CLOCK(CK), .nCLEAR(nCLEAR), .nLATCH(nSTROBE),
    .a(pull_resistor_1_node), .b(pull_resistor_4_node), .c(pull_resistor_8_node), .d(pull_resistor_6_node),
    .e(pull_resistor_5_node), .f(pull_resistor_3_node), .g(pull_resistor_7_node), .dp(pull_resistor_2_node),
    .nRBI(nRBI), .BI(BI), .nRBO(n74ls143_1_nrbo), .DP_INPUT(DP));  // open: nMAX_COUNT, QA, QB, QC, QD
  _7_Segment_Display #(.active("false")) u_7_segment_display_1 (
    .g(pull_resistor_7_node), .f(pull_resistor_3_node), .a(pull_resistor_1_node), .b(pull_resistor_4_node),
    .e(pull_resistor_5_node), .d(pull_resistor_6_node), .c(pull_resistor_8_node), .dp(pull_resistor_2_node));
  Pull_Resistor #(.pull(1)) pull_resistor_9 (.node(pull_resistor_9_node));
  Pull_Resistor #(.pull(1)) pull_resistor_10 (.node(pull_resistor_10_node));
  Pull_Resistor #(.pull(1)) pull_resistor_11 (.node(pull_resistor_11_node));
  Pull_Resistor #(.pull(1)) pull_resistor_12 (.node(pull_resistor_12_node));
  Pull_Resistor #(.pull(1)) pull_resistor_13 (.node(pull_resistor_13_node));
  Pull_Resistor #(.pull(1)) pull_resistor_14 (.node(pull_resistor_14_node));
  Pull_Resistor #(.pull(1)) pull_resistor_15 (.node(pull_resistor_15_node));
  Pull_Resistor #(.pull(1)) pull_resistor_16 (.node(pull_resistor_16_node));
  _74LS143 u_74ls143_2 (
    .nSCEI(in_4), .nPCEI(nPCEI), .CLOCK(CK), .nCLEAR(nCLEAR), .nLATCH(nSTROBE), .a(pull_resistor_11_node),
    .b(pull_resistor_10_node), .c(pull_resistor_14_node), .d(pull_resistor_9_node),
    .e(pull_resistor_13_node), .f(pull_resistor_15_node), .g(pull_resistor_12_node),
    .dp(pull_resistor_16_node), .nMAX_COUNT(n74ls143_2_nmax_count), .nRBI(n74ls143_1_nrbo), .BI(BI),
    .DP_INPUT(DP));  // open: QA, QB, QC, QD, nRBO
  _7_Segment_Display #(.active("false")) u_7_segment_display_2 (
    .g(pull_resistor_12_node), .f(pull_resistor_15_node), .a(pull_resistor_11_node),
    .b(pull_resistor_10_node), .e(pull_resistor_13_node), .d(pull_resistor_9_node),
    .c(pull_resistor_14_node), .dp(pull_resistor_16_node));

  // Notes on the sheet:
  //   TEST
  //   TEST
endmodule
