// Logisim project 74LS146.circ as structural Verilog: 1 circuit, main circuit 74LS146
module _74LS146 (
  input  nENABLE,
  input  A,
  input  B,
  input  C,
  output out_5,
  output out_6,
  output out_7,
  output out_8,
  output out_9,
  output out_10,
  output out_11,
  output out_12
);

  wire decoder_1_out0, decoder_1_out1, decoder_1_out2, decoder_1_out3, decoder_1_out4, decoder_1_out5,
       decoder_1_out6, decoder_1_out7, not_1_out;

  not not_1 (not_1_out, nENABLE);
  Decoder #(.select(3), .disabled(0)) decoder_1 (
    .out0(decoder_1_out0), .out1(decoder_1_out1), .out2(decoder_1_out2), .out3(decoder_1_out3),
    .out4(decoder_1_out4), .out5(decoder_1_out5), .out6(decoder_1_out6), .out7(decoder_1_out7),
    .sel({C, B, A}), .en(not_1_out));
  not not_2 (out_5, decoder_1_out0);
  not not_3 (out_6, decoder_1_out1);
  not not_4 (out_7, decoder_1_out2);
  not not_5 (out_8, decoder_1_out3);
  not not_6 (out_9, decoder_1_out4);
  not not_7 (out_10, decoder_1_out5);
  not not_8 (out_11, decoder_1_out6);
  not not_9 (out_12, decoder_1_out7);

  // Notes on the sheet:
  //   74LS146
endmodule
