// Logisim project 74LS147.circ as structural Verilog: 1 circuit, main circuit 74LS147
module _74LS147 (
  input  _1,
  input  _2,
  input  _3,
  input  _4,
  input  _5,
  input  _6,
  input  _7,
  input  _8,
  input  _9,
  output A,
  output B,
  output C,
  output D
);

  wire and_1_out, and_2_out, and_3_out, and_4_out, and_5_out, and_6_out, and_7_out, and_8_out, and_9_out,
       and_10_out, and_11_out, and_12_out, and_13_out, nor_1_out, not_1_out, not_2_out, not_3_out, not_4_out,
       not_5_out, not_6_out, not_7_out, not_8_out, not_9_out, not_10_out, not_11_out, not_12_out, not_13_out;

  not not_1 (not_1_out, _1);
  not not_2 (not_2_out, _2);
  not not_3 (not_3_out, _3);
  not not_4 (not_4_out, _4);
  not not_5 (not_5_out, _5);
  not not_6 (not_6_out, _6);
  not not_7 (not_7_out, _7);
  not not_8 (not_8_out, _8);
  not not_9 (not_9_out, _9);
  not not_10 (not_10_out, not_2_out);
  not not_11 (not_11_out, not_4_out);
  not not_12 (not_12_out, not_5_out);
  not not_13 (not_13_out, not_6_out);
  nor nor_1 (nor_1_out, not_8_out, not_9_out);
  and and_1 (and_1_out, not_1_out, not_10_out, not_11_out, not_13_out, nor_1_out);
  and and_2 (and_2_out, not_3_out, not_11_out, not_13_out, nor_1_out);
  and and_3 (and_3_out, not_5_out, not_13_out, nor_1_out);
  and and_4 (and_4_out, not_7_out, nor_1_out);
  and and_5 (and_5_out, not_9_out, not_9_out);
  and and_6 (and_6_out, not_2_out, not_11_out, not_12_out, nor_1_out);
  and and_7 (and_7_out, not_3_out, not_11_out, not_12_out, nor_1_out);
  and and_8 (and_8_out, not_6_out, nor_1_out);
  and and_9 (and_9_out, not_7_out, nor_1_out);
  and and_10 (and_10_out, not_4_out, nor_1_out);
  and and_11 (and_11_out, not_5_out, nor_1_out);
  and and_12 (and_12_out, not_6_out, nor_1_out);
  and and_13 (and_13_out, not_7_out, nor_1_out);
  nor nor_2 (A, and_1_out, and_2_out, and_3_out, and_4_out, and_5_out);
  nor nor_3 (B, and_6_out, and_7_out, and_8_out, and_9_out);
  nor nor_4 (C, and_10_out, and_11_out, and_12_out, and_13_out);
  nor nor_5 (D, not_8_out, not_9_out);

  // Notes on the sheet:
  //   74LS147
endmodule
