// Logisim project 74LS148.circ as structural Verilog: 1 circuit, main circuit 74LS148
module _74LS148 (
  input  _0,
  input  _1,
  input  _2,
  input  _3,
  input  _4,
  input  _5,
  input  _6,
  input  _7,
  input  nEI,
  output EO,
  output A0,
  output A1,
  output A2,
  output nGS
);

  wire not_1_out, not_2_out, not_3_out, not_4_out, not_5_out, not_6_out, not_7_out, not_8_out, not_11_out,
       priority_encoder_1_en_out, priority_encoder_1_gs;

  not not_1 (not_1_out, _0);
  not not_2 (not_2_out, _1);
  not not_3 (not_3_out, _2);
  not not_4 (not_4_out, _3);
  not not_5 (not_5_out, _4);
  not not_6 (not_6_out, _5);
  not not_7 (not_7_out, _6);
  not not_8 (not_8_out, _7);
  not not_9 (EO, priority_encoder_1_en_out);
  Pull_Resistor pull_resistor_1 (.node({A2, A1, A0}));
  Priority_Encoder #(.disabled(0)) priority_encoder_1 (
    .in0(not_1_out), .in1(not_2_out), .in2(not_3_out), .in3(not_4_out), .in4(not_5_out), .in5(not_6_out),
    .in6(not_7_out), .in7(not_8_out), .out({A2, A1, A0}), .en_in(not_11_out), .gs(priority_encoder_1_gs),
    .en_out(priority_encoder_1_en_out));
  not not_10 (nGS, priority_encoder_1_gs);
  not not_11 (not_11_out, nEI);

  // Notes on the sheet:
  //   74LS148
endmodule
