// Logisim project 74LS149.circ as structural Verilog: 1 circuit, main circuit 74LS149
module _74LS149 (
  input  nRI7,
  input  nRI6,
  input  nRI5,
  input  nRI4,
  input  nRI3,
  input  nRI2,
  input  nRI1,
  input  nRI0,
  input  nRQE,
  output nRO7,
  output nRO6,
  output nRO5,
  output nRO4,
  output nRO3,
  output nRO2,
  output nRO1,
  output nRO0,
  output nRQP
);

  wire nand_9_out, not_1_out, not_2_out, not_3_out, not_4_out, not_5_out, not_6_out, not_7_out, not_8_out,
       not_9_out, not_10_out, not_11_out, not_12_out, not_13_out, not_14_out, not_15_out, not_16_out,
       not_17_out;

  not not_1 (not_1_out, nRI7);
  not not_2 (not_2_out, nRI6);
  not not_3 (not_3_out, nRI5);
  not not_4 (not_4_out, nRI4);
  not not_5 (not_5_out, nRI3);
  not not_6 (not_6_out, nRI2);
  not not_7 (not_7_out, nRI1);
  not not_8 (not_8_out, nRI0);
  not not_9 (not_9_out, nRQE);
  not not_10 (not_10_out, not_1_out);
  not not_11 (not_11_out, not_2_out);
  not not_12 (not_12_out, not_3_out);
  not not_13 (not_13_out, not_4_out);
  not not_14 (not_14_out, not_5_out);
  not not_15 (not_15_out, not_6_out);
  not not_16 (not_16_out, not_7_out);
  not not_17 (not_17_out, not_8_out);
  nand nand_1 (nRO7, not_1_out, not_9_out);
  nand nand_2 (nRO6, not_10_out, not_2_out, not_9_out);
  nand nand_3 (nRO5, not_11_out, not_10_out, not_3_out, not_9_out);
  nand nand_4 (nRO4, not_12_out, not_11_out, not_10_out, not_4_out, not_9_out);
  nand nand_5 (nRO3, not_13_out, not_12_out, not_11_out, not_10_out, not_5_out, not_9_out);
  nand nand_6 (nRO2, not_14_out, not_13_out, not_12_out, not_11_out, not_10_out, not_6_out, not_9_out);
  nand nand_7 (nRO1, not_15_out, not_14_out, not_13_out, not_12_out, not_11_out, not_10_out, not_7_out, not_9_out);
  nand nand_8 (nRO0, not_16_out, not_15_out, not_14_out, not_13_out, not_12_out, not_11_out, not_10_out, not_8_out, not_9_out);
  nand nand_9 (nand_9_out, not_10_out, not_11_out, not_12_out, not_13_out, not_14_out, not_15_out, not_16_out, not_17_out);
  nand nand_10 (nRQP, not_9_out, nand_9_out);

  // Notes on the sheet:
  //   74LS149
endmodule
