// Logisim project 74LS151.circ as structural Verilog: 1 circuit, main circuit 74LS151
module _74LS151 (
  input  D0,
  input  D1,
  input  D2,
  input  D3,
  input  D4,
  input  D5,
  input  D6,
  input  D7,
  input  A,
  input  B,
  input  C,
  input  nG,
  output Y,
  output W
);

  wire not_1_out;

  not not_1 (not_1_out, nG);
  Multiplexer #(.select(3)) multiplexer_1 (
    .in0(D0), .in1(D1), .in2(D2), .in3(D3), .in4(D4), .in5(D5), .in6(D6), .in7(D7), .out(Y), .sel({C, B, A}),
    .en(not_1_out));
  not not_2 (W, Y);

  // Notes on the sheet:
  //   74LS151
endmodule
