// Logisim project 74LS152.circ as structural Verilog: 1 circuit, main circuit 74LS152
module _74LS152 (
  input  I0,
  input  I1,
  input  I2,
  input  I3,
  input  I4,
  input  I5,
  input  I6,
  input  I7,
  input  A,
  input  B,
  input  C,
  output Z
);

  Multiplexer #(.select(3), .enable("false")) multiplexer_1 (
    .in0(I0), .in1(I1), .in2(I2), .in3(I3), .in4(I4), .in5(I5), .in6(I6), .in7(I7), .out(Z), .sel({C, B, A}));

  // Notes on the sheet:
  //   74LS152
endmodule
