// Logisim project 74LS153.circ as structural Verilog: 1 circuit, main circuit 74LS153
module _74LS153 (
  input  _1_G,
  input  _1C0,
  input  _1C1,
  input  _1C2,
  input  _1C3,
  input  B,
  input  A,
  input  _2C0,
  input  _2C1,
  input  _2C2,
  input  _2C3,
  input  _2_G,
  output _1Y,
  output _2Y
);

  wire and_1_out, and_2_out, and_3_out, and_4_out, and_5_out, and_6_out, and_7_out, and_8_out, not_1_out,
       not_2_out, not_3_out, not_4_out, not_5_out, not_6_out;

  not not_1 (not_1_out, _1_G);
  not not_2 (not_2_out, B);
  not not_3 (not_3_out, A);
  not not_4 (not_4_out, _2_G);
  not not_5 (not_5_out, not_2_out);
  not not_6 (not_6_out, not_3_out);
  and and_1 (and_1_out, not_1_out, not_2_out, not_3_out, _1C0);
  and and_2 (and_2_out, not_1_out, not_2_out, not_6_out, _1C1);
  and and_3 (and_3_out, not_1_out, not_5_out, not_3_out, _1C2);
  and and_4 (and_4_out, not_1_out, not_5_out, not_6_out, _1C3);
  and and_5 (and_5_out, _2C0, not_2_out, not_3_out, not_4_out);
  and and_6 (and_6_out, _2C1, not_2_out, not_6_out, not_4_out);
  and and_7 (and_7_out, _2C2, not_5_out, not_3_out, not_4_out);
  and and_8 (and_8_out, _2C3, not_5_out, not_6_out, not_4_out);
  or or_1 (_1Y, and_1_out, and_2_out, and_3_out, and_4_out);
  or or_2 (_2Y, and_5_out, and_6_out, and_7_out, and_8_out);

  // Notes on the sheet:
  //   74LS153
endmodule
