// Logisim project 74LS154.circ as structural Verilog: 1 circuit, main circuit 74LS154
module _74LS154 (
  input  nG1,
  input  nG2,
  input  A,
  input  B,
  input  C,
  input  D,
  output _0,
  output _1,
  output _2,
  output _3,
  output _4,
  output _5,
  output _6,
  output _7,
  output _8,
  output _9,
  output _10,
  output _11,
  output _12,
  output _13,
  output _14,
  output _15
);

  wire and_1_out, decoder_1_out0, decoder_1_out1, decoder_1_out2, decoder_1_out3, decoder_1_out4,
       decoder_1_out5, decoder_1_out6, decoder_1_out7, decoder_1_out8, decoder_1_out9, decoder_1_out10,
       decoder_1_out11, decoder_1_out12, decoder_1_out13, decoder_1_out14, decoder_1_out15;

  and and_1 (and_1_out, ~nG1, ~nG2);  // AND_Gate
  not not_1 (_0, decoder_1_out0);
  not not_2 (_1, decoder_1_out1);
  not not_3 (_2, decoder_1_out2);
  not not_4 (_3, decoder_1_out3);
  not not_5 (_4, decoder_1_out4);
  not not_6 (_5, decoder_1_out5);
  not not_7 (_6, decoder_1_out6);
  not not_8 (_7, decoder_1_out7);
  not not_9 (_8, decoder_1_out8);
  not not_10 (_9, decoder_1_out9);
  not not_11 (_10, decoder_1_out10);
  not not_12 (_11, decoder_1_out11);
  not not_13 (_12, decoder_1_out12);
  not not_14 (_13, decoder_1_out13);
  not not_15 (_14, decoder_1_out14);
  not not_16 (_15, decoder_1_out15);
  Decoder #(.select(4), .disabled(0)) decoder_1 (
    .out0(decoder_1_out0), .out1(decoder_1_out1), .out2(decoder_1_out2), .out3(decoder_1_out3),
    .out4(decoder_1_out4), .out5(decoder_1_out5), .out6(decoder_1_out6), .out7(decoder_1_out7),
    .out8(decoder_1_out8), .out9(decoder_1_out9), .out10(decoder_1_out10), .out11(decoder_1_out11),
    .out12(decoder_1_out12), .out13(decoder_1_out13), .out14(decoder_1_out14), .out15(decoder_1_out15),
    .sel({D, C, B, A}), .en(and_1_out));

  // Notes on the sheet:
  //   74LS154
endmodule
