// Logisim project 74LS156.circ as structural Verilog: 1 circuit, main circuit 74LS156
module _74LS156 (
  input  STROBE_1_G,
  input  DATA_1C,
  input  SELECT_B,
  input  SELECT_A,
  input  DATA_2_C,
  input  STROBE_2_G,
  output OUTPUT_1Y0,
  output OUTPUT_1Y1,
  output OUTPUT_1Y2,
  output OUTPUT_1Y3,
  output OUTPUT_2Y0,
  output OUTPUT_2Y1,
  output OUTPUT_2Y2,
  output OUTPUT_2Y3
);

  wire and_1_out, and_2_out, not_1_out, not_2_out, not_3_out, not_4_out, not_5_out;

  not not_1 (not_1_out, DATA_1C);
  not not_2 (not_2_out, SELECT_B);
  not not_3 (not_3_out, SELECT_A);
  and and_1 (and_1_out, ~STROBE_1_G, ~not_1_out);  // AND_Gate
  not not_4 (not_4_out, not_2_out);
  not not_5 (not_5_out, not_3_out);
  and and_2 (and_2_out, ~DATA_2_C, ~STROBE_2_G);  // AND_Gate
  nand nand_1 (OUTPUT_1Y0, not_2_out, not_3_out, and_1_out);
  nand nand_2 (OUTPUT_1Y1, not_2_out, not_5_out, and_1_out);
  nand nand_3 (OUTPUT_1Y2, not_4_out, not_3_out, and_1_out);
  nand nand_4 (OUTPUT_1Y3, not_4_out, not_5_out, and_1_out);
  nand nand_5 (OUTPUT_2Y0, not_2_out, not_3_out, and_2_out);
  nand nand_6 (OUTPUT_2Y1, not_2_out, not_5_out, and_2_out);
  nand nand_7 (OUTPUT_2Y2, not_4_out, not_3_out, and_2_out);
  nand nand_8 (OUTPUT_2Y3, not_4_out, not_5_out, and_2_out);

  // Notes on the sheet:
  //   74LS155
  //   nand_1 drives only 0 and floats otherwise
  //   nand_2 drives only 0 and floats otherwise
  //   nand_3 drives only 0 and floats otherwise
  //   nand_4 drives only 0 and floats otherwise
  //   nand_5 drives only 0 and floats otherwise
  //   nand_6 drives only 0 and floats otherwise
  //   nand_7 drives only 0 and floats otherwise
  //   nand_8 drives only 0 and floats otherwise
endmodule
