// Logisim project 74LS158.circ as structural Verilog: 1 circuit, main circuit 74LS158
module _74LS158 (
  input  _1A,
  input  _1B,
  input  _2A,
  input  _2B,
  input  _3A,
  input  _3B,
  input  _4A,
  input  _4B,
  input  STROBE_nG,
  input  SELECT_A_B,
  output _1Y,
  output _2Y,
  output _3Y,
  output _4Y
);

  wire and_1_out, and_2_out, and_3_out, and_4_out, and_5_out, and_6_out, and_7_out, and_8_out, and_9_out,
       and_10_out, not_1_out;

  not not_1 (not_1_out, SELECT_A_B);
  and and_1 (and_1_out, ~STROBE_nG, ~SELECT_A_B);  // AND_Gate
  and and_2 (and_2_out, ~STROBE_nG, ~not_1_out);  // AND_Gate
  and and_3 (and_3_out, _1A, and_1_out);
  and and_4 (and_4_out, _1B, and_2_out);
  and and_5 (and_5_out, _2A, and_1_out);
  and and_6 (and_6_out, _2B, and_2_out);
  and and_7 (and_7_out, _3A, and_1_out);
  and and_8 (and_8_out, _3B, and_2_out);
  and and_9 (and_9_out, _4A, and_1_out);
  and and_10 (and_10_out, _4B, and_2_out);
  nor nor_1 (_1Y, and_3_out, and_4_out);
  nor nor_2 (_2Y, and_5_out, and_6_out);
  nor nor_3 (_3Y, and_7_out, and_8_out);
  nor nor_4 (_4Y, and_9_out, and_10_out);

  // Notes on the sheet:
  //   74LS158
endmodule
