// Logisim project 74LS160.circ as structural Verilog: 1 circuit, main circuit 74LS160
module _74LS160 (
  input  nLOAD,
  input  DATA_A,
  input  DATA_B,
  input  CLK,
  input  DATA_C,
  input  DATA_D,
  input  nCLR,
  input  ENP,
  input  ENT,
  output QA,
  output QB,
  output QC,
  output QD,
  output RCO
);

  wire and_1_out, and_2_out, and_3_out, and_4_out, and_5_out, and_6_out, and_7_out, and_8_out, and_9_out,
       and_10_out, and_11_out, and_12_out, and_13_out, j_k_ff_4_qn, nand_1_out, nand_2_out, nand_3_out,
       nand_4_out, nand_5_out, nand_6_out, nand_7_out, nand_8_out, not_1_out, not_2_out, not_3_out,
       not_4_out, not_5_out, not_6_out, not_7_out, or_1_out, or_2_out, or_3_out, or_4_out, or_5_out;

  not not_1 (not_1_out, nLOAD);
  not not_2 (not_2_out, CLK);
  not not_3 (not_3_out, nCLR);
  and and_1 (and_1_out, ENP, ENT);
  and and_2 (and_2_out, QA, and_1_out, j_k_ff_4_qn);
  and and_3 (and_3_out, QB, QA, and_1_out);
  and and_4 (and_4_out, QC, QB, QA, and_1_out);
  and and_5 (and_5_out, QA, and_1_out, QD);
  or or_1 (or_1_out, and_4_out, and_5_out);
  nand nand_1 (nand_1_out, not_1_out, nand_2_out);
  or or_2 (or_2_out, and_1_out, not_1_out);
  nand nand_2 (nand_2_out, DATA_A, not_1_out);
  nand nand_3 (nand_3_out, not_1_out, nand_4_out);
  or or_3 (or_3_out, and_2_out, not_1_out);
  nand nand_4 (nand_4_out, DATA_B, not_1_out);
  nand nand_5 (nand_5_out, not_1_out, nand_6_out);
  or or_4 (or_4_out, and_3_out, not_1_out);
  nand nand_6 (nand_6_out, DATA_C, not_1_out);
  nand nand_7 (nand_7_out, not_1_out, nand_8_out);
  or or_5 (or_5_out, or_1_out, not_1_out);
  nand nand_8 (nand_8_out, DATA_D, not_1_out);
  and and_6 (and_6_out, nand_1_out, or_2_out);
  and and_7 (and_7_out, or_2_out, nand_2_out);
  and and_8 (and_8_out, nand_3_out, or_3_out);
  and and_9 (and_9_out, or_3_out, nand_4_out);
  and and_10 (and_10_out, nand_5_out, or_4_out);
  and and_11 (and_11_out, or_4_out, nand_6_out);
  and and_12 (and_12_out, nand_7_out, or_5_out);
  and and_13 (and_13_out, or_5_out, nand_8_out);
  J_K_Flip_Flop j_k_ff_1 (
    .J(and_6_out), .clk(not_4_out), .K(and_7_out), .Q(QA), .reset(not_3_out));  // open: Qn, preset, en
  not not_4 (not_4_out, not_2_out);
  J_K_Flip_Flop j_k_ff_2 (
    .J(and_8_out), .clk(not_5_out), .K(and_9_out), .Q(QB), .reset(not_3_out));  // open: Qn, preset, en
  not not_5 (not_5_out, not_2_out);
  J_K_Flip_Flop j_k_ff_3 (
    .J(and_10_out), .clk(not_6_out), .K(and_11_out), .Q(QC), .reset(not_3_out));  // open: Qn, preset, en
  not not_6 (not_6_out, not_2_out);
  J_K_Flip_Flop j_k_ff_4 (
    .J(and_12_out), .clk(not_7_out), .K(and_13_out), .Q(QD), .Qn(j_k_ff_4_qn), .reset(not_3_out));  // open: preset, en
  not not_7 (not_7_out, not_2_out);
  and and_14 (RCO, QD, QA, ENT);

  // Notes on the sheet:
  //   74LS160
endmodule
