// Logisim project 74LS164.circ as structural Verilog: 1 circuit, main circuit 74LS164
module _74LS164 (
  input  A,
  input  B,
  input  CLOCK,
  input  nCLEAR,
  output QA,
  output QB,
  output QC,
  output QD,
  output QE,
  output QF,
  output QG,
  output QH
);

  wire nand_1_out, not_1_out, not_2_out, not_3_out, not_4_out, not_5_out, s_r_ff_1_qn, s_r_ff_2_qn,
       s_r_ff_3_qn, s_r_ff_4_qn, s_r_ff_5_qn, s_r_ff_6_qn, s_r_ff_7_qn;

  not not_1 (not_1_out, CLOCK);
  not not_2 (not_2_out, nCLEAR);
  not not_3 (not_3_out, nand_1_out);
  nand nand_1 (nand_1_out, A, B);
  not not_4 (not_4_out, not_2_out);
  not not_5 (not_5_out, not_4_out);
  S_R_Flip_Flop #(.trigger("falling")) s_r_ff_1 (
    .S(not_3_out), .clk(not_1_out), .R(nand_1_out), .Q(QA), .Qn(s_r_ff_1_qn), .reset(not_5_out));  // open: preset, en
  S_R_Flip_Flop #(.trigger("falling")) s_r_ff_2 (
    .S(QA), .clk(not_1_out), .R(s_r_ff_1_qn), .Q(QB), .Qn(s_r_ff_2_qn), .reset(not_5_out));  // open: preset, en
  S_R_Flip_Flop #(.trigger("falling")) s_r_ff_3 (
    .S(QB), .clk(not_1_out), .R(s_r_ff_2_qn), .Q(QC), .Qn(s_r_ff_3_qn), .reset(not_5_out));  // open: preset, en
  S_R_Flip_Flop #(.trigger("falling")) s_r_ff_4 (
    .S(QC), .clk(not_1_out), .R(s_r_ff_3_qn), .Q(QD), .Qn(s_r_ff_4_qn), .reset(not_5_out));  // open: preset, en
  S_R_Flip_Flop #(.trigger("falling")) s_r_ff_5 (
    .S(QD), .clk(not_1_out), .R(s_r_ff_4_qn), .Q(QE), .Qn(s_r_ff_5_qn), .reset(not_5_out));  // open: preset, en
  S_R_Flip_Flop #(.trigger("falling")) s_r_ff_6 (
    .S(QE), .clk(not_1_out), .R(s_r_ff_5_qn), .Q(QF), .Qn(s_r_ff_6_qn), .reset(not_5_out));  // open: preset, en
  S_R_Flip_Flop #(.trigger("falling")) s_r_ff_7 (
    .S(QF), .clk(not_1_out), .R(s_r_ff_6_qn), .Q(QG), .Qn(s_r_ff_7_qn), .reset(not_5_out));  // open: preset, en
  S_R_Flip_Flop #(.trigger("falling")) s_r_ff_8 (
    .S(QG), .clk(not_1_out), .R(s_r_ff_7_qn), .Q(QH), .reset(not_5_out));  // open: Qn, preset, en
endmodule
