// Logisim project 74LS165.circ as structural Verilog: 1 circuit, main circuit 74LS165
module _74LS165 (
  input  CLK_INH,
  input  CLK,
  input  SER,
  input  SH_nLD,
  input  A,
  input  B,
  input  C,
  input  D,
  input  E,
  input  F,
  input  G,
  input  H,
  output QH,
  output nQH
);

  wire d_ff_1_q, d_ff_2_q, d_ff_3_q, d_ff_4_q, d_ff_5_q, d_ff_6_q, d_ff_7_q, nand_1_out, nand_2_out,
       nand_3_out, nand_4_out, nand_5_out, nand_6_out, nand_7_out, nand_8_out, nand_9_out, nand_10_out,
       nand_11_out, nand_12_out, nand_13_out, nand_14_out, nand_15_out, nand_16_out, not_1_out, not_2_out,
       not_3_out, not_4_out, not_5_out, not_6_out, not_7_out, not_8_out, not_9_out, not_10_out, not_11_out,
       not_12_out, not_13_out, not_14_out, not_15_out, not_16_out, not_17_out, not_18_out, not_19_out,
       or_1_out;

  not not_1 (not_1_out, SER);
  not not_2 (not_2_out, SH_nLD);
  or or_1 (or_1_out, CLK_INH, CLK);
  D_Flip_Flop d_ff_1 (
    .clk(or_1_out), .D(not_3_out), .Q(d_ff_1_q), .preset(not_5_out), .reset(not_4_out));  // open: Qn, en
  not not_3 (not_3_out, not_1_out);
  not not_4 (not_4_out, nand_1_out);
  not not_5 (not_5_out, nand_2_out);
  nand nand_1 (nand_1_out, nand_2_out, not_2_out);
  nand nand_2 (nand_2_out, not_2_out, A);
  D_Flip_Flop d_ff_2 (
    .clk(or_1_out), .D(d_ff_1_q), .Q(d_ff_2_q), .preset(not_7_out), .reset(not_6_out));  // open: Qn, en
  not not_6 (not_6_out, nand_3_out);
  not not_7 (not_7_out, nand_4_out);
  nand nand_3 (nand_3_out, nand_4_out, not_2_out);
  nand nand_4 (nand_4_out, not_2_out, B);
  D_Flip_Flop d_ff_3 (
    .clk(or_1_out), .D(d_ff_2_q), .Q(d_ff_3_q), .preset(not_8_out), .reset(not_9_out));  // open: Qn, en
  not not_8 (not_8_out, nand_6_out);
  not not_9 (not_9_out, nand_5_out);
  nand nand_5 (nand_5_out, nand_6_out, not_2_out);
  nand nand_6 (nand_6_out, not_2_out, C);
  D_Flip_Flop d_ff_4 (
    .clk(or_1_out), .D(d_ff_3_q), .Q(d_ff_4_q), .preset(not_11_out), .reset(not_10_out));  // open: Qn, en
  not not_10 (not_10_out, nand_7_out);
  not not_11 (not_11_out, nand_8_out);
  nand nand_7 (nand_7_out, nand_8_out, not_2_out);
  nand nand_8 (nand_8_out, not_2_out, D);
  D_Flip_Flop d_ff_5 (
    .clk(or_1_out), .D(d_ff_4_q), .Q(d_ff_5_q), .preset(not_14_out), .reset(not_13_out));  // open: Qn, en
  not not_12 (not_12_out, nand_10_out);
  not not_13 (not_13_out, nand_9_out);
  not not_14 (not_14_out, nand_11_out);
  nand nand_9 (nand_9_out, nand_11_out, not_2_out);
  nand nand_10 (nand_10_out, not_2_out, F);
  nand nand_11 (nand_11_out, not_2_out, E);
  D_Flip_Flop d_ff_6 (
    .clk(or_1_out), .D(d_ff_5_q), .Q(d_ff_6_q), .preset(not_12_out), .reset(not_15_out));  // open: Qn, en
  not not_15 (not_15_out, nand_12_out);
  not not_16 (not_16_out, nand_13_out);
  nand nand_12 (nand_12_out, nand_10_out, not_2_out);
  nand nand_13 (nand_13_out, not_2_out, G);
  D_Flip_Flop d_ff_7 (
    .clk(or_1_out), .D(d_ff_6_q), .Q(d_ff_7_q), .preset(not_16_out), .reset(not_19_out));  // open: Qn, en
  not not_17 (not_17_out, nand_16_out);
  not not_18 (not_18_out, nand_15_out);
  not not_19 (not_19_out, nand_14_out);
  nand nand_14 (nand_14_out, nand_13_out, not_2_out);
  nand nand_15 (nand_15_out, not_2_out, H);
  D_Flip_Flop d_ff_8 (
    .clk(or_1_out), .D(d_ff_7_q), .Q(QH), .Qn(nQH), .preset(not_18_out), .reset(not_17_out));  // open: en
  nand nand_16 (nand_16_out, nand_15_out, not_2_out);

  // Notes on the sheet:
  //   74LS165
endmodule
