// Logisim project 74LS166.circ as structural Verilog: 2 circuits, main circuit 74LS166
module _74LS166 (
  input  nCLEAR,
  input  SERIAL_INPUT,
  input  SHIFT_LOAD,
  input  A,
  input  B,
  input  C,
  input  D,
  input  E,
  input  F,
  input  G,
  input  H,
  input  CLOCK,
  input  CLOCK_INHIBIT,
  output Q
);

  wire and_1_out, and_2_out, and_3_out, and_4_out, and_5_out, and_6_out, and_7_out, and_8_out, and_9_out,
       and_10_out, and_11_out, and_12_out, and_13_out, and_14_out, and_15_out, and_16_out, nor_1_out,
       nor_2_out, nor_3_out, nor_4_out, nor_5_out, nor_6_out, nor_7_out, nor_8_out, nor_9_out, not_1_out,
       not_2_out, not_3_out, not_4_out, not_5_out, not_6_out, not_7_out, not_8_out, not_9_out, not_10_out,
       not_11_out, not_12_out, sr_nck_nclr_1_q, sr_nck_nclr_2_q, sr_nck_nclr_3_q, sr_nck_nclr_4_q,
       sr_nck_nclr_5_q, sr_nck_nclr_6_q, sr_nck_nclr_7_q;

  not not_1 (not_1_out, nCLEAR);
  not not_2 (not_2_out, not_1_out);
  not not_3 (not_3_out, not_4_out);
  not not_4 (not_4_out, SHIFT_LOAD);
  nor nor_1 (nor_1_out, CLOCK, CLOCK_INHIBIT);
  and and_1 (and_1_out, SERIAL_INPUT, not_3_out);
  and and_2 (and_2_out, not_4_out, A);
  and and_3 (and_3_out, sr_nck_nclr_1_q, not_3_out);
  and and_4 (and_4_out, not_4_out, B);
  and and_5 (and_5_out, sr_nck_nclr_2_q, not_3_out);
  and and_6 (and_6_out, not_4_out, C);
  and and_7 (and_7_out, sr_nck_nclr_3_q, not_3_out);
  and and_8 (and_8_out, not_4_out, D);
  and and_9 (and_9_out, sr_nck_nclr_4_q, not_3_out);
  and and_10 (and_10_out, not_4_out, E);
  and and_11 (and_11_out, sr_nck_nclr_5_q, not_3_out);
  and and_12 (and_12_out, not_4_out, F);
  and and_13 (and_13_out, sr_nck_nclr_6_q, not_3_out);
  and and_14 (and_14_out, not_4_out, G);
  and and_15 (and_15_out, sr_nck_nclr_7_q, not_3_out);
  and and_16 (and_16_out, not_4_out, H);
  nor nor_2 (nor_2_out, and_1_out, and_2_out);
  nor nor_3 (nor_3_out, and_3_out, and_4_out);
  nor nor_4 (nor_4_out, and_5_out, and_6_out);
  nor nor_5 (nor_5_out, and_7_out, and_8_out);
  nor nor_6 (nor_6_out, and_9_out, and_10_out);
  nor nor_7 (nor_7_out, and_11_out, and_12_out);
  nor nor_8 (nor_8_out, and_13_out, and_14_out);
  nor nor_9 (nor_9_out, and_15_out, and_16_out);
  not not_5 (not_5_out, nor_2_out);
  SR_nCK_nCLR sr_nck_nclr_1 (.S(not_5_out), .nCK(nor_1_out), .R(nor_2_out), .nCLR(not_2_out), .Q(sr_nck_nclr_1_q));
  LED led_1 (.in(sr_nck_nclr_1_q));
  not not_6 (not_6_out, nor_3_out);
  SR_nCK_nCLR sr_nck_nclr_2 (.S(not_6_out), .nCK(nor_1_out), .R(nor_3_out), .nCLR(not_2_out), .Q(sr_nck_nclr_2_q));
  LED led_2 (.in(sr_nck_nclr_2_q));
  not not_7 (not_7_out, nor_4_out);
  SR_nCK_nCLR sr_nck_nclr_3 (.S(not_7_out), .nCK(nor_1_out), .R(nor_4_out), .nCLR(not_2_out), .Q(sr_nck_nclr_3_q));
  LED led_3 (.in(sr_nck_nclr_3_q));
  not not_8 (not_8_out, nor_5_out);
  SR_nCK_nCLR sr_nck_nclr_4 (.S(not_8_out), .nCK(nor_1_out), .R(nor_5_out), .nCLR(not_2_out), .Q(sr_nck_nclr_4_q));
  LED led_4 (.in(sr_nck_nclr_4_q));
  not not_9 (not_9_out, nor_6_out);
  SR_nCK_nCLR sr_nck_nclr_5 (.S(not_9_out), .nCK(nor_1_out), .R(nor_6_out), .nCLR(not_2_out), .Q(sr_nck_nclr_5_q));
  LED led_5 (.in(sr_nck_nclr_5_q));
  not not_10 (not_10_out, nor_7_out);
  SR_nCK_nCLR sr_nck_nclr_6 (.S(not_10_out), .nCK(nor_1_out), .R(nor_7_out), .nCLR(not_2_out), .Q(sr_nck_nclr_6_q));
  LED led_6 (.in(sr_nck_nclr_6_q));
  not not_11 (not_11_out, nor_8_out);
  SR_nCK_nCLR sr_nck_nclr_7 (.S(not_11_out), .nCK(nor_1_out), .R(nor_8_out), .nCLR(not_2_out), .Q(sr_nck_nclr_7_q));
  LED led_7 (.in(sr_nck_nclr_7_q));
  not not_12 (not_12_out, nor_9_out);
  SR_nCK_nCLR sr_nck_nclr_8 (.S(not_12_out), .nCK(nor_1_out), .R(nor_9_out), .nCLR(not_2_out), .Q(Q));

  // Notes on the sheet:
  //   74LS166
endmodule

module SR_nCK_nCLR (
  input  S,
  input  nCK,
  input  R,
  input  nCLR,
  output Q
);

  wire not_1_out;

  S_R_Flip_Flop #(.trigger("falling")) Falling_Edge (
    .S(S), .clk(nCK), .R(R), .Q(Q), .reset(not_1_out));  // open: Qn, preset, en
  not not_1 (not_1_out, nCLR);
endmodule
