// Logisim project 74LS167.circ as structural Verilog: 2 circuits, main circuit 74LS167
module _74LS167 (
  input  ENABLE_INPUT,
  input  SET_TO_9,
  input  CLEAR,
  input  CLOCK,
  input  STROBE,
  input  B3,
  input  B2,
  input  B1,
  input  B0,
  input  UNITY_CASCADE_INPUT,
  output ENABLE_OUTPUT,
  output Y_OUTPUT,
  output Z_OUTPUT
);

  wire A_out, and_1_out, and_2_out, and_3_out, and_4_out, and_5_out, and_6_out, B_out, C_out, D_out,
       nor_1_out, nor_2_out, not_1_out, not_2_out, not_3_out, not_4_out, or_1_out, tg_nclk_nclr_nset_1_nq,
       tg_nclk_nclr_nset_1_q, tg_nclk_nclr_nset_2_q, tg_nclk_nclr_nset_3_nq, tg_nclk_nclr_nset_3_q,
       tg_nclk_nclr_nset_4_nq, tg_nclk_nclr_nset_4_q;

  not not_1 (not_1_out, ENABLE_INPUT);
  not not_2 (not_2_out, SET_TO_9);
  not not_3 (not_3_out, CLEAR);
  not not_4 (not_4_out, CLOCK);
  and and_1 (and_1_out, ~CLOCK, ~STROBE);  // AND_Gate
  and and_2 (and_2_out, not_1_out, tg_nclk_nclr_nset_3_nq);
  TG_nCLK_nCLR_nSET tg_nclk_nclr_nset_1 (
    .G(and_2_out), .TCLK(not_4_out), .Q(tg_nclk_nclr_nset_1_q), .nQ(tg_nclk_nclr_nset_1_nq), .CLEAR(nor_1_out));  // open: PRESET
  nor nor_1 (nor_1_out, ~not_3_out, ~not_2_out);  // NOR_Gate
  and D (D_out, B3, and_1_out, tg_nclk_nclr_nset_3_nq);
  and and_3 (and_3_out, not_1_out, tg_nclk_nclr_nset_1_q);
  TG_nCLK_nCLR_nSET tg_nclk_nclr_nset_2 (
    .G(and_3_out), .TCLK(not_4_out), .Q(tg_nclk_nclr_nset_2_q), .CLEAR(nor_2_out));  // open: nQ, PRESET
  nor nor_2 (nor_2_out, ~not_3_out, ~not_2_out);  // NOR_Gate
  and C (C_out, B2, and_1_out, tg_nclk_nclr_nset_1_q);
  and and_4 (and_4_out, not_1_out, tg_nclk_nclr_nset_2_q, tg_nclk_nclr_nset_1_q);
  and and_5 (and_5_out, not_1_out, tg_nclk_nclr_nset_3_q);
  nor nor_3 (Z_OUTPUT, D_out, C_out, B_out, A_out);
  or or_1 (or_1_out, and_4_out, and_5_out);
  TG_nCLK_nCLR_nSET tg_nclk_nclr_nset_3 (
    .G(or_1_out), .TCLK(not_4_out), .Q(tg_nclk_nclr_nset_3_q), .nQ(tg_nclk_nclr_nset_3_nq),
    .PRESET(not_2_out), .CLEAR(not_3_out));
  and B (B_out, B1, and_1_out, tg_nclk_nclr_nset_1_nq, tg_nclk_nclr_nset_2_q);
  or or_2 (Y_OUTPUT, ~Z_OUTPUT, ~UNITY_CASCADE_INPUT);  // OR_Gate
  and and_6 (and_6_out, not_1_out, tg_nclk_nclr_nset_3_q);
  TG_nCLK_nCLR_nSET tg_nclk_nclr_nset_4 (
    .G(and_6_out), .TCLK(not_4_out), .Q(tg_nclk_nclr_nset_4_q), .nQ(tg_nclk_nclr_nset_4_nq),
    .PRESET(not_2_out), .CLEAR(not_3_out));
  and A (A_out, B0, and_1_out, tg_nclk_nclr_nset_3_q, tg_nclk_nclr_nset_4_nq);
  nand nand_1 (ENABLE_OUTPUT, not_1_out, tg_nclk_nclr_nset_3_q, tg_nclk_nclr_nset_4_q);
endmodule

module TG_nCLK_nCLR_nSET (
  input  PRESET,
  input  G,
  input  TCLK,
  input  CLEAR,
  output Q,
  output nQ
);

  wire not_1_out, not_2_out, not_3_out;

  not not_1 (not_1_out, TCLK);
  not not_2 (not_2_out, PRESET);
  T_Flip_Flop t_ff_1 (.clk(not_1_out), .T(G), .Q(Q), .Qn(nQ), .preset(not_2_out), .reset(not_3_out));  // open: en
  not not_3 (not_3_out, CLEAR);
endmodule
