// Logisim project 74LS168.circ as structural Verilog: 1 circuit, main circuit 74LS168
module _74LS168 (
  input  P0,
  input  P1,
  input  P2,
  input  P3,
  input  nPE,
  input  nCEP,
  input  nCET,
  input  U_D,
  input  CP,
  output nTC,
  output Q0,
  output Q1,
  output Q2,
  output Q3
);

  wire and_1_out, and_2_out, and_3_out, and_4_out, and_5_out, and_6_out, and_7_out, and_8_out, and_9_out,
       and_10_out, and_11_out, and_12_out, and_13_out, and_14_out, and_15_out, and_16_out, and_17_out,
       and_18_out, and_19_out, and_20_out, and_21_out, d_ff_1_qn, d_ff_2_qn, d_ff_3_qn, d_ff_4_qn,
       nand_1_out, nand_2_out, nand_3_out, nand_4_out, nand_5_out, nand_6_out, nand_7_out, not_1_out,
       not_2_out, not_3_out, not_4_out, not_5_out, or_1_out, or_2_out, or_3_out, or_4_out;

  not not_1 (not_1_out, nPE);
  and and_1 (and_1_out, ~nCEP, ~nCET);  // AND_Gate
  not not_2 (not_2_out, U_D);
  and and_2 (and_2_out, not_1_out, P0);
  not not_3 (not_3_out, not_1_out);
  not not_4 (not_4_out, nCET);
  not not_5 (not_5_out, not_2_out);
  and and_3 (and_3_out, not_3_out, ~and_1_out, Q0);  // AND_Gate
  and and_4 (and_4_out, and_1_out, not_3_out, ~Q0);  // AND_Gate
  or or_1 (or_1_out, and_3_out, and_2_out, and_4_out);
  nand nand_1 (nand_1_out, d_ff_1_qn, and_1_out);
  nand nand_2 (nand_2_out, d_ff_3_qn, d_ff_4_qn);
  and and_5 (and_5_out, nand_1_out, not_3_out, Q1, not_2_out);
  D_Flip_Flop d_ff_1 (.clk(CP), .D(or_1_out), .Q(Q0), .Qn(d_ff_1_qn));  // open: preset, en, reset
  and and_6 (and_6_out, not_1_out, P1);
  nand nand_3 (nand_3_out, Q0, and_1_out);
  and and_7 (and_7_out, d_ff_2_qn, nand_2_out, not_2_out, not_3_out, d_ff_1_qn, and_1_out);
  or or_2 (or_2_out, and_5_out, and_7_out, and_6_out, and_8_out, and_9_out);
  and and_8 (and_8_out, Q1, nand_3_out, not_3_out, not_5_out);
  and and_9 (and_9_out, ~Q1, not_3_out, not_5_out, and_1_out, Q0, d_ff_4_qn);  // AND_Gate
  D_Flip_Flop d_ff_2 (.clk(CP), .D(or_2_out), .Q(Q1), .Qn(d_ff_2_qn));  // open: preset, en, reset
  nand nand_4 (nand_4_out, Q1, Q0, and_1_out);
  and and_10 (and_10_out, nand_4_out, not_3_out, not_5_out, Q2);
  and and_11 (and_11_out, not_5_out, not_3_out, Q1, Q0, and_1_out, ~Q2);  // AND_Gate
  and and_12 (and_12_out, not_1_out, P2);
  nand nand_5 (nand_5_out, d_ff_2_qn, d_ff_1_qn, and_1_out);
  and and_13 (and_13_out, Q2, nand_5_out, not_3_out, not_2_out);
  or or_3 (or_3_out, and_10_out, and_11_out, and_12_out, and_13_out, and_14_out);
  D_Flip_Flop d_ff_3 (.clk(CP), .D(or_3_out), .Q(Q2), .Qn(d_ff_3_qn));  // open: preset, en, reset
  and and_14 (and_14_out, ~Q2, not_2_out, and_1_out, not_3_out, d_ff_2_qn, d_ff_1_qn, Q3);  // AND_Gate
  nand nand_6 (nand_6_out, d_ff_1_qn, and_1_out);
  and and_15 (and_15_out, nand_6_out, Q3, not_3_out, not_2_out);
  and and_16 (and_16_out, not_1_out, P3);
  nand nand_7 (nand_7_out, Q0, and_1_out);
  and and_17 (and_17_out, not_2_out, not_3_out, and_1_out, d_ff_3_qn, d_ff_2_qn, d_ff_1_qn, ~Q3);  // AND_Gate
  or or_4 (or_4_out, and_15_out, and_17_out, and_16_out, and_18_out, and_19_out);
  and and_18 (and_18_out, Q3, nand_7_out, not_3_out, not_5_out);
  and and_19 (and_19_out, ~Q3, not_3_out, not_5_out, and_1_out, Q2, Q1, Q0);  // AND_Gate
  D_Flip_Flop d_ff_4 (.clk(CP), .D(or_4_out), .Q(Q3), .Qn(d_ff_4_qn));  // open: preset, en, reset
  and and_20 (and_20_out, not_2_out, d_ff_1_qn, d_ff_2_qn, d_ff_3_qn, d_ff_4_qn, not_4_out);
  nor nor_1 (nTC, and_20_out, and_21_out);
  and and_21 (and_21_out, not_4_out, not_5_out, Q3, Q0);

  // Notes on the sheet:
  //   National Semicunductor datasheet is WRONG, and shows the schematic for the binary counter!
  //   Motorola Datasheet has a bug! See "bug fix" above Q1
  //   BUG
  //   FIX
endmodule
