// Logisim project 74LS169.circ as structural Verilog: 1 circuit, main circuit 74LS169
module _74LS169 (
  input  CLK,
  input  A,
  input  nLOAD,
  input  U_D,
  input  B,
  input  C,
  input  D,
  input  nENP,
  input  nENT,
  output QA,
  output QB,
  output QC,
  output QD,
  output nRCO
);

  wire and_1_out, and_2_out, and_3_out, and_4_out, and_5_out, and_6_out, and_7_out, and_8_out, and_9_out,
       and_10_out, and_11_out, and_12_out, and_13_out, and_14_out, and_15_out, and_16_out, and_17_out,
       and_18_out, and_19_out, and_20_out, and_21_out, and_22_out, and_23_out, d_ff_1_qn, d_ff_2_qn,
       d_ff_3_qn, d_ff_4_qn, nand_1_out, nand_2_out, nor_1_out, nor_2_out, nor_3_out, not_1_out, not_2_out,
       not_3_out, not_4_out, not_5_out, not_6_out, not_7_out, not_8_out, not_9_out, or_1_out, or_2_out,
       or_3_out, or_4_out, xnor_1_out, xnor_2_out, xnor_3_out, xnor_4_out;

  not not_1 (not_1_out, CLK);
  not not_2 (not_2_out, nLOAD);
  not not_3 (not_3_out, not_4_out);
  not not_4 (not_4_out, U_D);
  not not_5 (not_5_out, d_ff_1_qn);
  nand nand_1 (nand_1_out, d_ff_2_qn, d_ff_1_qn);
  nand nand_2 (nand_2_out, d_ff_3_qn, d_ff_2_qn, d_ff_1_qn);
  and and_1 (and_1_out, ~nENP, ~nENT);  // AND_Gate
  and and_2 (and_2_out, not_4_out, not_5_out);
  and and_3 (and_3_out, not_3_out, d_ff_1_qn);
  and and_4 (and_4_out, not_4_out, nand_1_out);
  and and_5 (and_5_out, not_3_out, d_ff_2_qn);
  and and_6 (and_6_out, not_3_out, d_ff_1_qn);
  and and_7 (and_7_out, not_4_out, nand_2_out);
  and and_8 (and_8_out, not_3_out, d_ff_3_qn);
  and and_9 (and_9_out, not_3_out, d_ff_2_qn);
  and and_10 (and_10_out, not_3_out, d_ff_1_qn);
  nor nor_1 (nor_1_out, and_2_out, and_3_out);
  and and_11 (and_11_out, nor_1_out, and_1_out);
  nor nor_2 (nor_2_out, and_4_out, and_5_out, and_6_out);
  and and_12 (and_12_out, nor_2_out, and_1_out);
  nor nor_3 (nor_3_out, and_7_out, and_8_out, and_9_out, and_10_out);
  and and_13 (and_13_out, nor_3_out, and_1_out);
  xnor xnor_1 (xnor_1_out, and_1_out, d_ff_1_qn);
  xnor xnor_2 (xnor_2_out, and_11_out, d_ff_2_qn);
  xnor xnor_3 (xnor_3_out, and_12_out, d_ff_3_qn);
  xnor xnor_4 (xnor_4_out, and_13_out, d_ff_4_qn);
  and and_14 (and_14_out, ~d_ff_4_qn, ~not_4_out, ~d_ff_3_qn, ~d_ff_2_qn, ~d_ff_1_qn, ~nENT);  // AND_Gate
  and and_15 (and_15_out, ~nENT, d_ff_4_qn, not_4_out, d_ff_3_qn, d_ff_2_qn, d_ff_1_qn);  // AND_Gate
  and and_16 (and_16_out, A, not_2_out);
  and and_17 (and_17_out, nLOAD, xnor_1_out);
  and and_18 (and_18_out, B, not_2_out);
  and and_19 (and_19_out, nLOAD, xnor_2_out);
  and and_20 (and_20_out, C, not_2_out);
  and and_21 (and_21_out, nLOAD, xnor_3_out);
  and and_22 (and_22_out, D, not_2_out);
  and and_23 (and_23_out, nLOAD, xnor_4_out);
  nor nor_4 (nRCO, and_14_out, and_15_out);
  not not_6 (not_6_out, not_1_out);
  or or_1 (or_1_out, and_16_out, and_17_out);
  not not_7 (not_7_out, not_1_out);
  or or_2 (or_2_out, and_18_out, and_19_out);
  not not_8 (not_8_out, not_1_out);
  or or_3 (or_3_out, and_20_out, and_21_out);
  not not_9 (not_9_out, not_1_out);
  or or_4 (or_4_out, and_22_out, and_23_out);
  D_Flip_Flop d_ff_1 (.clk(not_6_out), .D(or_1_out), .Q(QA), .Qn(d_ff_1_qn));  // open: preset, en, reset
  D_Flip_Flop d_ff_2 (.clk(not_7_out), .D(or_2_out), .Q(QB), .Qn(d_ff_2_qn));  // open: preset, en, reset
  D_Flip_Flop d_ff_3 (.clk(not_8_out), .D(or_3_out), .Q(QC), .Qn(d_ff_3_qn));  // open: preset, en, reset
  D_Flip_Flop d_ff_4 (.clk(not_9_out), .D(or_4_out), .Q(QD), .Qn(d_ff_4_qn));  // open: preset, en, reset

  // Notes on the sheet:
  //   74LS169
endmodule
