// Logisim project 74LS170.circ as structural Verilog: 1 circuit, main circuit 74LS170
module _74LS170 (
  input  D1,
  input  D2,
  input  D3,
  input  D4,
  input  nWE,
  input  RA0,
  input  RA1,
  input  WA0,
  input  WA1,
  input  nRE,
  output O1,
  output O2,
  output O3,
  output O4
);

  wire decoder_1_out0, decoder_1_out1, decoder_1_out2, decoder_1_out3, not_1_out, not_2_out;
  wire [3:0] multiplexer_1_out, Word_0_q, Word_1_q, Word_2_q, Word_3_q;

  Decoder #(.select(2), .disabled(0)) decoder_1 (
    .out0(decoder_1_out0), .out1(decoder_1_out1), .out2(decoder_1_out2), .out3(decoder_1_out3),
    .sel({WA1, WA0}), .en(not_1_out));
  not not_1 (not_1_out, nWE);
  Register #(.width(4), .trigger("high")) Word_0 (
    .D({D4, D3, D2, D1}), .Q(Word_0_q), .clk(decoder_1_out0));  // open: en, clr
  Register #(.width(4), .trigger("high")) Word_2 (
    .D({D4, D3, D2, D1}), .Q(Word_2_q), .clk(decoder_1_out2));  // open: en, clr
  Register #(.width(4), .trigger("high")) Word_1 (
    .D({D4, D3, D2, D1}), .Q(Word_1_q), .clk(decoder_1_out1));  // open: en, clr
  Register #(.width(4), .trigger("high")) Word_3 (
    .D({D4, D3, D2, D1}), .Q(Word_3_q), .clk(decoder_1_out3));  // open: en, clr
  not not_2 (not_2_out, nRE);
  Multiplexer #(.select(2), .width(4)) multiplexer_1 (
    .in0(Word_0_q), .in1(Word_1_q), .in2(Word_2_q), .in3(Word_3_q), .out(multiplexer_1_out),
    .sel({RA1, RA0}), .en(not_2_out));
  assign {O4, O3, O2, O1} = multiplexer_1_out;  // Buffer buffer_1, 4 bits wide

  // Notes on the sheet:
  //   74LS170
  //   buffer_1 drives only 0 and floats otherwise
  //   Open
  //   Collector
endmodule
