// Logisim project 74LS171.circ as structural Verilog: 1 circuit, main circuit 74LS171
module _74LS171 (
  input  nCLR,
  input  CLK,
  input  _1D,
  input  _2D,
  input  _3D,
  input  _4D,
  output _1Q,
  output _1_Q,
  output _2Q,
  output _2_Q,
  output _3Q,
  output _3_Q,
  output _4Q,
  output _4_Q
);

  wire not_1_out;

  not not_1 (not_1_out, nCLR);
  D_Flip_Flop d_ff_1 (.clk(CLK), .D(_1D), .Q(_1Q), .Qn(_1_Q), .reset(not_1_out));  // open: preset, en
  D_Flip_Flop d_ff_2 (.clk(CLK), .D(_2D), .Q(_2Q), .Qn(_2_Q), .reset(not_1_out));  // open: preset, en
  D_Flip_Flop d_ff_3 (.clk(CLK), .D(_3D), .Q(_3Q), .Qn(_3_Q), .reset(not_1_out));  // open: preset, en
  D_Flip_Flop d_ff_4 (.clk(CLK), .D(_4D), .Q(_4Q), .Qn(_4_Q), .reset(not_1_out));  // open: preset, en

  // Notes on the sheet:
  //   74LS171
endmodule
