// Logisim project 74LS172.circ as structural Verilog: 1 circuit, main circuit 74LS172
module _74LS172 (
  input  CLK,
  input  _1W0,
  input  _1W1,
  input  _1W2,
  input  _1DA,
  input  _1_GR,
  input  _1DB,
  input  _1R0,
  input  _1_GW,
  input  _1R1,
  input  _1R2,
  input  _2W0,
  input  _2W1,
  input  _2W2,
  input  _2DA,
  input  _2DB,
  input  _2_GW,
  input  _2_GR,
  output _1QA,
  output _1QB,
  output _2QA,
  output _2QB
);

  wire _1GW, _1SEL0, _1SEL1, _1SEL2, _1SEL3, _1SEL4, _1SEL5, _1SEL6, _1SEL7, _2GW, _2SEL0, _2SEL1, _2SEL2,
       _2SEL3, _2SEL4, _2SEL5, _2SEL6, _2SEL7, _12GWCLK, not_3_out, not_4_out, or_1_out, or_2_out, or_3_out,
       or_4_out, or_5_out, or_6_out, or_7_out, or_8_out, or_9_out;
  wire [1:0] _12D, multiplexer_1_out, multiplexer_2_out, multiplexer_3_out, multiplexer_4_out,
       multiplexer_5_out, multiplexer_6_out, multiplexer_7_out, multiplexer_8_out, O0, O1, O2, O3, O4, O5,
       O6, O7;

  not not_1 (_1GW, _1_GW);
  not not_2 (_2GW, _2_GW);
  Decoder #(.select(3), .disabled(0)) decoder_1 (
    .out0(_1SEL0), .out1(_1SEL1), .out2(_1SEL2), .out3(_1SEL3), .out4(_1SEL4), .out5(_1SEL5), .out6(_1SEL6),
    .out7(_1SEL7), .sel({_1W2, _1W1, _1W0}), .en(_1GW));
  Decoder #(.select(3), .disabled(0)) decoder_2 (
    .out0(_2SEL0), .out1(_2SEL1), .out2(_2SEL2), .out3(_2SEL3), .out4(_2SEL4), .out5(_2SEL5), .out6(_2SEL6),
    .out7(_2SEL7), .sel({_2W2, _2W1, _2W0}), .en(_2GW));
  assign _12D = {_1DB, _1DA} & {_2DB, _2DA};  // AND_Gate and_1, 2 bits wide
  or or_1 (or_1_out, _1GW, _2GW);
  and and_2 (_12GWCLK, or_1_out, CLK);
  Multiplexer #(.select(2), .width(2), .enable("false")) multiplexer_1 (
    .in0(2'b00), .in1({_1DB, _1DA}), .in2({_2DB, _2DA}), .in3(_12D), .out(multiplexer_1_out),
    .sel({_2SEL0, _1SEL0}));
  or or_2 (or_2_out, _2SEL0, _1SEL0);
  Multiplexer #(.select(2), .width(2), .enable("false")) multiplexer_2 (
    .in0(2'b00), .in1({_1DB, _1DA}), .in2({_2DB, _2DA}), .in3(_12D), .out(multiplexer_2_out),
    .sel({_2SEL1, _1SEL1}));
  or or_3 (or_3_out, _2SEL1, _1SEL1);
  Multiplexer #(.select(2), .width(2), .enable("false")) multiplexer_3 (
    .in0(2'b00), .in1({_1DB, _1DA}), .in2({_2DB, _2DA}), .in3(_12D), .out(multiplexer_3_out),
    .sel({_2SEL2, _1SEL2}));
  or or_4 (or_4_out, _2SEL2, _1SEL2);
  Multiplexer #(.select(2), .width(2), .enable("false")) multiplexer_4 (
    .in0(2'b00), .in1({_1DB, _1DA}), .in2({_2DB, _2DA}), .in3(_12D), .out(multiplexer_4_out),
    .sel({_2SEL3, _1SEL3}));
  or or_5 (or_5_out, _2SEL3, _1SEL3);
  Register #(.width(2)) register_1 (.D(multiplexer_1_out), .en(or_2_out), .Q(O0), .clk(_12GWCLK));  // open: clr
  Register #(.width(2)) register_2 (.D(multiplexer_2_out), .en(or_3_out), .Q(O1), .clk(_12GWCLK));  // open: clr
  Register #(.width(2)) register_3 (.D(multiplexer_3_out), .en(or_4_out), .Q(O2), .clk(_12GWCLK));  // open: clr
  Register #(.width(2)) register_4 (.D(multiplexer_4_out), .en(or_5_out), .Q(O3), .clk(_12GWCLK));  // open: clr
  Multiplexer #(.select(2), .width(2), .enable("false")) multiplexer_5 (
    .in0(2'b00), .in1({_1DB, _1DA}), .in2({_2DB, _2DA}), .in3(_12D), .out(multiplexer_5_out),
    .sel({_2SEL4, _1SEL4}));
  Register #(.width(2)) register_5 (.D(multiplexer_5_out), .en(or_6_out), .Q(O4), .clk(_12GWCLK));  // open: clr
  or or_6 (or_6_out, _2SEL4, _1SEL4);
  Multiplexer #(.select(2), .width(2), .enable("false")) multiplexer_6 (
    .in0(2'b00), .in1({_1DB, _1DA}), .in2({_2DB, _2DA}), .in3(_12D), .out(multiplexer_6_out),
    .sel({_2SEL5, _1SEL5}));
  Register #(.width(2)) register_6 (.D(multiplexer_6_out), .en(or_7_out), .Q(O5), .clk(_12GWCLK));  // open: clr
  or or_7 (or_7_out, _2SEL5, _1SEL5);
  Register #(.width(2)) register_7 (.D(multiplexer_7_out), .en(or_8_out), .Q(O6), .clk(_12GWCLK));  // open: clr
  Multiplexer #(.select(2), .width(2), .enable("false")) multiplexer_7 (
    .in0(2'b00), .in1({_1DB, _1DA}), .in2({_2DB, _2DA}), .in3(_12D), .out(multiplexer_7_out),
    .sel({_2SEL6, _1SEL6}));
  or or_8 (or_8_out, _2SEL6, _1SEL6);
  Register #(.width(2)) register_8 (.D(multiplexer_8_out), .en(or_9_out), .Q(O7), .clk(_12GWCLK));  // open: clr
  Multiplexer #(.select(2), .width(2), .enable("false")) multiplexer_8 (
    .in0(2'b00), .in1({_1DB, _1DA}), .in2({_2DB, _2DA}), .in3(_12D), .out(multiplexer_8_out),
    .sel({_2SEL7, _1SEL7}));
  or or_9 (or_9_out, _2SEL7, _1SEL7);
  Multiplexer #(.select(3), .width(2)) multiplexer_9 (
    .in0(O0), .in1(O1), .in2(O2), .in3(O3), .in4(O4), .in5(O5), .in6(O6), .in7(O7), .out({_1QB, _1QA}),
    .sel({_1R2, _1R1, _1R0}), .en(not_3_out));
  not not_3 (not_3_out, _1_GR);
  Multiplexer #(.select(3), .width(2)) multiplexer_10 (
    .in0(O0), .in1(O1), .in2(O2), .in3(O3), .in4(O4), .in5(O5), .in6(O6), .in7(O7), .out({_2QB, _2QA}),
    .sel({_2W2, _2W1, _2W0}), .en(not_4_out));
  not not_4 (not_4_out, _2_GR);

  // Other names for the same wires on the sheet: _1D[1:0] = {_1DB, _1DA}; _2D[1:0] = {_2DB, _2DA};
  //   _2R[2:0] = {_2W2, _2W1, _2W0}

  // Notes on the sheet:
  //   Section 1
  //   Section 2
  //   When both sections write
  //   to the same address
  //   zero wins
  //   74LS172
  //   Section 1
  //   Section 2
  //   3-state
  //   3-state
endmodule
