// Logisim project 74LS173.circ as structural Verilog: 1 circuit, main circuit 74LS173
module _74LS173 (
  input  nM,
  input  nN,
  input  _1D,
  input  nG1,
  input  nG2,
  input  _2D,
  input  CLK,
  input  _3D,
  input  _4D,
  input  CLR,
  output _1Q,
  output _2Q,
  output _3Q,
  output _4Q
);

  wire and_1_out, and_2_out, and_3_out, and_4_out, and_5_out, and_6_out, and_7_out, and_8_out, and_9_out,
       and_10_out, d_ff_1_q, d_ff_1_qn, d_ff_2_q, d_ff_2_qn, d_ff_3_q, d_ff_3_qn, d_ff_4_q, d_ff_4_qn,
       not_1_out, or_1_out, or_2_out, or_3_out, or_4_out;

  and and_1 (and_1_out, ~nM, ~nN);  // AND_Gate
  and and_2 (and_2_out, ~nG1, ~nG2);  // AND_Gate
  and and_3 (and_3_out, d_ff_1_q, not_1_out);
  and and_4 (and_4_out, _1D, and_2_out);
  not not_1 (not_1_out, and_2_out);
  and and_5 (and_5_out, d_ff_2_q, not_1_out);
  and and_6 (and_6_out, _2D, and_2_out);
  and and_7 (and_7_out, d_ff_3_q, not_1_out);
  and and_8 (and_8_out, _3D, and_2_out);
  and and_9 (and_9_out, d_ff_4_q, not_1_out);
  and and_10 (and_10_out, _4D, and_2_out);
  D_Flip_Flop d_ff_1 (.clk(CLK), .D(or_1_out), .Q(d_ff_1_q), .Qn(d_ff_1_qn), .reset(CLR));  // open: preset, en
  or or_1 (or_1_out, and_3_out, and_4_out);
  D_Flip_Flop d_ff_2 (.clk(CLK), .D(or_2_out), .Q(d_ff_2_q), .Qn(d_ff_2_qn), .reset(CLR));  // open: preset, en
  or or_2 (or_2_out, and_5_out, and_6_out);
  D_Flip_Flop d_ff_3 (.clk(CLK), .D(or_3_out), .Q(d_ff_3_q), .Qn(d_ff_3_qn), .reset(CLR));  // open: preset, en
  or or_3 (or_3_out, and_7_out, and_8_out);
  D_Flip_Flop d_ff_4 (.clk(CLK), .D(or_4_out), .Q(d_ff_4_q), .Qn(d_ff_4_qn), .reset(CLR));  // open: preset, en
  or or_4 (or_4_out, and_9_out, and_10_out);
  assign _1Q = and_1_out ? ~d_ff_1_qn : 1'bz;  // Controlled_Inverter controlled_inverter_1
  assign _2Q = and_1_out ? ~d_ff_2_qn : 1'bz;  // Controlled_Inverter controlled_inverter_2
  assign _3Q = and_1_out ? ~d_ff_3_qn : 1'bz;  // Controlled_Inverter controlled_inverter_3
  assign _4Q = and_1_out ? ~d_ff_4_qn : 1'bz;  // Controlled_Inverter controlled_inverter_4

  // Notes on the sheet:
  //   74LS173
  //   Three State
endmodule
