// Logisim project 74LS174.circ as structural Verilog: 1 circuit, main circuit 74LS174
module _74LS174 (
  input  _1D,
  input  _2D,
  input  _3D,
  input  _4D,
  input  _5D,
  input  _6D,
  input  CLK,
  input  nCLR,
  output _1Q,
  output _2Q,
  output _3Q,
  output _4Q,
  output _5Q,
  output _6Q
);

  wire not_1_out;

  not not_1 (not_1_out, nCLR);
  D_Flip_Flop d_ff_1 (.clk(CLK), .D(_1D), .Q(_1Q), .reset(not_1_out));  // open: Qn, preset, en
  D_Flip_Flop d_ff_2 (.clk(CLK), .D(_2D), .Q(_2Q), .reset(not_1_out));  // open: Qn, preset, en
  D_Flip_Flop d_ff_3 (.clk(CLK), .D(_3D), .Q(_3Q), .reset(not_1_out));  // open: Qn, preset, en
  D_Flip_Flop d_ff_4 (.clk(CLK), .D(_4D), .Q(_4Q), .reset(not_1_out));  // open: Qn, preset, en
  D_Flip_Flop d_ff_5 (.clk(CLK), .D(_5D), .Q(_5Q), .reset(not_1_out));  // open: Qn, preset, en
  D_Flip_Flop d_ff_6 (.clk(CLK), .D(_6D), .Q(_6Q), .reset(not_1_out));  // open: Qn, preset, en

  // Notes on the sheet:
  //   74LS174
endmodule
