// Logisim project 74LS180.circ as structural Verilog: 1 circuit, main circuit 74LS180
module _74LS180 (
  input  A,
  input  B,
  input  C,
  input  D,
  input  E,
  input  F,
  input  G,
  input  H,
  input  ODD_INPUT,
  input  EVEN_INPUT,
  output \Σ_EVEN_OUTPUT ,
  output \Σ_ODD_OUTPUT 
);

  wire and_1_out, and_2_out, and_3_out, and_4_out, not_1_out, xnor_1_out, xnor_2_out, xnor_3_out, xnor_4_out,
       xnor_5_out, xor_1_out, xor_2_out;

  xnor xnor_1 (xnor_1_out, A, B);
  xnor xnor_2 (xnor_2_out, C, D);
  xnor xnor_3 (xnor_3_out, E, F);
  xnor xnor_4 (xnor_4_out, G, H);
  xor xor_1 (xor_1_out, xnor_1_out, xnor_2_out);
  xnor xnor_5 (xnor_5_out, xor_1_out, xor_2_out);
  xor xor_2 (xor_2_out, xnor_3_out, xnor_4_out);
  not not_1 (not_1_out, xnor_5_out);
  and and_1 (and_1_out, xnor_5_out, ODD_INPUT);
  and and_2 (and_2_out, not_1_out, EVEN_INPUT);
  and and_3 (and_3_out, EVEN_INPUT, xnor_5_out);
  and and_4 (and_4_out, not_1_out, ODD_INPUT);
  and and_5 (\Σ_EVEN_OUTPUT , ~and_1_out, ~and_2_out);  // AND_Gate
  and and_6 (\Σ_ODD_OUTPUT , ~and_3_out, ~and_4_out);  // AND_Gate

  // Notes on the sheet:
  //   74LS180
endmodule
