// Logisim project 74LS181.circ as structural Verilog: 1 circuit, main circuit 74LS181
module _74LS181 (
  input  S0,
  input  S1,
  input  S2,
  input  S3,
  input  nB3,
  input  nA3,
  input  nB2,
  input  nA2,
  input  nB1,
  input  nA1,
  input  nB0,
  input  nA0,
  input  M,
  input  Cn,
  output nG,
  output Cn_4,
  output nP,
  output nF3,
  output nF2,
  output A_B,
  output nF1,
  output nF0
);

  wire and_1_out, and_2_out, and_3_out, and_4_out, and_5_out, and_6_out, and_7_out, and_8_out, and_9_out,
       and_10_out, and_11_out, and_12_out, and_13_out, and_14_out, and_15_out, and_16_out, and_17_out,
       and_18_out, and_19_out, and_20_out, and_21_out, and_22_out, and_23_out, and_24_out, and_25_out,
       and_26_out, and_27_out, and_28_out, buffer_1_out, buffer_2_out, buffer_3_out, buffer_4_out,
       buffer_5_out, nand_1_out, nand_3_out, nor_1_out, nor_2_out, nor_3_out, nor_4_out, nor_5_out,
       nor_6_out, nor_7_out, nor_8_out, nor_10_out, nor_11_out, nor_12_out, not_1_out, not_2_out, not_3_out,
       not_4_out, not_5_out, xor_1_out, xor_2_out, xor_3_out, xor_4_out;

  not not_1 (not_1_out, nB3);
  not not_2 (not_2_out, nB2);
  not not_3 (not_3_out, nB1);
  not not_4 (not_4_out, nB0);
  not not_5 (not_5_out, M);
  and and_1 (and_1_out, nB3, S3, nA3);
  and and_2 (and_2_out, nA3, S2, not_1_out);
  and and_3 (and_3_out, not_1_out, S1);
  and and_4 (and_4_out, S0, nB3);
  buf buffer_1 (buffer_1_out, nA3);
  and and_5 (and_5_out, nB2, S3, nA2);
  and and_6 (and_6_out, nA2, S2, not_2_out);
  and and_7 (and_7_out, not_2_out, S1);
  and and_8 (and_8_out, S0, nB2);
  buf buffer_2 (buffer_2_out, nA2);
  and and_9 (and_9_out, nB1, S3, nA1);
  and and_10 (and_10_out, nA1, S2, not_3_out);
  and and_11 (and_11_out, not_3_out, S1);
  and and_12 (and_12_out, S0, nB1);
  buf buffer_3 (buffer_3_out, nA1);
  and and_13 (and_13_out, nB0, S3, nA0);
  and and_14 (and_14_out, nA0, S2, not_4_out);
  and and_15 (and_15_out, not_4_out, S1);
  and and_16 (and_16_out, S0, nB0);
  buf buffer_4 (buffer_4_out, nA0);
  nor nor_1 (nor_1_out, and_1_out, and_2_out);
  nor nor_2 (nor_2_out, and_3_out, and_4_out, buffer_1_out);
  nor nor_3 (nor_3_out, and_5_out, and_6_out);
  nor nor_4 (nor_4_out, and_7_out, and_8_out, buffer_2_out);
  nor nor_5 (nor_5_out, and_9_out, and_10_out);
  nor nor_6 (nor_6_out, and_11_out, and_12_out, buffer_3_out);
  nor nor_7 (nor_7_out, and_13_out, and_14_out);
  nor nor_8 (nor_8_out, and_15_out, and_16_out, buffer_4_out);
  xor xor_1 (xor_1_out, nor_1_out, nor_2_out);
  xor xor_2 (xor_2_out, nor_3_out, nor_4_out);
  xor xor_3 (xor_3_out, nor_5_out, nor_6_out);
  xor xor_4 (xor_4_out, nor_7_out, nor_8_out);
  buf buffer_5 (buffer_5_out, nor_2_out);
  and and_17 (and_17_out, nor_1_out, nor_4_out);
  and and_18 (and_18_out, nor_1_out, nor_3_out, nor_6_out);
  and and_19 (and_19_out, nor_1_out, nor_3_out, nor_5_out, nor_8_out);
  nand nand_1 (nand_1_out, nor_1_out, nor_3_out, nor_5_out, nor_7_out, Cn);
  nand nand_2 (nP, nor_1_out, nor_3_out, nor_5_out, nor_7_out);
  and and_20 (and_20_out, Cn, nor_7_out, nor_5_out, nor_3_out, not_5_out);
  and and_21 (and_21_out, nor_5_out, nor_3_out, nor_8_out, not_5_out);
  and and_22 (and_22_out, nor_3_out, nor_6_out, not_5_out);
  and and_23 (and_23_out, nor_4_out, not_5_out);
  and and_24 (and_24_out, Cn, nor_7_out, nor_5_out, not_5_out);
  and and_25 (and_25_out, nor_5_out, nor_8_out, not_5_out);
  and and_26 (and_26_out, nor_6_out, not_5_out);
  and and_27 (and_27_out, Cn, nor_7_out, not_5_out);
  and and_28 (and_28_out, nor_8_out, not_5_out);
  nand nand_3 (nand_3_out, Cn, not_5_out);
  nor nor_9 (nG, buffer_5_out, and_17_out, and_18_out, and_19_out);
  nor nor_10 (nor_10_out, and_20_out, and_21_out, and_22_out, and_23_out);
  nor nor_11 (nor_11_out, and_24_out, and_25_out, and_26_out);
  nor nor_12 (nor_12_out, and_27_out, and_28_out);
  or or_1 (Cn_4, ~nG, ~nand_1_out);  // OR_Gate
  xor xor_5 (nF3, xor_1_out, nor_10_out);
  xor xor_6 (nF2, xor_2_out, nor_11_out);
  xor xor_7 (nF1, xor_3_out, nor_12_out);
  xor xor_8 (nF0, xor_4_out, nand_3_out);
  and and_29 (A_B, nF3, nF2, nF1, nF0);

  // Notes on the sheet:
  //   74LS181
  //   Open Collector
  //   and_29 drives only 0 and floats otherwise
endmodule
