// Logisim project 74LS182.circ as structural Verilog: 1 circuit, main circuit 74LS182
module _74LS182 (
  input  nP3,
  input  nG3,
  input  nP2,
  input  nG2,
  input  nP1,
  input  nG1,
  input  nP0,
  input  nG0,
  input  Cn,
  output nP,
  output nG,
  output Cn_z,
  output Cn_y,
  output Cn_x
);

  wire and_1_out, and_2_out, and_3_out, and_4_out, and_5_out, and_6_out, and_7_out, and_8_out, and_9_out,
       and_10_out, and_11_out, and_12_out, and_13_out, not_1_out;

  not not_1 (not_1_out, Cn);
  or or_1 (nP, nP3, nP2, nP1, nP0);
  and and_1 (and_1_out, nG3, nG2, nG1, nG0);
  and and_2 (and_2_out, nP1, nG3, nG2, nG1);
  and and_3 (and_3_out, nP2, nG3, nG2);
  and and_4 (and_4_out, nP3, nG3);
  and and_5 (and_5_out, nG2, nG1, nG0, not_1_out);
  and and_6 (and_6_out, nP0, nG2, nG1, nG0);
  and and_7 (and_7_out, nP1, nG2, nG1);
  and and_8 (and_8_out, nP2, nG2);
  and and_9 (and_9_out, nG1, nG0, not_1_out);
  and and_10 (and_10_out, nP0, nG1, nG0);
  and and_11 (and_11_out, nP1, nG1);
  and and_12 (and_12_out, nG0, not_1_out);
  and and_13 (and_13_out, nP0, nG0);
  or or_2 (nG, and_1_out, and_2_out, and_3_out, and_4_out);
  nor nor_1 (Cn_z, and_5_out, and_6_out, and_7_out, and_8_out);
  nor nor_2 (Cn_y, and_9_out, and_10_out, and_11_out);
  nor nor_3 (Cn_x, and_12_out, and_13_out);

  // Notes on the sheet:
  //   74LS182
endmodule
