// Logisim project 74LS183.circ as structural Verilog: 2 circuits, main circuit 74LS183
module _74LS183 (
  input  _1A,
  input  _1B,
  input  _1Cn,
  input  _2A,
  input  _2B,
  input  _2Cn,
  output \_1Σ ,
  output _1Cn_1,
  output \_2Σ ,
  output _2Cn_1
);

  Adder adder_1 (.Cn(_1Cn), .B(_1B), .A(_1A), .Cn_1(_1Cn_1), .\Σ (\_1Σ ));
  Adder adder_2 (.Cn(_2Cn), .B(_2B), .A(_2A), .Cn_1(_2Cn_1), .\Σ (\_2Σ ));

  // Notes on the sheet:
  //   74LS183
endmodule

module Adder (
  input  Cn,
  input  B,
  input  A,
  output Cn_1,
  output \Σ 
);

  wire and_1_out, and_2_out, and_3_out, and_4_out, and_5_out, and_6_out, and_7_out;

  and and_1 (and_1_out, ~Cn, ~B);  // AND_Gate
  and and_2 (and_2_out, ~B, ~A);  // AND_Gate
  and and_3 (and_3_out, ~Cn, ~A);  // AND_Gate
  and and_4 (and_4_out, Cn, ~B, A);  // AND_Gate
  and and_5 (and_5_out, ~Cn, B, A);  // AND_Gate
  and and_6 (and_6_out, ~Cn, ~B, ~A);  // AND_Gate
  and and_7 (and_7_out, Cn, B, ~A);  // AND_Gate
  nor nor_1 (Cn_1, and_1_out, and_2_out, and_3_out);
  nor nor_2 (\Σ , and_4_out, and_5_out, and_6_out, and_7_out);

  // Notes on the sheet:
  //   Full Adder
endmodule
