// Logisim project 74LS190.circ as structural Verilog: 2 circuits, main circuit 74LS190
module _74LS190 (
  input  CLK,
  input  D_U,
  input  A,
  input  nCTEN,
  input  B,
  input  C,
  input  D,
  input  nLOAD,
  output nRCO,
  output MAX_MIN,
  output QA,
  output QB,
  output QC,
  output QD
);

  wire and_1_out, and_2_out, and_3_out, and_4_out, and_5_out, and_6_out, and_7_out, and_8_out, and_9_out,
       and_10_out, and_11_out, jk_nclk_ns_nr_1_nq, jk_nclk_ns_nr_2_nq, jk_nclk_ns_nr_3_nq,
       jk_nclk_ns_nr_4_nq, nand_1_out, nand_2_out, nand_3_out, nand_4_out, nand_5_out, nand_6_out,
       nand_7_out, nand_8_out, nand_9_out, not_1_out, not_2_out, not_3_out, not_4_out, not_5_out, or_2_out,
       or_3_out, or_4_out;

  not not_1 (not_1_out, CLK);
  not not_2 (not_2_out, D_U);
  not not_3 (not_3_out, nLOAD);
  not not_4 (not_4_out, not_2_out);
  and and_1 (and_1_out, ~not_4_out, ~nCTEN);  // AND_Gate
  and and_2 (and_2_out, ~nCTEN, ~not_2_out);  // AND_Gate
  and and_3 (and_3_out, not_2_out, QA, QD);
  and and_4 (and_4_out, not_4_out, jk_nclk_ns_nr_1_nq, jk_nclk_ns_nr_2_nq, jk_nclk_ns_nr_3_nq, jk_nclk_ns_nr_4_nq);
  nand nand_1 (nand_1_out, A, not_3_out);
  not not_5 (not_5_out, nCTEN);
  nand nand_2 (nand_2_out, B, not_3_out);
  and and_5 (and_5_out, and_2_out, jk_nclk_ns_nr_1_nq, nand_3_out);
  and and_6 (and_6_out, QA, jk_nclk_ns_nr_4_nq, and_1_out);
  nand nand_3 (nand_3_out, jk_nclk_ns_nr_2_nq, jk_nclk_ns_nr_3_nq, jk_nclk_ns_nr_4_nq);
  nand nand_4 (nand_4_out, C, not_3_out);
  and and_7 (and_7_out, nand_3_out, and_2_out, jk_nclk_ns_nr_1_nq, jk_nclk_ns_nr_2_nq);
  and and_8 (and_8_out, QA, QB, and_1_out);
  nand nand_5 (nand_5_out, D, not_3_out);
  and and_9 (and_9_out, and_2_out, jk_nclk_ns_nr_1_nq, jk_nclk_ns_nr_2_nq, jk_nclk_ns_nr_3_nq);
  and and_10 (and_10_out, QA, QD, and_1_out);
  and and_11 (and_11_out, QA, QB, QC, and_1_out);
  or or_1 (MAX_MIN, and_3_out, and_4_out);
  nand nand_6 (nand_6_out, nand_1_out, not_3_out);
  or or_2 (or_2_out, and_5_out, and_6_out);
  nand nand_7 (nand_7_out, nand_2_out, not_3_out);
  or or_3 (or_3_out, and_7_out, and_8_out);
  nand nand_8 (nand_8_out, nand_4_out, not_3_out);
  or or_4 (or_4_out, and_9_out, and_10_out, and_11_out);
  nand nand_9 (nand_9_out, nand_5_out, not_3_out);
  nand nand_10 (nRCO, not_1_out, not_5_out, MAX_MIN);
  JK_nCLK_nS_nR jk_nclk_ns_nr_1 (
    .J(not_5_out), .nCLK(not_1_out), .K(not_5_out), .Q(QA), .nQ(jk_nclk_ns_nr_1_nq), .nS(nand_1_out),
    .nR(nand_6_out));
  JK_nCLK_nS_nR jk_nclk_ns_nr_2 (
    .J(or_2_out), .nCLK(not_1_out), .K(or_2_out), .Q(QB), .nQ(jk_nclk_ns_nr_2_nq), .nS(nand_2_out),
    .nR(nand_7_out));
  JK_nCLK_nS_nR jk_nclk_ns_nr_3 (
    .J(or_3_out), .nCLK(not_1_out), .K(or_3_out), .Q(QC), .nQ(jk_nclk_ns_nr_3_nq), .nS(nand_4_out),
    .nR(nand_8_out));
  JK_nCLK_nS_nR jk_nclk_ns_nr_4 (
    .J(or_4_out), .nCLK(not_1_out), .K(or_4_out), .Q(QD), .nQ(jk_nclk_ns_nr_4_nq), .nS(nand_5_out),
    .nR(nand_9_out));

  // Notes on the sheet:
  //   74LS190
endmodule

module JK_nCLK_nS_nR (
  input  J,
  input  nCLK,
  input  K,
  input  nS,
  input  nR,
  output Q,
  output nQ
);

  wire not_1_out, not_2_out;

  J_K_Flip_Flop #(.trigger("falling")) Fall (
    .J(J), .clk(nCLK), .K(K), .Q(Q), .Qn(nQ), .preset(not_2_out), .reset(not_1_out));  // open: en
  not not_1 (not_1_out, nR);
  not not_2 (not_2_out, nS);
endmodule
