// Logisim project 74LS192.circ as structural Verilog: 1 circuit, main circuit 74LS192
module _74LS192 (
  input  A,
  input  DOWN,
  input  UP,
  input  B,
  input  C,
  input  D,
  input  CLR,
  input  nLOAD,
  output nBO,
  output nCO,
  output QA,
  output QB,
  output QC,
  output QD
);

  wire and_1_out, and_2_out, and_3_out, and_4_out, and_5_out, and_6_out, and_7_out, Fall_2_qn, Fall_3_qn,
       Fall_4_qn, Fall_qn, nand_1_out, nand_2_out, nand_3_out, nand_4_out, nand_5_out, nand_8_out,
       nand_9_out, nand_10_out, nand_11_out, not_1_out, not_2_out, not_3_out, not_4_out, not_5_out,
       not_6_out, not_7_out, not_8_out, or_1_out, or_2_out, or_3_out, or_4_out, or_5_out, or_6_out, or_7_out,
       or_8_out;

  not not_1 (not_1_out, DOWN);
  not not_2 (not_2_out, UP);
  not not_3 (not_3_out, CLR);
  not not_4 (not_4_out, nLOAD);
  nand nand_1 (nand_1_out, A, not_4_out, not_3_out);
  nand nand_2 (nand_2_out, B, not_4_out, not_3_out);
  and and_1 (and_1_out, not_1_out, Fall_qn, nand_3_out);
  and and_2 (and_2_out, QA, Fall_4_qn, not_2_out);
  nand nand_3 (nand_3_out, Fall_2_qn, Fall_3_qn, Fall_4_qn);
  nand nand_4 (nand_4_out, C, not_4_out, not_3_out);
  and and_3 (and_3_out, nand_3_out, not_1_out, Fall_qn, Fall_2_qn);
  and and_4 (and_4_out, QA, QB, not_2_out);
  nand nand_5 (nand_5_out, D, not_4_out, not_3_out);
  and and_5 (and_5_out, not_1_out, Fall_qn, Fall_2_qn, Fall_3_qn);
  and and_6 (and_6_out, QA, QD, not_2_out);
  and and_7 (and_7_out, QA, QB, QC, not_2_out);
  nand nand_6 (nBO, not_1_out, Fall_qn, Fall_2_qn, Fall_3_qn, Fall_4_qn);
  nand nand_7 (nCO, QA, QD, not_2_out);
  or or_1 (or_1_out, not_1_out, not_2_out);
  or or_2 (or_2_out, and_1_out, and_2_out);
  or or_3 (or_3_out, and_3_out, and_4_out);
  or or_4 (or_4_out, and_5_out, and_6_out, and_7_out);
  nand nand_8 (nand_8_out, nand_1_out, not_4_out);
  nand nand_9 (nand_9_out, nand_2_out, not_4_out);
  nand nand_10 (nand_10_out, nand_4_out, not_4_out);
  not not_5 (not_5_out, nand_5_out);
  nand nand_11 (nand_11_out, nand_5_out, not_4_out);
  not not_6 (not_6_out, nand_1_out);
  T_Flip_Flop #(.trigger("falling")) Fall (
    .clk(or_1_out), .T(1'b1), .Q(QA), .Qn(Fall_qn), .preset(not_6_out), .reset(or_5_out));  // open: en
  or or_5 (or_5_out, ~not_3_out, ~nand_8_out);  // OR_Gate
  not not_7 (not_7_out, nand_2_out);
  T_Flip_Flop #(.trigger("falling")) Fall_2 (
    .clk(or_2_out), .T(1'b1), .Q(QB), .Qn(Fall_2_qn), .preset(not_7_out), .reset(or_6_out));  // open: en
  or or_6 (or_6_out, ~not_3_out, ~nand_9_out);  // OR_Gate
  not not_8 (not_8_out, nand_4_out);
  T_Flip_Flop #(.trigger("falling")) Fall_3 (
    .clk(or_3_out), .T(1'b1), .Q(QC), .Qn(Fall_3_qn), .preset(not_8_out), .reset(or_7_out));  // open: en
  or or_7 (or_7_out, ~not_3_out, ~nand_10_out);  // OR_Gate
  T_Flip_Flop #(.trigger("falling")) Fall_4 (
    .clk(or_4_out), .T(1'b1), .Q(QD), .Qn(Fall_4_qn), .preset(not_5_out), .reset(or_8_out));  // open: en
  or or_8 (or_8_out, ~not_3_out, ~nand_11_out);  // OR_Gate

  // Notes on the sheet:
  //   74LS192
endmodule
