// Logisim project 74LS194.circ as structural Verilog: 1 circuit, main circuit 74LS194
module _74LS194 (
  input  A,
  input  B,
  input  C,
  input  D,
  input  S1,
  input  S0,
  input  SR_SER,
  input  SL_SER,
  input  CLK,
  input  nCLR,
  output QA,
  output QB,
  output QC,
  output QD
);

  wire and_1_out, and_2_out, and_3_out, and_4_out, and_5_out, and_6_out, and_7_out, and_8_out, and_9_out,
       and_10_out, and_11_out, and_12_out, and_13_out, and_14_out, and_15_out, and_16_out, nor_1_out,
       nor_2_out, nor_3_out, nor_4_out, not_1_out, not_2_out, not_3_out, not_4_out, not_5_out, not_6_out,
       not_7_out, not_8_out, not_9_out, not_10_out;

  not not_1 (not_1_out, S1);
  not not_2 (not_2_out, S0);
  and and_1 (and_1_out, SR_SER, not_1_out, S0);
  and and_2 (and_2_out, not_2_out, S1, QB);
  and and_3 (and_3_out, S0, S1, A);
  nor nor_1 (nor_1_out, and_1_out, and_3_out, and_2_out, and_4_out);
  not not_3 (not_3_out, nor_1_out);
  and and_4 (and_4_out, not_2_out, not_1_out, QA);
  S_R_Flip_Flop s_r_ff_1 (.S(not_3_out), .clk(CLK), .R(nor_1_out), .Q(QA), .reset(not_4_out));  // open: Qn, preset, en
  not not_4 (not_4_out, nCLR);
  and and_5 (and_5_out, QA, not_1_out, S0);
  and and_6 (and_6_out, S0, S1, B);
  nor nor_2 (nor_2_out, and_5_out, and_6_out, and_8_out, and_7_out);
  and and_7 (and_7_out, not_2_out, not_1_out, QB);
  and and_8 (and_8_out, not_2_out, S1, QC);
  not not_5 (not_5_out, nor_2_out);
  S_R_Flip_Flop s_r_ff_2 (.S(not_5_out), .clk(CLK), .R(nor_2_out), .Q(QB), .reset(not_6_out));  // open: Qn, preset, en
  not not_6 (not_6_out, nCLR);
  and and_9 (and_9_out, S0, S1, C);
  and and_10 (and_10_out, QB, not_1_out, S0);
  and and_11 (and_11_out, not_2_out, S1, QD);
  and and_12 (and_12_out, not_2_out, not_1_out, QC);
  nor nor_3 (nor_3_out, and_10_out, and_9_out, and_11_out, and_12_out);
  not not_7 (not_7_out, nor_3_out);
  not not_8 (not_8_out, nCLR);
  and and_13 (and_13_out, QC, not_1_out, S0);
  S_R_Flip_Flop s_r_ff_3 (.S(not_7_out), .clk(CLK), .R(nor_3_out), .Q(QC), .reset(not_8_out));  // open: Qn, preset, en
  and and_14 (and_14_out, S0, S1, D);
  and and_15 (and_15_out, not_2_out, S1, SL_SER);
  nor nor_4 (nor_4_out, and_13_out, and_14_out, and_15_out, and_16_out);
  not not_9 (not_9_out, nor_4_out);
  and and_16 (and_16_out, not_2_out, not_1_out, QD);
  S_R_Flip_Flop s_r_ff_4 (.S(not_9_out), .clk(CLK), .R(nor_4_out), .Q(QD), .reset(not_10_out));  // open: Qn, preset, en
  not not_10 (not_10_out, nCLR);

  // Notes on the sheet:
  //   74LS194
endmodule
