// Logisim project 74LS195.circ as structural Verilog: 1 circuit, main circuit 74LS195
module _74LS195 (
  input  J,
  input  nK,
  input  A,
  input  B,
  input  C,
  input  D,
  input  SH_LD,
  input  CLK,
  input  nCLR,
  output QA,
  output QB,
  output QC,
  output QD,
  output nQD
);

  wire and_1_out, and_2_out, and_3_out, and_4_out, and_5_out, and_6_out, and_7_out, and_8_out, and_9_out,
       and_10_out, nor_1_out, nor_2_out, nor_3_out, nor_4_out, not_1_out, not_2_out, not_3_out, not_4_out,
       not_5_out, not_6_out, s_r_ff_1_qn;

  not not_1 (not_1_out, SH_LD);
  and and_1 (and_1_out, s_r_ff_1_qn, J, SH_LD);
  and and_2 (and_2_out, SH_LD, nK, QA);
  nor nor_1 (nor_1_out, and_1_out, and_2_out, and_4_out);
  not not_2 (not_2_out, nor_1_out);
  and and_3 (and_3_out, CLK, nCLR);
  not not_3 (not_3_out, nCLR);
  and and_4 (and_4_out, not_1_out, A);
  and and_5 (and_5_out, QA, SH_LD);
  S_R_Flip_Flop s_r_ff_1 (
    .S(not_2_out), .clk(and_3_out), .R(nor_1_out), .Q(QA), .Qn(s_r_ff_1_qn), .reset(not_3_out));  // open: preset, en
  and and_6 (and_6_out, not_1_out, B);
  nor nor_2 (nor_2_out, and_5_out, and_6_out);
  S_R_Flip_Flop s_r_ff_2 (
    .S(not_4_out), .clk(and_3_out), .R(nor_2_out), .Q(QB), .reset(not_3_out));  // open: Qn, preset, en
  not not_4 (not_4_out, nor_2_out);
  and and_7 (and_7_out, QB, SH_LD);
  and and_8 (and_8_out, not_1_out, C);
  nor nor_3 (nor_3_out, and_7_out, and_8_out);
  not not_5 (not_5_out, nor_3_out);
  and and_9 (and_9_out, not_1_out, D);
  and and_10 (and_10_out, QC, SH_LD);
  nor nor_4 (nor_4_out, and_10_out, and_9_out);
  S_R_Flip_Flop s_r_ff_3 (
    .S(not_5_out), .clk(and_3_out), .R(nor_3_out), .Q(QC), .reset(not_3_out));  // open: Qn, preset, en
  not not_6 (not_6_out, nor_4_out);
  S_R_Flip_Flop s_r_ff_4 (
    .S(not_6_out), .clk(and_3_out), .R(nor_4_out), .Q(QD), .Qn(nQD), .reset(not_3_out));  // open: preset, en
endmodule
