// Logisim project 74LS196.circ as structural Verilog: 1 circuit, main circuit 74LS196
module _74LS196 (
  input  A,
  input  nLOAD,
  input  nCLR,
  input  CLK1,
  input  B,
  input  CLK2,
  input  C,
  input  D,
  output QA,
  output QB,
  output QC,
  output QD
);

  wire and_1_out, Fall_4_qn, nand_1_out, nand_2_out, nand_3_out, nand_4_out, nand_5_out, nand_6_out,
       nand_7_out, nand_8_out, not_1_out, not_2_out, not_3_out, not_4_out, not_5_out, not_6_out, not_7_out,
       not_8_out, or_1_out;

  or or_1 (or_1_out, ~nLOAD, ~nCLR);  // OR_Gate
  nand nand_1 (nand_1_out, A, or_1_out, nCLR);
  nand nand_2 (nand_2_out, B, or_1_out, nCLR);
  nand nand_3 (nand_3_out, C, or_1_out, nCLR);
  nand nand_4 (nand_4_out, D, or_1_out, nCLR);
  not not_1 (not_1_out, nand_1_out);
  nand nand_5 (nand_5_out, nand_1_out, or_1_out);
  not not_2 (not_2_out, nand_2_out);
  nand nand_6 (nand_6_out, nand_2_out, or_1_out);
  not not_3 (not_3_out, nand_3_out);
  nand nand_7 (nand_7_out, nand_3_out, or_1_out);
  not not_4 (not_4_out, nand_4_out);
  and and_1 (and_1_out, QB, QC);
  nand nand_8 (nand_8_out, nand_4_out, or_1_out);
  T_Flip_Flop #(.trigger("falling")) Fall (
    .clk(CLK1), .T(1'b1), .Q(QA), .preset(not_1_out), .reset(not_5_out));  // open: Qn, en
  not not_5 (not_5_out, nand_5_out);
  J_K_Flip_Flop #(.trigger("falling")) Fall_2 (
    .J(Fall_4_qn), .clk(CLK2), .K(Fall_4_qn), .Q(QB), .preset(not_2_out), .reset(not_6_out));  // open: Qn, en
  not not_6 (not_6_out, nand_6_out);
  T_Flip_Flop #(.trigger("falling")) Fall_3 (
    .clk(QB), .T(1'b1), .Q(QC), .preset(not_3_out), .reset(not_7_out));  // open: Qn, en
  not not_7 (not_7_out, nand_7_out);
  J_K_Flip_Flop #(.trigger("falling")) Fall_4 (
    .J(and_1_out), .clk(CLK2), .K(QD), .Q(QD), .Qn(Fall_4_qn), .preset(not_4_out), .reset(not_8_out));  // open: en
  not not_8 (not_8_out, nand_8_out);

  // Notes on the sheet:
  //   74LS196
endmodule
