// Logisim project 74LS198.circ as structural Verilog: 2 circuits, main circuit 74LS198
module _74LS198 (
  input  CLK,
  input  SR_SER,
  input  S1,
  input  S0,
  input  A,
  input  B,
  input  C,
  input  D,
  input  E,
  input  F,
  input  G,
  input  H,
  input  SL_SER,
  input  nCLR,
  output QA,
  output QB,
  output QC,
  output QD,
  output QE,
  output QF,
  output QG,
  output QH
);

  wire and_1_out, and_2_out, and_3_out, and_4_out, and_5_out, and_6_out, and_7_out, and_8_out, and_9_out,
       and_10_out, and_11_out, and_12_out, and_13_out, and_14_out, and_15_out, and_16_out, and_17_out,
       and_18_out, and_19_out, and_20_out, and_21_out, and_22_out, and_23_out, and_24_out, and_25_out,
       nor_1_out, nor_2_out, nor_3_out, nor_4_out, nor_5_out, nor_6_out, nor_7_out, nor_8_out, nor_9_out,
       nor_10_out, not_1_out, not_2_out;

  not not_1 (not_1_out, S1);
  not not_2 (not_2_out, S0);
  and and_1 (and_1_out, not_2_out, not_1_out);
  nor nor_1 (nor_1_out, not_1_out, not_2_out);
  nor nor_2 (nor_2_out, CLK, and_1_out);
  and and_2 (and_2_out, SR_SER, not_1_out);
  and and_3 (and_3_out, nor_1_out, A);
  and and_4 (and_4_out, not_2_out, QB);
  and and_5 (and_5_out, QA, not_1_out);
  and and_6 (and_6_out, nor_1_out, B);
  and and_7 (and_7_out, not_2_out, QC);
  and and_8 (and_8_out, QB, not_1_out);
  and and_9 (and_9_out, nor_1_out, C);
  and and_10 (and_10_out, not_2_out, QD);
  and and_11 (and_11_out, QC, not_1_out);
  and and_12 (and_12_out, nor_1_out, D);
  and and_13 (and_13_out, not_2_out, QE);
  and and_14 (and_14_out, QD, not_1_out);
  and and_15 (and_15_out, nor_1_out, E);
  and and_16 (and_16_out, not_2_out, QF);
  and and_17 (and_17_out, QE, not_1_out);
  and and_18 (and_18_out, nor_1_out, F);
  and and_19 (and_19_out, not_2_out, QG);
  and and_20 (and_20_out, QF, not_1_out);
  and and_21 (and_21_out, nor_1_out, G);
  and and_22 (and_22_out, not_2_out, QH);
  and and_23 (and_23_out, QG, not_1_out);
  and and_24 (and_24_out, nor_1_out, H);
  and and_25 (and_25_out, not_2_out, SL_SER);
  nor nor_3 (nor_3_out, and_2_out, and_3_out, and_4_out);
  nor nor_4 (nor_4_out, and_5_out, and_6_out, and_7_out);
  nor nor_5 (nor_5_out, and_8_out, and_9_out, and_10_out);
  nor nor_6 (nor_6_out, and_11_out, and_12_out, and_13_out);
  nor nor_7 (nor_7_out, and_14_out, and_15_out, and_16_out);
  nor nor_8 (nor_8_out, and_17_out, and_18_out, and_19_out);
  nor nor_9 (nor_9_out, and_20_out, and_21_out, and_22_out);
  nor nor_10 (nor_10_out, and_23_out, and_24_out, and_25_out);
  SR_nCK_nS_nCLR sr_nck_ns_nclr_1 (.nS(nor_3_out), .nCK(nor_2_out), .R(nor_3_out), .Q(QA), .nCLR(nCLR));
  SR_nCK_nS_nCLR sr_nck_ns_nclr_2 (.nS(nor_4_out), .nCK(nor_2_out), .R(nor_4_out), .Q(QB), .nCLR(nCLR));
  SR_nCK_nS_nCLR sr_nck_ns_nclr_3 (.nS(nor_5_out), .nCK(nor_2_out), .R(nor_5_out), .Q(QC), .nCLR(nCLR));
  SR_nCK_nS_nCLR sr_nck_ns_nclr_4 (.nS(nor_6_out), .nCK(nor_2_out), .R(nor_6_out), .Q(QD), .nCLR(nCLR));
  SR_nCK_nS_nCLR sr_nck_ns_nclr_5 (.nS(nor_7_out), .nCK(nor_2_out), .R(nor_7_out), .Q(QE), .nCLR(nCLR));
  SR_nCK_nS_nCLR sr_nck_ns_nclr_6 (.nS(nor_8_out), .nCK(nor_2_out), .R(nor_8_out), .Q(QF), .nCLR(nCLR));
  SR_nCK_nS_nCLR sr_nck_ns_nclr_7 (.nS(nor_9_out), .nCK(nor_2_out), .R(nor_9_out), .Q(QG), .nCLR(nCLR));
  SR_nCK_nS_nCLR sr_nck_ns_nclr_8 (.nS(nor_10_out), .nCK(nor_2_out), .R(nor_10_out), .Q(QH), .nCLR(nCLR));

  // Notes on the sheet:
  //   74LS198
endmodule

module SR_nCK_nS_nCLR (
  input  nS,
  input  nCK,
  input  R,
  input  nCLR,
  output Q
);

  wire not_1_out, not_2_out;

  S_R_Flip_Flop #(.trigger("falling")) Fall (
    .S(not_1_out), .clk(nCK), .R(R), .Q(Q), .reset(not_2_out));  // open: Qn, preset, en
  not not_1 (not_1_out, nS);
  not not_2 (not_2_out, nCLR);
endmodule
