// Logisim project 74LS199.circ as structural Verilog: 2 circuits, main circuit 74LS199
module _74LS199 (
  input  CLK,
  input  CLK_INH,
  input  J,
  input  nK,
  input  SH_LD,
  input  A,
  input  B,
  input  C,
  input  D,
  input  E,
  input  F,
  input  G,
  input  H,
  input  nCLR,
  output QA,
  output QB,
  output QC,
  output QD,
  output QE,
  output QF,
  output QG,
  output QH
);

  wire and_1_out, and_2_out, and_3_out, and_4_out, and_5_out, and_6_out, and_7_out, and_8_out, and_9_out,
       and_10_out, and_11_out, and_12_out, and_13_out, and_14_out, and_15_out, and_16_out, and_17_out,
       nor_1_out, nor_2_out, nor_3_out, nor_4_out, nor_5_out, nor_6_out, nor_7_out, nor_8_out, nor_9_out,
       not_1_out, not_2_out, sr_nck_ns_nclr_1_nq;

  not not_1 (not_1_out, SH_LD);
  nor nor_1 (nor_1_out, CLK, CLK_INH);
  not not_2 (not_2_out, not_1_out);
  and and_1 (and_1_out, J, not_2_out, sr_nck_ns_nclr_1_nq);
  and and_2 (and_2_out, not_1_out, A);
  nor nor_2 (nor_2_out, and_1_out, and_2_out, and_3_out);
  and and_3 (and_3_out, nK, not_2_out, QA);
  and and_4 (and_4_out, QA, not_2_out);
  nor nor_3 (nor_3_out, and_4_out, and_5_out);
  and and_5 (and_5_out, not_1_out, B);
  and and_6 (and_6_out, QB, not_2_out);
  nor nor_4 (nor_4_out, and_6_out, and_7_out);
  and and_7 (and_7_out, not_1_out, C);
  and and_8 (and_8_out, QC, not_2_out);
  nor nor_5 (nor_5_out, and_8_out, and_9_out);
  and and_9 (and_9_out, not_1_out, D);
  and and_10 (and_10_out, QD, not_2_out);
  nor nor_6 (nor_6_out, and_10_out, and_11_out);
  and and_11 (and_11_out, not_1_out, E);
  and and_12 (and_12_out, QE, not_2_out);
  nor nor_7 (nor_7_out, and_12_out, and_13_out);
  and and_13 (and_13_out, not_1_out, F);
  and and_14 (and_14_out, QF, not_2_out);
  nor nor_8 (nor_8_out, and_14_out, and_15_out);
  and and_15 (and_15_out, not_1_out, G);
  and and_16 (and_16_out, QG, not_2_out);
  nor nor_9 (nor_9_out, and_16_out, and_17_out);
  and and_17 (and_17_out, not_1_out, H);
  SR_nCK_nS_nCLR sr_nck_ns_nclr_1 (
    .nS(nor_2_out), .nCK(nor_1_out), .R(nor_2_out), .Q(QA), .nCLR(nCLR), .nQ(sr_nck_ns_nclr_1_nq));
  SR_nCK_nS_nCLR sr_nck_ns_nclr_2 (.nS(nor_3_out), .nCK(nor_1_out), .R(nor_3_out), .Q(QB), .nCLR(nCLR));  // open: nQ
  SR_nCK_nS_nCLR sr_nck_ns_nclr_3 (.nS(nor_4_out), .nCK(nor_1_out), .R(nor_4_out), .Q(QC), .nCLR(nCLR));  // open: nQ
  SR_nCK_nS_nCLR sr_nck_ns_nclr_4 (.nS(nor_5_out), .nCK(nor_1_out), .R(nor_5_out), .Q(QD), .nCLR(nCLR));  // open: nQ
  SR_nCK_nS_nCLR sr_nck_ns_nclr_5 (.nS(nor_6_out), .nCK(nor_1_out), .R(nor_6_out), .Q(QE), .nCLR(nCLR));  // open: nQ
  SR_nCK_nS_nCLR sr_nck_ns_nclr_6 (.nS(nor_7_out), .nCK(nor_1_out), .R(nor_7_out), .Q(QF), .nCLR(nCLR));  // open: nQ
  SR_nCK_nS_nCLR sr_nck_ns_nclr_7 (.nS(nor_8_out), .nCK(nor_1_out), .R(nor_8_out), .Q(QG), .nCLR(nCLR));  // open: nQ
  SR_nCK_nS_nCLR sr_nck_ns_nclr_8 (.nS(nor_9_out), .nCK(nor_1_out), .R(nor_9_out), .Q(QH), .nCLR(nCLR));  // open: nQ

  // Notes on the sheet:
  //   74LS199
endmodule

module SR_nCK_nS_nCLR (
  input  nS,
  input  nCK,
  input  R,
  input  nCLR,
  output Q,
  output nQ
);

  wire not_1_out, not_2_out;

  S_R_Flip_Flop #(.trigger("falling")) Fall (
    .S(not_1_out), .clk(nCK), .R(R), .Q(Q), .Qn(nQ), .reset(not_2_out));  // open: preset, en
  not not_1 (not_1_out, nS);
  not not_2 (not_2_out, nCLR);
endmodule
