// Logisim project 74LS200.circ as structural Verilog: 1 circuit, main circuit 74LS200
module _74LS200 (
  input  DATA_INPUT,
  input  A,
  input  B,
  input  C,
  input  D,
  input  E,
  input  F,
  input  G,
  input  H,
  input  nME1,
  input  nME2,
  input  nME3,
  input  nWE,
  output OUTPUT_Y
);

  wire and_1_out, and_2_out, controlled_buffer_1_out, not_1_out;

  and and_1 (and_1_out, ~nME1, ~nME2, ~nME3);  // AND_Gate
  assign controlled_buffer_1_out = not_1_out ? DATA_INPUT : 1'bz;  // Controlled_Buffer controlled_buffer_1
  not not_1 (not_1_out, nWE);
  RAM #(.dataWidth(1), .bus("asynch")) ram_1 (
    .addr({H, G, F, E, D, C, B, A}), .data(controlled_buffer_1_out), .sel(and_1_out), .ld(nWE));  // open: clr
  assign OUTPUT_Y = and_2_out ? ~controlled_buffer_1_out : 1'bz;  // Controlled_Inverter controlled_inverter_1
  and and_2 (and_2_out, and_1_out, nWE);

  // Notes on the sheet:
  //   74LS200
endmodule
