// Logisim project 74LS208.circ as structural Verilog: 1 circuit, main circuit 74LS208
module _74LS208 (
  input  AD_A,
  input  AD_B,
  input  AD_C,
  input  AD_D,
  input  AD_E,
  input  AD_F,
  input  AD_G,
  input  AD_H,
  input  DI1,
  input  DI2,
  input  DI3,
  input  DI4,
  input  nOE,
  input  W,
  output DO1,
  output DO2,
  output DO3,
  output DO4
);

  wire not_1_out;

  not not_1 (not_1_out, nOE);
  RAM #(.dataWidth(4), .bus("separate")) ram_1 (
    .addr({AD_H, AD_G, AD_F, AD_E, AD_D, AD_C, AD_B, AD_A}), .din({DI4, DI3, DI2, DI1}),
    .data({DO4, DO3, DO2, DO1}), .clk(W), .ld(not_1_out));  // open: str, sel, clr

  // Notes on the sheet:
  //   74LS208
endmodule
