// Logisim project 74LS209.circ as structural Verilog: 1 circuit, main circuit 74LS209
module _74LS209 (
  input  A,
  input  B,
  input  DATA_IN,
  input  C,
  input  D,
  input  E,
  input  F,
  input  G,
  input  H,
  input  I,
  input  J,
  input  R_W,
  input  nCE,
  output OUTPUT_D0
);

  wire controlled_buffer_1_out, not_1_out, not_2_out;

  not not_1 (not_1_out, nCE);
  assign controlled_buffer_1_out = not_2_out ? DATA_IN : 1'bz;  // Controlled_Buffer controlled_buffer_1
  not not_2 (not_2_out, R_W);
  RAM #(.addrWidth(10), .dataWidth(1), .bus("asynch")) ram_1 (
    .addr({J, I, H, G, F, E, D, C, B, A}), .data(controlled_buffer_1_out), .sel(not_1_out), .ld(R_W));  // open: clr
  assign OUTPUT_D0 = R_W ? controlled_buffer_1_out : 1'bz;  // Controlled_Buffer controlled_buffer_2

  // Notes on the sheet:
  //   74LS209
endmodule
