// Logisim project 74LS210.circ as structural Verilog: 1 circuit, main circuit 74LS210
module _74LS210 (
  input  nE1,
  input  _1A1,
  input  _1A2,
  input  _1A3,
  input  _1A4,
  input  E2,
  input  _2A1,
  input  _2A2,
  input  _2A3,
  input  _2A4,
  output _1_Y1,
  output _1_Y2,
  output _1_Y3,
  output _1_Y4,
  output _2_Y1,
  output _2_Y2,
  output _2_Y3,
  output _2_Y4
);

  wire not_1_out;

  not not_1 (not_1_out, nE1);
  assign _1_Y1 = not_1_out ? ~_1A1 : 1'bz;  // Controlled_Inverter controlled_inverter_1
  assign _1_Y2 = not_1_out ? ~_1A2 : 1'bz;  // Controlled_Inverter controlled_inverter_2
  assign _1_Y3 = not_1_out ? ~_1A3 : 1'bz;  // Controlled_Inverter controlled_inverter_3
  assign _1_Y4 = not_1_out ? ~_1A4 : 1'bz;  // Controlled_Inverter controlled_inverter_4
  assign _2_Y1 = E2 ? ~_2A1 : 1'bz;  // Controlled_Inverter controlled_inverter_5
  assign _2_Y2 = E2 ? ~_2A2 : 1'bz;  // Controlled_Inverter controlled_inverter_6
  assign _2_Y3 = E2 ? ~_2A3 : 1'bz;  // Controlled_Inverter controlled_inverter_7
  assign _2_Y4 = E2 ? ~_2A4 : 1'bz;  // Controlled_Inverter controlled_inverter_8

  // Notes on the sheet:
  //   74LS210
endmodule
