// Logisim project 74LS226.circ as structural Verilog: 1 circuit, main circuit 74LS226
module _74LS226 (
  input  A1,
  input  B1,
  input  A2,
  input  B2,
  input  A3,
  input  B3,
  input  A4,
  input  B4,
  input  STROBE_GAB,
  input  STROBE_GBA,
  input  S1,
  input  S2,
  output B1_2,
  output A1_2,
  output B2_2,
  output A2_2,
  output B3_2,
  output A3_2,
  output B4_2,
  output A4_2
);

  wire A___B, and_1_out, and_2_out, and_3_out, and_4_out, B___A, High_3_q, High_5_q, High_7_q, High_9_q,
       High_10_q, High_11_q, High_12_q, High_q, or_1_out, or_2_out, or_3_out, or_4_out, OUTPUT_STORED,
       STORE_A_AND_B;

  and and_1 (and_1_out, or_1_out, ~STROBE_GAB);  // AND_Gate
  or or_1 (or_1_out, A___B, STORE_A_AND_B);
  D_Flip_Flop #(.trigger("high")) High (.clk(and_1_out), .D(A1), .Q(High_q));  // open: Qn, preset, en, reset
  D_Flip_Flop #(.trigger("high")) High_2 (.clk(and_2_out), .D(High_q), .Q(B1_2));  // open: Qn, preset, en, reset
  D_Flip_Flop #(.trigger("high")) High_3 (.clk(and_1_out), .D(A2), .Q(High_3_q));  // open: Qn, preset, en, reset
  D_Flip_Flop #(.trigger("high")) High_4 (.clk(and_2_out), .D(High_3_q), .Q(B2_2));  // open: Qn, preset, en, reset
  D_Flip_Flop #(.trigger("high")) High_5 (.clk(and_1_out), .D(A3), .Q(High_5_q));  // open: Qn, preset, en, reset
  D_Flip_Flop #(.trigger("high")) High_6 (.clk(and_2_out), .D(High_5_q), .Q(B3_2));  // open: Qn, preset, en, reset
  D_Flip_Flop #(.trigger("high")) High_7 (.clk(and_1_out), .D(A4), .Q(High_7_q));  // open: Qn, preset, en, reset
  D_Flip_Flop #(.trigger("high")) High_8 (.clk(and_2_out), .D(High_7_q), .Q(B4_2));  // open: Qn, preset, en, reset
  and and_2 (and_2_out, ~STROBE_GAB, or_2_out);  // AND_Gate
  or or_2 (or_2_out, A___B, OUTPUT_STORED);
  Decoder #(.select(2), .enable("false")) decoder_1 (
    .out0(B___A), .out1(OUTPUT_STORED), .out2(A___B), .out3(STORE_A_AND_B), .sel({S2, S1}));
  and and_3 (and_3_out, or_3_out, ~STROBE_GBA);  // AND_Gate
  or or_3 (or_3_out, B___A, STORE_A_AND_B);
  D_Flip_Flop #(.trigger("high")) High_9 (.clk(and_3_out), .D(B1), .Q(High_9_q));  // open: Qn, preset, en, reset
  D_Flip_Flop #(.trigger("high")) High_10 (.clk(and_3_out), .D(B2), .Q(High_10_q));  // open: Qn, preset, en, reset
  D_Flip_Flop #(.trigger("high")) High_11 (.clk(and_3_out), .D(B3), .Q(High_11_q));  // open: Qn, preset, en, reset
  D_Flip_Flop #(.trigger("high")) High_12 (.clk(and_3_out), .D(B4), .Q(High_12_q));  // open: Qn, preset, en, reset
  and and_4 (and_4_out, ~STROBE_GBA, or_4_out);  // AND_Gate
  or or_4 (or_4_out, B___A, OUTPUT_STORED);
  D_Flip_Flop #(.trigger("high")) High_13 (.clk(and_4_out), .D(High_9_q), .Q(A1_2));  // open: Qn, preset, en, reset
  D_Flip_Flop #(.trigger("high")) High_14 (.clk(and_4_out), .D(High_10_q), .Q(A2_2));  // open: Qn, preset, en, reset
  D_Flip_Flop #(.trigger("high")) High_15 (.clk(and_4_out), .D(High_11_q), .Q(A3_2));  // open: Qn, preset, en, reset
  D_Flip_Flop #(.trigger("high")) High_16 (.clk(and_4_out), .D(High_12_q), .Q(A4_2));  // open: Qn, preset, en, reset

  // Notes on the sheet:
  //   74LS226
endmodule
