// Logisim project 74LS237.circ as structural Verilog: 1 circuit, main circuit 74LS237
module _74LS237 (
  input  nOE1,
  input  OE0,
  input  nLE,
  input  A0,
  input  A1,
  input  A2,
  output Y0,
  output Y1,
  output Y2,
  output Y3,
  output Y4,
  output Y5,
  output Y6,
  output Y7
);

  wire nor_1_out, not_1_out;
  wire [2:0] Low_Level_q;

  nor nor_1 (nor_1_out, nOE1, not_1_out);
  not not_1 (not_1_out, OE0);
  D_Flip_Flop #(.trigger("low")) Low_Level (.clk(nLE), .D(A0), .Q(Low_Level_q[0]));  // open: Qn, preset, en, reset
  D_Flip_Flop #(.trigger("low")) Low_Level_2 (.clk(nLE), .D(A1), .Q(Low_Level_q[1]));  // open: Qn, preset, en, reset
  D_Flip_Flop #(.trigger("low")) Low_Level_3 (.clk(nLE), .D(A2), .Q(Low_Level_q[2]));  // open: Qn, preset, en, reset
  Demultiplexer #(.select(3), .disabled(0)) demultiplexer_1 (
    .out0(Y0), .out1(Y1), .out2(Y2), .out3(Y3), .out4(Y4), .out5(Y5), .out6(Y6), .out7(Y7), .in(1'b1),
    .sel(Low_Level_q), .en(nor_1_out));

  // Notes on the sheet:
  //   74LS237
endmodule
