// Logisim project 74LS238.circ as structural Verilog: 1 circuit, main circuit 74LS238
module _74LS238 (
  input  G1,
  input  nG2_A,
  input  nG2_B,
  input  A,
  input  B,
  input  C,
  output Y0,
  output Y1,
  output Y2,
  output Y3,
  output Y4,
  output Y5,
  output Y6,
  output Y7
);

  wire and_1_out, not_1_out, not_2_out, not_3_out, not_4_out, not_5_out, not_6_out, not_7_out;

  not not_1 (not_1_out, G1);
  not not_2 (not_2_out, C);
  and and_1 (and_1_out, ~not_1_out, ~nG2_A, ~nG2_B);  // AND_Gate
  not not_3 (not_3_out, A);
  not not_4 (not_4_out, B);
  not not_5 (not_5_out, not_3_out);
  not not_6 (not_6_out, not_4_out);
  not not_7 (not_7_out, not_2_out);
  and and_2 (Y0, not_3_out, not_4_out, not_2_out, and_1_out);
  and and_3 (Y1, not_5_out, not_4_out, not_2_out, and_1_out);
  and and_4 (Y2, not_3_out, not_6_out, not_2_out, and_1_out);
  and and_5 (Y3, not_5_out, not_6_out, not_2_out, and_1_out);
  and and_6 (Y4, not_3_out, not_4_out, not_7_out, and_1_out);
  and and_7 (Y5, not_4_out, not_7_out, not_5_out, and_1_out);
  and and_8 (Y6, not_3_out, not_7_out, not_6_out, and_1_out);
  and and_9 (Y7, and_1_out, not_6_out, not_5_out, not_7_out);

  // Notes on the sheet:
  //   74LS238
endmodule
