// Logisim project 74LS239.circ as structural Verilog: 1 circuit, main circuit 74LS239
module _74LS239 (
  input  _1_G,
  input  _1A,
  input  _1B,
  input  _2_G,
  input  _2A,
  input  _2B,
  output _1Y0,
  output _1Y1,
  output _1Y2,
  output _1Y3,
  output _2Y0,
  output _2Y1,
  output _2Y2,
  output _2Y3
);

  wire not_1_out, not_2_out, not_3_out, not_4_out, not_5_out, not_6_out, not_7_out, not_8_out, not_9_out,
       not_10_out;

  not not_1 (not_1_out, _1_G);
  not not_2 (not_2_out, _1A);
  not not_3 (not_3_out, _1B);
  not not_4 (not_4_out, _2_G);
  not not_5 (not_5_out, _2A);
  not not_6 (not_6_out, _2B);
  not not_7 (not_7_out, not_2_out);
  not not_8 (not_8_out, not_3_out);
  not not_9 (not_9_out, not_5_out);
  not not_10 (not_10_out, not_6_out);
  and and_1 (_1Y0, not_2_out, not_3_out, not_1_out);
  and and_2 (_1Y1, not_1_out, not_3_out, not_7_out);
  and and_3 (_1Y2, not_1_out, not_2_out, not_8_out);
  and and_4 (_1Y3, not_1_out, not_7_out, not_8_out);
  and and_5 (_2Y0, not_5_out, not_6_out, not_4_out);
  and and_6 (_2Y1, not_4_out, not_6_out, not_9_out);
  and and_7 (_2Y2, not_4_out, not_5_out, not_10_out);
  and and_8 (_2Y3, not_4_out, not_9_out, not_10_out);

  // Notes on the sheet:
  //   74LS239
endmodule
