// Logisim project 74LS241.circ as structural Verilog: 1 circuit, main circuit 74LS241
module _74LS241 (
  input  _1_G,
  input  _1A1,
  input  _1A2,
  input  _1A3,
  input  _1A4,
  input  _2G,
  input  _2A1,
  input  _2A2,
  input  _2A3,
  input  _2A4,
  output _1Y1,
  output _1Y2,
  output _1Y3,
  output _1Y4,
  output _2Y1,
  output _2Y2,
  output _2Y3,
  output _2Y4
);

  wire buffer_1_out, not_1_out;

  not not_1 (not_1_out, _1_G);
  buf buffer_1 (buffer_1_out, _2G);
  assign _1Y1 = not_1_out ? _1A1 : 1'bz;  // Controlled_Buffer controlled_buffer_1
  assign _1Y2 = not_1_out ? _1A2 : 1'bz;  // Controlled_Buffer controlled_buffer_2
  assign _1Y3 = not_1_out ? _1A3 : 1'bz;  // Controlled_Buffer controlled_buffer_3
  assign _1Y4 = not_1_out ? _1A4 : 1'bz;  // Controlled_Buffer controlled_buffer_4
  assign _2Y1 = buffer_1_out ? _2A1 : 1'bz;  // Controlled_Buffer controlled_buffer_5
  assign _2Y2 = buffer_1_out ? _2A2 : 1'bz;  // Controlled_Buffer controlled_buffer_6
  assign _2Y3 = buffer_1_out ? _2A3 : 1'bz;  // Controlled_Buffer controlled_buffer_7
  assign _2Y4 = buffer_1_out ? _2A4 : 1'bz;  // Controlled_Buffer controlled_buffer_8

  // Notes on the sheet:
  //   74LS241
endmodule
