// Logisim project 74LS243.circ as structural Verilog: 1 circuit, main circuit 74LS243
module _74LS243 (
  input  nGAB,
  input  GBA,
  input  A1,
  input  B1,
  input  A2,
  input  B2,
  input  A3,
  input  B3,
  input  A4,
  input  B4,
  output B1_2,
  output A1_2,
  output B2_2,
  output A2_2,
  output B3_2,
  output A3_2,
  output B4_2,
  output A4_2
);

  wire not_1_out;

  not not_1 (not_1_out, nGAB);
  assign B1_2 = not_1_out ? A1 : 1'bz;  // Controlled_Buffer controlled_buffer_1
  assign B2_2 = not_1_out ? A2 : 1'bz;  // Controlled_Buffer controlled_buffer_2
  assign B3_2 = not_1_out ? A3 : 1'bz;  // Controlled_Buffer controlled_buffer_3
  assign B4_2 = not_1_out ? A4 : 1'bz;  // Controlled_Buffer controlled_buffer_4
  assign A1_2 = GBA ? B1 : 1'bz;  // Controlled_Buffer controlled_buffer_5
  assign A2_2 = GBA ? B2 : 1'bz;  // Controlled_Buffer controlled_buffer_6
  assign A3_2 = GBA ? B3 : 1'bz;  // Controlled_Buffer controlled_buffer_7
  assign A4_2 = GBA ? B4 : 1'bz;  // Controlled_Buffer controlled_buffer_8

  // Notes on the sheet:
  //   74LS243
endmodule
