// Logisim project 74LS245.circ as structural Verilog: 1 circuit, main circuit 74LS245
module _74LS245 (
  input  DIR,
  input  nOE,
  input  A1in,
  input  B1in,
  input  A2in,
  input  B2in,
  input  A3in,
  input  B3in,
  input  A4in,
  input  B4in,
  input  A5in,
  input  B5in,
  input  A6in,
  input  B6in,
  input  A7in,
  input  B7in,
  input  A8in,
  input  B8in,
  output B1out,
  output A1out,
  output B2out,
  output A2out,
  output B3out,
  output A3out,
  output B4out,
  output A4out,
  output B5out,
  output A5out,
  output B6out,
  output A6out,
  output B7out,
  output A7out,
  output B8out,
  output A8out
);

  wire and_1_out, and_2_out;

  and and_1 (and_1_out, DIR, ~nOE);  // AND_Gate
  assign B1out = and_1_out ? A1in : 1'bz;  // Controlled_Buffer controlled_buffer_1
  assign B2out = and_1_out ? A2in : 1'bz;  // Controlled_Buffer controlled_buffer_2
  assign B3out = and_1_out ? A3in : 1'bz;  // Controlled_Buffer controlled_buffer_3
  assign B4out = and_1_out ? A4in : 1'bz;  // Controlled_Buffer controlled_buffer_4
  assign B5out = and_1_out ? A5in : 1'bz;  // Controlled_Buffer controlled_buffer_5
  assign B6out = and_1_out ? A6in : 1'bz;  // Controlled_Buffer controlled_buffer_6
  assign B7out = and_1_out ? A7in : 1'bz;  // Controlled_Buffer controlled_buffer_7
  assign B8out = and_1_out ? A8in : 1'bz;  // Controlled_Buffer controlled_buffer_8
  and and_2 (and_2_out, ~DIR, ~nOE);  // AND_Gate
  assign A1out = and_2_out ? B1in : 1'bz;  // Controlled_Buffer controlled_buffer_9
  assign A2out = and_2_out ? B2in : 1'bz;  // Controlled_Buffer controlled_buffer_10
  assign A3out = and_2_out ? B3in : 1'bz;  // Controlled_Buffer controlled_buffer_11
  assign A4out = and_2_out ? B4in : 1'bz;  // Controlled_Buffer controlled_buffer_12
  assign A5out = and_2_out ? B5in : 1'bz;  // Controlled_Buffer controlled_buffer_13
  assign A6out = and_2_out ? B6in : 1'bz;  // Controlled_Buffer controlled_buffer_14
  assign A7out = and_2_out ? B7in : 1'bz;  // Controlled_Buffer controlled_buffer_15
  assign A8out = and_2_out ? B8in : 1'bz;  // Controlled_Buffer controlled_buffer_16

  // Notes on the sheet:
  //   74LS245
endmodule
