// Logisim project 74LS248.circ as structural Verilog: 1 circuit, main circuit 74LS248
module _74LS248 (
  input  A,
  input  B,
  input  C,
  input  D,
  input  nBI,
  input  nLT,
  input  nRBI,
  output a_2,
  output b_2,
  output c_2,
  output d_2,
  output nRBO,
  output e,
  output f,
  output g
);

  wire and_1_out, and_2_out, and_3_out, and_4_out, and_5_out, and_6_out, and_7_out, and_8_out, and_9_out,
       and_10_out, and_11_out, and_12_out, and_13_out, and_14_out, and_15_out, and_16_out, and_17_out,
       and_18_out, buffer_2_out, nand_1_out, nand_2_out, nand_3_out, nand_4_out, nand_5_out, nand_6_out,
       nand_7_out, nand_8_out, not_1_out, not_2_out;

  nand nand_1 (nand_1_out, A, nLT);
  nand nand_2 (nand_2_out, B, nLT);
  nand nand_3 (nand_3_out, C, nLT);
  not not_1 (not_1_out, D);
  Pull_Resistor #(.pull(1)) pull_resistor_1 (.node(nBI));
  buf buffer_1 (nRBO, nand_8_out);
  not not_2 (not_2_out, nRBI);
  Pull_Resistor #(.pull(1)) pull_resistor_2 (.node(nRBI));
  nand nand_4 (nand_4_out, nand_1_out, and_1_out);
  nand nand_5 (nand_5_out, nand_2_out, and_1_out);
  nand nand_6 (nand_6_out, nand_3_out, and_1_out);
  nand nand_7 (nand_7_out, not_1_out, and_1_out);
  and and_1 (and_1_out, nBI, nand_8_out);
  nand nand_8 (nand_8_out, nLT, not_2_out, not_1_out, nand_3_out, nand_2_out, nand_1_out);
  and and_2 (and_2_out, nand_5_out, nand_7_out);
  and and_3 (and_3_out, nand_1_out, nand_2_out, nand_6_out);
  and and_4 (and_4_out, nand_4_out, nand_2_out, nand_3_out, not_1_out);
  and and_5 (and_5_out, nand_5_out, nand_7_out);
  and and_6 (and_6_out, nand_4_out, nand_2_out, nand_6_out);
  and and_7 (and_7_out, nand_1_out, nand_5_out, nand_6_out);
  and and_8 (and_8_out, nand_6_out, nand_7_out);
  and and_9 (and_9_out, nand_1_out, nand_5_out, nand_3_out);
  and and_10 (and_10_out, nand_4_out, nand_2_out, nand_3_out, not_1_out);
  and and_11 (and_11_out, nand_1_out, nand_2_out, nand_6_out);
  and and_12 (and_12_out, nand_4_out, nand_5_out, nand_6_out);
  buf buffer_2 (buffer_2_out, nand_4_out);
  and and_13 (and_13_out, nand_2_out, nand_6_out);
  and and_14 (and_14_out, nand_4_out, nand_5_out);
  and and_15 (and_15_out, nand_5_out, nand_3_out);
  and and_16 (and_16_out, nand_4_out, nand_3_out, not_1_out);
  and and_17 (and_17_out, nand_4_out, nand_5_out, nand_6_out);
  and and_18 (and_18_out, nand_2_out, nand_3_out, not_1_out, nLT);
  and and_19 (a_2, ~and_2_out, ~and_3_out, ~and_4_out);  // AND_Gate
  and and_20 (b_2, ~and_5_out, ~and_6_out, ~and_7_out);  // AND_Gate
  and and_21 (c_2, ~and_8_out, ~and_9_out);  // AND_Gate
  and and_22 (d_2, ~and_10_out, ~and_11_out, ~and_12_out);  // AND_Gate
  and and_23 (e, ~buffer_2_out, ~and_13_out);  // AND_Gate
  and and_24 (f, ~and_14_out, ~and_15_out, ~and_16_out);  // AND_Gate
  and and_25 (g, ~and_17_out, ~and_18_out);  // AND_Gate

  // Notes on the sheet:
  //   74LS248
  //   buffer_1 drives only 0 and floats otherwise
endmodule
