// Logisim project 74LS249.circ as structural Verilog: 1 circuit, main circuit 74LS249
module _74LS249 (
  input  A,
  input  B,
  input  C,
  input  D,
  input  nBI,
  input  nLT,
  input  nRBI,
  output a_2,
  output b_2,
  output c_2,
  output d_2,
  output nRBO,
  output e,
  output f,
  output g
);

  wire and_1_out, and_2_out, and_3_out, and_4_out, and_5_out, and_6_out, and_7_out, and_8_out, and_9_out,
       and_10_out, and_11_out, and_12_out, and_13_out, and_14_out, and_15_out, and_16_out, and_17_out,
       and_18_out, and_19_out, and_20_out, and_21_out, and_22_out, and_23_out, and_24_out, and_25_out,
       buffer_2_out, nand_1_out, nand_2_out, nand_3_out, nand_4_out, nand_5_out, nand_6_out, nand_7_out,
       nand_8_out, not_1_out, not_2_out;

  nand nand_1 (nand_1_out, A, nLT);
  nand nand_2 (nand_2_out, B, nLT);
  nand nand_3 (nand_3_out, C, nLT);
  not not_1 (not_1_out, D);
  Pull_Resistor #(.pull(1)) pull_resistor_1 (.node(nBI));
  buf buffer_1 (nRBO, nand_8_out);
  not not_2 (not_2_out, nRBI);
  Pull_Resistor #(.pull(1)) pull_resistor_2 (.node(nRBI));
  nand nand_4 (nand_4_out, nand_1_out, and_1_out);
  nand nand_5 (nand_5_out, nand_2_out, and_1_out);
  nand nand_6 (nand_6_out, nand_3_out, and_1_out);
  nand nand_7 (nand_7_out, not_1_out, and_1_out);
  and and_1 (and_1_out, nBI, nand_8_out);
  nand nand_8 (nand_8_out, nLT, not_2_out, not_1_out, nand_3_out, nand_2_out, nand_1_out);
  and and_2 (and_2_out, nand_5_out, nand_7_out);
  and and_3 (and_3_out, nand_1_out, nand_2_out, nand_6_out);
  and and_4 (and_4_out, nand_4_out, nand_2_out, nand_3_out, not_1_out);
  and and_5 (and_5_out, nand_5_out, nand_7_out);
  and and_6 (and_6_out, nand_4_out, nand_2_out, nand_6_out);
  and and_7 (and_7_out, nand_1_out, nand_5_out, nand_6_out);
  and and_8 (and_8_out, nand_6_out, nand_7_out);
  and and_9 (and_9_out, nand_1_out, nand_5_out, nand_3_out);
  and and_10 (and_10_out, nand_4_out, nand_2_out, nand_3_out, not_1_out);
  and and_11 (and_11_out, nand_1_out, nand_2_out, nand_6_out);
  and and_12 (and_12_out, nand_4_out, nand_5_out, nand_6_out);
  buf buffer_2 (buffer_2_out, nand_4_out);
  and and_13 (and_13_out, nand_2_out, nand_6_out);
  and and_14 (and_14_out, nand_4_out, nand_5_out);
  and and_15 (and_15_out, nand_5_out, nand_3_out);
  and and_16 (and_16_out, nand_4_out, nand_3_out, not_1_out);
  and and_17 (and_17_out, nand_4_out, nand_5_out, nand_6_out);
  and and_18 (and_18_out, nand_2_out, nand_3_out, not_1_out, nLT);
  and and_19 (and_19_out, ~and_2_out, ~and_3_out, ~and_4_out);  // AND_Gate
  buf buffer_3 (a_2, and_19_out);
  and and_20 (and_20_out, ~and_5_out, ~and_6_out, ~and_7_out);  // AND_Gate
  buf buffer_4 (b_2, and_20_out);
  buf buffer_5 (c_2, and_21_out);
  and and_21 (and_21_out, ~and_8_out, ~and_9_out);  // AND_Gate
  and and_22 (and_22_out, ~and_10_out, ~and_11_out, ~and_12_out);  // AND_Gate
  buf buffer_6 (d_2, and_22_out);
  buf buffer_7 (e, and_23_out);
  and and_23 (and_23_out, ~buffer_2_out, ~and_13_out);  // AND_Gate
  and and_24 (and_24_out, ~and_14_out, ~and_15_out, ~and_16_out);  // AND_Gate
  buf buffer_8 (f, and_24_out);
  and and_25 (and_25_out, ~and_17_out, ~and_18_out);  // AND_Gate
  buf buffer_9 (g, and_25_out);

  // Notes on the sheet:
  //   74LS249
  //   buffer_1 drives only 0 and floats otherwise
  //   buffer_3 drives only 0 and floats otherwise
  //   buffer_4 drives only 0 and floats otherwise
  //   buffer_5 drives only 0 and floats otherwise
  //   buffer_6 drives only 0 and floats otherwise
  //   buffer_7 drives only 0 and floats otherwise
  //   buffer_8 drives only 0 and floats otherwise
  //   buffer_9 drives only 0 and floats otherwise
endmodule
