// Logisim project 74LS251.circ as structural Verilog: 1 circuit, main circuit 74LS251
module _74LS251 (
  input  D0,
  input  D1,
  input  D2,
  input  D3,
  input  D4,
  input  D5,
  input  D6,
  input  D7,
  input  A,
  input  B,
  input  C,
  input  nG,
  output Y,
  output W
);

  wire multiplexer_1_out, not_1_out;

  not not_1 (not_1_out, nG);
  Multiplexer #(.select(3), .enable("false")) multiplexer_1 (
    .in0(D0), .in1(D1), .in2(D2), .in3(D3), .in4(D4), .in5(D5), .in6(D6), .in7(D7), .out(multiplexer_1_out),
    .sel({C, B, A}));
  assign Y = not_1_out ? multiplexer_1_out : 1'bz;  // Controlled_Buffer controlled_buffer_1
  not not_2 (W, Y);

  // Notes on the sheet:
  //   74LS251
endmodule
