// Logisim project 74LS253.circ as structural Verilog: 1 circuit, main circuit 74LS253
module _74LS253 (
  input  _1C0,
  input  _2C0,
  input  _1C1,
  input  _2C1,
  input  _1C2,
  input  _2C2,
  input  _1C3,
  input  _2C3,
  input  B,
  input  A,
  input  _1_G,
  input  _2_G,
  output _1Y,
  output _2Y
);

  wire bitselector_1_out, bitselector_2_out, not_1_out, not_2_out;

  BitSelector #(.width(4)) bitselector_1 (.in({_1C3, _1C2, _1C1, _1C0}), .out(bitselector_1_out), .sel({B, A}));
  assign _1Y = not_1_out ? bitselector_1_out : 1'bz;  // Controlled_Buffer controlled_buffer_1
  not not_1 (not_1_out, _1_G);
  BitSelector #(.width(4)) bitselector_2 (.in({_2C3, _2C2, _2C1, _2C0}), .out(bitselector_2_out), .sel({B, A}));
  not not_2 (not_2_out, _2_G);
  assign _2Y = not_2_out ? bitselector_2_out : 1'bz;  // Controlled_Buffer controlled_buffer_2

  // Notes on the sheet:
  //   74LS253
endmodule
