// Logisim project 74LS255.circ as structural Verilog: 1 circuit, main circuit 74LS255
module _74LS255 (
  input  _1C,
  input  _2C,
  input  _1_G,
  input  _2_G,
  input  A,
  input  B,
  output _1Y0,
  output _2Y0,
  output _1Y1,
  output _2Y1,
  output _1Y2,
  output _2Y2,
  output _1Y3,
  output _2Y3
);

  wire demultiplexer_1_out0, demultiplexer_1_out1, demultiplexer_1_out2, demultiplexer_1_out3,
       demultiplexer_2_out0, demultiplexer_2_out1, demultiplexer_2_out2, demultiplexer_2_out3, not_1_out,
       not_2_out, not_3_out;

  Demultiplexer #(.select(2), .enable("false")) demultiplexer_1 (
    .out0(demultiplexer_1_out0), .out1(demultiplexer_1_out1), .out2(demultiplexer_1_out2),
    .out3(demultiplexer_1_out3), .in(_1C), .sel({B, A}));
  not not_1 (not_1_out, _1_G);
  assign _1Y0 = not_1_out ? ~demultiplexer_1_out0 : 1'bz;  // Controlled_Inverter controlled_inverter_1
  assign _1Y1 = not_1_out ? ~demultiplexer_1_out1 : 1'bz;  // Controlled_Inverter controlled_inverter_2
  assign _1Y2 = not_1_out ? ~demultiplexer_1_out2 : 1'bz;  // Controlled_Inverter controlled_inverter_3
  assign _1Y3 = not_1_out ? ~demultiplexer_1_out3 : 1'bz;  // Controlled_Inverter controlled_inverter_4
  not not_2 (not_2_out, _2C);
  Demultiplexer #(.select(2), .enable("false")) demultiplexer_2 (
    .out0(demultiplexer_2_out0), .out1(demultiplexer_2_out1), .out2(demultiplexer_2_out2),
    .out3(demultiplexer_2_out3), .in(not_2_out), .sel({B, A}));
  not not_3 (not_3_out, _2_G);
  assign _2Y0 = not_3_out ? ~demultiplexer_2_out0 : 1'bz;  // Controlled_Inverter controlled_inverter_5
  assign _2Y1 = not_3_out ? ~demultiplexer_2_out1 : 1'bz;  // Controlled_Inverter controlled_inverter_6
  assign _2Y2 = not_3_out ? ~demultiplexer_2_out2 : 1'bz;  // Controlled_Inverter controlled_inverter_7
  assign _2Y3 = not_3_out ? ~demultiplexer_2_out3 : 1'bz;  // Controlled_Inverter controlled_inverter_8

  // Notes on the sheet:
  //   74LS255
endmodule
