// Logisim project 74LS256.circ as structural Verilog: 1 circuit, main circuit 74LS256
module _74LS256 (
  input  nE,
  input  Da,
  input  A0,
  input  nMR,
  input  Db,
  input  A1,
  output Q0a,
  output Q1a,
  output Q2a,
  output Q3a,
  output Q0b,
  output Q1b,
  output Q2b,
  output Q3b
);

  wire and_1_out, and_2_out, and_3_out, and_4_out, and_5_out, and_6_out, and_8_out, and_9_out, CLR, or_1_out,
       or_2_out, or_3_out, or_4_out, or_5_out, or_6_out, or_7_out, or_8_out, S0, S1, S2, S3;

  D_Flip_Flop #(.trigger("low")) Low (.clk(nE), .D(Da), .Q(Q0a), .en(S0), .reset(or_1_out));  // open: Qn, preset
  or or_1 (or_1_out, and_1_out, CLR);
  and and_1 (and_1_out, ~S0, ~nMR, ~nE);  // AND_Gate
  D_Flip_Flop #(.trigger("low")) Low_2 (.clk(nE), .D(Db), .Q(Q0b), .en(S0), .reset(or_2_out));  // open: Qn, preset
  or or_2 (or_2_out, and_2_out, CLR);
  and and_2 (and_2_out, ~S0, ~nMR, ~nE);  // AND_Gate
  Decoder #(.select(2), .enable("false")) decoder_1 (.out0(S0), .out1(S1), .out2(S2), .out3(S3), .sel({A1, A0}));
  D_Flip_Flop #(.trigger("low")) Low_3 (.clk(nE), .D(Da), .Q(Q1a), .en(S1), .reset(or_3_out));  // open: Qn, preset
  or or_3 (or_3_out, and_3_out, CLR);
  and and_3 (and_3_out, ~S1, ~nMR, ~nE);  // AND_Gate
  D_Flip_Flop #(.trigger("low")) Low_4 (.clk(nE), .D(Db), .Q(Q1b), .en(S1), .reset(or_4_out));  // open: Qn, preset
  or or_4 (or_4_out, and_4_out, CLR);
  and and_4 (and_4_out, ~S1, ~nMR, ~nE);  // AND_Gate
  and and_5 (and_5_out, ~S2, ~nMR, ~nE);  // AND_Gate
  and and_6 (and_6_out, ~S2, ~nMR, ~nE);  // AND_Gate
  D_Flip_Flop #(.trigger("low")) Low_5 (.clk(nE), .D(Da), .Q(Q2a), .en(S2), .reset(or_5_out));  // open: Qn, preset
  or or_5 (or_5_out, and_5_out, CLR);
  D_Flip_Flop #(.trigger("low")) Low_6 (.clk(nE), .D(Db), .Q(Q2b), .en(S2), .reset(or_6_out));  // open: Qn, preset
  or or_6 (or_6_out, and_6_out, CLR);
  and and_7 (CLR, nE, ~nMR);  // AND_Gate
  and and_8 (and_8_out, ~S3, ~nMR, ~nE);  // AND_Gate
  and and_9 (and_9_out, ~S3, ~nMR, ~nE);  // AND_Gate
  D_Flip_Flop #(.trigger("low")) Low_7 (.clk(nE), .D(Da), .Q(Q3a), .en(S3), .reset(or_7_out));  // open: Qn, preset
  or or_7 (or_7_out, and_8_out, CLR);
  D_Flip_Flop #(.trigger("low")) Low_8 (.clk(nE), .D(Db), .Q(Q3b), .en(S3), .reset(or_8_out));  // open: Qn, preset
  or or_8 (or_8_out, and_9_out, CLR);

  // Notes on the sheet:
  //   74LS256
endmodule
