// Logisim project 74LS258.circ as structural Verilog: 1 circuit, main circuit 74LS258
module _74LS258 (
  input  _1A,
  input  _2A,
  input  _3A,
  input  _4A,
  input  _1B,
  input  _2B,
  input  _3B,
  input  _4B,
  input  nA_B,
  input  nG,
  output _1Y,
  output _2Y,
  output _3Y,
  output _4Y
);

  wire multiplexer_1_out, multiplexer_2_out, multiplexer_3_out, multiplexer_4_out, not_1_out;

  Multiplexer #(.enable("false")) multiplexer_1 (.in0(_1A), .in1(_1B), .out(multiplexer_1_out), .sel(nA_B));
  not not_1 (not_1_out, nG);
  assign _1Y = not_1_out ? ~multiplexer_1_out : 1'bz;  // Controlled_Inverter controlled_inverter_1
  Multiplexer #(.enable("false")) multiplexer_2 (.in0(_2A), .in1(_2B), .out(multiplexer_2_out), .sel(nA_B));
  assign _2Y = not_1_out ? ~multiplexer_2_out : 1'bz;  // Controlled_Inverter controlled_inverter_2
  Multiplexer #(.enable("false")) multiplexer_3 (.in0(_3A), .in1(_3B), .out(multiplexer_3_out), .sel(nA_B));
  assign _3Y = not_1_out ? ~multiplexer_3_out : 1'bz;  // Controlled_Inverter controlled_inverter_3
  Multiplexer #(.enable("false")) multiplexer_4 (.in0(_4A), .in1(_4B), .out(multiplexer_4_out), .sel(nA_B));
  assign _4Y = not_1_out ? ~multiplexer_4_out : 1'bz;  // Controlled_Inverter controlled_inverter_4

  // Notes on the sheet:
  //   74LS258
endmodule
