// Logisim project 74LS261.circ as structural Verilog: 2 circuits, main circuit 74LS261
module _74LS261 (
  input  B0,
  input  B1,
  input  B2,
  input  B3,
  input  B4,
  input  M0,
  input  M1,
  input  M2,
  input  C,
  output Q0,
  output Q1,
  output Q2,
  output Q3,
  output nQ4
);

  wire and_1_out, and_2_out, and_3_out, and_4_out, and_5_out, and_6_out, and_7_out, and_8_out, and_9_out,
       and_10_out, and_11_out, and_12_out, and_13_out, and_14_out, and_15_out, and_16_out, and_17_out,
       and_18_out, and_19_out, and_20_out, and_21_out, and_22_out, and_23_out, and_24_out, and_25_out,
       and_26_out, and_27_out, nor_1_out, nor_2_out, nor_3_out, not_1_out, not_2_out, not_3_out, not_4_out,
       not_5_out, not_6_out, not_7_out, not_8_out, not_9_out, not_10_out, not_11_out, not_12_out, or_1_out,
       pulse_1_pulse;

  pulse pulse_1 (.Pulse(pulse_1_pulse));
  not not_1 (not_1_out, B0);
  not not_2 (not_2_out, B1);
  not not_3 (not_3_out, B2);
  not not_4 (not_4_out, B3);
  not not_5 (not_5_out, B4);
  and and_1 (and_1_out, M0, M1);
  nor nor_1 (nor_1_out, M0, M1);
  nor nor_2 (nor_2_out, M2, not_6_out);
  not not_6 (not_6_out, or_1_out);
  or or_1 (or_1_out, C, pulse_1_pulse);
  not not_7 (not_7_out, not_1_out);
  not not_8 (not_8_out, not_2_out);
  not not_9 (not_9_out, not_3_out);
  not not_10 (not_10_out, not_4_out);
  not not_11 (not_11_out, not_5_out);
  nor nor_3 (nor_3_out, and_1_out, nor_1_out);
  and and_2 (and_2_out, ~nor_2_out, ~not_6_out);  // AND_Gate
  and and_3 (and_3_out, not_7_out, and_1_out, nor_2_out);
  and and_4 (and_4_out, not_1_out, nor_1_out, and_2_out);
  and and_5 (and_5_out, not_8_out, nor_3_out, nor_2_out);
  and and_6 (and_6_out, not_2_out, nor_3_out, and_2_out);
  and and_7 (and_7_out, not_6_out, Q0);
  and and_8 (and_8_out, not_8_out, and_1_out, nor_2_out);
  and and_9 (and_9_out, not_2_out, nor_1_out, and_2_out);
  and and_10 (and_10_out, not_9_out, nor_3_out, nor_2_out);
  and and_11 (and_11_out, not_3_out, nor_3_out, and_2_out);
  and and_12 (and_12_out, not_6_out, Q1);
  and and_13 (and_13_out, not_9_out, and_1_out, nor_2_out);
  and and_14 (and_14_out, not_3_out, nor_1_out, and_2_out);
  and and_15 (and_15_out, not_10_out, nor_3_out, nor_2_out);
  and and_16 (and_16_out, not_4_out, nor_3_out, and_2_out);
  and and_17 (and_17_out, not_6_out, Q2);
  and and_18 (and_18_out, not_10_out, nor_2_out, and_1_out);
  and and_19 (and_19_out, not_4_out, nor_1_out, and_2_out);
  and and_20 (and_20_out, not_11_out, nor_3_out, nor_2_out);
  and and_21 (and_21_out, nor_3_out, not_5_out, and_2_out);
  and and_22 (and_22_out, not_6_out, Q3);
  and and_23 (and_23_out, not_11_out, and_1_out, nor_2_out);
  and and_24 (and_24_out, not_5_out, nor_1_out, and_2_out);
  and and_25 (and_25_out, not_11_out, nor_3_out, nor_2_out);
  and and_26 (and_26_out, nor_3_out, not_5_out, and_2_out);
  and and_27 (and_27_out, not_6_out, not_12_out);
  or or_2 (Q0, and_3_out, and_4_out, and_5_out, and_6_out, and_7_out);
  or or_3 (Q1, and_8_out, and_9_out, and_10_out, and_11_out, and_12_out);
  or or_4 (Q2, and_13_out, and_14_out, and_15_out, and_16_out, and_17_out);
  or or_5 (Q3, and_18_out, and_19_out, and_20_out, and_21_out, and_22_out);
  nor nor_4 (nQ4, and_23_out, and_24_out, and_25_out, and_26_out, and_27_out);
  not not_12 (not_12_out, nQ4);

  // Notes on the sheet:
  //   74LS261
endmodule

module pulse (
  output Pulse
);

  wire and_1_out, counter_1_carry, d_ff_1_q, pull_resistor_1_node;

  Pull_Resistor #(.pull(1)) pull_resistor_1 (.node(pull_resistor_1_node));
  D_Flip_Flop #(.trigger("high")) d_ff_1 (
    .clk(pull_resistor_1_node), .D(pull_resistor_1_node), .Q(d_ff_1_q), .reset(and_1_out));  // open: Qn, preset, en
  and and_1 (and_1_out, Pulse, d_ff_1_q);
  Counter #(.width(6), .max('h3f), .ongoal("stay")) counter_1 (
    .carry(counter_1_carry), .clk(d_ff_1_q));  // open: load, D, count, Q, clr
  not not_1 (Pulse, counter_1_carry);

  // Notes on the sheet:
  //   Generate a tiny 0-1-0 pulse after CTRL-R
endmodule
