// Logisim project 74LS264.circ as structural Verilog: 1 circuit, main circuit 74LS264
module _74LS264 (
  input  CE,
  input  B3,
  input  A3,
  input  B2,
  input  A2,
  input  B1,
  input  A1,
  input  B0,
  input  A0,
  output RCOB,
  output RCOA,
  output C2,
  output C1,
  output C0
);

  wire and_1_out, and_2_out, and_3_out, and_4_out, and_5_out, and_6_out, and_7_out, and_8_out, and_9_out,
       and_10_out, and_11_out, and_12_out, and_13_out;

  or or_1 (RCOB, B0, B1, B2, B3, CE);
  and and_1 (and_1_out, CE, A0, A1, A2, A3);
  and and_2 (and_2_out, B1, A3, A2, A1);
  or or_2 (RCOA, and_1_out, and_2_out, and_3_out, and_4_out);
  and and_3 (and_3_out, B2, A3, A2);
  and and_4 (and_4_out, B3, A3);
  and and_5 (and_5_out, A2, A1, A0, CE);
  and and_6 (and_6_out, B0, A2, A1, A0);
  or or_3 (C2, and_5_out, and_6_out, and_7_out, and_8_out);
  and and_7 (and_7_out, B1, A2, A1);
  and and_8 (and_8_out, B2, A2);
  and and_9 (and_9_out, A1, A0, CE);
  and and_10 (and_10_out, B0, A1, A0);
  or or_4 (C1, and_9_out, and_10_out, and_11_out);
  and and_11 (and_11_out, B1, A1);
  and and_12 (and_12_out, A0, CE);
  or or_5 (C0, and_12_out, and_13_out);
  and and_13 (and_13_out, B0, A0);

  // Notes on the sheet:
  //   74LS264
endmodule
