// Logisim project 74LS265.circ as structural Verilog: 1 circuit, main circuit 74LS265
module _74LS265 (
  input  _1A,
  input  _2A,
  input  _2B,
  input  _3A,
  input  _3B,
  input  _4A,
  output _1Y,
  output _1W,
  output _2Y,
  output _2W,
  output _3Y,
  output _3W,
  output _4Y,
  output _4W
);

  wire and_1_out, and_2_out;

  and and_1 (and_1_out, _2A, _2B);
  and and_2 (and_2_out, _3A, _3B);
  not not_1 (_1Y, _1A);
  buf buffer_1 (_1W, _1A);
  not not_2 (_2Y, and_1_out);
  buf buffer_2 (_2W, and_1_out);
  not not_3 (_3Y, and_2_out);
  buf buffer_3 (_3W, and_2_out);
  not not_4 (_4Y, _4A);
  buf buffer_4 (_4W, _4A);

  // Notes on the sheet:
  //   74LS265
endmodule
