// Logisim project 74LS268.circ as structural Verilog: 1 circuit, main circuit 74LS268
module _74LS268 (
  input  nOC,
  input  C,
  input  _1D,
  input  _2D,
  input  _3D,
  input  _4D,
  input  _5D,
  input  _6D,
  output _1Q,
  output _2Q,
  output _3Q,
  output _4Q,
  output _5Q,
  output _6Q
);

  wire High_2_q, High_3_q, High_4_q, High_5_q, High_6_q, High_q, not_1_out;

  not not_1 (not_1_out, nOC);
  D_Flip_Flop #(.trigger("high")) High (.clk(C), .D(_1D), .Q(High_q));  // open: Qn, preset, en, reset
  assign _1Q = not_1_out ? High_q : 1'bz;  // Controlled_Buffer controlled_buffer_1
  D_Flip_Flop #(.trigger("high")) High_2 (.clk(C), .D(_2D), .Q(High_2_q));  // open: Qn, preset, en, reset
  assign _2Q = not_1_out ? High_2_q : 1'bz;  // Controlled_Buffer controlled_buffer_2
  D_Flip_Flop #(.trigger("high")) High_3 (.clk(C), .D(_3D), .Q(High_3_q));  // open: Qn, preset, en, reset
  assign _3Q = not_1_out ? High_3_q : 1'bz;  // Controlled_Buffer controlled_buffer_3
  D_Flip_Flop #(.trigger("high")) High_4 (.clk(C), .D(_4D), .Q(High_4_q));  // open: Qn, preset, en, reset
  assign _4Q = not_1_out ? High_4_q : 1'bz;  // Controlled_Buffer controlled_buffer_4
  D_Flip_Flop #(.trigger("high")) High_5 (.clk(C), .D(_5D), .Q(High_5_q));  // open: Qn, preset, en, reset
  assign _5Q = not_1_out ? High_5_q : 1'bz;  // Controlled_Buffer controlled_buffer_5
  assign _6Q = not_1_out ? High_6_q : 1'bz;  // Controlled_Buffer controlled_buffer_6
  D_Flip_Flop #(.trigger("high")) High_6 (.clk(C), .D(_6D), .Q(High_6_q));  // open: Qn, preset, en, reset

  // Notes on the sheet:
  //   74LS268
endmodule
