// Logisim project 74LS269.circ as structural Verilog: 2 circuits, main circuit 74LS269
module _74LS269 (
  input  P0,
  input  P1,
  input  P2,
  input  P3,
  input  P4,
  input  P5,
  input  P6,
  input  P7,
  input  nPE,
  input  CP,
  input  U_D,
  input  nCEP,
  input  nCET,
  output Q0,
  output Q1,
  output Q2,
  output Q3,
  output Q4,
  output Q5,
  output Q6,
  output Q7,
  output nTC
);

  wire and_1_out, and_2_out, and_3_out, and_4_out, and_5_out, and_6_out, and_7_out, and_8_out, and_9_out,
       and_10_out, and_11_out, and_12_out, and_13_out, and_14_out, and_15_out, and_16_out, and_17_out,
       detail_a_1_nq, detail_a_1_q, detail_a_2_nq, detail_a_2_q, detail_a_3_nq, detail_a_3_q, detail_a_4_nq,
       detail_a_4_q, detail_a_5_nq, detail_a_5_q, detail_a_6_nq, detail_a_6_q, detail_a_7_nq, detail_a_7_q,
       detail_a_8_nq, detail_a_8_q, nor_1_out, nor_2_out, nor_3_out, nor_4_out, nor_5_out, nor_6_out,
       nor_7_out, not_1_out, not_2_out, not_3_out, not_4_out, not_5_out, not_6_out;

  not not_1 (not_1_out, nPE);
  not not_2 (not_2_out, CP);
  not not_3 (not_3_out, nCEP);
  not not_4 (not_4_out, nCET);
  not not_5 (not_5_out, and_1_out);
  detail_a detail_a_1 (
    .Pn_DATA(P0), .nQ(detail_a_1_nq), .Q(detail_a_1_q), .nTOGGLE(not_5_out), .nPE(not_1_out),
    .nCLOCK(not_2_out));
  nor nor_1 (nor_1_out, and_2_out, and_10_out);
  detail_a detail_a_2 (
    .Pn_DATA(P1), .nQ(detail_a_2_nq), .Q(detail_a_2_q), .nTOGGLE(nor_1_out), .nPE(not_1_out),
    .nCLOCK(not_2_out));
  nor nor_2 (nor_2_out, and_3_out, and_11_out);
  detail_a detail_a_3 (
    .Pn_DATA(P2), .nQ(detail_a_3_nq), .Q(detail_a_3_q), .nTOGGLE(nor_2_out), .nPE(not_1_out),
    .nCLOCK(not_2_out));
  nor nor_3 (nor_3_out, and_4_out, and_12_out);
  detail_a detail_a_4 (
    .Pn_DATA(P3), .nQ(detail_a_4_nq), .Q(detail_a_4_q), .nTOGGLE(nor_3_out), .nPE(not_1_out),
    .nCLOCK(not_2_out));
  nor nor_4 (nor_4_out, and_5_out, and_13_out);
  detail_a detail_a_5 (
    .Pn_DATA(P4), .nQ(detail_a_5_nq), .Q(detail_a_5_q), .nTOGGLE(nor_4_out), .nPE(not_1_out),
    .nCLOCK(not_2_out));
  nor nor_5 (nor_5_out, and_6_out, and_14_out);
  detail_a detail_a_6 (
    .Pn_DATA(P5), .nQ(detail_a_6_nq), .Q(detail_a_6_q), .nTOGGLE(nor_5_out), .nPE(not_1_out),
    .nCLOCK(not_2_out));
  nor nor_6 (nor_6_out, and_7_out, and_15_out);
  detail_a detail_a_7 (
    .Pn_DATA(P6), .nQ(detail_a_7_nq), .Q(detail_a_7_q), .nTOGGLE(nor_6_out), .nPE(not_1_out),
    .nCLOCK(not_2_out));
  nor nor_7 (nor_7_out, and_8_out, and_16_out);
  detail_a detail_a_8 (
    .Pn_DATA(P7), .nQ(detail_a_8_nq), .Q(detail_a_8_q), .nTOGGLE(nor_7_out), .nPE(not_1_out),
    .nCLOCK(not_2_out));
  not not_6 (not_6_out, U_D);
  and and_1 (and_1_out, not_3_out, not_4_out);
  and and_2 (and_2_out, and_1_out, U_D, detail_a_1_q);
  and and_3 (and_3_out, and_1_out, U_D, detail_a_2_q, detail_a_1_q);
  and and_4 (and_4_out, and_1_out, U_D, detail_a_3_q, detail_a_2_q, detail_a_1_q);
  and and_5 (and_5_out, and_1_out, U_D, detail_a_4_q, detail_a_3_q, detail_a_2_q, detail_a_1_q);
  and and_6 (and_6_out, and_1_out, U_D, detail_a_5_q, detail_a_4_q, detail_a_3_q, detail_a_2_q, detail_a_1_q);
  and and_7 (and_7_out, and_1_out, U_D, detail_a_6_q, detail_a_5_q, detail_a_4_q, detail_a_3_q, detail_a_2_q, detail_a_1_q);
  and and_8 (and_8_out, and_1_out, U_D, detail_a_7_q, detail_a_6_q, detail_a_5_q, detail_a_4_q, detail_a_3_q, detail_a_2_q, detail_a_1_q);
  and and_9 (and_9_out, U_D, detail_a_8_q, detail_a_7_q, detail_a_6_q, detail_a_5_q, detail_a_4_q, detail_a_3_q, detail_a_2_q, detail_a_1_q, not_4_out);
  and and_10 (and_10_out, and_1_out, not_6_out, detail_a_1_nq);
  and and_11 (and_11_out, and_1_out, not_6_out, detail_a_2_nq, detail_a_1_nq);
  and and_12 (and_12_out, and_1_out, not_6_out, detail_a_3_nq, detail_a_2_nq, detail_a_1_nq);
  and and_13 (and_13_out, and_1_out, not_6_out, detail_a_4_nq, detail_a_3_nq, detail_a_2_nq, detail_a_1_nq);
  and and_14 (and_14_out, and_1_out, not_6_out, detail_a_5_nq, detail_a_4_nq, detail_a_3_nq, detail_a_2_nq, detail_a_1_nq);
  and and_15 (and_15_out, and_1_out, not_6_out, detail_a_6_nq, detail_a_5_nq, detail_a_4_nq, detail_a_3_nq, detail_a_2_nq, detail_a_1_nq);
  and and_16 (and_16_out, and_1_out, not_6_out, detail_a_7_nq, detail_a_6_nq, detail_a_5_nq, detail_a_4_nq, detail_a_3_nq, detail_a_2_nq, detail_a_1_nq);
  and and_17 (and_17_out, not_4_out, not_6_out, detail_a_8_nq, detail_a_7_nq, detail_a_6_nq, detail_a_5_nq, detail_a_4_nq, detail_a_3_nq, detail_a_2_nq, detail_a_1_nq);
  not not_7 (Q0, detail_a_1_nq);
  not not_8 (Q1, detail_a_2_nq);
  not not_9 (Q2, detail_a_3_nq);
  not not_10 (Q3, detail_a_4_nq);
  not not_11 (Q4, detail_a_5_nq);
  not not_12 (Q5, detail_a_6_nq);
  not not_13 (Q6, detail_a_7_nq);
  not not_14 (Q7, detail_a_8_nq);
  nor nor_8 (nTC, and_17_out, and_9_out);

  // Notes on the sheet:
  //   74LS269
  //   * BUG in Motorola datasheet fixed
  //   ** Two bugs in detail A
  //   *** /CE is actually called /PE
  //   *
endmodule

module detail_a (
  input  nTOGGLE,
  input  Pn_DATA,
  input  nPE,
  input  nCLOCK,
  output nQ,
  output Q
);

  wire and_1_out, and_2_out, and_3_out, not_1_out, not_2_out, or_1_out;

  not not_1 (not_1_out, nPE);
  not not_2 (not_2_out, nTOGGLE);
  and and_1 (and_1_out, Pn_DATA, nPE);
  and and_2 (and_2_out, not_1_out, Q, nTOGGLE);
  and and_3 (and_3_out, not_1_out, nQ, not_2_out);
  or or_1 (or_1_out, and_1_out, and_2_out, and_3_out);
  D_Flip_Flop #(.trigger("falling")) Fall (.clk(nCLOCK), .D(or_1_out), .Q(Q), .Qn(nQ));  // open: preset, en, reset

  // Notes on the sheet:
  //   *
  //   * Another BUG in the Motorola datasheet
  //   These are inverters, not buffers
  //   * Third bug, D latches on falling edge!
endmodule
