// Logisim project 74LS273.circ as structural Verilog: 1 circuit, main circuit 74LS273
module _74LS273 (
  input  D1,
  input  D2,
  input  D3,
  input  D4,
  input  D5,
  input  D6,
  input  D7,
  input  D8,
  input  CLOCK,
  input  nCLEAR,
  output Q1,
  output Q2,
  output Q3,
  output Q4,
  output Q5,
  output Q6,
  output Q7,
  output Q8
);

  wire not_1_out;

  D_Flip_Flop d_ff_1 (.clk(CLOCK), .D(D1), .Q(Q1), .reset(not_1_out));  // open: Qn, preset, en
  not not_1 (not_1_out, nCLEAR);
  D_Flip_Flop d_ff_2 (.clk(CLOCK), .D(D2), .Q(Q2), .reset(not_1_out));  // open: Qn, preset, en
  D_Flip_Flop d_ff_3 (.clk(CLOCK), .D(D3), .Q(Q3), .reset(not_1_out));  // open: Qn, preset, en
  D_Flip_Flop d_ff_4 (.clk(CLOCK), .D(D4), .Q(Q4), .reset(not_1_out));  // open: Qn, preset, en
  D_Flip_Flop d_ff_5 (.clk(CLOCK), .D(D5), .Q(Q5), .reset(not_1_out));  // open: Qn, preset, en
  D_Flip_Flop d_ff_6 (.clk(CLOCK), .D(D6), .Q(Q6), .reset(not_1_out));  // open: Qn, preset, en
  D_Flip_Flop d_ff_7 (.clk(CLOCK), .D(D7), .Q(Q7), .reset(not_1_out));  // open: Qn, preset, en
  D_Flip_Flop d_ff_8 (.clk(CLOCK), .D(D8), .Q(Q8), .reset(not_1_out));  // open: Qn, preset, en

  // Notes on the sheet:
  //   74LS273
endmodule
