// Logisim project 74LS274.circ as structural Verilog: 1 circuit, main circuit 74LS274
module _74LS274 (
  input  A2n,
  input  A2n_1,
  input  A2n_2,
  input  A2n_3,
  input  B2n,
  input  B2n_1,
  input  B2n_2,
  input  B2n_3,
  input  nG1,
  input  nG2,
  output _2n,
  output _2n_1,
  output _2n_2,
  output _2n_3,
  output _2n_4,
  output _2n_5,
  output _2n_6,
  output _2n_7
);

  wire and_1_out;
  wire [3:0] multiplier_1_cout, multiplier_1_out;

  and and_1 (and_1_out, ~nG1, ~nG2);  // AND_Gate
  Multiplier #(.width(4)) multiplier_1 (
    .a({A2n_3, A2n_2, A2n_1, A2n}), .b({B2n_3, B2n_2, B2n_1, B2n}), .out(multiplier_1_out),
    .cout(multiplier_1_cout));  // open: cin
  assign {_2n_7, _2n_6, _2n_5, _2n_4} = and_1_out ? multiplier_1_cout : 4'bz;  // Controlled_Buffer controlled_buffer_1
  assign {_2n_3, _2n_2, _2n_1, _2n} = and_1_out ? multiplier_1_out : 4'bz;  // Controlled_Buffer controlled_buffer_2

  // Notes on the sheet:
  //   74LS274
endmodule
