// Logisim project 74LS275.circ as structural Verilog: 2 circuits, main circuit 74LS275
module _74LS275 (
  input  C,
  input  C_2,
  input  B,
  input  A,
  input  C_3,
  input  B_2,
  input  A_2,
  input  C2n,
  input  C2n_2,
  input  nG,
  output out_11,
  output out_12,
  output out_13,
  output out_14
);

  wire adder_1_c_2, \adder_1_σ , adder_2_c_2, \adder_2_σ , adder_3_c_2, \adder_3_σ , adder_4_c_2,
       \adder_4_σ , adder_5_c_2, \adder_5_σ , not_1_out;

  adder adder_1 (.C(C_2), .B(B), .A(A), .C_2(adder_1_c_2), .\Σ (\adder_1_σ ));
  adder adder_2 (.C(adder_1_c_2), .B(adder_3_c_2), .A(adder_4_c_2), .C_2(adder_2_c_2), .\Σ (\adder_2_σ ));
  not not_1 (not_1_out, nG);
  assign out_11 = not_1_out ? adder_2_c_2 : 1'bz;  // Controlled_Buffer controlled_buffer_1
  adder adder_3 (.C(C_3), .B(B_2), .A(A_2), .C_2(adder_3_c_2), .\Σ (\adder_3_σ ));
  adder adder_4 (.C(C), .B(\adder_1_σ ), .A(\adder_3_σ ), .C_2(adder_4_c_2), .\Σ (\adder_4_σ ));
  assign out_13 = not_1_out ? adder_5_c_2 : 1'bz;  // Controlled_Buffer controlled_buffer_2
  assign out_12 = not_1_out ? \adder_2_σ  : 1'bz;  // Controlled_Buffer controlled_buffer_3
  adder adder_5 (.C(\adder_4_σ ), .B(C2n), .A(C2n_2), .C_2(adder_5_c_2), .\Σ (\adder_5_σ ));
  assign out_14 = not_1_out ? \adder_5_σ  : 1'bz;  // Controlled_Buffer controlled_buffer_4

  // Notes on the sheet:
  //   74LS275
endmodule

module adder (
  input  C,
  input  B,
  input  A,
  output C_2,
  output \Σ 
);

  Adder #(.width(1)) adder_1 (.a(A), .b(B), .out(\Σ ), .cin(C), .cout(C_2));
endmodule
