// Logisim project 74LS276.circ as structural Verilog: 1 circuit, main circuit 74LS276
module _74LS276 (
  input  nPRE,
  input  nCLR,
  input  J,
  input  _1_CLK,
  input  nK,
  input  J_2,
  input  _1_CLK_2,
  input  nK_2,
  input  J_3,
  input  _1_CLK_3,
  input  nK_3,
  input  J_4,
  input  _1_CLK_4,
  input  nK_4,
  output out_15,
  output out_16,
  output out_17,
  output out_18
);

  wire and_1_out, and_2_out, and_3_out, and_4_out, not_1_out, not_2_out, not_3_out, not_4_out, not_5_out,
       not_6_out;

  not not_1 (not_1_out, nPRE);
  not not_2 (not_2_out, nCLR);
  not not_3 (not_3_out, nK);
  not not_4 (not_4_out, nK_2);
  not not_5 (not_5_out, nK_3);
  not not_6 (not_6_out, nK_4);
  J_K_Flip_Flop #(.trigger("falling")) Fall (
    .J(J), .clk(_1_CLK), .K(not_3_out), .Q(out_15), .preset(not_1_out), .reset(and_1_out));  // open: Qn, en
  and and_1 (and_1_out, ~not_1_out, not_2_out);  // AND_Gate
  J_K_Flip_Flop #(.trigger("falling")) Fall_2 (
    .J(J_2), .clk(_1_CLK_2), .K(not_4_out), .Q(out_16), .preset(not_1_out), .reset(and_2_out));  // open: Qn, en
  and and_2 (and_2_out, ~not_1_out, not_2_out);  // AND_Gate
  J_K_Flip_Flop #(.trigger("falling")) Fall_3 (
    .J(J_3), .clk(_1_CLK_3), .K(not_5_out), .Q(out_17), .preset(not_1_out), .reset(and_3_out));  // open: Qn, en
  and and_3 (and_3_out, ~not_1_out, not_2_out);  // AND_Gate
  J_K_Flip_Flop #(.trigger("falling")) Fall_4 (
    .J(J_4), .clk(_1_CLK_4), .K(not_6_out), .Q(out_18), .preset(not_1_out), .reset(and_4_out));  // open: Qn, en
  and and_4 (and_4_out, ~not_1_out, not_2_out);  // AND_Gate

  // Notes on the sheet:
  //   74LS276
  //   L L = H, but might not persist
endmodule
