// Logisim project 74LS278.circ as structural Verilog: 2 circuits, main circuit 74LS278
module _74LS278 (
  input  P0,
  input  G,
  input  D4,
  input  D3,
  input  D2,
  input  D1,
  output P1,
  output Y4,
  output Y3,
  output Y2,
  output Y1
);

  wire and_1_out, and_2_out, and_3_out, and_4_out, and_5_out, and_6_out, and_7_out, and_8_out, not_1_out,
       not_2_out, not_3_out, not_4_out, sr_1_out_3, sr_1_out_4, sr_2_out_3, sr_2_out_4, sr_3_out_3,
       sr_3_out_4, sr_4_out_3, sr_4_out_4;

  not not_1 (not_1_out, D4);
  and and_1 (and_1_out, G, not_1_out);
  and and_2 (and_2_out, G, D4);
  SR sr_1 (.in_1(and_1_out), .in_2(and_2_out), .out_3(sr_1_out_3), .out_4(sr_1_out_4));
  nor nor_1 (P1, P0, sr_1_out_3, sr_2_out_3, sr_3_out_3, sr_4_out_3);
  nor nor_2 (Y4, P0, sr_1_out_4, sr_2_out_3, sr_3_out_3, sr_4_out_3);
  not not_2 (not_2_out, D3);
  and and_3 (and_3_out, G, not_2_out);
  SR sr_2 (.in_1(and_3_out), .in_2(and_5_out), .out_3(sr_2_out_3), .out_4(sr_2_out_4));
  and and_4 (and_4_out, G, not_3_out);
  and and_5 (and_5_out, G, D3);
  nor nor_3 (Y3, P0, sr_2_out_4, sr_3_out_3, sr_4_out_3);
  not not_3 (not_3_out, D2);
  and and_6 (and_6_out, G, D2);
  SR sr_3 (.in_1(and_4_out), .in_2(and_6_out), .out_3(sr_3_out_3), .out_4(sr_3_out_4));
  nor nor_4 (Y2, P0, sr_3_out_4, sr_4_out_3);
  not not_4 (not_4_out, D1);
  and and_7 (and_7_out, G, not_4_out);
  SR sr_4 (.in_1(and_7_out), .in_2(and_8_out), .out_3(sr_4_out_3), .out_4(sr_4_out_4));
  nor nor_5 (Y1, P0, sr_4_out_4);
  and and_8 (and_8_out, G, D1);

  // Notes on the sheet:
  //   74LS278
endmodule

module SR (
  input  in_1,
  input  in_2,
  output out_3,
  output out_4
);

  S_R_Flip_Flop #(.trigger("high")) s_r_ff_1 (
    .S(in_1), .clk(1'b1), .R(in_2), .Q(out_4), .Qn(out_3));  // open: preset, reset, en
endmodule
