// Logisim project 74LS279.circ as structural Verilog: 1 circuit, main circuit 74LS279
module _74LS279 (
  input  _1_S1,
  input  _2_S,
  input  _1_S2,
  input  _2_R,
  input  _1_R,
  input  _3_S1,
  input  _4_S,
  input  _3_S2,
  input  _4_R,
  input  _3_R,
  output _2Q,
  output _1Q,
  output _4Q,
  output _1Q_2
);

  wire and_1_out, and_2_out, and_3_out, and_4_out, nor_1_out, nor_2_out;

  nor nor_1 (nor_1_out, ~_1_S1, ~_1_S2);  // NOR_Gate
  nor nor_2 (nor_2_out, ~_3_S1, ~_3_S2);  // NOR_Gate
  S_R_Flip_Flop #(.trigger("low")) Low (
    .S(nor_1_out), .clk(1'b0), .R(_1_R), .Qn(_1Q), .reset(and_1_out));  // open: Q, preset, en
  and and_1 (and_1_out, ~nor_1_out, ~_1_R);  // AND_Gate
  S_R_Flip_Flop #(.trigger("low")) Low_2 (
    .S(nor_2_out), .clk(1'b0), .R(_3_R), .Qn(_1Q_2), .reset(and_2_out));  // open: Q, preset, en
  and and_2 (and_2_out, ~nor_2_out, ~_3_R);  // AND_Gate
  S_R_Flip_Flop #(.trigger("low")) Low_3 (
    .S(_2_S), .clk(1'b0), .R(_2_R), .Qn(_2Q), .reset(and_3_out));  // open: Q, preset, en
  and and_3 (and_3_out, ~_2_S, ~_2_R);  // AND_Gate
  S_R_Flip_Flop #(.trigger("low")) Low_4 (
    .S(_4_S), .clk(1'b0), .R(_4_R), .Qn(_4Q), .reset(and_4_out));  // open: Q, preset, en
  and and_4 (and_4_out, ~_4_S, ~_4_R);  // AND_Gate

  // Notes on the sheet:
  //   74LS279
  //   * No unstable startup when /R and /S are both high
  //   ** When /R and /S are both low, Q is high, but might not persist after transition to LH or HL as per the datasheet
endmodule
