// Logisim project 74LS281.circ as structural Verilog: 1 circuit, main circuit 74LS281
module _74LS281 (
  input  Cn,
  input  M,
  input  A0,
  input  B0,
  input  A1,
  input  B1,
  input  A2,
  input  B2,
  input  A3,
  input  B3,
  input  S0,
  input  S1,
  input  S2,
  input  S3,
  output F0,
  output F1,
  output A_B,
  output F2,
  output F3,
  output P,
  output Cn_4,
  output G
);

  wire and_1_out, and_2_out, and_3_out, and_4_out, and_5_out, and_6_out, and_7_out, and_8_out, and_9_out,
       and_11_out, and_12_out, and_13_out, and_14_out, and_15_out, and_16_out, and_17_out, and_18_out,
       and_19_out, and_20_out, and_21_out, and_22_out, and_23_out, and_24_out, and_25_out, and_26_out,
       and_27_out, and_28_out, and_29_out, and_30_out, and_31_out, and_32_out, and_33_out, and_34_out,
       and_35_out, and_36_out, and_37_out, and_38_out, nand_1_out, nand_3_out, nor_1_out, nor_2_out,
       nor_3_out, nor_4_out, nor_5_out, nor_6_out, nor_7_out, nor_8_out, nor_9_out, nor_10_out, nor_11_out,
       not_1_out, not_2_out, not_3_out, not_4_out, not_5_out;

  nand nand_1 (nand_1_out, Cn, not_1_out);
  not not_1 (not_1_out, M);
  and and_1 (and_1_out, A0, A0);
  and and_2 (and_2_out, ~nor_1_out, nor_3_out);  // AND_Gate
  xor xor_1 (F0, nand_1_out, and_2_out);
  not not_2 (not_2_out, B0);
  and and_3 (and_3_out, B0, S0);
  and and_4 (and_4_out, S1, not_2_out);
  nor nor_1 (nor_1_out, and_1_out, and_3_out, and_4_out);
  and and_5 (and_5_out, not_1_out, nor_1_out);
  and and_6 (and_6_out, not_1_out, nor_3_out, Cn);
  nor nor_2 (nor_2_out, and_5_out, and_6_out);
  xor xor_2 (F1, nor_2_out, and_9_out);
  and and_7 (and_7_out, not_2_out, S2, A0);
  and and_8 (and_8_out, A0, B0, S3);
  nor nor_3 (nor_3_out, and_7_out, and_8_out);
  and and_9 (and_9_out, ~nor_4_out, nor_6_out);  // AND_Gate
  and and_10 (A_B, F0, F1, F2, F3);
  and and_11 (and_11_out, B1, S0);
  and and_12 (and_12_out, A1, A1);
  nor nor_4 (nor_4_out, and_12_out, and_11_out, and_16_out);
  and and_13 (and_13_out, not_1_out, nor_1_out, nor_4_out);
  and and_14 (and_14_out, not_1_out, nor_4_out);
  nor nor_5 (nor_5_out, and_14_out, and_13_out, and_18_out);
  xor xor_3 (F2, nor_5_out, and_17_out);
  not not_3 (not_3_out, B1);
  and and_15 (and_15_out, not_3_out, S2, A1);
  and and_16 (and_16_out, S1, not_3_out);
  and and_17 (and_17_out, ~nor_7_out, nor_9_out);  // AND_Gate
  and and_18 (and_18_out, not_1_out, Cn, nor_3_out, nor_6_out);
  and and_19 (and_19_out, A1, B1, S3);
  nor nor_6 (nor_6_out, and_15_out, and_19_out);
  and and_20 (and_20_out, not_1_out, nor_7_out);
  and and_21 (and_21_out, not_1_out, nor_4_out, nor_9_out);
  and and_22 (and_22_out, A2, A2);
  and and_23 (and_23_out, B2, S0);
  nor nor_7 (nor_7_out, and_22_out, and_23_out, and_26_out);
  and and_24 (and_24_out, not_1_out, nor_1_out, nor_6_out, nor_9_out);
  nor nor_8 (nor_8_out, and_20_out, and_21_out, and_24_out, and_27_out);
  xor xor_4 (F3, nor_8_out, and_29_out);
  not not_4 (not_4_out, B2);
  and and_25 (and_25_out, not_4_out, S2, A2);
  and and_26 (and_26_out, S1, not_4_out);
  and and_27 (and_27_out, not_1_out, Cn, nor_3_out, nor_6_out, nor_9_out);
  and and_28 (and_28_out, A2, B2, S3);
  nor nor_9 (nor_9_out, and_25_out, and_28_out);
  and and_29 (and_29_out, ~nor_10_out, nor_11_out);  // AND_Gate
  nand nand_2 (P, nor_3_out, nor_6_out, nor_9_out, nor_11_out);
  and and_30 (and_30_out, B3, S0);
  and and_31 (and_31_out, A3, A3);
  nor nor_10 (nor_10_out, and_31_out, and_30_out, and_33_out);
  nand nand_3 (nand_3_out, Cn, nor_3_out, nor_6_out, nor_9_out, nor_11_out);
  or or_1 (Cn_4, ~nand_3_out, ~G);  // OR_Gate
  not not_5 (not_5_out, B3);
  and and_32 (and_32_out, not_5_out, S2, A3);
  and and_33 (and_33_out, S1, not_5_out);
  nor nor_11 (nor_11_out, and_32_out, and_36_out);
  and and_34 (and_34_out, nor_1_out, nor_6_out, nor_9_out, nor_11_out);
  and and_35 (and_35_out, nor_4_out, nor_9_out, nor_11_out);
  and and_36 (and_36_out, A3, B3, S3);
  and and_37 (and_37_out, nor_7_out, nor_11_out);
  and and_38 (and_38_out, nor_10_out, nor_10_out);
  nor nor_12 (G, and_34_out, and_35_out, and_37_out, and_38_out);

  // Notes on the sheet:
  //   74LS281
endmodule
