// Logisim project 74LS283.circ as structural Verilog: 1 circuit, main circuit 74LS283
module _74LS283 (
  input  CI,
  input  A1,
  input  A2,
  input  A3,
  input  A4,
  input  B1,
  input  B2,
  input  B3,
  input  B4,
  output \Σ1 ,
  output \Σ2 ,
  output \Σ3 ,
  output \Σ4 ,
  output CO
);

  Adder #(.width(4)) adder_1 (
    .a({A4, A3, A2, A1}), .b({B4, B3, B2, B1}), .out({\Σ4 , \Σ3 , \Σ2 , \Σ1 }), .cin(CI), .cout(CO));

  // Notes on the sheet:
  //   74LS283
endmodule
