// Logisim project 74LS285.circ as structural Verilog: 1 circuit, main circuit 74LS285
module _74LS285 (
  input  _1A,
  input  _1B,
  input  _1C,
  input  _1D,
  input  _2A,
  input  _2B,
  input  _2C,
  input  _2D,
  input  nGA,
  input  nGB,
  output Y0,
  output Y1,
  output Y2,
  output Y3
);

  wire and_1_out;
  wire [7:0] multiplier_1_out;
  wire [7:4] controlled_buffer_1_out;

  and and_1 (and_1_out, ~nGA, ~nGB);  // AND_Gate
  Multiplier multiplier_1 (
    .a({4'b0000, _1D, _1C, _1B, _1A}), .b({4'b0000, _2D, _2C, _2B, _2A}), .out(multiplier_1_out));  // open: cin, cout
  assign {controlled_buffer_1_out, Y3, Y2, Y1, Y0} = and_1_out ? multiplier_1_out : 8'bz;  // Controlled_Buffer controlled_buffer_1

  // Notes on the sheet:
  //   74LS285
endmodule
