// Logisim project 74LS286.circ as structural Verilog: 1 circuit, main circuit 74LS286
module _74LS286 (
  input  A,
  input  B,
  input  C,
  input  D,
  input  E,
  input  F,
  input  G,
  input  H,
  input  I,
  input  PARITY_I,
  input  nXMIT,
  output PARITY_ERROR,
  output PARITY_O
);

  wire not_1_out, not_2_out, not_3_out, not_4_out, xnor_1_out, xnor_2_out, xnor_3_out, xnor_4_out,
       xnor_5_out, xnor_6_out, xnor_7_out, xnor_8_out, xnor_9_out;

  not not_1 (not_1_out, nXMIT);
  xnor xnor_1 (xnor_1_out, A, B);
  xnor xnor_2 (xnor_2_out, xnor_1_out, ~C);  // XNOR_Gate
  xnor xnor_3 (xnor_3_out, D, E);
  xnor xnor_4 (xnor_4_out, xnor_3_out, ~F);  // XNOR_Gate
  xnor xnor_5 (xnor_5_out, G, H);
  xnor xnor_6 (xnor_6_out, xnor_5_out, ~I);  // XNOR_Gate
  xnor xnor_7 (xnor_7_out, xnor_2_out, xnor_4_out);
  assign PARITY_O = not_1_out ? ~xnor_8_out : 1'bz;  // Controlled_Inverter controlled_inverter_1
  xnor xnor_8 (xnor_8_out, xnor_7_out, ~xnor_6_out);  // XNOR_Gate
  not not_2 (not_2_out, PARITY_I);
  not not_3 (not_3_out, xnor_8_out);
  xnor xnor_9 (xnor_9_out, not_3_out, not_2_out);
  not not_4 (not_4_out, not_1_out);
  nand nand_1 (PARITY_ERROR, xnor_9_out, not_4_out);

  // Notes on the sheet:
  //   74LS286
endmodule
