// Logisim project 74LS289.circ as structural Verilog: 1 circuit, main circuit 74LS289
module _74LS289 (
  input  A0,
  input  A1,
  input  A2,
  input  A3,
  input  DI1,
  input  DI2,
  input  DI3,
  input  DI4,
  input  nS,
  input  nW,
  output nDO1,
  output nDO2,
  output nDO3,
  output nDO4
);

  wire and_1_out, CS, not_2_out;
  wire [3:0] ram_1_data;

  not not_1 (CS, nS);
  RAM #(.addrWidth(4), .dataWidth(4), .bus("asynch")) ram_1 (
    .addr({A3, A2, A1, A0}), .data(ram_1_data), .sel(CS), .ld(nW));  // open: clr
  assign ram_1_data = not_2_out ? {DI4, DI3, DI2, DI1} : 4'bz;  // Controlled_Buffer controlled_buffer_1
  not not_2 (not_2_out, and_1_out);
  and and_1 (and_1_out, CS, nW);
  assign {nDO4, nDO3, nDO2, nDO1} = and_1_out ? ~ram_1_data : 4'bz;  // Controlled_Inverter controlled_inverter_1

  // Other names for the same wires on the sheet: R = nW

  // Notes on the sheet:
  //   74LS289
endmodule
