// Logisim project 74LS290.circ as structural Verilog: 1 circuit, main circuit 74LS290
module _74LS290 (
  input  R9_1,
  input  R9_2,
  input  INPUT_A,
  input  INPUT_B,
  input  R0_1,
  input  R0_2,
  output QA,
  output QB,
  output QC,
  output QD
);

  wire and_1_out, Fall_4_qn, nand_1_out, nand_2_out, not_1_out, not_2_out, not_3_out, not_4_out, or_1_out,
       or_2_out;

  nand nand_1 (nand_1_out, R9_1, R9_2);
  nand nand_2 (nand_2_out, R0_1, R0_2);
  not not_1 (not_1_out, nand_1_out);
  or or_1 (or_1_out, ~nand_2_out, ~nand_1_out);  // OR_Gate
  or or_2 (or_2_out, ~nand_2_out, ~nand_1_out);  // OR_Gate
  not not_2 (not_2_out, nand_1_out);
  and and_1 (and_1_out, QC, QB);
  J_K_Flip_Flop #(.trigger("falling")) Fall (
    .J(1'b1), .clk(INPUT_A), .K(1'b1), .Q(QA), .preset(not_1_out), .reset(not_3_out));  // open: Qn, en
  not not_3 (not_3_out, nand_2_out);
  J_K_Flip_Flop #(.trigger("falling")) Fall_2 (
    .J(Fall_4_qn), .clk(INPUT_B), .K(1'b1), .Q(QB), .reset(or_1_out));  // open: Qn, preset, en
  J_K_Flip_Flop #(.trigger("falling")) Fall_3 (
    .J(1'b1), .clk(QB), .K(1'b1), .Q(QC), .reset(or_2_out));  // open: Qn, preset, en
  S_R_Flip_Flop #(.trigger("falling")) Fall_4 (
    .S(and_1_out), .clk(INPUT_B), .R(QD), .Q(QD), .Qn(Fall_4_qn), .preset(not_2_out), .reset(not_4_out));  // open: en
  not not_4 (not_4_out, nand_2_out);

  // Notes on the sheet:
  //   74LS290
endmodule
