// Logisim project 74LS292.circ as structural Verilog: 3 circuits, main circuit 74LS292
module _74LS292 (
  input  nCLR,
  input  CK1,
  input  CK2,
  input  B,
  input  C,
  input  D,
  input  E,
  input  A,
  output TP1,
  output TP2,
  output TP3,
  output Q
);

  wire CK3, controlled_inverter_1_out, controlled_inverter_3_out, controlled_inverter_5_out,
       controlled_inverter_7_out, controlled_inverter_9_out, controlled_inverter_11_out,
       controlled_inverter_13_out, controlled_inverter_15_out, controlled_inverter_17_out,
       controlled_inverter_19_out, controlled_inverter_21_out, controlled_inverter_23_out,
       controlled_inverter_25_out, controlled_inverter_27_out, controlled_inverter_29_out, nand_1_out,
       nand_2_out, nand_3_out, nand_4_out, nand_5_out, nand_6_out, nand_7_out, nand_8_out, nand_9_out,
       nand_10_out, nand_11_out, nand_12_out, nand_13_out, nand_28_out, nand_29_out, nand_30_out,
       nand_31_out, nand_32_out, nand_33_out, nand_34_out, nand_35_out, nand_36_out, nand_37_out,
       nand_38_out, nor_1_out, nor_2_out, not_1_out, not_2_out, not_3_out, not_4_out, not_5_out, not_6_out,
       not_7_out, not_8_out, not_9_out, not_10_out, not_11_out, not_12_out, not_13_out, not_14_out,
       not_15_out, not_16_out, not_17_out, not_18_out, not_19_out, not_20_out, not_21_out, not_22_out,
       not_23_out, not_24_out, not_25_out, not_26_out, nS0, nS1, nS2, nS3, nS4, nS5, nS6, nS7, nS8, nS9,
       nS10, nS11, nS12, nS13, nS14, S0, S1, S2, S3, S4, S5, S6, S7, S8, S9, S10, S11, S12, S13, S14,
       trq_q_1_q, trq_q_2_q, trq_q_3_nq, trq_q_4_nq, trq_q_5_nq, trq_q_6_nq, trq_q_7_nq, trq_q_8_nq,
       trq_q_9_nq, trq_q_10_nq, trq_q_11_nq, trq_q_12_nq, trq_q_13_nq, trq_q_14_nq, trq_q_15_nq, trq_q_16_nq,
       trq_q_17_nq, trq_q_18_nq, trq_q_19_nq, trq_q_20_nq, trq_q_21_nq, trq_q_22_nq, trq_q_23_nq,
       trq_q_24_nq, trq_q_25_nq, trq_q_26_nq, trq_q_27_nq, trq_q_28_nq, trq_q_29_nq, trq_q_30_nq, trq_q_31_nq;

  not not_1 (not_1_out, nCLR);
  nand nand_1 (nand_1_out, ~CK1, ~CK2);  // NAND_Gate
  not not_2 (not_2_out, B);
  not not_3 (not_3_out, not_2_out);
  not not_4 (not_4_out, C);
  not not_5 (not_5_out, not_4_out);
  not not_6 (not_6_out, not_7_out);
  not not_7 (not_7_out, D);
  not not_8 (not_8_out, not_9_out);
  not not_9 (not_9_out, E);
  TRQ_Q trq_q_1 (.CLK(nor_1_out), .R(not_1_out), .Q(trq_q_1_q));  // open: nQ
  nor nor_1 (nor_1_out, nand_1_out, not_26_out);
  not not_10 (not_10_out, not_3_out);
  not not_11 (not_11_out, not_2_out);
  not not_12 (not_12_out, not_5_out);
  not not_13 (not_13_out, not_4_out);
  not not_14 (not_14_out, not_6_out);
  not not_15 (not_15_out, not_7_out);
  not not_16 (not_16_out, not_8_out);
  not not_17 (not_17_out, not_9_out);
  TRQ_Q trq_q_2 (.CLK(trq_q_1_q), .R(not_1_out), .Q(trq_q_2_q), .nQ(CK3));
  TRQ_Q trq_q_3 (.CLK(nand_37_out), .R(not_1_out), .nQ(trq_q_3_nq));  // open: Q
  assign controlled_inverter_1_out = S10 ? ~trq_q_3_nq : 1'bz;  // Controlled_Inverter controlled_inverter_1
  assign controlled_inverter_1_out = nS10 ? ~CK3 : 1'bz;  // Controlled_Inverter controlled_inverter_2
  TRQ_Q trq_q_4 (.CLK(controlled_inverter_27_out), .R(not_1_out), .nQ(trq_q_4_nq));  // open: Q
  not not_18 (not_18_out, nand_2_out);
  nand nand_2 (nand_2_out, not_10_out, not_12_out);
  nand nand_3 (nand_3_out, not_11_out, not_12_out);
  not not_19 (not_19_out, nand_3_out);
  nand nand_4 (nand_4_out, not_10_out, not_13_out);
  not not_20 (not_20_out, nand_4_out);
  nand nand_5 (nand_5_out, not_11_out, not_13_out);
  not not_21 (not_21_out, nand_5_out);
  not not_22 (not_22_out, nand_6_out);
  nand nand_6 (nand_6_out, not_14_out, not_16_out);
  not not_23 (not_23_out, nand_7_out);
  nand nand_7 (nand_7_out, not_15_out, not_16_out);
  nand nand_8 (nand_8_out, not_14_out, not_17_out);
  not not_24 (not_24_out, nand_8_out);
  not not_25 (not_25_out, nand_9_out);
  nand nand_9 (nand_9_out, not_15_out, not_17_out);
  TRQ_Q trq_q_5 (.CLK(trq_q_2_q), .R(not_1_out), .nQ(trq_q_5_nq));  // open: Q
  TRQ_Q trq_q_6 (.CLK(controlled_inverter_1_out), .R(not_1_out), .nQ(trq_q_6_nq));  // open: Q
  TRQ_Q trq_q_7 (.CLK(nand_38_out), .R(not_1_out), .nQ(trq_q_7_nq));  // open: Q
  assign controlled_inverter_3_out = S6 ? ~trq_q_7_nq : 1'bz;  // Controlled_Inverter controlled_inverter_3
  assign controlled_inverter_3_out = nS6 ? ~CK3 : 1'bz;  // Controlled_Inverter controlled_inverter_4
  nand nand_10 (nand_10_out, S2, trq_q_4_nq);
  TRQ_Q trq_q_8 (.CLK(nand_11_out), .R(not_1_out), .nQ(trq_q_8_nq));  // open: Q
  nand nand_11 (nand_11_out, S13, trq_q_5_nq);
  TRQ_Q trq_q_9 (.CLK(nand_12_out), .R(not_1_out), .nQ(trq_q_9_nq));  // open: Q
  nand nand_12 (nand_12_out, S9, trq_q_6_nq);
  TRQ_Q trq_q_10 (.CLK(controlled_inverter_3_out), .R(not_1_out), .nQ(trq_q_10_nq));  // open: Q
  TRQ_Q trq_q_11 (.CLK(nand_10_out), .R(not_1_out), .nQ(trq_q_11_nq));  // open: Q
  assign controlled_inverter_5_out = S2 ? ~trq_q_11_nq : 1'bz;  // Controlled_Inverter controlled_inverter_5
  assign controlled_inverter_5_out = nS2 ? ~CK3 : 1'bz;  // Controlled_Inverter controlled_inverter_6
  nand nand_13 (nand_13_out, not_18_out, not_22_out);
  not not_26 (not_26_out, nand_13_out);
  nand nand_14 (S0, not_19_out, not_22_out);
  not not_27 (nS0, S0);
  nand nand_15 (S1, not_20_out, not_22_out);
  not not_28 (nS1, S1);
  nand nand_16 (S2, not_22_out, not_21_out);
  not not_29 (nS2, S2);
  nand nand_17 (S3, not_18_out, not_23_out);
  not not_30 (nS3, S3);
  nand nand_18 (S4, not_19_out, not_23_out);
  not not_31 (nS4, S4);
  nand nand_19 (S5, not_20_out, not_23_out);
  not not_32 (nS5, S5);
  nand nand_20 (S6, not_21_out, not_23_out);
  not not_33 (nS6, S6);
  nand nand_21 (S7, not_18_out, not_24_out);
  not not_34 (nS7, S7);
  nand nand_22 (S8, not_19_out, not_24_out);
  not not_35 (nS8, S8);
  nand nand_23 (S9, not_20_out, not_24_out);
  not not_36 (nS9, S9);
  nand nand_24 (S10, not_21_out, not_24_out);
  not not_37 (nS10, S10);
  nand nand_25 (S11, not_18_out, not_25_out);
  not not_38 (nS11, S11);
  nand nand_26 (S12, not_19_out, not_25_out);
  not not_39 (nS12, S12);
  nand nand_27 (S13, not_20_out, not_25_out);
  not not_40 (nS13, S13);
  not not_41 (S14, A);
  not not_42 (nS14, S14);
  TRQ_Q trq_q_12 (.CLK(controlled_inverter_7_out), .R(not_1_out), .nQ(trq_q_12_nq));  // open: Q
  assign controlled_inverter_7_out = S13 ? ~trq_q_8_nq : 1'bz;  // Controlled_Inverter controlled_inverter_7
  assign controlled_inverter_7_out = nS13 ? ~CK3 : 1'bz;  // Controlled_Inverter controlled_inverter_8
  TRQ_Q trq_q_13 (.CLK(controlled_inverter_9_out), .R(not_1_out), .nQ(trq_q_13_nq));  // open: Q
  assign controlled_inverter_9_out = S9 ? ~trq_q_9_nq : 1'bz;  // Controlled_Inverter controlled_inverter_9
  assign controlled_inverter_9_out = nS9 ? ~CK3 : 1'bz;  // Controlled_Inverter controlled_inverter_10
  TRQ_Q trq_q_14 (.CLK(nand_28_out), .R(not_1_out), .nQ(trq_q_14_nq));  // open: Q
  nand nand_28 (nand_28_out, S5, trq_q_10_nq);
  TRQ_Q trq_q_15 (.CLK(controlled_inverter_5_out), .R(not_1_out), .nQ(trq_q_15_nq));  // open: Q
  TRQ_Q trq_q_16 (.CLK(nand_29_out), .R(not_1_out), .nQ(trq_q_16_nq));  // open: Q
  nand nand_29 (nand_29_out, S12, trq_q_12_nq);
  TRQ_Q trq_q_17 (.CLK(nand_30_out), .R(not_1_out), .nQ(trq_q_17_nq));  // open: Q
  nand nand_30 (nand_30_out, S8, trq_q_13_nq);
  TRQ_Q trq_q_18 (.CLK(controlled_inverter_11_out), .R(not_1_out), .nQ(trq_q_18_nq));  // open: Q
  assign controlled_inverter_11_out = S5 ? ~trq_q_14_nq : 1'bz;  // Controlled_Inverter controlled_inverter_11
  assign controlled_inverter_11_out = nS5 ? ~CK3 : 1'bz;  // Controlled_Inverter controlled_inverter_12
  TRQ_Q trq_q_19 (.CLK(nand_31_out), .R(not_1_out), .nQ(trq_q_19_nq));  // open: Q
  nand nand_31 (nand_31_out, S1, trq_q_15_nq);
  TRQ_Q trq_q_20 (.CLK(controlled_inverter_13_out), .R(not_1_out), .nQ(trq_q_20_nq));  // open: Q
  assign controlled_inverter_13_out = S12 ? ~trq_q_16_nq : 1'bz;  // Controlled_Inverter controlled_inverter_13
  assign controlled_inverter_13_out = nS12 ? ~CK3 : 1'bz;  // Controlled_Inverter controlled_inverter_14
  TRQ_Q trq_q_21 (.CLK(controlled_inverter_15_out), .R(not_1_out), .nQ(trq_q_21_nq));  // open: Q
  assign controlled_inverter_15_out = S8 ? ~trq_q_17_nq : 1'bz;  // Controlled_Inverter controlled_inverter_15
  assign controlled_inverter_15_out = nS8 ? ~CK3 : 1'bz;  // Controlled_Inverter controlled_inverter_16
  TRQ_Q trq_q_22 (.CLK(nand_32_out), .R(not_1_out), .nQ(trq_q_22_nq));  // open: Q
  nand nand_32 (nand_32_out, S4, trq_q_18_nq);
  TRQ_Q trq_q_23 (.CLK(controlled_inverter_17_out), .R(not_1_out), .nQ(trq_q_23_nq));  // open: Q
  assign controlled_inverter_17_out = S1 ? ~trq_q_19_nq : 1'bz;  // Controlled_Inverter controlled_inverter_17
  assign controlled_inverter_17_out = nS1 ? ~CK3 : 1'bz;  // Controlled_Inverter controlled_inverter_18
  nand nand_33 (nand_33_out, S11, trq_q_20_nq);
  nand nand_34 (nand_34_out, S7, trq_q_21_nq);
  TRQ_Q trq_q_24 (.CLK(controlled_inverter_19_out), .R(not_1_out), .nQ(trq_q_24_nq));  // open: Q
  assign controlled_inverter_19_out = S4 ? ~trq_q_22_nq : 1'bz;  // Controlled_Inverter controlled_inverter_19
  assign controlled_inverter_19_out = nS4 ? ~CK3 : 1'bz;  // Controlled_Inverter controlled_inverter_20
  TRQ_Q trq_q_25 (.CLK(nand_35_out), .R(not_1_out), .nQ(trq_q_25_nq));  // open: Q
  nand nand_35 (nand_35_out, S0, trq_q_23_nq);
  TRQ_Q trq_q_26 (.CLK(nand_33_out), .R(not_1_out), .nQ(trq_q_26_nq));  // open: Q
  assign controlled_inverter_21_out = S11 ? ~trq_q_26_nq : 1'bz;  // Controlled_Inverter controlled_inverter_21
  assign controlled_inverter_21_out = nS11 ? ~CK3 : 1'bz;  // Controlled_Inverter controlled_inverter_22
  TRQ_Q trq_q_27 (.CLK(nand_34_out), .R(not_1_out), .nQ(trq_q_27_nq));  // open: Q
  assign controlled_inverter_23_out = S7 ? ~trq_q_27_nq : 1'bz;  // Controlled_Inverter controlled_inverter_23
  assign controlled_inverter_23_out = nS7 ? ~CK3 : 1'bz;  // Controlled_Inverter controlled_inverter_24
  nand nand_36 (nand_36_out, S3, trq_q_24_nq);
  assign controlled_inverter_25_out = S0 ? ~trq_q_25_nq : 1'bz;  // Controlled_Inverter controlled_inverter_25
  assign controlled_inverter_25_out = nS0 ? ~CK3 : 1'bz;  // Controlled_Inverter controlled_inverter_26
  TRQ_Q trq_q_28 (.CLK(controlled_inverter_21_out), .R(not_1_out), .nQ(trq_q_28_nq));  // open: Q
  TRQ_Q trq_q_29 (.CLK(controlled_inverter_23_out), .R(not_1_out), .nQ(trq_q_29_nq));  // open: Q
  TRQ_Q trq_q_30 (.CLK(nand_36_out), .R(not_1_out), .nQ(trq_q_30_nq));  // open: Q
  nor nor_2 (nor_2_out, controlled_inverter_25_out, S14);
  nand nand_37 (nand_37_out, trq_q_28_nq, S10);
  not not_43 (TP1, nand_37_out);
  nand nand_38 (nand_38_out, trq_q_29_nq, S6);
  not not_44 (TP2, nand_38_out);
  assign controlled_inverter_27_out = nS3 ? ~CK3 : 1'bz;  // Controlled_Inverter controlled_inverter_27
  assign controlled_inverter_27_out = S3 ? ~trq_q_30_nq : 1'bz;  // Controlled_Inverter controlled_inverter_28
  not not_45 (TP3, controlled_inverter_27_out);
  TRQ_Q trq_q_31 (.CLK(nor_2_out), .R(not_1_out), .nQ(trq_q_31_nq));  // open: Q
  assign controlled_inverter_29_out = nS14 ? ~trq_q_31_nq : 1'bz;  // Controlled_Inverter controlled_inverter_29
  assign controlled_inverter_29_out = S14 ? ~controlled_inverter_25_out : 1'bz;  // Controlled_Inverter controlled_inverter_30
  not not_46 (Q, controlled_inverter_29_out);

  // Notes on the sheet:
  //   74LS292
  //   1-14 => /S0-/S13
  //   * Replace by Decoder?
  //   ** Toshiba and SGS Datasheet
endmodule

module TRQ_Q (
  input  CLK,
  input  R,
  output Q,
  output nQ
);

  T_Flip_Flop #(.trigger("falling")) Fall (.clk(CLK), .T(1'b1), .Q(Q), .Qn(nQ), .reset(R));  // open: preset, en
endmodule

module test (
  input  in_1,
  input  in_2,
  input  in_3,
  input  in_4,
  input  in_5,
  input  in_6,
  input  in_7
);

  wire clock_1_out, n74ls292_1_q, n74ls292_1_tp1, n74ls292_1_tp2, n74ls292_1_tp3;

  Counter #(.width(32), .max('hffffffff)) counter_1 (.clk(clock_1_out));  // open: load, D, count, Q, carry, clr
  Clock clock_1 (.out(clock_1_out));
  _74LS292 u_74ls292_1 (
    .nCLR(in_1), .CK1(clock_1_out), .CK2(in_2), .B(in_4), .C(in_5), .D(in_6), .E(in_7), .A(in_3),
    .TP1(n74ls292_1_tp1), .TP2(n74ls292_1_tp2), .TP3(n74ls292_1_tp3), .Q(n74ls292_1_q));
  Counter #(.width(32), .max('hffffffff)) counter_2 (.clk(n74ls292_1_tp1));  // open: load, D, count, Q, carry, clr
  Counter #(.width(32), .max('hffffffff)) counter_3 (.clk(n74ls292_1_tp3));  // open: load, D, count, Q, carry, clr
  Counter #(.width(32), .max('hffffffff)) counter_4 (.clk(n74ls292_1_tp2));  // open: load, D, count, Q, carry, clr
  Counter #(.width(32), .max('hffffffff)) counter_5 (.clk(n74ls292_1_q));  // open: load, D, count, Q, carry, clr
endmodule
