// Logisim project 74LS293.circ as structural Verilog: 1 circuit, main circuit 74LS293
module _74LS293 (
  input  INPUT_A,
  input  INPUT_B,
  input  R0_1,
  input  R0_2,
  output QA,
  output QB,
  output QC,
  output QD
);

  wire nand_1_out, not_1_out, not_2_out, not_3_out, not_4_out;

  nand nand_1 (nand_1_out, R0_1, R0_2);
  J_K_Flip_Flop #(.trigger("falling")) Fall (
    .J(1'b1), .clk(INPUT_A), .K(1'b1), .Q(QA), .reset(not_1_out));  // open: Qn, preset, en
  not not_1 (not_1_out, nand_1_out);
  J_K_Flip_Flop #(.trigger("falling")) Fall_2 (
    .J(1'b1), .clk(INPUT_B), .K(1'b1), .Q(QB), .reset(not_2_out));  // open: Qn, preset, en
  not not_2 (not_2_out, nand_1_out);
  J_K_Flip_Flop #(.trigger("falling")) Fall_3 (
    .J(1'b1), .clk(QB), .K(1'b1), .Q(QC), .reset(not_3_out));  // open: Qn, preset, en
  not not_3 (not_3_out, nand_1_out);
  J_K_Flip_Flop #(.trigger("falling")) Fall_4 (
    .J(1'b1), .clk(QC), .K(1'b1), .Q(QD), .reset(not_4_out));  // open: Qn, preset, en
  not not_4 (not_4_out, nand_1_out);

  // Notes on the sheet:
  //   74LS293
endmodule
