// Logisim project 74LS294.circ as structural Verilog: 3 circuits, main circuit 74LS294
module _74LS294 (
  input  nCLR,
  input  CK1,
  input  CK2,
  input  A,
  input  B,
  input  C,
  input  D,
  output Q,
  output TP
);

  wire _2_2, _2_3, _2_4, _2_5, _2_6, _2_7, _2_8, _2_9, _2_10, _2_11, _2_12, _2_13, _2_14, _2_15, nand_1_out,
       not_1_out, trq_1_q;

  not not_1 (not_1_out, nCLR);
  TRQ trq_1 (.CLK(nand_1_out), .R(not_1_out), .Q(trq_1_q));
  nand nand_1 (nand_1_out, ~CK1, ~CK2);  // NAND_Gate
  TRQ trq_2 (.CLK(trq_1_q), .R(not_1_out), .Q(_2_2));
  TRQ trq_3 (.CLK(_2_2), .R(not_1_out), .Q(_2_3));
  TRQ trq_4 (.CLK(_2_3), .R(not_1_out), .Q(_2_4));
  Multiplexer #(.select(4), .enable("false")) multiplexer_1 (
    .in0(1'b0), .in1(1'b0), .in2(_2_2), .in3(_2_3), .in4(_2_4), .in5(_2_5), .in6(_2_6), .in7(_2_7),
    .in8(_2_8), .in9(_2_9), .in10(_2_10), .in11(_2_11), .in12(_2_12), .in13(_2_13), .in14(_2_14),
    .in15(_2_15), .out(Q), .sel({D, C, B, A}));
  TRQ trq_5 (.CLK(_2_4), .R(not_1_out), .Q(_2_5));
  TRQ trq_6 (.CLK(_2_5), .R(not_1_out), .Q(_2_6));
  TRQ trq_7 (.CLK(_2_6), .R(not_1_out), .Q(_2_7));
  TRQ trq_8 (.CLK(_2_8), .R(not_1_out), .Q(_2_9));
  TRQ trq_9 (.CLK(_2_7), .R(not_1_out), .Q(_2_8));
  TRQ trq_10 (.CLK(_2_9), .R(not_1_out), .Q(_2_10));
  Multiplexer #(.select(4), .enable("false")) multiplexer_2 (
    .in0(1'b0), .in1(1'b0), .in2(_2_9), .in3(_2_9), .in4(_2_9), .in5(_2_9), .in6(_2_9), .in7(1'b0),
    .in8(_2_2), .in9(_2_3), .in10(_2_4), .in11(_2_5), .in12(_2_6), .in13(_2_7), .in14(_2_8), .in15(_2_9),
    .out(TP), .sel({D, C, B, A}));
  TRQ trq_11 (.CLK(_2_10), .R(not_1_out), .Q(_2_11));
  TRQ trq_12 (.CLK(_2_11), .R(not_1_out), .Q(_2_12));
  TRQ trq_13 (.CLK(_2_12), .R(not_1_out), .Q(_2_13));
  TRQ trq_14 (.CLK(_2_13), .R(not_1_out), .Q(_2_14));
  TRQ trq_15 (.CLK(_2_14), .R(not_1_out), .Q(_2_15));

  // Notes on the sheet:
  //   74LS294
  //   * NOTE: Redo LS292 like this
endmodule

module TRQ (
  input  CLK,
  input  R,
  output Q
);

  T_Flip_Flop #(.trigger("falling")) Fall (.clk(CLK), .T(1'b1), .Q(Q), .reset(R));  // open: Qn, preset, en
endmodule

module test (
  input  in_1,
  input  in_2,
  input  in_3,
  input  in_4,
  input  in_5,
  input  in_6
);

  wire clock_1_out, n74ls294_1_q, n74ls294_1_tp;

  Counter #(.width(32), .max('hffffffff)) counter_1 (.clk(clock_1_out));  // open: load, D, count, Q, carry, clr
  Clock clock_1 (.out(clock_1_out));
  _74LS294 u_74ls294_1 (
    .nCLR(in_1), .CK1(clock_1_out), .CK2(in_2), .A(in_3), .B(in_4), .C(in_5), .D(in_6), .Q(n74ls294_1_q),
    .TP(n74ls294_1_tp));
  Counter #(.width(32), .max('hffffffff)) counter_2 (.clk(n74ls294_1_tp));  // open: load, D, count, Q, carry, clr
  Counter #(.width(32), .max('hffffffff)) counter_3 (.clk(n74ls294_1_q));  // open: load, D, count, Q, carry, clr
endmodule
