// Logisim project 74LS295.circ as structural Verilog: 1 circuit, main circuit 74LS295
module _74LS295 (
  input  A,
  input  B,
  input  C,
  input  D,
  input  LD_SH,
  input  SER,
  input  CLK,
  input  OC,
  output QA,
  output QB,
  output QC,
  output QD
);

  wire and_1_out, and_2_out, and_3_out, and_4_out, and_5_out, and_6_out, and_7_out, and_8_out, Fall_2_q,
       Fall_3_q, Fall_4_q, Fall_q, nor_1_out, nor_2_out, nor_3_out, nor_4_out, not_1_out, not_2_out,
       not_3_out, not_4_out, not_5_out, not_6_out;

  not not_1 (not_1_out, LD_SH);
  not not_2 (not_2_out, not_1_out);
  and and_1 (and_1_out, not_2_out, A);
  and and_2 (and_2_out, SER, not_1_out);
  nor nor_1 (nor_1_out, and_2_out, and_1_out);
  not not_3 (not_3_out, nor_1_out);
  S_R_Flip_Flop #(.trigger("falling")) Fall (
    .S(not_3_out), .clk(CLK), .R(nor_1_out), .Q(Fall_q));  // open: Qn, preset, reset, en
  and and_3 (and_3_out, not_2_out, B);
  and and_4 (and_4_out, Fall_q, not_1_out);
  nor nor_2 (nor_2_out, and_4_out, and_3_out);
  not not_4 (not_4_out, nor_2_out);
  assign QA = OC ? Fall_q : 1'bz;  // Controlled_Buffer controlled_buffer_1
  S_R_Flip_Flop #(.trigger("falling")) Fall_2 (
    .S(not_4_out), .clk(CLK), .R(nor_2_out), .Q(Fall_2_q));  // open: Qn, preset, reset, en
  and and_5 (and_5_out, not_2_out, C);
  and and_6 (and_6_out, Fall_2_q, not_1_out);
  nor nor_3 (nor_3_out, and_6_out, and_5_out);
  not not_5 (not_5_out, nor_3_out);
  assign QB = OC ? Fall_2_q : 1'bz;  // Controlled_Buffer controlled_buffer_2
  S_R_Flip_Flop #(.trigger("falling")) Fall_3 (
    .S(not_5_out), .clk(CLK), .R(nor_3_out), .Q(Fall_3_q));  // open: Qn, preset, reset, en
  and and_7 (and_7_out, Fall_3_q, not_1_out);
  and and_8 (and_8_out, not_2_out, D);
  nor nor_4 (nor_4_out, and_7_out, and_8_out);
  assign QC = OC ? Fall_3_q : 1'bz;  // Controlled_Buffer controlled_buffer_3
  not not_6 (not_6_out, nor_4_out);
  S_R_Flip_Flop #(.trigger("falling")) Fall_4 (
    .S(not_6_out), .clk(CLK), .R(nor_4_out), .Q(Fall_4_q));  // open: Qn, preset, reset, en
  assign QD = OC ? Fall_4_q : 1'bz;  // Controlled_Buffer controlled_buffer_4

  // Notes on the sheet:
  //   74LS295
endmodule
