// Logisim project 74LS298.circ as structural Verilog: 1 circuit, main circuit 74LS298
module _74LS298 (
  input  A1,
  input  WS,
  input  A2,
  input  B1,
  input  B2,
  input  C1,
  input  C2,
  input  D1,
  input  D2,
  input  CLK,
  output QA,
  output QB,
  output QC,
  output QD
);

  wire and_1_out, and_2_out, and_3_out, and_4_out, and_5_out, and_6_out, and_7_out, and_8_out, nor_1_out,
       nor_2_out, nor_3_out, nor_4_out, not_1_out, not_2_out, not_3_out, not_4_out, not_5_out, not_6_out;

  not not_1 (not_1_out, WS);
  not not_2 (not_2_out, not_1_out);
  and and_1 (and_1_out, A1, not_1_out);
  and and_2 (and_2_out, not_2_out, A2);
  and and_3 (and_3_out, B1, not_1_out);
  and and_4 (and_4_out, not_2_out, B2);
  and and_5 (and_5_out, C1, not_1_out);
  and and_6 (and_6_out, not_2_out, C2);
  and and_7 (and_7_out, D1, not_1_out);
  and and_8 (and_8_out, not_2_out, D2);
  not not_3 (not_3_out, nor_1_out);
  nor nor_1 (nor_1_out, and_1_out, and_2_out);
  nor nor_2 (nor_2_out, and_3_out, and_4_out);
  not not_4 (not_4_out, nor_2_out);
  nor nor_3 (nor_3_out, and_5_out, and_6_out);
  not not_5 (not_5_out, nor_3_out);
  not not_6 (not_6_out, nor_4_out);
  nor nor_4 (nor_4_out, and_7_out, and_8_out);
  S_R_Flip_Flop #(.trigger("falling")) Fall (
    .S(not_3_out), .clk(CLK), .R(nor_1_out), .Q(QA));  // open: Qn, preset, reset, en
  S_R_Flip_Flop #(.trigger("falling")) Fall_2 (
    .S(not_4_out), .clk(CLK), .R(nor_2_out), .Q(QB));  // open: Qn, preset, reset, en
  S_R_Flip_Flop #(.trigger("falling")) Fall_3 (
    .S(not_5_out), .clk(CLK), .R(nor_3_out), .Q(QC));  // open: Qn, preset, reset, en
  S_R_Flip_Flop #(.trigger("falling")) Fall_4 (
    .S(not_6_out), .clk(CLK), .R(nor_4_out), .Q(QD));  // open: Qn, preset, reset, en

  // Notes on the sheet:
  //   74LS298
endmodule
