// Logisim project 74LS299.circ as structural Verilog: 2 circuits, main circuit 74LS299
module _74LS299 (
  input  S0,
  input  S1,
  input  SH_R_IN,
  input  CLK,
  input  SH_L_IN,
  input  nCLR,
  input  nG1,
  input  nG2,
  input  A_QA,
  input  B_QB,
  input  C_QC,
  input  D_QD,
  input  E_QE,
  input  F_QF,
  input  G_QG,
  input  H_QH,
  output QH_prime,
  output QA_prime,
  output A_QA_2,
  output B_QB_2,
  output C_QC_2,
  output D_QD_2,
  output E_QE_2,
  output F_QF_2,
  output G_QG_2,
  output H_QH_2
);

  wire and_1_out, CHANNEL_A_q, CHANNEL_B_q, CHANNEL_B_q_2, CHANNEL_C_q, CHANNEL_C_q_2, CHANNEL_D_q,
       CHANNEL_D_q_2, CHANNEL_E_q, CHANNEL_E_q_2, CHANNEL_F_q, CHANNEL_F_q_2, CHANNEL_G_q, CHANNEL_G_q_2,
       CHANNEL_H_q_2, nor_1_out, not_1_out, not_2_out, not_3_out, not_4_out, not_5_out;

  not not_1 (not_1_out, S0);
  not not_2 (not_2_out, S1);
  not not_3 (not_3_out, not_1_out);
  not not_4 (not_4_out, not_2_out);
  nor nor_1 (nor_1_out, ~S1, ~S0);  // NOR_Gate
  not not_5 (not_5_out, CLK);
  and and_1 (and_1_out, ~nor_1_out, ~nG1, ~nG2);  // AND_Gate
  one_channel CHANNEL_A (
    .S0(not_3_out), .nS0(not_1_out), .nS1(not_2_out), .S1(not_4_out), .SER_RIGHT_IN(SH_R_IN),
    .nCLK(not_5_out), .Q_2(QA_prime), .nCLR(nCLR), .G(and_1_out), .Q(CHANNEL_A_q),
    .SER_LEFT_IN(CHANNEL_B_q_2), .x_Qx_out(A_QA_2), .x_Qx_in(A_QA));
  one_channel CHANNEL_B (
    .S0(not_3_out), .nS0(not_1_out), .nS1(not_2_out), .S1(not_4_out), .SER_RIGHT_IN(CHANNEL_A_q),
    .nCLK(not_5_out), .Q_2(CHANNEL_B_q_2), .nCLR(nCLR), .G(and_1_out), .Q(CHANNEL_B_q),
    .SER_LEFT_IN(CHANNEL_C_q_2), .x_Qx_out(B_QB_2), .x_Qx_in(B_QB));
  one_channel CHANNEL_C (
    .S0(not_3_out), .nS0(not_1_out), .nS1(not_2_out), .S1(not_4_out), .SER_RIGHT_IN(CHANNEL_B_q),
    .nCLK(not_5_out), .Q_2(CHANNEL_C_q_2), .nCLR(nCLR), .G(and_1_out), .Q(CHANNEL_C_q),
    .SER_LEFT_IN(CHANNEL_D_q_2), .x_Qx_out(C_QC_2), .x_Qx_in(C_QC));
  one_channel CHANNEL_D (
    .S0(not_3_out), .nS0(not_1_out), .nS1(not_2_out), .S1(not_4_out), .SER_RIGHT_IN(CHANNEL_C_q),
    .nCLK(not_5_out), .Q_2(CHANNEL_D_q_2), .nCLR(nCLR), .G(and_1_out), .Q(CHANNEL_D_q),
    .SER_LEFT_IN(CHANNEL_E_q_2), .x_Qx_out(D_QD_2), .x_Qx_in(D_QD));
  one_channel CHANNEL_E (
    .S0(not_3_out), .nS0(not_1_out), .nS1(not_2_out), .S1(not_4_out), .SER_RIGHT_IN(CHANNEL_D_q),
    .nCLK(not_5_out), .Q_2(CHANNEL_E_q_2), .nCLR(nCLR), .G(and_1_out), .Q(CHANNEL_E_q),
    .SER_LEFT_IN(CHANNEL_F_q_2), .x_Qx_out(E_QE_2), .x_Qx_in(E_QE));
  one_channel CHANNEL_F (
    .S0(not_3_out), .nS0(not_1_out), .nS1(not_2_out), .S1(not_4_out), .SER_RIGHT_IN(CHANNEL_E_q),
    .nCLK(not_5_out), .Q_2(CHANNEL_F_q_2), .nCLR(nCLR), .G(and_1_out), .Q(CHANNEL_F_q),
    .SER_LEFT_IN(CHANNEL_G_q_2), .x_Qx_out(F_QF_2), .x_Qx_in(F_QF));
  one_channel CHANNEL_G (
    .S0(not_3_out), .nS0(not_1_out), .nS1(not_2_out), .S1(not_4_out), .SER_RIGHT_IN(CHANNEL_F_q),
    .nCLK(not_5_out), .Q_2(CHANNEL_G_q_2), .nCLR(nCLR), .G(and_1_out), .Q(CHANNEL_G_q),
    .SER_LEFT_IN(CHANNEL_H_q_2), .x_Qx_out(G_QG_2), .x_Qx_in(G_QG));
  one_channel CHANNEL_H (
    .S0(not_3_out), .nS0(not_1_out), .nS1(not_2_out), .S1(not_4_out), .SER_RIGHT_IN(CHANNEL_G_q),
    .nCLK(not_5_out), .Q_2(CHANNEL_H_q_2), .nCLR(nCLR), .G(and_1_out), .Q(QH_prime), .SER_LEFT_IN(SH_L_IN),
    .x_Qx_out(H_QH_2), .x_Qx_in(H_QH));

  // Notes on the sheet:
  //   74LS299
endmodule

module one_channel (
  input  S0,
  input  nS0,
  input  nS1,
  input  S1,
  input  SER_RIGHT_IN,
  input  nCLK,
  input  SER_LEFT_IN,
  input  nCLR,
  input  G,
  input  x_Qx_in,
  output Q,
  output Q_2,
  output x_Qx_out
);

  wire and_1_out, and_2_out, and_3_out, and_4_out, not_1_out, or_1_out;

  and and_1 (and_1_out, SER_RIGHT_IN, S0, nS1);
  and and_2 (and_2_out, S1, S0, x_Qx_in);
  and and_3 (and_3_out, S1, nS0, SER_LEFT_IN);
  or or_1 (or_1_out, and_1_out, and_3_out, and_2_out, and_4_out);
  assign x_Qx_out = G ? Q : 1'bz;  // Controlled_Buffer controlled_buffer_1
  and and_4 (and_4_out, nS1, nS0, Q);
  D_Flip_Flop #(.trigger("falling")) Fall (.clk(nCLK), .D(or_1_out), .Q(Q), .reset(not_1_out));  // open: Qn, preset, en
  not not_1 (not_1_out, nCLR);

  assign Q_2 = Q;
endmodule
