// Logisim project 74LS302.circ as structural Verilog: 1 circuit, main circuit 74LS302
module _74LS302 (
  input  DI,
  input  A0,
  input  A1,
  input  A2,
  input  A3,
  input  A4,
  input  A5,
  input  A6,
  input  A7,
  input  nS1,
  input  nS2,
  input  nS3,
  input  nWE,
  output DO
);

  wire and_1_out, and_2_out, controlled_buffer_1_out, controlled_buffer_2_out, not_1_out;

  and and_1 (and_1_out, ~nS1, ~nS2, ~nS3);  // AND_Gate
  assign controlled_buffer_1_out = not_1_out ? DI : 1'bz;  // Controlled_Buffer controlled_buffer_1
  not not_1 (not_1_out, nWE);
  RAM #(.dataWidth(1), .bus("asynch")) ram_1 (
    .addr({A7, A6, A5, A4, A3, A2, A1, A0}), .data(controlled_buffer_1_out), .sel(and_1_out), .ld(nWE));  // open: clr
  Pull_Resistor #(.pull(1)) pull_resistor_1 (.node(controlled_buffer_1_out));
  assign controlled_buffer_2_out = and_2_out ? controlled_buffer_1_out : 1'bz;  // Controlled_Buffer controlled_buffer_2
  buf buffer_1 (DO, controlled_buffer_2_out);
  and and_2 (and_2_out, and_1_out, nWE);

  // Notes on the sheet:
  //   74LS302
  //   buffer_1 drives only 0 and floats otherwise
endmodule
