// Logisim project 74LS303.circ as structural Verilog: 1 circuit, main circuit 74LS303
module _74LS303 (
  input  CLK,
  input  nPRE,
  input  nCLR,
  output Q1,
  output Q2,
  output Q3,
  output Q4,
  output Q5,
  output Q6,
  output nQ7,
  output nQ8
);

  wire not_1_out, not_2_out;

  T_Flip_Flop t_ff_1 (.clk(CLK), .T(1'b1), .Q(Q1), .Qn(nQ7), .preset(not_1_out), .reset(not_2_out));  // open: en
  not not_1 (not_1_out, nPRE);
  not not_2 (not_2_out, nCLR);

  assign nQ8 = nQ7;
  assign Q2 = Q1;
  assign Q3 = Q1;
  assign Q4 = Q1;
  assign Q5 = Q1;
  assign Q6 = Q1;

  // Notes on the sheet:
  //   74LS303
endmodule
