// Logisim project 74LS304.circ as structural Verilog: 1 circuit, main circuit 74LS304
module _74LS304 (
  input  CLK,
  input  nPRE,
  input  nCLR,
  output Q1,
  output Q2,
  output Q3,
  output Q4,
  output Q5,
  output Q6,
  output Q7,
  output Q8
);

  wire not_1_out, not_2_out, t_ff_1_qn;

  T_Flip_Flop t_ff_1 (.clk(CLK), .T(1'b1), .Q(Q1), .Qn(t_ff_1_qn), .preset(not_2_out), .reset(not_1_out));  // open: en
  not not_1 (not_1_out, nCLR);
  not not_2 (not_2_out, nPRE);

  assign Q2 = Q1;
  assign Q3 = Q1;
  assign Q4 = Q1;
  assign Q5 = Q1;
  assign Q6 = Q1;
  assign Q7 = Q1;
  assign Q8 = Q1;

  // Notes on the sheet:
  //   74LS304
endmodule
