// Logisim project 74LS305.circ as structural Verilog: 1 circuit, main circuit 74LS305
module _74LS305 (
  input  CLK,
  input  nPRE,
  input  nCLR,
  output Q1,
  output Q2,
  output Q3,
  output Q4,
  output nQ5,
  output nQ6,
  output nQ7,
  output nQ8
);

  wire not_1_out, not_2_out;

  T_Flip_Flop t_ff_1 (.clk(CLK), .T(1'b1), .Q(Q1), .Qn(nQ5), .preset(not_2_out), .reset(not_1_out));  // open: en
  not not_1 (not_1_out, nCLR);
  not not_2 (not_2_out, nPRE);

  assign nQ6 = nQ5;
  assign nQ7 = nQ5;
  assign nQ8 = nQ5;
  assign Q2 = Q1;
  assign Q3 = Q1;
  assign Q4 = Q1;

  // Notes on the sheet:
  //   74LS305
endmodule
