// Logisim project 74LS306.circ as structural Verilog: 1 circuit, main circuit 74LS306
module _74LS306 (
  input  DIR,
  input  nOE,
  input  A1in,
  input  B1in,
  input  A2in,
  input  B2in,
  input  A3in,
  input  B3in,
  input  A4in,
  input  B4in,
  input  A5in,
  input  B5in,
  input  A6in,
  input  B6in,
  input  A7in,
  input  B7in,
  input  A8in,
  input  B8in,
  output B1out,
  output A1out,
  output B2out,
  output A2out,
  output B3out,
  output A3out,
  output B4out,
  output A4out,
  output B5out,
  output A5out,
  output B6out,
  output A6out,
  output B7out,
  output A7out,
  output B8out,
  output A8out
);

  wire and_1_out, and_2_out, buffer_1_out, buffer_2_out, buffer_3_out, buffer_4_out, buffer_5_out,
       buffer_6_out, buffer_7_out, buffer_8_out, buffer_9_out, buffer_10_out, buffer_11_out, buffer_12_out,
       buffer_13_out, buffer_14_out, buffer_15_out, buffer_16_out;

  and and_1 (and_1_out, ~DIR, ~nOE);  // AND_Gate
  and and_2 (and_2_out, DIR, ~nOE);  // AND_Gate
  buf buffer_1 (buffer_1_out, A1in);
  assign A1out = and_1_out ? buffer_2_out : 1'bz;  // Controlled_Buffer controlled_buffer_1
  buf buffer_2 (buffer_2_out, B1in);
  buf buffer_3 (buffer_3_out, A2in);
  assign A2out = and_1_out ? buffer_4_out : 1'bz;  // Controlled_Buffer controlled_buffer_2
  buf buffer_4 (buffer_4_out, B2in);
  buf buffer_5 (buffer_5_out, A3in);
  assign A3out = and_1_out ? buffer_6_out : 1'bz;  // Controlled_Buffer controlled_buffer_3
  buf buffer_6 (buffer_6_out, B3in);
  buf buffer_7 (buffer_7_out, A4in);
  buf buffer_8 (buffer_8_out, B4in);
  assign A4out = and_1_out ? buffer_8_out : 1'bz;  // Controlled_Buffer controlled_buffer_4
  buf buffer_9 (buffer_9_out, A5in);
  buf buffer_10 (buffer_10_out, B5in);
  assign A5out = and_1_out ? buffer_10_out : 1'bz;  // Controlled_Buffer controlled_buffer_5
  buf buffer_11 (buffer_11_out, A6in);
  assign A6out = and_1_out ? buffer_12_out : 1'bz;  // Controlled_Buffer controlled_buffer_6
  buf buffer_12 (buffer_12_out, B6in);
  buf buffer_13 (buffer_13_out, A7in);
  assign A7out = and_1_out ? buffer_14_out : 1'bz;  // Controlled_Buffer controlled_buffer_7
  buf buffer_14 (buffer_14_out, B7in);
  buf buffer_15 (buffer_15_out, A8in);
  buf buffer_16 (buffer_16_out, B8in);
  assign A8out = and_1_out ? buffer_16_out : 1'bz;  // Controlled_Buffer controlled_buffer_8
  and and_3 (B1out, and_2_out, buffer_1_out);
  and and_4 (B2out, and_2_out, buffer_3_out);
  and and_5 (B3out, and_2_out, buffer_5_out);
  and and_6 (B4out, and_2_out, buffer_7_out);
  and and_7 (B5out, and_2_out, buffer_9_out);
  and and_8 (B6out, and_2_out, buffer_11_out);
  and and_9 (B7out, and_2_out, buffer_13_out);
  and and_10 (B8out, and_2_out, buffer_15_out);

  // Notes on the sheet:
  //   74LS306
  //   and_3 drives only 0 and floats otherwise
  //   and_4 drives only 0 and floats otherwise
  //   and_5 drives only 0 and floats otherwise
  //   and_6 drives only 0 and floats otherwise
  //   and_7 drives only 0 and floats otherwise
  //   and_8 drives only 0 and floats otherwise
  //   and_9 drives only 0 and floats otherwise
  //   and_10 drives only 0 and floats otherwise
endmodule
