// Logisim project 74LS309.circ as structural Verilog: 1 circuit, main circuit 74LS309
module _74LS309 (
  input  A,
  input  B,
  input  DATA_IN,
  input  C,
  input  D,
  input  E,
  input  F,
  input  G,
  input  H,
  input  I,
  input  J,
  input  R_W,
  input  nCE,
  output OUTPUT_D0
);

  wire controlled_buffer_1_out, controlled_buffer_2_out, not_1_out, not_2_out;

  not not_1 (not_1_out, nCE);
  assign controlled_buffer_1_out = not_2_out ? DATA_IN : 1'bz;  // Controlled_Buffer controlled_buffer_1
  not not_2 (not_2_out, R_W);
  RAM #(.addrWidth(10), .dataWidth(1), .bus("asynch")) ram_1 (
    .addr({J, I, H, G, F, E, D, C, B, A}), .data(controlled_buffer_1_out), .sel(not_1_out), .ld(R_W));  // open: clr
  assign controlled_buffer_2_out = R_W ? controlled_buffer_1_out : 1'bz;  // Controlled_Buffer controlled_buffer_2
  buf buffer_1 (OUTPUT_D0, controlled_buffer_2_out);

  // Notes on the sheet:
  //   74LS309
  //   buffer_1 drives only 0 and floats otherwise
endmodule
