// Logisim project 74LS315.circ as structural Verilog: 1 circuit, main circuit 74LS315
module _74LS315 (
  input  DI,
  input  A0,
  input  A1,
  input  A2,
  input  A3,
  input  A4,
  input  A5,
  input  A6,
  input  A7,
  input  A8,
  input  A9,
  input  nE_S,
  input  nW,
  output DO
);

  wire controlled_buffer_1_out, controlled_buffer_2_out, not_1_out, not_2_out;

  not not_1 (not_1_out, nE_S);
  assign controlled_buffer_1_out = not_2_out ? DI : 1'bz;  // Controlled_Buffer controlled_buffer_1
  not not_2 (not_2_out, nW);
  RAM #(.addrWidth(10), .dataWidth(1), .bus("asynch")) ram_1 (
    .addr({A9, A8, A7, A6, A5, A4, A3, A2, A1, A0}), .data(controlled_buffer_1_out), .sel(not_1_out), .ld(nW));  // open: clr
  buf buffer_1 (DO, controlled_buffer_2_out);
  assign controlled_buffer_2_out = nW ? controlled_buffer_1_out : 1'bz;  // Controlled_Buffer controlled_buffer_2

  // Notes on the sheet:
  //   74LS315
  //   buffer_1 drives only 0 and floats otherwise
endmodule
