// Logisim project 74LS316.circ as structural Verilog: 1 circuit, main circuit 74LS316
module _74LS316 (
  input  D0,
  input  D1,
  input  D2,
  input  D3,
  input  A0,
  input  A1,
  input  A2,
  input  A3,
  input  A4,
  input  A5,
  input  nS1,
  input  nS2,
  input  nS3,
  input  R_W,
  output Q0,
  output Q1,
  output Q2,
  output Q3
);

  wire and_1_out, not_1_out;
  wire [3:0] controlled_buffer_2_out, ram_1_data;

  and and_1 (and_1_out, ~nS1, ~nS2, ~nS3);  // AND_Gate
  not not_1 (not_1_out, R_W);
  RAM #(.addrWidth(6), .dataWidth(4), .bus("asynch")) ram_1 (
    .addr({A5, A4, A3, A2, A1, A0}), .data(ram_1_data), .sel(and_1_out), .ld(R_W));  // open: clr
  assign ram_1_data = not_1_out ? {D3, D2, D1, D0} : 4'bz;  // Controlled_Buffer controlled_buffer_1
  assign controlled_buffer_2_out = R_W ? ram_1_data : 4'bz;  // Controlled_Buffer controlled_buffer_2
  assign {Q3, Q2, Q1, Q0} = controlled_buffer_2_out;  // Buffer buffer_1, 4 bits wide

  // Notes on the sheet:
  //   74LS316
  //   buffer_1 drives only 0 and floats otherwise
endmodule
