// Logisim project 74LS318.circ as structural Verilog: 1 circuit, main circuit 74LS318
module _74LS318 (
  input  D0,
  input  D1,
  input  D2,
  input  D3,
  input  D4,
  input  D5,
  input  D6,
  input  D7,
  input  A0,
  input  A1,
  input  A2,
  input  A3,
  input  A4,
  input  nS1,
  input  nS2,
  input  nS3,
  input  R_W,
  output Q0,
  output Q1,
  output Q2,
  output Q3,
  output Q4,
  output Q5,
  output Q6,
  output Q7
);

  wire and_1_out, not_1_out;
  wire [7:0] controlled_buffer_2_out, ram_1_data;

  and and_1 (and_1_out, ~nS1, ~nS2, ~nS3);  // AND_Gate
  RAM #(.addrWidth(5), .bus("asynch")) ram_1 (
    .addr({A4, A3, A2, A1, A0}), .data(ram_1_data), .sel(and_1_out), .ld(R_W));  // open: clr
  assign ram_1_data = not_1_out ? {D7, D6, D5, D4, D3, D2, D1, D0} : 8'bz;  // Controlled_Buffer controlled_buffer_1
  not not_1 (not_1_out, R_W);
  assign controlled_buffer_2_out = R_W ? ram_1_data : 8'bz;  // Controlled_Buffer controlled_buffer_2
  assign {Q7, Q6, Q5, Q4, Q3, Q2, Q1, Q0} = controlled_buffer_2_out;  // Buffer buffer_1, 8 bits wide

  // Notes on the sheet:
  //   74LS318
  //   buffer_1 drives only 0 and floats otherwise
endmodule
