// Logisim project 74LS322.circ as structural Verilog: 1 circuit, main circuit 74LS322
module _74LS322 (
  input  nG,
  input  S_P,
  input  nSE,
  input  D1,
  input  DS,
  input  D0,
  input  CLK,
  input  nCLR,
  input  nOE,
  input  A,
  input  B,
  input  C,
  input  D,
  input  E,
  input  F,
  input  G,
  input  H,
  output QH_prime,
  output QA,
  output QB,
  output QC,
  output QD,
  output QE,
  output QF,
  output QG,
  output QH
);

  wire and_1_out, and_2_out, and_3_out, and_4_out, and_5_out, and_6_out, and_7_out, and_8_out, and_9_out,
       and_10_out, and_11_out, and_12_out, and_13_out, and_14_out, and_15_out, and_16_out, and_17_out,
       and_18_out, and_19_out, and_20_out, and_21_out, and_22_out, and_23_out, and_24_out, and_25_out,
       and_26_out, and_27_out, nor_1_out, nor_2_out, not_1_out, not_2_out, not_3_out, or_1_out, or_2_out,
       or_3_out, or_4_out, or_5_out, or_6_out, or_7_out, or_8_out, Rise_2_q, Rise_2_qn, Rise_3_q, Rise_3_qn,
       Rise_4_q, Rise_4_qn, Rise_5_q, Rise_5_qn, Rise_6_q, Rise_6_qn, Rise_7_q, Rise_7_qn, Rise_8_qn, Rise_q,
       Rise_qn;

  nor nor_1 (nor_1_out, nG, S_P);
  not not_1 (not_1_out, DS);
  not not_2 (not_2_out, nCLR);
  nor nor_2 (nor_2_out, nG, nor_1_out);
  not not_3 (not_3_out, nSE);
  and and_1 (and_1_out, D1, nor_2_out, nSE, DS);
  and and_2 (and_2_out, not_1_out, nor_2_out, nSE, D0);
  and and_3 (and_3_out, nor_1_out, A);
  and and_4 (and_4_out, not_3_out, nor_2_out, Rise_q);
  or or_1 (or_1_out, and_2_out, and_1_out, and_3_out, and_4_out, and_6_out);
  and and_5 (and_5_out, ~nor_1_out, ~nOE);  // AND_Gate
  and and_6 (and_6_out, nG, Rise_q);
  D_Flip_Flop Rise (.clk(CLK), .D(or_1_out), .Q(Rise_q), .Qn(Rise_qn), .reset(not_2_out));  // open: preset, en
  assign QA = and_5_out ? ~Rise_qn : 1'bz;  // Controlled_Inverter controlled_inverter_1
  and and_7 (and_7_out, nor_1_out, B);
  and and_8 (and_8_out, Rise_q, nor_2_out);
  or or_2 (or_2_out, and_8_out, and_7_out, and_9_out);
  and and_9 (and_9_out, nG, Rise_2_q);
  and and_10 (and_10_out, Rise_2_q, nor_2_out);
  D_Flip_Flop Rise_2 (.clk(CLK), .D(or_2_out), .Q(Rise_2_q), .Qn(Rise_2_qn), .reset(not_2_out));  // open: preset, en
  assign QB = and_5_out ? ~Rise_2_qn : 1'bz;  // Controlled_Inverter controlled_inverter_2
  and and_11 (and_11_out, nG, Rise_3_q);
  and and_12 (and_12_out, nor_1_out, C);
  or or_3 (or_3_out, and_10_out, and_12_out, and_11_out);
  and and_13 (and_13_out, Rise_3_q, nor_2_out);
  D_Flip_Flop Rise_3 (.clk(CLK), .D(or_3_out), .Q(Rise_3_q), .Qn(Rise_3_qn), .reset(not_2_out));  // open: preset, en
  assign QC = and_5_out ? ~Rise_3_qn : 1'bz;  // Controlled_Inverter controlled_inverter_3
  and and_14 (and_14_out, nor_1_out, D);
  and and_15 (and_15_out, nG, Rise_4_q);
  or or_4 (or_4_out, and_13_out, and_14_out, and_15_out);
  and and_16 (and_16_out, Rise_4_q, nor_2_out);
  D_Flip_Flop Rise_4 (.clk(CLK), .D(or_4_out), .Q(Rise_4_q), .Qn(Rise_4_qn), .reset(not_2_out));  // open: preset, en
  assign QD = and_5_out ? ~Rise_4_qn : 1'bz;  // Controlled_Inverter controlled_inverter_4
  and and_17 (and_17_out, nor_1_out, E);
  and and_18 (and_18_out, nG, Rise_5_q);
  or or_5 (or_5_out, and_16_out, and_17_out, and_18_out);
  D_Flip_Flop Rise_5 (.clk(CLK), .D(or_5_out), .Q(Rise_5_q), .Qn(Rise_5_qn), .reset(not_2_out));  // open: preset, en
  and and_19 (and_19_out, Rise_5_q, nor_2_out);
  assign QE = and_5_out ? ~Rise_5_qn : 1'bz;  // Controlled_Inverter controlled_inverter_5
  and and_20 (and_20_out, nG, Rise_6_q);
  and and_21 (and_21_out, nor_1_out, F);
  or or_6 (or_6_out, and_19_out, and_21_out, and_20_out);
  D_Flip_Flop Rise_6 (.clk(CLK), .D(or_6_out), .Q(Rise_6_q), .Qn(Rise_6_qn), .reset(not_2_out));  // open: preset, en
  and and_22 (and_22_out, nor_1_out, G);
  and and_23 (and_23_out, Rise_6_q, nor_2_out);
  or or_7 (or_7_out, and_23_out, and_22_out, and_24_out);
  assign QF = and_5_out ? ~Rise_6_qn : 1'bz;  // Controlled_Inverter controlled_inverter_6
  and and_24 (and_24_out, nG, Rise_7_q);
  D_Flip_Flop Rise_7 (.clk(CLK), .D(or_7_out), .Q(Rise_7_q), .Qn(Rise_7_qn), .reset(not_2_out));  // open: preset, en
  assign QG = and_5_out ? ~Rise_7_qn : 1'bz;  // Controlled_Inverter controlled_inverter_7
  and and_25 (and_25_out, Rise_7_q, nor_2_out);
  and and_26 (and_26_out, nor_1_out, H);
  or or_8 (or_8_out, and_25_out, and_26_out, and_27_out);
  and and_27 (and_27_out, nG, QH_prime);
  D_Flip_Flop Rise_8 (.clk(CLK), .D(or_8_out), .Q(QH_prime), .Qn(Rise_8_qn), .reset(not_2_out));  // open: preset, en
  assign QH = and_5_out ? ~Rise_8_qn : 1'bz;  // Controlled_Inverter controlled_inverter_8

  // Notes on the sheet:
  //   74LS322
endmodule
