// Logisim project 74LS323.circ as structural Verilog: 2 circuits, main circuit 74LS323
module _74LS323 (
  input  S1,
  input  S0,
  input  nCLR,
  input  SR,
  input  CLK,
  input  SL,
  input  nG1,
  input  A,
  input  B,
  input  C,
  input  D,
  input  E,
  input  F,
  input  G,
  input  H,
  input  nG2,
  output QH_prime,
  output QA_prime,
  output QA,
  output QB,
  output QC,
  output QD,
  output QE,
  output QF,
  output QG,
  output QH
);

  wire and_1_out, Channel_A_sr_out, Channel_B_sl_out, Channel_B_sr_out, Channel_C_sl_out, Channel_C_sr_out,
       Channel_D_sl_out, Channel_D_sr_out, Channel_E_sl_out, Channel_E_sr_out, Channel_F_sl_out,
       Channel_F_sr_out, Channel_G_sl_out, Channel_G_sr_out, Channel_H_sl_out, nor_1_out, nor_2_out,
       nor_3_out, not_1_out, not_2_out, not_3_out;

  not not_1 (not_1_out, nCLR);
  not not_2 (not_2_out, S1);
  not not_3 (not_3_out, not_2_out);
  nor nor_1 (nor_1_out, ~S0, ~S1);  // NOR_Gate
  nor nor_2 (nor_2_out, not_1_out, S0);
  nor nor_3 (nor_3_out, not_1_out, nor_2_out);
  and and_1 (and_1_out, ~nor_1_out, ~nG1, ~nG2);  // AND_Gate
  channel Channel_A (
    .in_1(nor_3_out), .in_2(nor_2_out), .in_3(not_2_out), .in_4(not_3_out), .SR_in(SR), .CLK(CLK),
    .SL_out(QA_prime), .nG(and_1_out), .SL_in(Channel_B_sl_out), .QX(QA), .X(A), .SR_out(Channel_A_sr_out));
  channel Channel_B (
    .in_1(nor_3_out), .in_2(nor_2_out), .in_3(not_2_out), .in_4(not_3_out), .SR_in(Channel_A_sr_out),
    .CLK(CLK), .SL_out(Channel_B_sl_out), .nG(and_1_out), .SL_in(Channel_C_sl_out), .QX(QB), .X(B),
    .SR_out(Channel_B_sr_out));
  channel Channel_C (
    .in_1(nor_3_out), .in_2(nor_2_out), .in_3(not_2_out), .in_4(not_3_out), .SR_in(Channel_B_sr_out),
    .CLK(CLK), .SL_out(Channel_C_sl_out), .nG(and_1_out), .SL_in(Channel_D_sl_out), .QX(QC), .X(C),
    .SR_out(Channel_C_sr_out));
  channel Channel_D (
    .in_1(nor_3_out), .in_2(nor_2_out), .in_3(not_2_out), .in_4(not_3_out), .SR_in(Channel_C_sr_out),
    .CLK(CLK), .SL_out(Channel_D_sl_out), .nG(and_1_out), .SL_in(Channel_E_sl_out), .QX(QD), .X(D),
    .SR_out(Channel_D_sr_out));
  channel Channel_E (
    .in_1(nor_3_out), .in_2(nor_2_out), .in_3(not_2_out), .in_4(not_3_out), .SR_in(Channel_D_sr_out),
    .CLK(CLK), .SL_out(Channel_E_sl_out), .nG(and_1_out), .SL_in(Channel_F_sl_out), .QX(QE), .X(E),
    .SR_out(Channel_E_sr_out));
  channel Channel_F (
    .in_1(nor_3_out), .in_2(nor_2_out), .in_3(not_2_out), .in_4(not_3_out), .SR_in(Channel_E_sr_out),
    .CLK(CLK), .SL_out(Channel_F_sl_out), .nG(and_1_out), .SL_in(Channel_G_sl_out), .QX(QF), .X(F),
    .SR_out(Channel_F_sr_out));
  channel Channel_G (
    .in_1(nor_3_out), .in_2(nor_2_out), .in_3(not_2_out), .in_4(not_3_out), .SR_in(Channel_F_sr_out),
    .CLK(CLK), .SL_out(Channel_G_sl_out), .nG(and_1_out), .SL_in(Channel_H_sl_out), .QX(QG), .X(G),
    .SR_out(Channel_G_sr_out));
  channel Channel_H (
    .in_1(nor_3_out), .in_2(nor_2_out), .in_3(not_2_out), .in_4(not_3_out), .SR_in(Channel_G_sr_out),
    .CLK(CLK), .SL_out(Channel_H_sl_out), .nG(and_1_out), .SL_in(SL), .QX(QH), .X(H), .SR_out(QH_prime));

  // Notes on the sheet:
  //   74LS323
endmodule

module channel (
  input  in_1,
  input  in_2,
  input  in_3,
  input  in_4,
  input  SR_in,
  input  CLK,
  input  SL_in,
  input  nG,
  input  X,
  output SR_out,
  output SL_out,
  output QX
);

  wire and_1_out, and_2_out, and_3_out, and_4_out, or_1_out;

  and and_1 (and_1_out, SR_in, in_1, in_3);
  and and_2 (and_2_out, in_4, in_2, SL_in);
  and and_3 (and_3_out, in_4, in_1, X);
  or or_1 (or_1_out, and_1_out, and_2_out, and_3_out, and_4_out);
  and and_4 (and_4_out, in_3, in_2, SL_out);
  D_Flip_Flop d_ff_1 (.clk(CLK), .D(or_1_out), .Q(SL_out));  // open: Qn, preset, en, reset
  assign QX = nG ? SL_out : 1'bz;  // Controlled_Buffer controlled_buffer_1

  assign SR_out = SL_out;
endmodule
