// Logisim project 74LS337.circ as structural Verilog: 1 circuit, main circuit 74LS337
module _74LS337 (
  input  nG,
  input  CLK,
  input  nCLR,
  output Y1,
  output Y2,
  output Y3,
  output Y4,
  output Q1,
  output Q2,
  output Q3,
  output Q4
);

  wire not_1_out, not_2_out, t_ff_1_q, t_ff_2_q, t_ff_3_q, t_ff_4_q;

  not not_1 (not_1_out, nG);
  not not_2 (not_2_out, nCLR);
  T_Flip_Flop t_ff_1 (.clk(CLK), .T(1'b1), .Q(t_ff_1_q), .reset(not_2_out));  // open: Qn, preset, en
  T_Flip_Flop t_ff_2 (.clk(CLK), .T(1'b1), .Q(t_ff_2_q), .reset(not_2_out));  // open: Qn, preset, en
  T_Flip_Flop t_ff_3 (.clk(CLK), .T(1'b1), .Q(t_ff_3_q), .reset(not_2_out));  // open: Qn, preset, en
  T_Flip_Flop t_ff_4 (.clk(CLK), .T(1'b1), .Q(t_ff_4_q), .reset(not_2_out));  // open: Qn, preset, en
  assign Y1 = not_1_out ? CLK : 1'bz;  // Controlled_Buffer controlled_buffer_1
  assign Y2 = not_1_out ? CLK : 1'bz;  // Controlled_Buffer controlled_buffer_2
  assign Y3 = not_1_out ? CLK : 1'bz;  // Controlled_Buffer controlled_buffer_3
  assign Y4 = not_1_out ? CLK : 1'bz;  // Controlled_Buffer controlled_buffer_4
  assign Q1 = not_1_out ? t_ff_1_q : 1'bz;  // Controlled_Buffer controlled_buffer_5
  assign Q2 = not_1_out ? t_ff_2_q : 1'bz;  // Controlled_Buffer controlled_buffer_6
  assign Q3 = not_1_out ? t_ff_3_q : 1'bz;  // Controlled_Buffer controlled_buffer_7
  assign Q4 = not_1_out ? t_ff_4_q : 1'bz;  // Controlled_Buffer controlled_buffer_8

  // Notes on the sheet:
  //   74LS337
endmodule
