// Logisim project 74LS350.circ as structural Verilog: 1 circuit, main circuit 74LS350
module _74LS350 (
  input  D_3,
  input  D_2,
  input  D_1,
  input  D0,
  input  D1,
  input  D2,
  input  D3,
  input  S0,
  input  S1,
  input  nGE,
  output Y0,
  output Y1,
  output Y2,
  output Y3
);

  wire not_1_out;
  wire [2:0] controlled_buffer_1_out;
  wire [6:0] shifter_1_out;

  not not_1 (not_1_out, nGE);
  Shifter #(.width(7)) shifter_1 (.in({D3, D2, D1, D0, D_1, D_2, D_3}), .\dist ({1'b0, S1, S0}), .out(shifter_1_out));
  assign {Y3, Y2, Y1, Y0, controlled_buffer_1_out} = not_1_out ? shifter_1_out : 7'bz;  // Controlled_Buffer controlled_buffer_1

  // Notes on the sheet:
  //   74LS350
endmodule
