// Logisim project 74LS351.circ as structural Verilog: 1 circuit, main circuit 74LS351
module _74LS351 (
  input  nG,
  input  _1D0,
  input  _1D1,
  input  _1D2,
  input  _1D3,
  input  D4,
  input  D5,
  input  D6,
  input  D7,
  input  _2D0,
  input  _2D1,
  input  _2D2,
  input  _2D3,
  input  A,
  input  B,
  input  C,
  output _1_Y,
  output _2_Y
);

  wire multiplexer_1_out, multiplexer_2_out, not_1_out;

  not not_1 (not_1_out, nG);
  Multiplexer #(.select(3), .enable("false")) multiplexer_1 (
    .in0(_1D0), .in1(_1D1), .in2(_1D2), .in3(_1D3), .in4(D4), .in5(D5), .in6(D6), .in7(D7),
    .out(multiplexer_1_out), .sel({C, B, A}));
  Multiplexer #(.select(3), .enable("false")) multiplexer_2 (
    .in0(_2D0), .in1(_2D1), .in2(_2D2), .in3(_2D3), .in4(D4), .in5(D5), .in6(D6), .in7(D7),
    .out(multiplexer_2_out), .sel({C, B, A}));
  assign _1_Y = not_1_out ? ~multiplexer_1_out : 1'bz;  // Controlled_Inverter controlled_inverter_1
  assign _2_Y = not_1_out ? ~multiplexer_2_out : 1'bz;  // Controlled_Inverter controlled_inverter_2

  // Notes on the sheet:
  //   74LS351
endmodule
