// Logisim project 74LS352.circ as structural Verilog: 1 circuit, main circuit 74LS352
module _74LS352 (
  input  _1_G,
  input  _1C0,
  input  _1C1,
  input  _1C2,
  input  _1C3,
  input  _2_G,
  input  _2C0,
  input  _2C1,
  input  _2C2,
  input  _2C3,
  input  A,
  input  B,
  output _1_Y,
  output _2_Y
);

  wire multiplexer_1_out, multiplexer_2_out, not_1_out, not_2_out;

  not not_1 (not_1_out, _1_G);
  not not_2 (not_2_out, _2_G);
  Multiplexer #(.select(2), .enable("false")) multiplexer_1 (
    .in0(_1C0), .in1(_1C1), .in2(_1C2), .in3(_1C3), .out(multiplexer_1_out), .sel({B, A}));
  assign _1_Y = not_1_out ? ~multiplexer_1_out : 1'bz;  // Controlled_Inverter controlled_inverter_1
  Multiplexer #(.select(2), .enable("false")) multiplexer_2 (
    .in0(_2C0), .in1(_2C1), .in2(_2C2), .in3(_2C3), .out(multiplexer_2_out), .sel({B, A}));
  assign _2_Y = not_2_out ? ~multiplexer_2_out : 1'bz;  // Controlled_Inverter controlled_inverter_2
  Pull_Resistor #(.pull(1)) pull_resistor_1 (.node(_1_Y));
  Pull_Resistor #(.pull(1)) pull_resistor_2 (.node(_2_Y));

  // Notes on the sheet:
  //   74LS352
endmodule
