// Logisim project 74LS355.circ as structural Verilog: 1 circuit, main circuit 74LS355
module _74LS355 (
  input  nOE1,
  input  nOE2,
  input  OE3,
  input  nE,
  input  D0,
  input  D1,
  input  D2,
  input  nLE,
  input  S0,
  input  D3,
  input  S1,
  input  D4,
  input  S2,
  input  D5,
  input  D6,
  input  D7,
  output Y,
  output nY
);

  wire and_1_out, controlled_buffer_1_out, controlled_inverter_1_out, Low_2_q, Low_3_q, Low_4_q, Low_5_q,
       Low_6_q, Low_7_q, Low_8_q, Low_q, multiplexer_1_out;
  wire [2:0] Low_9_q;

  and and_1 (and_1_out, ~nOE1, ~nOE2, OE3);  // AND_Gate
  D_Flip_Flop #(.trigger("low")) Low (.clk(nE), .D(D0), .Q(Low_q));  // open: Qn, preset, en, reset
  D_Flip_Flop #(.trigger("low")) Low_2 (.clk(nE), .D(D1), .Q(Low_2_q));  // open: Qn, preset, en, reset
  D_Flip_Flop #(.trigger("low")) Low_3 (.clk(nE), .D(D2), .Q(Low_3_q));  // open: Qn, preset, en, reset
  D_Flip_Flop #(.trigger("low")) Low_4 (.clk(nE), .D(D3), .Q(Low_4_q));  // open: Qn, preset, en, reset
  D_Flip_Flop #(.trigger("low")) Low_5 (.clk(nE), .D(D4), .Q(Low_5_q));  // open: Qn, preset, en, reset
  D_Flip_Flop #(.trigger("low")) Low_6 (.clk(nE), .D(D5), .Q(Low_6_q));  // open: Qn, preset, en, reset
  D_Flip_Flop #(.trigger("low")) Low_7 (.clk(nE), .D(D6), .Q(Low_7_q));  // open: Qn, preset, en, reset
  D_Flip_Flop #(.trigger("low")) Low_8 (.clk(nE), .D(D7), .Q(Low_8_q));  // open: Qn, preset, en, reset
  D_Flip_Flop #(.trigger("low")) Low_9 (.clk(nLE), .D(S0), .Q(Low_9_q[0]));  // open: Qn, preset, en, reset
  D_Flip_Flop #(.trigger("low")) Low_10 (.clk(nLE), .D(S1), .Q(Low_9_q[1]));  // open: Qn, preset, en, reset
  D_Flip_Flop #(.trigger("low")) Low_11 (.clk(nLE), .D(S2), .Q(Low_9_q[2]));  // open: Qn, preset, en, reset
  Multiplexer #(.select(3), .enable("false")) multiplexer_1 (
    .in0(Low_q), .in1(Low_2_q), .in2(Low_3_q), .in3(Low_4_q), .in4(Low_5_q), .in5(Low_6_q), .in6(Low_7_q),
    .in7(Low_8_q), .out(multiplexer_1_out), .sel(Low_9_q));
  assign controlled_buffer_1_out = and_1_out ? multiplexer_1_out : 1'bz;  // Controlled_Buffer controlled_buffer_1
  buf buffer_1 (Y, controlled_buffer_1_out);
  assign controlled_inverter_1_out = and_1_out ? ~multiplexer_1_out : 1'bz;  // Controlled_Inverter controlled_inverter_1
  buf buffer_2 (nY, controlled_inverter_1_out);

  // Notes on the sheet:
  //   74LS355
  //   open collector
  //   buffer_1 drives only 0 and floats otherwise
  //   buffer_2 drives only 0 and floats otherwise
endmodule
