// Logisim project 74LS357.circ as structural Verilog: 1 circuit, main circuit 74LS357
module _74LS357 (
  input  nOE1,
  input  nOE2,
  input  OE3,
  input  CLK,
  input  D0,
  input  D1,
  input  D2,
  input  nLE,
  input  S0,
  input  D3,
  input  S1,
  input  D4,
  input  S2,
  input  D5,
  input  D6,
  input  D7,
  output Y,
  output nY
);

  wire and_1_out, controlled_buffer_1_out, controlled_inverter_1_out, multiplexer_1_out, Rise_2_q, Rise_3_q,
       Rise_4_q, Rise_5_q, Rise_6_q, Rise_7_q, Rise_8_q, Rise_q;
  wire [2:0] Low_q;

  and and_1 (and_1_out, ~nOE1, ~nOE2, OE3);  // AND_Gate
  D_Flip_Flop Rise (.clk(CLK), .D(D0), .Q(Rise_q));  // open: Qn, preset, en, reset
  D_Flip_Flop Rise_2 (.clk(CLK), .D(D1), .Q(Rise_2_q));  // open: Qn, preset, en, reset
  D_Flip_Flop Rise_3 (.clk(CLK), .D(D2), .Q(Rise_3_q));  // open: Qn, preset, en, reset
  D_Flip_Flop Rise_4 (.clk(CLK), .D(D3), .Q(Rise_4_q));  // open: Qn, preset, en, reset
  D_Flip_Flop Rise_5 (.clk(CLK), .D(D4), .Q(Rise_5_q));  // open: Qn, preset, en, reset
  D_Flip_Flop Rise_6 (.clk(CLK), .D(D5), .Q(Rise_6_q));  // open: Qn, preset, en, reset
  D_Flip_Flop Rise_7 (.clk(CLK), .D(D6), .Q(Rise_7_q));  // open: Qn, preset, en, reset
  D_Flip_Flop Rise_8 (.clk(CLK), .D(D7), .Q(Rise_8_q));  // open: Qn, preset, en, reset
  D_Flip_Flop #(.trigger("low")) Low (.clk(nLE), .D(S0), .Q(Low_q[0]));  // open: Qn, preset, en, reset
  D_Flip_Flop #(.trigger("low")) Low_2 (.clk(nLE), .D(S1), .Q(Low_q[1]));  // open: Qn, preset, en, reset
  D_Flip_Flop #(.trigger("low")) Low_3 (.clk(nLE), .D(S2), .Q(Low_q[2]));  // open: Qn, preset, en, reset
  Multiplexer #(.select(3), .enable("false")) multiplexer_1 (
    .in0(Rise_q), .in1(Rise_2_q), .in2(Rise_3_q), .in3(Rise_4_q), .in4(Rise_5_q), .in5(Rise_6_q),
    .in6(Rise_7_q), .in7(Rise_8_q), .out(multiplexer_1_out), .sel(Low_q));
  assign controlled_buffer_1_out = and_1_out ? multiplexer_1_out : 1'bz;  // Controlled_Buffer controlled_buffer_1
  buf buffer_1 (Y, controlled_buffer_1_out);
  buf buffer_2 (nY, controlled_inverter_1_out);
  assign controlled_inverter_1_out = and_1_out ? ~multiplexer_1_out : 1'bz;  // Controlled_Inverter controlled_inverter_1

  // Notes on the sheet:
  //   74LS357
  //   open collector
  //   buffer_1 drives only 0 and floats otherwise
  //   buffer_2 drives only 0 and floats otherwise
endmodule
