// Logisim project 74LS362.circ as structural Verilog: 1 circuit, main circuit 74LS362
module _74LS362 (
  input  OSC,
  input  OSCIN,
  input  FFD,
  output OSCOUT,
  output \ϕ1 ,
  output \ϕ2 ,
  output \ϕ3 ,
  output \ϕ4 ,
  output \nϕ1 ,
  output \nϕ2 ,
  output \nϕ3 ,
  output \nϕ4 ,
  output FFQ
);

  wire Fall_2_q, Fall_2_qn, Fall_3_q, Fall_3_qn, Fall_4_q, Fall_4_qn, Fall_q, nand_1_out, not_1_out;

  D_Flip_Flop #(.trigger("falling")) Fall (
    .clk(OSC), .D(Fall_2_qn), .Q(Fall_q), .preset(not_1_out));  // open: Qn, en, reset
  not not_1 (not_1_out, OSCIN);
  D_Flip_Flop #(.trigger("falling")) Fall_2 (
    .clk(OSC), .D(Fall_q), .Q(Fall_2_q), .Qn(Fall_2_qn), .preset(not_1_out));  // open: en, reset
  D_Flip_Flop #(.trigger("falling")) Fall_3 (
    .clk(nand_1_out), .D(Fall_4_qn), .Q(Fall_3_q), .Qn(Fall_3_qn));  // open: preset, en, reset
  D_Flip_Flop #(.trigger("falling")) Fall_4 (
    .clk(nand_1_out), .D(Fall_3_q), .Q(Fall_4_q), .Qn(Fall_4_qn));  // open: preset, en, reset
  D_Flip_Flop Rise (.clk(\nϕ3 ), .D(FFD), .Q(FFQ));  // open: Qn, preset, en, reset
  nand nand_1 (nand_1_out, Fall_2_q, Fall_q, OSCIN);
  nand nand_2 (\nϕ1 , nand_1_out, Fall_4_qn, Fall_3_qn);
  nand nand_3 (\nϕ2 , nand_1_out, Fall_3_q, Fall_4_qn);
  nand nand_4 (\nϕ3 , nand_1_out, Fall_3_q, Fall_4_q);
  nand nand_5 (\nϕ4 , nand_1_out, Fall_3_qn, Fall_4_q);
  not not_2 (OSCOUT, nand_1_out);
  not not_3 (\ϕ1 , \nϕ1 );
  not not_4 (\ϕ2 , \nϕ2 );
  not not_5 (\ϕ3 , \nϕ3 );
  not not_6 (\ϕ4 , \nϕ4 );

  // Notes on the sheet:
  //   74LS362
endmodule
