// Logisim project 74LS363.circ as structural Verilog: 1 circuit, main circuit 74LS363
module _74LS363 (
  input  nOE,
  input  G,
  input  _1D,
  input  _2D,
  input  _3D,
  input  _4D,
  input  _5D,
  input  _6D,
  input  _7D,
  input  _8D,
  output out_11,
  output out_12,
  output out_13,
  output out_14,
  output out_15,
  output out_16,
  output out_17,
  output out_18
);

  wire High_2_q, High_3_q, High_4_q, High_5_q, High_6_q, High_7_q, High_8_q, High_q, not_1_out;

  not not_1 (not_1_out, nOE);
  assign out_11 = not_1_out ? High_q : 1'bz;  // Controlled_Buffer controlled_buffer_1
  D_Flip_Flop #(.trigger("high")) High (.clk(G), .D(_1D), .Q(High_q));  // open: Qn, preset, en, reset
  D_Flip_Flop #(.trigger("high")) High_2 (.clk(G), .D(_2D), .Q(High_2_q));  // open: Qn, preset, en, reset
  assign out_12 = not_1_out ? High_2_q : 1'bz;  // Controlled_Buffer controlled_buffer_2
  assign out_13 = not_1_out ? High_3_q : 1'bz;  // Controlled_Buffer controlled_buffer_3
  D_Flip_Flop #(.trigger("high")) High_3 (.clk(G), .D(_3D), .Q(High_3_q));  // open: Qn, preset, en, reset
  assign out_14 = not_1_out ? High_4_q : 1'bz;  // Controlled_Buffer controlled_buffer_4
  D_Flip_Flop #(.trigger("high")) High_4 (.clk(G), .D(_4D), .Q(High_4_q));  // open: Qn, preset, en, reset
  D_Flip_Flop #(.trigger("high")) High_5 (.clk(G), .D(_5D), .Q(High_5_q));  // open: Qn, preset, en, reset
  assign out_15 = not_1_out ? High_5_q : 1'bz;  // Controlled_Buffer controlled_buffer_5
  assign out_16 = not_1_out ? High_6_q : 1'bz;  // Controlled_Buffer controlled_buffer_6
  D_Flip_Flop #(.trigger("high")) High_6 (.clk(G), .D(_6D), .Q(High_6_q));  // open: Qn, preset, en, reset
  assign out_17 = not_1_out ? High_7_q : 1'bz;  // Controlled_Buffer controlled_buffer_7
  D_Flip_Flop #(.trigger("high")) High_7 (.clk(G), .D(_7D), .Q(High_7_q));  // open: Qn, preset, en, reset
  assign out_18 = not_1_out ? High_8_q : 1'bz;  // Controlled_Buffer controlled_buffer_8
  D_Flip_Flop #(.trigger("high")) High_8 (.clk(G), .D(_8D), .Q(High_8_q));  // open: Qn, preset, en, reset

  // Notes on the sheet:
  //   74LS363
endmodule
