// Logisim project 74LS364.circ as structural Verilog: 1 circuit, main circuit 74LS364
module _74LS364 (
  input  nOE,
  input  G,
  input  _1D,
  input  _2D,
  input  _3D,
  input  _4D,
  input  _5D,
  input  _6D,
  input  _7D,
  input  _8D,
  output out_11,
  output out_12,
  output out_13,
  output out_14,
  output out_15,
  output out_16,
  output out_17,
  output out_18
);

  wire not_1_out, Rise_2_q, Rise_3_q, Rise_4_q, Rise_5_q, Rise_6_q, Rise_7_q, Rise_8_q, Rise_q;

  not not_1 (not_1_out, nOE);
  assign out_11 = not_1_out ? Rise_q : 1'bz;  // Controlled_Buffer controlled_buffer_1
  D_Flip_Flop Rise (.clk(G), .D(_1D), .Q(Rise_q));  // open: Qn, preset, en, reset
  assign out_12 = not_1_out ? Rise_2_q : 1'bz;  // Controlled_Buffer controlled_buffer_2
  D_Flip_Flop Rise_2 (.clk(G), .D(_2D), .Q(Rise_2_q));  // open: Qn, preset, en, reset
  D_Flip_Flop Rise_3 (.clk(G), .D(_3D), .Q(Rise_3_q));  // open: Qn, preset, en, reset
  assign out_13 = not_1_out ? Rise_3_q : 1'bz;  // Controlled_Buffer controlled_buffer_3
  assign out_14 = not_1_out ? Rise_4_q : 1'bz;  // Controlled_Buffer controlled_buffer_4
  D_Flip_Flop Rise_4 (.clk(G), .D(_4D), .Q(Rise_4_q));  // open: Qn, preset, en, reset
  D_Flip_Flop Rise_5 (.clk(G), .D(_5D), .Q(Rise_5_q));  // open: Qn, preset, en, reset
  assign out_15 = not_1_out ? Rise_5_q : 1'bz;  // Controlled_Buffer controlled_buffer_5
  D_Flip_Flop Rise_6 (.clk(G), .D(_6D), .Q(Rise_6_q));  // open: Qn, preset, en, reset
  assign out_16 = not_1_out ? Rise_6_q : 1'bz;  // Controlled_Buffer controlled_buffer_6
  D_Flip_Flop Rise_7 (.clk(G), .D(_7D), .Q(Rise_7_q));  // open: Qn, preset, en, reset
  assign out_17 = not_1_out ? Rise_7_q : 1'bz;  // Controlled_Buffer controlled_buffer_7
  assign out_18 = not_1_out ? Rise_8_q : 1'bz;  // Controlled_Buffer controlled_buffer_8
  D_Flip_Flop Rise_8 (.clk(G), .D(_8D), .Q(Rise_8_q));  // open: Qn, preset, en, reset

  // Notes on the sheet:
  //   74LS364
endmodule
