// Logisim project 74LS365.circ as structural Verilog: 1 circuit, main circuit 74LS365
module _74LS365 (
  input  nG1,
  input  nG2,
  input  A1,
  input  A2,
  input  A3,
  input  A4,
  input  A5,
  input  A6,
  input  A7,
  input  A8,
  output Y1,
  output Y2,
  output Y3,
  output Y4,
  output Y5,
  output Y6,
  output Y7,
  output Y8
);

  wire and_1_out;

  and and_1 (and_1_out, ~nG1, ~nG2);  // AND_Gate
  assign Y1 = and_1_out ? A1 : 1'bz;  // Controlled_Buffer controlled_buffer_1
  assign Y2 = and_1_out ? A2 : 1'bz;  // Controlled_Buffer controlled_buffer_2
  assign Y3 = and_1_out ? A3 : 1'bz;  // Controlled_Buffer controlled_buffer_3
  assign Y4 = and_1_out ? A4 : 1'bz;  // Controlled_Buffer controlled_buffer_4
  assign Y5 = and_1_out ? A5 : 1'bz;  // Controlled_Buffer controlled_buffer_5
  assign Y6 = and_1_out ? A6 : 1'bz;  // Controlled_Buffer controlled_buffer_6
  assign Y7 = and_1_out ? A7 : 1'bz;  // Controlled_Buffer controlled_buffer_7
  assign Y8 = and_1_out ? A8 : 1'bz;  // Controlled_Buffer controlled_buffer_8

  // Notes on the sheet:
  //   74LS365
endmodule
