// Logisim project 74LS367.circ as structural Verilog: 1 circuit, main circuit 74LS367
module _74LS367 (
  input  nG1,
  input  _1A1,
  input  _1A2,
  input  _1A3,
  input  _1A4,
  input  nG2,
  input  _2A1,
  input  _2A2,
  output _1Y1,
  output _1Y2,
  output _1Y3,
  output _1Y4,
  output _2Y1,
  output _2Y2
);

  wire not_1_out, not_2_out;

  not not_1 (not_1_out, nG1);
  assign _1Y1 = not_1_out ? _1A1 : 1'bz;  // Controlled_Buffer controlled_buffer_1
  assign _1Y2 = not_1_out ? _1A2 : 1'bz;  // Controlled_Buffer controlled_buffer_2
  assign _1Y3 = not_1_out ? _1A3 : 1'bz;  // Controlled_Buffer controlled_buffer_3
  assign _1Y4 = not_1_out ? _1A4 : 1'bz;  // Controlled_Buffer controlled_buffer_4
  not not_2 (not_2_out, nG2);
  assign _2Y1 = not_2_out ? _2A1 : 1'bz;  // Controlled_Buffer controlled_buffer_5
  assign _2Y2 = not_2_out ? _2A2 : 1'bz;  // Controlled_Buffer controlled_buffer_6

  // Notes on the sheet:
  //   74LS367
endmodule
