// Logisim project 74LS368.circ as structural Verilog: 1 circuit, main circuit 74LS368
module _74LS368 (
  input  nG1,
  input  _1A1,
  input  _1A2,
  input  _1A3,
  input  _1A4,
  input  nG2,
  input  _2A1,
  input  _2A2,
  output _1_Y1,
  output _1_Y2,
  output _1_Y3,
  output _1_Y4,
  output _2_Y1,
  output _2_Y2
);

  wire not_1_out, not_2_out;

  not not_1 (not_1_out, nG1);
  assign _1_Y1 = not_1_out ? ~_1A1 : 1'bz;  // Controlled_Inverter controlled_inverter_1
  assign _1_Y2 = not_1_out ? ~_1A2 : 1'bz;  // Controlled_Inverter controlled_inverter_2
  assign _1_Y3 = not_1_out ? ~_1A3 : 1'bz;  // Controlled_Inverter controlled_inverter_3
  assign _1_Y4 = not_1_out ? ~_1A4 : 1'bz;  // Controlled_Inverter controlled_inverter_4
  not not_2 (not_2_out, nG2);
  assign _2_Y1 = not_2_out ? ~_2A1 : 1'bz;  // Controlled_Inverter controlled_inverter_5
  assign _2_Y2 = not_2_out ? ~_2A2 : 1'bz;  // Controlled_Inverter controlled_inverter_6

  // Notes on the sheet:
  //   74LS368
endmodule
