// Logisim project 74LS373.circ as structural Verilog: 1 circuit, main circuit 74LS373
module _74LS373 (
  input  nOE,
  input  C,
  input  _1D,
  input  _2D,
  input  _3D,
  input  _4D,
  input  _5D,
  input  _6D,
  input  _7D,
  input  _8D,
  output _1Q,
  output _2Q,
  output _3Q,
  output _4Q,
  output _5Q,
  output _6Q,
  output _7Q,
  output _8Q
);

  wire High_2_q, High_3_q, High_4_q, High_5_q, High_6_q, High_7_q, High_8_q, High_q, not_1_out;

  not not_1 (not_1_out, nOE);
  D_Flip_Flop #(.trigger("high")) High (.clk(C), .D(_1D), .Q(High_q));  // open: Qn, preset, en, reset
  D_Flip_Flop #(.trigger("high")) High_2 (.clk(C), .D(_2D), .Q(High_2_q));  // open: Qn, preset, en, reset
  D_Flip_Flop #(.trigger("high")) High_3 (.clk(C), .D(_3D), .Q(High_3_q));  // open: Qn, preset, en, reset
  D_Flip_Flop #(.trigger("high")) High_4 (.clk(C), .D(_4D), .Q(High_4_q));  // open: Qn, preset, en, reset
  D_Flip_Flop #(.trigger("high")) High_5 (.clk(C), .D(_5D), .Q(High_5_q));  // open: Qn, preset, en, reset
  D_Flip_Flop #(.trigger("high")) High_6 (.clk(C), .D(_6D), .Q(High_6_q));  // open: Qn, preset, en, reset
  D_Flip_Flop #(.trigger("high")) High_7 (.clk(C), .D(_7D), .Q(High_7_q));  // open: Qn, preset, en, reset
  D_Flip_Flop #(.trigger("high")) High_8 (.clk(C), .D(_8D), .Q(High_8_q));  // open: Qn, preset, en, reset
  assign _1Q = not_1_out ? High_q : 1'bz;  // Controlled_Buffer controlled_buffer_1
  assign _2Q = not_1_out ? High_2_q : 1'bz;  // Controlled_Buffer controlled_buffer_2
  assign _3Q = not_1_out ? High_3_q : 1'bz;  // Controlled_Buffer controlled_buffer_3
  assign _4Q = not_1_out ? High_4_q : 1'bz;  // Controlled_Buffer controlled_buffer_4
  assign _5Q = not_1_out ? High_5_q : 1'bz;  // Controlled_Buffer controlled_buffer_5
  assign _6Q = not_1_out ? High_6_q : 1'bz;  // Controlled_Buffer controlled_buffer_6
  assign _7Q = not_1_out ? High_7_q : 1'bz;  // Controlled_Buffer controlled_buffer_7
  assign _8Q = not_1_out ? High_8_q : 1'bz;  // Controlled_Buffer controlled_buffer_8

  // Notes on the sheet:
  //   74LS373
endmodule
