// Logisim project 74LS374.circ as structural Verilog: 1 circuit, main circuit 74LS374
module _74LS374 (
  input  nOE,
  input  C,
  input  _1D,
  input  _2D,
  input  _3D,
  input  _4D,
  input  _5D,
  input  _6D,
  input  _7D,
  input  _8D,
  output _1Q,
  output _2Q,
  output _3Q,
  output _4Q,
  output _5Q,
  output _6Q,
  output _7Q,
  output _8Q
);

  wire not_1_out, Rise_2_q, Rise_3_q, Rise_4_q, Rise_5_q, Rise_6_q, Rise_7_q, Rise_8_q, Rise_q;

  not not_1 (not_1_out, nOE);
  D_Flip_Flop Rise (.clk(C), .D(_1D), .Q(Rise_q));  // open: Qn, preset, en, reset
  D_Flip_Flop Rise_2 (.clk(C), .D(_2D), .Q(Rise_2_q));  // open: Qn, preset, en, reset
  D_Flip_Flop Rise_3 (.clk(C), .D(_3D), .Q(Rise_3_q));  // open: Qn, preset, en, reset
  D_Flip_Flop Rise_4 (.clk(C), .D(_4D), .Q(Rise_4_q));  // open: Qn, preset, en, reset
  D_Flip_Flop Rise_5 (.clk(C), .D(_5D), .Q(Rise_5_q));  // open: Qn, preset, en, reset
  D_Flip_Flop Rise_6 (.clk(C), .D(_6D), .Q(Rise_6_q));  // open: Qn, preset, en, reset
  D_Flip_Flop Rise_7 (.clk(C), .D(_7D), .Q(Rise_7_q));  // open: Qn, preset, en, reset
  D_Flip_Flop Rise_8 (.clk(C), .D(_8D), .Q(Rise_8_q));  // open: Qn, preset, en, reset
  assign _1Q = not_1_out ? Rise_q : 1'bz;  // Controlled_Buffer controlled_buffer_1
  assign _2Q = not_1_out ? Rise_2_q : 1'bz;  // Controlled_Buffer controlled_buffer_2
  assign _3Q = not_1_out ? Rise_3_q : 1'bz;  // Controlled_Buffer controlled_buffer_3
  assign _4Q = not_1_out ? Rise_4_q : 1'bz;  // Controlled_Buffer controlled_buffer_4
  assign _5Q = not_1_out ? Rise_5_q : 1'bz;  // Controlled_Buffer controlled_buffer_5
  assign _6Q = not_1_out ? Rise_6_q : 1'bz;  // Controlled_Buffer controlled_buffer_6
  assign _7Q = not_1_out ? Rise_7_q : 1'bz;  // Controlled_Buffer controlled_buffer_7
  assign _8Q = not_1_out ? Rise_8_q : 1'bz;  // Controlled_Buffer controlled_buffer_8

  // Notes on the sheet:
  //   74LS374
endmodule
