// Logisim project 74LS375.circ as structural Verilog: 1 circuit, main circuit 74LS375
module _74LS375 (
  input  _1C_2C,
  input  _1D,
  input  _2D,
  input  _3C_4C,
  input  _3D,
  input  _4D,
  output _1Q,
  output _1_Q,
  output _2Q,
  output _2_Q,
  output _3Q,
  output _3_Q,
  output _4Q,
  output _4_Q
);

  D_Flip_Flop #(.trigger("high")) High (.clk(_1C_2C), .D(_1D), .Q(_1Q), .Qn(_1_Q));  // open: preset, en, reset
  D_Flip_Flop #(.trigger("high")) High_2 (.clk(_1C_2C), .D(_2D), .Q(_2Q), .Qn(_2_Q));  // open: preset, en, reset
  D_Flip_Flop #(.trigger("high")) High_3 (.clk(_3C_4C), .D(_3D), .Q(_3Q), .Qn(_3_Q));  // open: preset, en, reset
  D_Flip_Flop #(.trigger("high")) High_4 (.clk(_3C_4C), .D(_4D), .Q(_4Q), .Qn(_4_Q));  // open: preset, en, reset

  // Notes on the sheet:
  //   74LS375
endmodule
