// Logisim project 74LS376.circ as structural Verilog: 1 circuit, main circuit 74LS376
module _74LS376 (
  input  nCLR,
  input  CLK,
  input  _1J,
  input  _1_K,
  input  _2J,
  input  _2_K,
  input  _1J_2,
  input  _1_K_2,
  input  _1J_3,
  input  _1_K_3,
  output _1Q,
  output _2Q,
  output _3Q,
  output _4Q
);

  wire not_1_out, not_2_out, not_3_out, not_4_out, not_5_out;

  not not_1 (not_1_out, nCLR);
  not not_2 (not_2_out, _1_K);
  not not_3 (not_3_out, _2_K);
  not not_4 (not_4_out, _1_K_2);
  not not_5 (not_5_out, _1_K_3);
  J_K_Flip_Flop Rise (.J(_1J), .clk(CLK), .K(not_2_out), .Q(_1Q), .reset(not_1_out));  // open: Qn, preset, en
  J_K_Flip_Flop Rise_2 (.J(_2J), .clk(CLK), .K(not_3_out), .Q(_2Q), .reset(not_1_out));  // open: Qn, preset, en
  J_K_Flip_Flop Rise_3 (.J(_1J_2), .clk(CLK), .K(not_4_out), .Q(_3Q), .reset(not_1_out));  // open: Qn, preset, en
  J_K_Flip_Flop Rise_4 (.J(_1J_3), .clk(CLK), .K(not_5_out), .Q(_4Q), .reset(not_1_out));  // open: Qn, preset, en

  // Notes on the sheet:
  //   74LS376
endmodule
