// Logisim project 74LS377.circ as structural Verilog: 1 circuit, main circuit 74LS377
module _74LS377 (
  input  CLK,
  input  _1D,
  input  _2D,
  input  _3D,
  input  _4D,
  input  _5D,
  input  _6D,
  input  _7D,
  input  _8D,
  input  nG,
  output _1Q,
  output _2Q,
  output _3Q,
  output _4Q,
  output _5Q,
  output _6Q,
  output _7Q,
  output _8Q
);

  wire not_1_out;

  not not_1 (not_1_out, nG);
  D_Flip_Flop Rise (.clk(CLK), .D(_1D), .Q(_1Q), .en(not_1_out));  // open: Qn, preset, reset
  D_Flip_Flop Rise_2 (.clk(CLK), .D(_5D), .Q(_5Q), .en(not_1_out));  // open: Qn, preset, reset
  D_Flip_Flop Rise_3 (.clk(CLK), .D(_2D), .Q(_2Q), .en(not_1_out));  // open: Qn, preset, reset
  D_Flip_Flop Rise_4 (.clk(CLK), .D(_6D), .Q(_6Q), .en(not_1_out));  // open: Qn, preset, reset
  D_Flip_Flop Rise_5 (.clk(CLK), .D(_3D), .Q(_3Q), .en(not_1_out));  // open: Qn, preset, reset
  D_Flip_Flop Rise_6 (.clk(CLK), .D(_7D), .Q(_7Q), .en(not_1_out));  // open: Qn, preset, reset
  D_Flip_Flop Rise_7 (.clk(CLK), .D(_4D), .Q(_4Q), .en(not_1_out));  // open: Qn, preset, reset
  D_Flip_Flop Rise_8 (.clk(CLK), .D(_8D), .Q(_8Q), .en(not_1_out));  // open: Qn, preset, reset

  // Notes on the sheet:
  //   74LS377
endmodule
