// Logisim project 74LS380.circ as structural Verilog: 2 circuits, main circuit 74LS380
module _74LS380 (
  input  CK,
  input  nCLR,
  input  nPR,
  input  POL,
  input  nLD,
  input  D0,
  input  D1,
  input  D2,
  input  D3,
  input  D4,
  input  D5,
  input  D6,
  input  D7,
  input  nOE,
  output Q0,
  output Q1,
  output Q2,
  output Q3,
  output Q4,
  output Q5,
  output Q6,
  output Q7
);

  wire not_1_out;
  wire [7:0] and_1_out, and_2_out, and_3_out, and_4_out, n1_to_8_1_out_2, n1_to_8_2_out_2, n1_to_8_3_out_2,
       n1_to_8_4_out_2, not_2_out, not_3_out, not_4_out, not_5_out, or_1_out, register_1_q;

  _1_to_8 u_1_to_8_1 (.in_1(nCLR), .out_2(n1_to_8_1_out_2));
  _1_to_8 u_1_to_8_2 (.in_1(nPR), .out_2(n1_to_8_2_out_2));
  _1_to_8 u_1_to_8_3 (.in_1(POL), .out_2(n1_to_8_3_out_2));
  _1_to_8 u_1_to_8_4 (.in_1(nLD), .out_2(n1_to_8_4_out_2));
  not not_1 (not_1_out, nOE);
  assign not_2_out = ~n1_to_8_2_out_2;  // NOT_Gate not_2, 8 bits wide
  assign not_3_out = ~n1_to_8_3_out_2;  // NOT_Gate not_3, 8 bits wide
  assign not_4_out = ~n1_to_8_4_out_2;  // NOT_Gate not_4, 8 bits wide
  assign not_5_out = ~{D7, D6, D5, D4, D3, D2, D1, D0};  // NOT_Gate not_5, 8 bits wide
  assign and_1_out = n1_to_8_1_out_2 & not_2_out;  // AND_Gate and_1, 8 bits wide
  assign and_2_out = n1_to_8_1_out_2 & register_1_q & n1_to_8_4_out_2;  // AND_Gate and_2, 8 bits wide
  assign and_3_out = {D7, D6, D5, D4, D3, D2, D1, D0} & n1_to_8_1_out_2 & not_4_out & n1_to_8_3_out_2;  // AND_Gate and_3, 8 bits wide
  assign and_4_out = not_5_out & n1_to_8_1_out_2 & not_4_out & not_3_out;  // AND_Gate and_4, 8 bits wide
  assign or_1_out = and_1_out | and_2_out | and_3_out | and_4_out;  // OR_Gate or_1, 8 bits wide
  Register register_1 (.D(or_1_out), .Q(register_1_q), .clk(CK));  // open: en, clr
  assign {Q7, Q6, Q5, Q4, Q3, Q2, Q1, Q0} = not_1_out ? register_1_q : 8'bz;  // Controlled_Buffer controlled_buffer_1

  // Notes on the sheet:
  //   74LS380
  //   * MMI and NS datasheet have a bug in the D0 circuit
  //   ** Both have a second bug that inverts the function of /LD
  //   Both bugs are fixed here!
endmodule

module _1_to_8 (
  input  in_1,
  output [7:0] out_2
);


  assign out_2 = {8{in_1}};
endmodule
