// Logisim project 74LS382.circ as structural Verilog: 2 circuits, main circuit 74LS382
module _74LS382 (
  input  S0,
  input  S1,
  input  S2,
  input  Cn,
  input  A0,
  input  B0,
  input  A1,
  input  B1,
  input  A2,
  input  B2,
  input  A3,
  input  B3,
  output F0,
  output F1,
  output F2,
  output F3,
  output OVR,
  output Cn_4
);

  wire and_1_out, and_2_out, and_3_out, and_4_out, and_5_out, and_6_out, and_7_out, and_8_out, and_9_out,
       and_10_out, and_11_out, and_12_out, and_13_out, and_14_out, and_15_out, and_16_out, and_17_out,
       and_18_out, and_19_out, and_20_out, and_21_out, and_22_out, and_23_out, and_24_out, and_25_out,
       and_26_out, buffer_1_out, buffer_2_out, det_1_1_bottom, det_1_1_top, det_1_2_bottom, det_1_2_top,
       det_1_3_bottom, det_1_3_top, det_1_4_bottom, det_1_4_top, nand_1_out, nand_2_out, nand_3_out,
       nand_4_out, nand_5_out, nor_1_out, nor_2_out, nor_3_out, nor_4_out, nor_5_out, nor_6_out, nor_7_out,
       nor_8_out, not_1_out, not_2_out, not_3_out, or_1_out;

  not not_1 (not_1_out, S0);
  not not_2 (not_2_out, S1);
  not not_3 (not_3_out, S2);
  and and_1 (and_1_out, not_3_out, not_2_out, S0);
  and and_2 (and_2_out, not_3_out, S1, not_1_out);
  nor nor_1 (nor_1_out, and_1_out, and_2_out, and_4_out);
  det_1 det_1_1 (
    .A(A0), .B(B0), .top(det_1_1_top), .bottom(det_1_1_bottom), ._1(nor_1_out), ._2(nor_2_out),
    ._3(nor_3_out), ._4(nand_3_out), ._5(nand_4_out), ._6(nand_5_out));
  det_1 det_1_2 (
    .A(A1), .B(B1), .top(det_1_2_top), .bottom(det_1_2_bottom), ._1(nor_1_out), ._2(nor_2_out),
    ._3(nor_3_out), ._4(nand_3_out), ._5(nand_4_out), ._6(nand_5_out));
  det_1 det_1_3 (
    .A(A2), .B(B2), .top(det_1_3_top), .bottom(det_1_3_bottom), ._1(nor_1_out), ._2(nor_2_out),
    ._3(nor_3_out), ._4(nand_3_out), ._5(nand_4_out), ._6(nand_5_out));
  det_1 det_1_4 (
    .A(A3), .B(B3), .top(det_1_4_top), .bottom(det_1_4_bottom), ._1(nor_1_out), ._2(nor_2_out),
    ._3(nor_3_out), ._4(nand_3_out), ._5(nand_4_out), ._6(nand_5_out));
  and and_3 (and_3_out, not_2_out, S0);
  and and_4 (and_4_out, S2, S1, S0);
  and and_5 (and_5_out, S1, not_1_out);
  and and_6 (and_6_out, S1, S0);
  and and_7 (and_7_out, S2, S0);
  nor nor_2 (nor_2_out, and_3_out, and_7_out, and_5_out);
  nand nand_1 (nand_1_out, or_1_out, Cn);
  and and_8 (and_8_out, or_1_out, Cn, det_1_1_top);
  and and_9 (and_9_out, or_1_out, det_1_1_bottom);
  and and_10 (and_10_out, or_1_out, Cn, det_1_1_top, det_1_2_top);
  and and_11 (and_11_out, or_1_out, det_1_2_top, det_1_1_bottom);
  and and_12 (and_12_out, or_1_out, det_1_2_bottom);
  and and_13 (and_13_out, or_1_out, Cn, det_1_1_top, det_1_2_top, det_1_3_top);
  and and_14 (and_14_out, or_1_out, det_1_2_top, det_1_3_top, det_1_1_bottom);
  and and_15 (and_15_out, det_1_2_bottom, det_1_3_top, or_1_out);
  and and_16 (and_16_out, or_1_out, det_1_3_bottom);
  and and_17 (and_17_out, Cn, det_1_1_top, det_1_2_top, det_1_3_top, det_1_4_top);
  and and_18 (and_18_out, det_1_2_top, det_1_3_top, det_1_4_top, det_1_1_bottom);
  and and_19 (and_19_out, det_1_3_top, det_1_4_top, det_1_2_bottom);
  and and_20 (and_20_out, det_1_4_top, det_1_3_bottom);
  buf buffer_1 (buffer_1_out, det_1_4_bottom);
  nand nand_2 (nand_2_out, det_1_1_top, det_1_2_top, det_1_3_top, det_1_4_top);
  and and_21 (and_21_out, det_1_2_top, det_1_3_top, det_1_4_top, det_1_1_bottom);
  and and_22 (and_22_out, det_1_3_top, det_1_4_top, det_1_2_bottom);
  and and_23 (and_23_out, det_1_4_top, det_1_3_bottom);
  buf buffer_2 (buffer_2_out, det_1_4_bottom);
  and and_24 (and_24_out, S2, not_2_out);
  nand nand_3 (nand_3_out, not_3_out, not_2_out, S0);
  nor nor_3 (nor_3_out, and_6_out, and_24_out);
  nor nor_4 (nor_4_out, and_8_out, and_9_out);
  nor nor_5 (nor_5_out, and_10_out, and_11_out, and_12_out);
  nor nor_6 (nor_6_out, and_13_out, and_14_out, and_15_out, and_16_out);
  nor nor_7 (nor_7_out, and_17_out, and_18_out, and_19_out, and_20_out, buffer_1_out);
  nor nor_8 (nor_8_out, and_21_out, and_22_out, and_23_out, buffer_2_out);
  nand nand_4 (nand_4_out, not_3_out, S1, S0);
  nand nand_5 (nand_5_out, not_3_out, S1, not_1_out);
  xnor xnor_1 (F0, det_1_1_top, nand_1_out);
  xnor xnor_2 (F1, det_1_2_top, nor_4_out);
  xnor xnor_3 (F2, det_1_3_top, nor_5_out);
  xnor xnor_4 (F3, det_1_4_top, nor_6_out);
  xor xor_1 (OVR, nor_6_out, nor_7_out);
  not not_4 (Cn_4, nor_7_out);
  and and_25 (and_25_out, not_3_out, S1);
  and and_26 (and_26_out, not_3_out, S0);
  or or_1 (or_1_out, and_26_out, and_25_out);

  // Notes on the sheet:
  //   74LS382
  //   /P
  //   'LS381
  //   /G
endmodule

module det_1 (
  input  _1,
  input  _2,
  input  _3,
  input  _4,
  input  _5,
  input  _6,
  input  A,
  input  B,
  output top,
  output bottom
);

  wire and_1_out, and_2_out, and_3_out, and_4_out, and_5_out, and_6_out, and_7_out, and_8_out, not_1_out,
       not_2_out;

  not not_1 (not_1_out, A);
  not not_2 (not_2_out, B);
  and and_1 (and_1_out, _3, A, not_2_out);
  and and_2 (and_2_out, _2, A, B);
  nor nor_1 (top, and_1_out, and_2_out, and_3_out, and_4_out);
  and and_3 (and_3_out, _3, not_1_out, B);
  and and_4 (and_4_out, _1, not_1_out, not_2_out);
  and and_5 (and_5_out, _6, A, not_2_out);
  and and_6 (and_6_out, _5, A, B);
  nor nor_2 (bottom, and_5_out, and_6_out, and_7_out, and_8_out);
  and and_7 (and_7_out, _4, not_1_out, B);
  and and_8 (and_8_out, not_1_out, not_2_out);
endmodule
