// Logisim project 74LS383.circ as structural Verilog: 1 circuit, main circuit 74LS383
module _74LS383 (
  input  _1D,
  input  _2D,
  input  _3D,
  input  _4D,
  input  _5D,
  input  _6D,
  input  _7D,
  input  _8D,
  input  CK,
  input  nCKEN,
  output _1Q,
  output _2Q,
  output _3Q,
  output _4Q,
  output _5Q,
  output _6Q,
  output _7Q,
  output _8Q
);

  wire not_1_out;
  wire [7:0] register_1_q;

  not not_1 (not_1_out, nCKEN);
  assign {_8Q, _7Q, _6Q, _5Q, _4Q, _3Q, _2Q, _1Q} = register_1_q;  // Buffer buffer_1, 8 bits wide
  Register register_1 (
    .D({_8D, _7D, _6D, _5D, _4D, _3D, _2D, _1D}), .en(not_1_out), .Q(register_1_q), .clk(CK));  // open: clr

  // Notes on the sheet:
  //   74LS383
  //   buffer_1 drives only 0 and floats otherwise
endmodule
