// Logisim project 74LS385.circ as structural Verilog: 1 circuit, main circuit 74LS385
module _74LS385 (
  input  CLK,
  input  _1A,
  input  _2A,
  input  _1B,
  input  _2B,
  input  _1S_A,
  input  _2S_A,
  input  nCLR,
  input  _3A,
  input  _4A,
  input  _3B,
  input  _4B,
  input  _3S_A,
  input  _4S_A,
  output \_1Σ ,
  output \_2Σ ,
  output \_3Σ ,
  output \_4Σ 
);

  wire and_1_out, and_2_out, and_3_out, and_4_out, and_5_out, and_6_out, and_7_out, and_8_out, and_9_out,
       and_10_out, and_11_out, and_12_out, and_13_out, and_14_out, and_15_out, and_16_out, and_17_out,
       and_18_out, and_19_out, and_20_out, CLR, nor_1_out, nor_2_out, nor_3_out, nor_4_out, not_1_out,
       not_2_out, not_3_out, not_5_out, not_6_out, not_7_out, not_8_out, not_9_out, not_10_out, not_11_out,
       not_12_out, not_13_out, Rise_2_qn, Rise_5_qn, Rise_6_qn, Rise_qn, xnor_1_out, xnor_2_out, xnor_3_out,
       xnor_4_out, xnor_5_out, xnor_6_out, xnor_7_out, xnor_8_out, xor_1_out, xor_2_out, xor_3_out, xor_4_out;

  not not_1 (not_1_out, _1A);
  not not_2 (not_2_out, _1B);
  not not_3 (not_3_out, _1S_A);
  not not_4 (CLR, nCLR);
  not not_5 (not_5_out, _3A);
  not not_6 (not_6_out, _3B);
  not not_7 (not_7_out, _3S_A);
  xnor xnor_1 (xnor_1_out, not_2_out, not_3_out);
  xnor xnor_2 (xnor_2_out, not_6_out, not_7_out);
  xnor xnor_3 (xnor_3_out, not_1_out, Rise_qn);
  and and_1 (and_1_out, not_1_out, xnor_1_out);
  nor nor_1 (nor_1_out, and_1_out, and_2_out, and_3_out);
  and and_2 (and_2_out, not_1_out, Rise_qn);
  and and_3 (and_3_out, xnor_1_out, Rise_qn);
  xnor xnor_4 (xnor_4_out, not_5_out, Rise_2_qn);
  and and_4 (and_4_out, not_5_out, xnor_2_out);
  nor nor_2 (nor_2_out, and_4_out, and_5_out, and_6_out);
  and and_5 (and_5_out, not_5_out, Rise_2_qn);
  and and_6 (and_6_out, xnor_2_out, Rise_2_qn);
  xor xor_1 (xor_1_out, xnor_3_out, xnor_1_out);
  D_Flip_Flop Rise (.clk(CLK), .D(nor_1_out), .Qn(Rise_qn), .preset(and_7_out), .reset(and_8_out));  // open: Q, en
  and and_7 (and_7_out, ~not_3_out, CLR);  // AND_Gate
  and and_8 (and_8_out, not_3_out, CLR);
  xor xor_2 (xor_2_out, xnor_4_out, xnor_2_out);
  D_Flip_Flop Rise_2 (.clk(CLK), .D(nor_2_out), .Qn(Rise_2_qn), .preset(and_10_out), .reset(and_9_out));  // open: Q, en
  and and_9 (and_9_out, not_7_out, CLR);
  and and_10 (and_10_out, ~not_7_out, CLR);  // AND_Gate
  D_Flip_Flop Rise_3 (.clk(CLK), .D(xor_1_out), .Q(\_1Σ ), .reset(CLR));  // open: Qn, preset, en
  D_Flip_Flop Rise_4 (.clk(CLK), .D(xor_2_out), .Q(\_3Σ ), .reset(CLR));  // open: Qn, preset, en
  not not_8 (not_8_out, _2A);
  not not_9 (not_9_out, _2B);
  not not_10 (not_10_out, _2S_A);
  not not_11 (not_11_out, _4A);
  not not_12 (not_12_out, _4B);
  not not_13 (not_13_out, _4S_A);
  xnor xnor_5 (xnor_5_out, not_9_out, not_10_out);
  xnor xnor_6 (xnor_6_out, not_12_out, not_13_out);
  xnor xnor_7 (xnor_7_out, not_8_out, Rise_5_qn);
  xor xor_3 (xor_3_out, xnor_7_out, xnor_5_out);
  and and_11 (and_11_out, not_8_out, xnor_5_out);
  nor nor_3 (nor_3_out, and_11_out, and_12_out, and_13_out);
  and and_12 (and_12_out, not_8_out, Rise_5_qn);
  and and_13 (and_13_out, xnor_5_out, Rise_5_qn);
  xnor xnor_8 (xnor_8_out, not_11_out, Rise_6_qn);
  xor xor_4 (xor_4_out, xnor_8_out, xnor_6_out);
  and and_14 (and_14_out, not_11_out, xnor_6_out);
  and and_15 (and_15_out, not_11_out, Rise_6_qn);
  nor nor_4 (nor_4_out, and_14_out, and_15_out, and_16_out);
  and and_16 (and_16_out, xnor_6_out, Rise_6_qn);
  D_Flip_Flop Rise_5 (
    .clk(CLK), .D(nor_3_out), .Qn(Rise_5_qn), .preset(and_18_out), .reset(and_17_out));  // open: Q, en
  and and_17 (and_17_out, not_10_out, CLR);
  and and_18 (and_18_out, ~not_10_out, CLR);  // AND_Gate
  D_Flip_Flop Rise_6 (
    .clk(CLK), .D(nor_4_out), .Qn(Rise_6_qn), .preset(and_20_out), .reset(and_19_out));  // open: Q, en
  and and_19 (and_19_out, not_13_out, CLR);
  and and_20 (and_20_out, ~not_13_out, CLR);  // AND_Gate
  D_Flip_Flop Rise_7 (.clk(CLK), .D(xor_3_out), .Q(\_2Σ ), .reset(CLR));  // open: Qn, preset, en
  D_Flip_Flop Rise_8 (.clk(CLK), .D(xor_4_out), .Q(\_4Σ ), .reset(CLR));  // open: Qn, preset, en

  // Notes on the sheet:
  //   74LS385
endmodule
