// Logisim project 74LS393.circ as structural Verilog: 1 circuit, main circuit 74LS393
module _74LS393 (
  input  _1CKA,
  input  _2CKA,
  input  _1CLR,
  input  _2CLR,
  output _1QA,
  output _2QA,
  output _1QB,
  output _2QB,
  output _1QC,
  output _2QC,
  output _1QD,
  output _2QD
);

  wire not_1_out, not_2_out, not_3_out, not_4_out, not_5_out, not_6_out, not_7_out, not_8_out, not_9_out,
       not_10_out, not_11_out, not_12_out, t_ff_1_qn, t_ff_2_qn, t_ff_3_qn, t_ff_5_qn, t_ff_6_qn, t_ff_7_qn;

  not not_1 (not_1_out, _1CKA);
  not not_2 (not_2_out, not_6_out);
  not not_3 (not_3_out, not_6_out);
  not not_4 (not_4_out, not_6_out);
  not not_5 (not_5_out, not_6_out);
  not not_6 (not_6_out, _1CLR);
  T_Flip_Flop t_ff_1 (.clk(not_1_out), .T(1'b1), .Q(_1QA), .Qn(t_ff_1_qn), .reset(not_2_out));  // open: preset, en
  T_Flip_Flop t_ff_2 (.clk(t_ff_1_qn), .T(1'b1), .Q(_1QB), .Qn(t_ff_2_qn), .reset(not_3_out));  // open: preset, en
  T_Flip_Flop t_ff_3 (.clk(t_ff_2_qn), .T(1'b1), .Q(_1QC), .Qn(t_ff_3_qn), .reset(not_4_out));  // open: preset, en
  T_Flip_Flop t_ff_4 (.clk(t_ff_3_qn), .T(1'b1), .Q(_1QD), .reset(not_5_out));  // open: Qn, preset, en
  not not_7 (not_7_out, _2CLR);
  T_Flip_Flop t_ff_5 (.clk(not_8_out), .T(1'b1), .Q(_2QA), .Qn(t_ff_5_qn), .reset(not_9_out));  // open: preset, en
  not not_8 (not_8_out, _2CKA);
  not not_9 (not_9_out, not_7_out);
  T_Flip_Flop t_ff_6 (.clk(t_ff_5_qn), .T(1'b1), .Q(_2QB), .Qn(t_ff_6_qn), .reset(not_10_out));  // open: preset, en
  not not_10 (not_10_out, not_7_out);
  T_Flip_Flop t_ff_7 (.clk(t_ff_6_qn), .T(1'b1), .Q(_2QC), .Qn(t_ff_7_qn), .reset(not_11_out));  // open: preset, en
  not not_11 (not_11_out, not_7_out);
  T_Flip_Flop t_ff_8 (.clk(t_ff_7_qn), .T(1'b1), .Q(_2QD), .reset(not_12_out));  // open: Qn, preset, en
  not not_12 (not_12_out, not_7_out);

  // Notes on the sheet:
  //   74LS393
endmodule
