// Logisim project 74LS395.circ as structural Verilog: 1 circuit, main circuit 74LS395
module _74LS395 (
  input  A,
  input  B,
  input  C,
  input  D,
  input  LD_SH,
  input  SER,
  input  CLK,
  input  nCLR,
  input  nOC,
  output QA,
  output QB,
  output QC,
  output QD,
  output QD_prime
);

  wire and_1_out, and_2_out, and_3_out, and_4_out, and_5_out, and_6_out, and_7_out, and_8_out, Fall_2_q,
       Fall_2_qn, Fall_3_q, Fall_3_qn, Fall_4_qn, Fall_q, Fall_qn, nor_1_out, nor_2_out, nor_3_out,
       nor_4_out, not_1_out, not_2_out, not_3_out, not_4_out, not_5_out, not_6_out, not_7_out;

  not not_1 (not_1_out, LD_SH);
  not not_2 (not_2_out, nCLR);
  not not_3 (not_3_out, nOC);
  and and_1 (and_1_out, SER, not_1_out);
  and and_2 (and_2_out, LD_SH, A);
  nor nor_1 (nor_1_out, and_1_out, and_2_out);
  not not_4 (not_4_out, nor_1_out);
  and and_3 (and_3_out, Fall_q, not_1_out);
  S_R_Flip_Flop #(.trigger("falling")) Fall (
    .S(not_4_out), .clk(CLK), .R(nor_1_out), .Q(Fall_q), .Qn(Fall_qn), .reset(not_2_out));  // open: preset, en
  assign QA = not_3_out ? ~Fall_qn : 1'bz;  // Controlled_Inverter controlled_inverter_1
  and and_4 (and_4_out, LD_SH, B);
  nor nor_2 (nor_2_out, and_3_out, and_4_out);
  not not_5 (not_5_out, nor_2_out);
  and and_5 (and_5_out, Fall_2_q, not_1_out);
  nor nor_3 (nor_3_out, and_5_out, and_6_out);
  S_R_Flip_Flop #(.trigger("falling")) Fall_2 (
    .S(not_5_out), .clk(CLK), .R(nor_2_out), .Q(Fall_2_q), .Qn(Fall_2_qn), .reset(not_2_out));  // open: preset, en
  assign QB = not_3_out ? ~Fall_2_qn : 1'bz;  // Controlled_Inverter controlled_inverter_2
  and and_6 (and_6_out, LD_SH, C);
  not not_6 (not_6_out, nor_3_out);
  S_R_Flip_Flop #(.trigger("falling")) Fall_3 (
    .S(not_6_out), .clk(CLK), .R(nor_3_out), .Q(Fall_3_q), .Qn(Fall_3_qn), .reset(not_2_out));  // open: preset, en
  and and_7 (and_7_out, LD_SH, D);
  and and_8 (and_8_out, Fall_3_q, not_1_out);
  nor nor_4 (nor_4_out, and_8_out, and_7_out);
  not not_7 (not_7_out, nor_4_out);
  assign QC = not_3_out ? ~Fall_3_qn : 1'bz;  // Controlled_Inverter controlled_inverter_3
  S_R_Flip_Flop #(.trigger("falling")) Fall_4 (
    .S(not_7_out), .clk(CLK), .R(nor_4_out), .Q(QD_prime), .Qn(Fall_4_qn), .reset(not_2_out));  // open: preset, en
  assign QD = not_3_out ? ~Fall_4_qn : 1'bz;  // Controlled_Inverter controlled_inverter_4

  // Notes on the sheet:
  //   74LS395
endmodule
