// Logisim project 74LS396.circ as structural Verilog: 1 circuit, main circuit 74LS396
module _74LS396 (
  input  CLOCK,
  input  D1,
  input  D2,
  input  D3,
  input  D4,
  input  STROBE_nG,
  output _1Q1,
  output _2Q1,
  output _1Q2,
  output _2Q2,
  output _1Q3,
  output _2Q3,
  output _1Q4,
  output _2Q4
);

  wire d_ff_1_q, d_ff_1_qn, d_ff_2_q, d_ff_2_qn, d_ff_3_q, d_ff_3_qn, d_ff_4_q, d_ff_4_qn, d_ff_5_qn,
       d_ff_6_qn, d_ff_7_qn, d_ff_8_qn;

  D_Flip_Flop d_ff_1 (.clk(CLOCK), .D(D1), .Q(d_ff_1_q), .Qn(d_ff_1_qn));  // open: preset, en, reset
  D_Flip_Flop d_ff_2 (.clk(CLOCK), .D(D2), .Q(d_ff_2_q), .Qn(d_ff_2_qn));  // open: preset, en, reset
  D_Flip_Flop d_ff_3 (.clk(CLOCK), .D(D3), .Q(d_ff_3_q), .Qn(d_ff_3_qn));  // open: preset, en, reset
  D_Flip_Flop d_ff_4 (.clk(CLOCK), .D(D4), .Q(d_ff_4_q), .Qn(d_ff_4_qn));  // open: preset, en, reset
  and and_1 (_1Q1, ~d_ff_1_qn, ~STROBE_nG);  // AND_Gate
  D_Flip_Flop d_ff_5 (.clk(CLOCK), .D(d_ff_1_q), .Qn(d_ff_5_qn));  // open: Q, preset, en, reset
  and and_2 (_2Q1, ~d_ff_5_qn, ~STROBE_nG);  // AND_Gate
  and and_3 (_1Q2, ~d_ff_2_qn, ~STROBE_nG);  // AND_Gate
  D_Flip_Flop d_ff_6 (.clk(CLOCK), .D(d_ff_2_q), .Qn(d_ff_6_qn));  // open: Q, preset, en, reset
  and and_4 (_2Q2, ~d_ff_6_qn, ~STROBE_nG);  // AND_Gate
  and and_5 (_1Q3, ~d_ff_3_qn, ~STROBE_nG);  // AND_Gate
  D_Flip_Flop d_ff_7 (.clk(CLOCK), .D(d_ff_3_q), .Qn(d_ff_7_qn));  // open: Q, preset, en, reset
  and and_6 (_2Q3, ~d_ff_7_qn, ~STROBE_nG);  // AND_Gate
  and and_7 (_1Q4, ~d_ff_4_qn, ~STROBE_nG);  // AND_Gate
  D_Flip_Flop d_ff_8 (.clk(CLOCK), .D(d_ff_4_q), .Qn(d_ff_8_qn));  // open: Q, preset, en, reset
  and and_8 (_2Q4, ~d_ff_8_qn, ~STROBE_nG);  // AND_Gate

  // Notes on the sheet:
  //   74LS396
endmodule
