// Logisim project 74LS398.circ as structural Verilog: 1 circuit, main circuit 74L398
module _74L398 (
  input  A1,
  input  WORD_SELECT,
  input  A2,
  input  B1,
  input  B2,
  input  C1,
  input  C2,
  input  D1,
  input  D2,
  input  CLOCK,
  output QA,
  output nQA,
  output QA_2,
  output nQA_2,
  output QA_3,
  output nQA_3,
  output QA_4,
  output nQA_4
);

  wire and_1_out, and_2_out, and_3_out, and_4_out, and_5_out, and_6_out, and_7_out, and_8_out, nor_1_out,
       nor_2_out, nor_3_out, nor_4_out, not_1_out, not_2_out, not_3_out, not_4_out;

  and and_1 (and_1_out, A1, ~WORD_SELECT);  // AND_Gate
  and and_2 (and_2_out, WORD_SELECT, A2);
  and and_3 (and_3_out, B1, ~WORD_SELECT);  // AND_Gate
  and and_4 (and_4_out, WORD_SELECT, B2);
  and and_5 (and_5_out, C1, ~WORD_SELECT);  // AND_Gate
  and and_6 (and_6_out, WORD_SELECT, C2);
  and and_7 (and_7_out, D1, ~WORD_SELECT);  // AND_Gate
  and and_8 (and_8_out, WORD_SELECT, D2);
  nor nor_1 (nor_1_out, and_1_out, and_2_out);
  not not_1 (not_1_out, nor_1_out);
  nor nor_2 (nor_2_out, and_3_out, and_4_out);
  not not_2 (not_2_out, nor_2_out);
  not not_3 (not_3_out, nor_3_out);
  nor nor_3 (nor_3_out, and_5_out, and_6_out);
  not not_4 (not_4_out, nor_4_out);
  nor nor_4 (nor_4_out, and_7_out, and_8_out);
  S_R_Flip_Flop s_r_ff_1 (.S(not_1_out), .clk(CLOCK), .R(nor_1_out), .Q(QA), .Qn(nQA));  // open: preset, reset, en
  S_R_Flip_Flop s_r_ff_2 (.S(not_2_out), .clk(CLOCK), .R(nor_2_out), .Q(QA_2), .Qn(nQA_2));  // open: preset, reset, en
  S_R_Flip_Flop s_r_ff_3 (.S(not_3_out), .clk(CLOCK), .R(nor_3_out), .Q(QA_3), .Qn(nQA_3));  // open: preset, reset, en
  S_R_Flip_Flop s_r_ff_4 (.S(not_4_out), .clk(CLOCK), .R(nor_4_out), .Q(QA_4), .Qn(nQA_4));  // open: preset, reset, en

  // Notes on the sheet:
  //   74LS398
endmodule
