// Logisim project 74LS405.circ as structural Verilog: 1 circuit, main circuit 74LS405
module _74LS405 (
  input  A0,
  input  A1,
  input  A2,
  input  nE1,
  input  nE2,
  input  E3,
  output out_7,
  output out_8,
  output out_9,
  output out_10,
  output out_11,
  output out_12,
  output out_13,
  output out_14
);

  wire nor_1_out;

  nor nor_1 (nor_1_out, nE1, nE2, ~E3);  // NOR_Gate
  or or_1 (out_7, A0, A1, A2, nor_1_out);
  or or_2 (out_8, ~A0, A1, A2, nor_1_out);  // OR_Gate
  or or_3 (out_9, A0, ~A1, A2, nor_1_out);  // OR_Gate
  or or_4 (out_10, ~A0, ~A1, A2, nor_1_out);  // OR_Gate
  or or_5 (out_11, A0, A1, ~A2, nor_1_out);  // OR_Gate
  or or_6 (out_12, ~A0, A1, ~A2, nor_1_out);  // OR_Gate
  or or_7 (out_13, A0, ~A1, ~A2, nor_1_out);  // OR_Gate
  or or_8 (out_14, ~A0, ~A1, ~A2, nor_1_out);  // OR_Gate

  // Notes on the sheet:
  //   74LS405
  //   * error in Polish datasheet corrected
  //   (output is OR not NOR gates)
endmodule
