// Logisim project 74LS408.circ as structural Verilog: 1 circuit, main circuit 74LS408
module _74LS408 (
  input  _1A,
  input  _1B,
  input  _1C,
  input  _1D,
  input  _1E,
  input  _1F,
  input  _1G,
  input  _1H,
  input  _2A,
  input  _2B,
  output _1Q,
  output _2Q
);

  wire xnor_1_out, xnor_2_out, xnor_3_out, xnor_4_out, xnor_5_out, xnor_6_out;

  xnor xnor_1 (xnor_1_out, _1A, _1B);
  xnor xnor_2 (xnor_2_out, _1C, _1D);
  xnor xnor_3 (xnor_3_out, _1E, _1F);
  xnor xnor_4 (xnor_4_out, _1G, _1H);
  xnor xnor_5 (xnor_5_out, xnor_1_out, xnor_2_out);
  xnor xnor_6 (xnor_6_out, xnor_3_out, xnor_4_out);
  xnor xnor_7 (_2Q, _2A, _2B);
  xnor xnor_8 (_1Q, xnor_5_out, xnor_6_out);

  // Notes on the sheet:
  //   74LS408
endmodule
