// Logisim project 74LS41.circ as structural Verilog: 1 circuit, main circuit 74LS41
module _74LS41 (
  input  A,
  input  B,
  input  C,
  input  D,
  output _0,
  output _1,
  output _2,
  output _3,
  output _4,
  output _6,
  output _7,
  output _8,
  output _9,
  output _5
);

  wire and_1_out, and_2_out, and_3_out, and_4_out, and_5_out, and_6_out, and_8_out, and_9_out, and_11_out,
       and_12_out, and_14_out, and_15_out, nA, nB, nC, nD;

  not not_1 (nA, A);
  not not_2 (nB, B);
  not not_3 (nC, C);
  not not_4 (nD, D);
  and and_1 (and_1_out, nA, nB, nC, nD);
  and and_2 (and_2_out, nA, B, nC, D);
  and and_3 (and_3_out, A, nB, C, nD);
  and and_4 (and_4_out, A, B, C, D);
  or or_1 (_0, and_1_out, and_2_out);
  or or_2 (_5, and_3_out, and_4_out);
  and and_5 (and_5_out, A, nB, nC, nD);
  or or_3 (_1, and_5_out, and_6_out);
  and and_6 (and_6_out, A, B, nC, D);
  and and_7 (_6, nA, B, C, nD);
  and and_8 (and_8_out, nA, B, nC, nD);
  or or_4 (_2, and_8_out, and_9_out);
  and and_9 (and_9_out, nA, nB, C, D);
  and and_10 (_7, A, B, C, nD);
  and and_11 (and_11_out, A, B, nC, nD);
  and and_12 (and_12_out, A, nB, C, D);
  and and_13 (_8, nA, nB, nC, D);
  or or_5 (_3, and_11_out, and_12_out);
  and and_14 (and_14_out, nA, nB, C, nD);
  and and_15 (and_15_out, nA, B, C, D);
  and and_16 (_9, A, nB, nC, D);
  or or_6 (_4, and_14_out, and_15_out);

  // Notes on the sheet:
  //   74LS41
endmodule
