// Logisim project 74LS412.circ as structural Verilog: 1 circuit, main circuit 74LS412
module _74LS412 (
  input  STB,
  input  M,
  input  nS1,
  input  S2,
  input  DI1,
  input  DI2,
  input  DI3,
  input  DI4,
  input  DI5,
  input  DI6,
  input  DI7,
  input  DI8,
  input  nCLR,
  output nINT,
  output DO1,
  output DO2,
  output DO3,
  output DO4,
  output DO5,
  output DO6,
  output DO7,
  output DO8
);

  wire and_1_out, and_2_out, and_3_out, Fall_q, High_2_q, High_3_q, High_4_q, High_5_q, High_6_q, High_7_q,
       High_8_q, High_q, nor_1_out, not_1_out, not_2_out, not_3_out, not_4_out, not_5_out, not_6_out,
       not_7_out, not_8_out, not_9_out, or_1_out, or_2_out;

  and and_1 (and_1_out, ~nS1, S2);  // AND_Gate
  or or_1 (or_1_out, M, and_1_out);
  and and_2 (and_2_out, STB, ~M);  // AND_Gate
  and and_3 (and_3_out, M, and_1_out);
  nor nor_1 (nor_1_out, ~nCLR, and_1_out);  // NOR_Gate
  D_Flip_Flop #(.trigger("falling")) Fall (.clk(STB), .D(1'b0), .Q(Fall_q), .preset(not_1_out));  // open: Qn, en, reset
  not not_1 (not_1_out, nor_1_out);
  or or_2 (or_2_out, and_2_out, and_3_out);
  not not_2 (not_2_out, nCLR);
  not not_3 (not_3_out, nCLR);
  not not_4 (not_4_out, nCLR);
  not not_5 (not_5_out, nCLR);
  not not_6 (not_6_out, nCLR);
  not not_7 (not_7_out, nCLR);
  not not_8 (not_8_out, nCLR);
  not not_9 (not_9_out, nCLR);
  D_Flip_Flop #(.trigger("high")) High (
    .clk(or_2_out), .D(DI1), .Q(High_q), .reset(not_2_out));  // open: Qn, preset, en
  assign DO1 = or_1_out ? High_q : 1'bz;  // Controlled_Buffer controlled_buffer_1
  assign DO2 = or_1_out ? High_2_q : 1'bz;  // Controlled_Buffer controlled_buffer_2
  D_Flip_Flop #(.trigger("high")) High_2 (
    .clk(or_2_out), .D(DI2), .Q(High_2_q), .reset(not_3_out));  // open: Qn, preset, en
  assign DO3 = or_1_out ? High_3_q : 1'bz;  // Controlled_Buffer controlled_buffer_3
  D_Flip_Flop #(.trigger("high")) High_3 (
    .clk(or_2_out), .D(DI3), .Q(High_3_q), .reset(not_4_out));  // open: Qn, preset, en
  D_Flip_Flop #(.trigger("high")) High_4 (
    .clk(or_2_out), .D(DI4), .Q(High_4_q), .reset(not_5_out));  // open: Qn, preset, en
  assign DO4 = or_1_out ? High_4_q : 1'bz;  // Controlled_Buffer controlled_buffer_4
  assign DO5 = or_1_out ? High_5_q : 1'bz;  // Controlled_Buffer controlled_buffer_5
  D_Flip_Flop #(.trigger("high")) High_5 (
    .clk(or_2_out), .D(DI5), .Q(High_5_q), .reset(not_6_out));  // open: Qn, preset, en
  D_Flip_Flop #(.trigger("high")) High_6 (
    .clk(or_2_out), .D(DI6), .Q(High_6_q), .reset(not_7_out));  // open: Qn, preset, en
  assign DO6 = or_1_out ? High_6_q : 1'bz;  // Controlled_Buffer controlled_buffer_6
  D_Flip_Flop #(.trigger("high")) High_7 (
    .clk(or_2_out), .D(DI7), .Q(High_7_q), .reset(not_8_out));  // open: Qn, preset, en
  assign DO7 = or_1_out ? High_7_q : 1'bz;  // Controlled_Buffer controlled_buffer_7
  D_Flip_Flop #(.trigger("high")) High_8 (
    .clk(or_2_out), .D(DI8), .Q(High_8_q), .reset(not_9_out));  // open: Qn, preset, en
  assign DO8 = or_1_out ? High_8_q : 1'bz;  // Controlled_Buffer controlled_buffer_8
  nor nor_2 (nINT, ~Fall_q, and_1_out);  // NOR_Gate

  // Notes on the sheet:
  //   74LS412
endmodule
