// Logisim project 74LS416.circ as structural Verilog: 1 circuit, main circuit 74LS416
module _74LS416 (
  input  Clock,
  input  nMR,
  input  Gate,
  input  nPE,
  input  D0,
  input  D1,
  input  D2,
  input  D3,
  output Q0,
  output Q1,
  output Q2,
  output Q3,
  output R,
  output Bus
);

  wire and_1_out, and_2_out, and_3_out, and_4_out, and_5_out, and_6_out, and_7_out, d_ff_1_qn, d_ff_2_qn,
       d_ff_3_qn, d_ff_4_qn, nand_1_out, nand_2_out, nand_3_out, nand_4_out, nand_5_out, nand_6_out,
       nand_7_out, nand_8_out, nor_1_out, not_1_out, not_2_out, not_3_out, not_4_out, not_5_out, not_6_out,
       not_7_out, not_8_out, not_9_out, not_10_out;

  and and_1 (and_1_out, Gate, nPE);
  and and_2 (and_2_out, nPE, not_10_out);
  and and_3 (and_3_out, d_ff_1_qn, d_ff_1_qn);
  not not_1 (not_1_out, nand_1_out);
  nand nand_1 (nand_1_out, nMR, D0, nor_1_out);
  nor nor_1 (nor_1_out, and_1_out, and_2_out);
  D_Flip_Flop d_ff_1 (
    .clk(Clock), .D(and_3_out), .Q(Q0), .Qn(d_ff_1_qn), .preset(not_1_out), .reset(not_2_out));  // open: en
  not not_2 (not_2_out, nand_2_out);
  nand nand_2 (nand_2_out, nand_1_out, nor_1_out);
  D_Flip_Flop d_ff_2 (
    .clk(Q0), .D(and_4_out), .Q(Q1), .Qn(d_ff_2_qn), .preset(not_4_out), .reset(not_3_out));  // open: en
  and and_4 (and_4_out, d_ff_2_qn, not_6_out);
  not not_3 (not_3_out, nand_3_out);
  not not_4 (not_4_out, nand_4_out);
  nand nand_3 (nand_3_out, nand_4_out, nor_1_out);
  nand nand_4 (nand_4_out, nMR, D1, nor_1_out);
  and and_5 (and_5_out, d_ff_3_qn, d_ff_3_qn);
  not not_5 (not_5_out, nand_5_out);
  nand nand_5 (nand_5_out, nMR, D2, nor_1_out);
  not not_6 (not_6_out, and_6_out);
  D_Flip_Flop d_ff_3 (
    .clk(Q1), .D(and_5_out), .Q(Q2), .Qn(d_ff_3_qn), .preset(not_5_out), .reset(not_7_out));  // open: en
  not not_7 (not_7_out, nand_6_out);
  nand nand_6 (nand_6_out, nand_5_out, nor_1_out);
  and and_6 (and_6_out, d_ff_4_qn, d_ff_3_qn, d_ff_2_qn);
  not not_8 (not_8_out, nand_7_out);
  not not_9 (not_9_out, nand_8_out);
  nand nand_7 (nand_7_out, nand_8_out, nor_1_out);
  nand nand_8 (nand_8_out, nMR, D3, nor_1_out);
  D_Flip_Flop d_ff_4 (
    .clk(Q0), .D(and_6_out), .Q(Q3), .Qn(d_ff_4_qn), .preset(not_9_out), .reset(not_8_out));  // open: en
  and and_7 (and_7_out, d_ff_4_qn, d_ff_3_qn, d_ff_2_qn, d_ff_1_qn);
  not not_10 (not_10_out, and_7_out);
  Pull_Resistor #(.pull(1)) pull_resistor_1 (.node(R));
  buf buffer_1 (Bus, and_7_out);

  // Notes on the sheet:
  //   74LS416
  //   buffer_1 drives only 0 and floats otherwise
endmodule
