// Logisim project 74LS425.circ as structural Verilog: 1 circuit, main circuit 74LS425
module _74LS425 (
  input  _1A,
  input  _1_G,
  input  _2A,
  input  _2_G,
  input  _3A,
  input  _3_G,
  input  _4A,
  input  _4_G,
  output _1Y,
  output _2Y,
  output _3Y,
  output _4Y
);

  wire not_1_out, not_2_out, not_3_out, not_4_out;

  not not_1 (not_1_out, _1_G);
  not not_2 (not_2_out, _2_G);
  not not_3 (not_3_out, _3_G);
  not not_4 (not_4_out, _4_G);
  assign _1Y = not_1_out ? _1A : 1'bz;  // Controlled_Buffer controlled_buffer_1
  assign _2Y = not_2_out ? _2A : 1'bz;  // Controlled_Buffer controlled_buffer_2
  assign _3Y = not_3_out ? _3A : 1'bz;  // Controlled_Buffer controlled_buffer_3
  assign _4Y = not_4_out ? _4A : 1'bz;  // Controlled_Buffer controlled_buffer_4

  // Notes on the sheet:
  //   74LS425
endmodule
