// Logisim project 74LS432.circ as structural Verilog: 1 circuit, main circuit 74LS432
module _74LS432 (
  input  STB,
  input  M,
  input  nS1,
  input  S2,
  input  D0,
  input  D1,
  input  D2,
  input  D3,
  input  D4,
  input  D5,
  input  D6,
  input  D7,
  input  nCLR,
  output nINT,
  output nQ0,
  output nQ1,
  output nQ2,
  output nQ3,
  output nQ4,
  output nQ5,
  output nQ6,
  output nQ7
);

  wire and_1_out, and_2_out, and_3_out, Fall_q, High_2_q, High_3_q, High_4_q, High_5_q, High_6_q, High_7_q,
       High_8_q, High_q, nor_1_out, not_1_out, not_2_out, or_1_out, or_2_out;

  and and_1 (and_1_out, ~nS1, S2);  // AND_Gate
  or or_1 (or_1_out, M, and_1_out);
  nor nor_1 (nor_1_out, not_2_out, and_1_out);
  and and_2 (and_2_out, STB, ~M);  // AND_Gate
  or or_2 (or_2_out, and_2_out, and_3_out);
  and and_3 (and_3_out, M, and_1_out);
  D_Flip_Flop #(.trigger("falling")) Fall (.clk(STB), .D(1'b0), .Q(Fall_q), .preset(not_1_out));  // open: Qn, en, reset
  not not_1 (not_1_out, nor_1_out);
  D_Flip_Flop #(.trigger("high")) High (.clk(or_2_out), .D(D0), .Q(High_q), .reset(not_2_out));  // open: Qn, preset, en
  D_Flip_Flop #(.trigger("high")) High_2 (
    .clk(or_2_out), .D(D1), .Q(High_2_q), .reset(not_2_out));  // open: Qn, preset, en
  D_Flip_Flop #(.trigger("high")) High_3 (
    .clk(or_2_out), .D(D2), .Q(High_3_q), .reset(not_2_out));  // open: Qn, preset, en
  D_Flip_Flop #(.trigger("high")) High_4 (
    .clk(or_2_out), .D(D3), .Q(High_4_q), .reset(not_2_out));  // open: Qn, preset, en
  D_Flip_Flop #(.trigger("high")) High_5 (
    .clk(or_2_out), .D(D4), .Q(High_5_q), .reset(not_2_out));  // open: Qn, preset, en
  D_Flip_Flop #(.trigger("high")) High_6 (
    .clk(or_2_out), .D(D5), .Q(High_6_q), .reset(not_2_out));  // open: Qn, preset, en
  D_Flip_Flop #(.trigger("high")) High_7 (
    .clk(or_2_out), .D(D6), .Q(High_7_q), .reset(not_2_out));  // open: Qn, preset, en
  D_Flip_Flop #(.trigger("high")) High_8 (
    .clk(or_2_out), .D(D7), .Q(High_8_q), .reset(not_2_out));  // open: Qn, preset, en
  not not_2 (not_2_out, nCLR);
  nor nor_2 (nINT, ~Fall_q, and_1_out);  // NOR_Gate
  assign nQ0 = or_1_out ? ~High_q : 1'bz;  // Controlled_Inverter controlled_inverter_1
  assign nQ1 = or_1_out ? ~High_2_q : 1'bz;  // Controlled_Inverter controlled_inverter_2
  assign nQ2 = or_1_out ? ~High_3_q : 1'bz;  // Controlled_Inverter controlled_inverter_3
  assign nQ3 = or_1_out ? ~High_4_q : 1'bz;  // Controlled_Inverter controlled_inverter_4
  assign nQ4 = or_1_out ? ~High_5_q : 1'bz;  // Controlled_Inverter controlled_inverter_5
  assign nQ5 = or_1_out ? ~High_6_q : 1'bz;  // Controlled_Inverter controlled_inverter_6
  assign nQ6 = or_1_out ? ~High_7_q : 1'bz;  // Controlled_Inverter controlled_inverter_7
  assign nQ7 = or_1_out ? ~High_8_q : 1'bz;  // Controlled_Inverter controlled_inverter_8

  // Notes on the sheet:
  //   74LS432
endmodule
