// Logisim project 74LS436.circ as structural Verilog: 1 circuit, main circuit 74LS436
module _74LS436 (
  input  _1A,
  input  _2A,
  input  _3A,
  input  _4A,
  input  _5A,
  input  _6A,
  input  nG1,
  input  nG2,
  output _1_Y,
  output _2_Y,
  output _3_Y,
  output _4_Y,
  output _5_Y,
  output _6_Y
);

  wire nor_1_out;

  nor nor_1 (nor_1_out, nG1, nG2);
  nand nand_1 (_1_Y, _1A, nor_1_out);
  nand nand_2 (_2_Y, _2A, nor_1_out);
  nand nand_3 (_3_Y, _3A, nor_1_out);
  nand nand_4 (_4_Y, _4A, nor_1_out);
  nand nand_5 (_5_Y, _5A, nor_1_out);
  nand nand_6 (_6_Y, _6A, nor_1_out);

  // Notes on the sheet:
  //   74LS436
endmodule
