// Logisim project 74LS444.circ as structural Verilog: 2 circuits, main circuit 74LS444
module _74LS444 (
  input  nCS,
  input  nGA,
  input  nGB,
  input  nGC,
  input  S0,
  input  S1,
  input  A1,
  input  B1,
  input  C1,
  input  A2,
  input  B2,
  input  C2,
  input  A3,
  input  B3,
  input  C3,
  input  A4,
  input  B4,
  input  C4,
  output A1out,
  output B1out,
  output C1out,
  output A2out,
  output B2out,
  output C2out,
  output A3out,
  output B3out,
  output C3out,
  output A4out,
  output B4out,
  output C4out
);

  wire and_1_out, and_2_out, and_3_out, not_1_out, not_2_out, xnor_1_out;

  not not_1 (not_1_out, S0);
  not not_2 (not_2_out, S1);
  xnor xnor_1 (xnor_1_out, S0, S1);
  and and_1 (and_1_out, ~S1, ~nGC, ~nCS);  // AND_Gate
  transceiver_inverted_and_non_inverted transceiver_inverted_and_non_inverted_1 (
    .S1(S1), .nS1(not_2_out), .S0(S0), .nS0(not_1_out), .Ain(A1), .Bin(B1), .Cin(C1), .ENC(and_1_out),
    .ENB(and_3_out), .ENA(and_2_out), .Aout(A1out), .Bout(B1out), .Cout(C1out));
  transceiver_inverted_and_non_inverted transceiver_inverted_and_non_inverted_2 (
    .S1(S1), .nS1(not_2_out), .S0(S0), .nS0(not_1_out), .Ain(A2), .Bin(B2), .Cin(C2), .ENC(and_1_out),
    .ENB(and_3_out), .ENA(and_2_out), .Aout(A2out), .Bout(B2out), .Cout(C2out));
  transceiver_inverted_and_non_inverted transceiver_inverted_and_non_inverted_3 (
    .S1(S1), .nS1(not_2_out), .S0(S0), .nS0(not_1_out), .Ain(A3), .Bin(B3), .Cin(C3), .ENC(and_1_out),
    .ENB(and_3_out), .ENA(and_2_out), .Aout(A3out), .Bout(B3out), .Cout(C3out));
  transceiver_inverted_and_non_inverted transceiver_inverted_and_non_inverted_4 (
    .S1(S1), .nS1(not_2_out), .S0(S0), .nS0(not_1_out), .Ain(A4), .Bin(B4), .Cin(C4), .ENC(and_1_out),
    .ENB(and_3_out), .ENA(and_2_out), .Aout(A4out), .Bout(B4out), .Cout(C4out));
  and and_2 (and_2_out, ~xnor_1_out, ~nGA, ~nCS);  // AND_Gate
  and and_3 (and_3_out, ~S0, ~nGB, ~nCS);  // AND_Gate

  // Notes on the sheet:
  //   74LS444
  //   tri-state
endmodule

module transceiver_inverted_and_non_inverted (
  input  S1,
  input  nS1,
  input  S0,
  input  nS0,
  input  ENC,
  input  ENB,
  input  ENA,
  input  Ain,
  input  Bin,
  input  Cin,
  output Aout,
  output Bout,
  output Cout
);

  wire and_1_out, and_2_out, and_3_out, and_4_out, and_5_out, and_6_out, nor_1_out, nor_2_out, nor_3_out;

  and and_1 (and_1_out, S1, Bin, nS0);
  and and_2 (and_2_out, nS1, Cin, S0);
  and and_3 (and_3_out, nS1, Ain, nS0);
  and and_4 (and_4_out, nS1, ~Cin, S0);  // AND_Gate
  and and_5 (and_5_out, nS1, Ain, nS0);
  and and_6 (and_6_out, S1, ~Bin, nS0);  // AND_Gate
  assign Aout = ENA ? nor_1_out : 1'bz;  // Controlled_Buffer controlled_buffer_1
  nor nor_1 (nor_1_out, and_1_out, and_2_out);
  assign Bout = ENB ? nor_2_out : 1'bz;  // Controlled_Buffer controlled_buffer_2
  nor nor_2 (nor_2_out, and_3_out, and_4_out);
  assign Cout = ENC ? nor_3_out : 1'bz;  // Controlled_Buffer controlled_buffer_3
  nor nor_3 (nor_3_out, and_5_out, and_6_out);
endmodule
