// Logisim project 74LS445.circ as structural Verilog: 1 circuit, main circuit 74LS445
module _74LS445 (
  input  A,
  input  B,
  input  C,
  input  D,
  output _0,
  output _1,
  output _2,
  output _3,
  output _4,
  output _5,
  output _6,
  output _7,
  output _8,
  output _9
);

  wire decoder_1_out0, decoder_1_out1, decoder_1_out2, decoder_1_out3, decoder_1_out4, decoder_1_out5,
       decoder_1_out6, decoder_1_out7, decoder_1_out8, decoder_1_out9;

  Decoder #(.select(4), .enable("false")) decoder_1 (
    .out0(decoder_1_out0), .out1(decoder_1_out1), .out2(decoder_1_out2), .out3(decoder_1_out3),
    .out4(decoder_1_out4), .out5(decoder_1_out5), .out6(decoder_1_out6), .out7(decoder_1_out7),
    .out8(decoder_1_out8), .out9(decoder_1_out9), .sel({D, C, B, A}));  // open: out10, out11, out12, out13, out14, out15
  not not_1 (_0, decoder_1_out0);
  not not_2 (_1, decoder_1_out1);
  not not_3 (_2, decoder_1_out2);
  not not_4 (_3, decoder_1_out3);
  not not_5 (_4, decoder_1_out4);
  not not_6 (_5, decoder_1_out5);
  not not_7 (_6, decoder_1_out6);
  not not_8 (_7, decoder_1_out7);
  not not_9 (_8, decoder_1_out8);
  not not_10 (_9, decoder_1_out9);

  // Notes on the sheet:
  //   74LS445
  //   0/floating
  //   not_1 drives only 0 and floats otherwise
  //   not_2 drives only 0 and floats otherwise
  //   not_3 drives only 0 and floats otherwise
  //   not_4 drives only 0 and floats otherwise
  //   not_5 drives only 0 and floats otherwise
  //   not_6 drives only 0 and floats otherwise
  //   not_7 drives only 0 and floats otherwise
  //   not_8 drives only 0 and floats otherwise
  //   not_9 drives only 0 and floats otherwise
  //   not_10 drives only 0 and floats otherwise
endmodule
