// Logisim project 74LS446.circ as structural Verilog: 1 circuit, main circuit 74LS446
module _74LS446 (
  input  nGBA,
  input  nGAB,
  input  DIR1,
  input  A1in,
  input  B1in,
  input  DIR2,
  input  A2in,
  input  B2in,
  input  DIR3,
  input  A3in,
  input  B3in,
  input  DIR4,
  input  A4in,
  input  B4in,
  output B1out,
  output A1out,
  output B2out,
  output A2out,
  output B3out,
  output A3out,
  output B4out,
  output A4out
);

  wire and_1_out, and_2_out, and_3_out, and_4_out, and_5_out, and_6_out, and_7_out, and_8_out, not_1_out,
       not_2_out, not_3_out, not_4_out, not_5_out, not_6_out;

  not not_1 (not_1_out, nGBA);
  not not_2 (not_2_out, nGAB);
  not not_3 (not_3_out, DIR1);
  not not_4 (not_4_out, DIR2);
  not not_5 (not_5_out, DIR3);
  not not_6 (not_6_out, DIR4);
  and and_1 (and_1_out, not_2_out, DIR1);
  and and_2 (and_2_out, not_3_out, not_1_out);
  assign A1out = and_2_out ? ~B1in : 1'bz;  // Controlled_Inverter controlled_inverter_1
  and and_3 (and_3_out, not_2_out, DIR2);
  and and_4 (and_4_out, not_4_out, not_1_out);
  assign A2out = and_4_out ? ~B2in : 1'bz;  // Controlled_Inverter controlled_inverter_2
  and and_5 (and_5_out, not_2_out, DIR3);
  and and_6 (and_6_out, not_5_out, not_1_out);
  assign A3out = and_6_out ? ~B3in : 1'bz;  // Controlled_Inverter controlled_inverter_3
  and and_7 (and_7_out, not_2_out, DIR4);
  and and_8 (and_8_out, not_6_out, not_1_out);
  assign A4out = and_8_out ? ~B4in : 1'bz;  // Controlled_Inverter controlled_inverter_4
  assign B1out = and_1_out ? ~A1in : 1'bz;  // Controlled_Inverter controlled_inverter_5
  assign B2out = and_3_out ? ~A2in : 1'bz;  // Controlled_Inverter controlled_inverter_6
  assign B3out = and_5_out ? ~A3in : 1'bz;  // Controlled_Inverter controlled_inverter_7
  assign B4out = and_7_out ? ~A4in : 1'bz;  // Controlled_Inverter controlled_inverter_8

  // Notes on the sheet:
  //   74LS446
endmodule
