// Logisim project 74LS447.circ as structural Verilog: 1 circuit, main circuit 74LS447
module _74LS447 (
  input  A,
  input  B,
  input  C,
  input  D,
  input  nBI,
  input  nLT,
  input  nRBI,
  output a_2,
  output b_2,
  output c_2,
  output d_2,
  output nRBO,
  output e,
  output f,
  output g
);

  wire and_1_out, and_2_out, and_3_out, and_4_out, and_5_out, and_6_out, and_7_out, and_8_out, and_9_out,
       and_10_out, and_11_out, and_12_out, and_13_out, and_14_out, and_15_out, and_16_out, and_17_out,
       and_18_out, buffer_2_out, nand_1_out, nand_2_out, nand_3_out, nand_4_out, nand_5_out, nand_6_out,
       nand_7_out, nand_8_out, nor_1_out, nor_2_out, nor_3_out, nor_4_out, nor_5_out, nor_6_out, nor_7_out,
       not_1_out, not_2_out;

  nand nand_1 (nand_1_out, A, nLT);
  nand nand_2 (nand_2_out, B, nLT);
  nand nand_3 (nand_3_out, C, nLT);
  not not_1 (not_1_out, D);
  Pull_Resistor #(.pull(1)) pull_resistor_1 (.node(nBI));
  buf buffer_1 (nRBO, nand_8_out);
  not not_2 (not_2_out, nRBI);
  Pull_Resistor #(.pull(1)) pull_resistor_2 (.node(nRBI));
  nand nand_4 (nand_4_out, nand_1_out, and_1_out);
  nand nand_5 (nand_5_out, nand_2_out, and_1_out);
  nand nand_6 (nand_6_out, nand_3_out, and_1_out);
  nand nand_7 (nand_7_out, not_1_out, and_1_out);
  and and_1 (and_1_out, nBI, nand_8_out);
  nand nand_8 (nand_8_out, nLT, not_2_out, not_1_out, nand_3_out, nand_2_out, nand_1_out);
  and and_2 (and_2_out, nand_5_out, nand_7_out);
  and and_3 (and_3_out, nand_1_out, nand_2_out, nand_6_out);
  and and_4 (and_4_out, nand_4_out, nand_2_out, nand_3_out, not_1_out);
  and and_5 (and_5_out, nand_5_out, nand_7_out);
  and and_6 (and_6_out, nand_4_out, nand_2_out, nand_6_out);
  and and_7 (and_7_out, nand_1_out, nand_5_out, nand_6_out);
  and and_8 (and_8_out, nand_6_out, nand_7_out);
  and and_9 (and_9_out, nand_1_out, nand_5_out, nand_3_out);
  and and_10 (and_10_out, nand_4_out, nand_2_out, nand_3_out, not_1_out);
  and and_11 (and_11_out, nand_1_out, nand_2_out, nand_6_out);
  and and_12 (and_12_out, nand_4_out, nand_5_out, nand_6_out);
  buf buffer_2 (buffer_2_out, nand_4_out);
  and and_13 (and_13_out, nand_2_out, nand_6_out);
  and and_14 (and_14_out, nand_4_out, nand_5_out);
  and and_15 (and_15_out, nand_5_out, nand_3_out);
  and and_16 (and_16_out, nand_4_out, nand_3_out, not_1_out);
  and and_17 (and_17_out, nand_4_out, nand_5_out, nand_6_out);
  and and_18 (and_18_out, nand_2_out, nand_3_out, not_1_out, nLT);
  nor nor_1 (nor_1_out, and_2_out, and_3_out, and_4_out);
  not not_3 (a_2, nor_1_out);
  not not_4 (b_2, nor_2_out);
  nor nor_2 (nor_2_out, and_5_out, and_6_out, and_7_out);
  nor nor_3 (nor_3_out, and_8_out, and_9_out);
  not not_5 (c_2, nor_3_out);
  not not_6 (d_2, nor_4_out);
  nor nor_4 (nor_4_out, and_10_out, and_11_out, and_12_out);
  nor nor_5 (nor_5_out, buffer_2_out, and_13_out);
  not not_7 (e, nor_5_out);
  nor nor_6 (nor_6_out, and_14_out, and_15_out, and_16_out);
  not not_8 (f, nor_6_out);
  nor nor_7 (nor_7_out, and_17_out, and_18_out);
  not not_9 (g, nor_7_out);

  // Notes on the sheet:
  //   74LS447 is low voltage version of:
  //   74LS247
  //   buffer_1 drives only 0 and floats otherwise
  //   not_3 drives only 0 and floats otherwise
  //   not_4 drives only 0 and floats otherwise
  //   not_5 drives only 0 and floats otherwise
  //   not_6 drives only 0 and floats otherwise
  //   not_7 drives only 0 and floats otherwise
  //   not_8 drives only 0 and floats otherwise
  //   not_9 drives only 0 and floats otherwise
endmodule
