// Logisim project 74LS448.circ as structural Verilog: 2 circuits, main circuit 74LS448
module _74LS448 (
  input  nCS,
  input  nGA,
  input  nGB,
  input  nGC,
  input  S0,
  input  S1,
  input  A1,
  input  B1,
  input  C1,
  input  A2,
  input  B2,
  input  C2,
  input  A3,
  input  B3,
  input  C3,
  input  A4,
  input  B4,
  input  C4,
  output A1out,
  output B1out,
  output C1out,
  output A2out,
  output B2out,
  output C2out,
  output A3out,
  output B3out,
  output C3out,
  output A4out,
  output B4out,
  output C4out
);

  wire and_1_out, and_2_out, and_3_out, not_1_out, not_2_out, transceiver_inverted_and_non_inverted_1_aout,
       transceiver_inverted_and_non_inverted_1_bout, transceiver_inverted_and_non_inverted_1_cout,
       transceiver_inverted_and_non_inverted_2_aout, transceiver_inverted_and_non_inverted_2_bout,
       transceiver_inverted_and_non_inverted_2_cout, transceiver_inverted_and_non_inverted_3_aout,
       transceiver_inverted_and_non_inverted_3_bout, transceiver_inverted_and_non_inverted_3_cout,
       transceiver_inverted_and_non_inverted_4_aout, transceiver_inverted_and_non_inverted_4_bout,
       transceiver_inverted_and_non_inverted_4_cout, xnor_1_out;

  not not_1 (not_1_out, S0);
  not not_2 (not_2_out, S1);
  xnor xnor_1 (xnor_1_out, S0, S1);
  and and_1 (and_1_out, ~S1, ~nGC, ~nCS);  // AND_Gate
  transceiver_inverted_and_non_inverted transceiver_inverted_and_non_inverted_1 (
    .S1(S1), .nS1(not_2_out), .S0(S0), .nS0(not_1_out), .Ain(A1), .Bin(B1), .Cin(C1), .ENC(and_1_out),
    .ENB(and_2_out), .ENA(and_3_out), .Aout(transceiver_inverted_and_non_inverted_1_aout),
    .Bout(transceiver_inverted_and_non_inverted_1_bout), .Cout(transceiver_inverted_and_non_inverted_1_cout));
  transceiver_inverted_and_non_inverted transceiver_inverted_and_non_inverted_2 (
    .S1(S1), .nS1(not_2_out), .S0(S0), .nS0(not_1_out), .Ain(A2), .Bin(B2), .Cin(C2), .ENC(and_1_out),
    .ENB(and_2_out), .ENA(and_3_out), .Aout(transceiver_inverted_and_non_inverted_2_aout),
    .Bout(transceiver_inverted_and_non_inverted_2_bout), .Cout(transceiver_inverted_and_non_inverted_2_cout));
  transceiver_inverted_and_non_inverted transceiver_inverted_and_non_inverted_3 (
    .S1(S1), .nS1(not_2_out), .S0(S0), .nS0(not_1_out), .Ain(A3), .Bin(B3), .Cin(C3), .ENC(and_1_out),
    .ENB(and_2_out), .ENA(and_3_out), .Aout(transceiver_inverted_and_non_inverted_3_aout),
    .Bout(transceiver_inverted_and_non_inverted_3_bout), .Cout(transceiver_inverted_and_non_inverted_3_cout));
  transceiver_inverted_and_non_inverted transceiver_inverted_and_non_inverted_4 (
    .S1(S1), .nS1(not_2_out), .S0(S0), .nS0(not_1_out), .Ain(A4), .Bin(B4), .Cin(C4), .ENC(and_1_out),
    .ENB(and_2_out), .ENA(and_3_out), .Aout(transceiver_inverted_and_non_inverted_4_aout),
    .Bout(transceiver_inverted_and_non_inverted_4_bout), .Cout(transceiver_inverted_and_non_inverted_4_cout));
  and and_2 (and_2_out, ~S0, ~nGB, ~nCS);  // AND_Gate
  and and_3 (and_3_out, ~xnor_1_out, ~nGA, ~nCS);  // AND_Gate
  buf buffer_1 (A1out, transceiver_inverted_and_non_inverted_1_aout);
  buf buffer_2 (B1out, transceiver_inverted_and_non_inverted_1_bout);
  buf buffer_3 (C1out, transceiver_inverted_and_non_inverted_1_cout);
  buf buffer_4 (A2out, transceiver_inverted_and_non_inverted_2_aout);
  buf buffer_5 (B2out, transceiver_inverted_and_non_inverted_2_bout);
  buf buffer_6 (C2out, transceiver_inverted_and_non_inverted_2_cout);
  buf buffer_7 (A3out, transceiver_inverted_and_non_inverted_3_aout);
  buf buffer_8 (B3out, transceiver_inverted_and_non_inverted_3_bout);
  buf buffer_9 (C3out, transceiver_inverted_and_non_inverted_3_cout);
  buf buffer_10 (A4out, transceiver_inverted_and_non_inverted_4_aout);
  buf buffer_11 (B4out, transceiver_inverted_and_non_inverted_4_bout);
  buf buffer_12 (C4out, transceiver_inverted_and_non_inverted_4_cout);

  // Notes on the sheet:
  //   74LS448
  //   open-collector
  //   buffer_1 drives only 0 and floats otherwise
  //   buffer_2 drives only 0 and floats otherwise
  //   buffer_3 drives only 0 and floats otherwise
  //   buffer_4 drives only 0 and floats otherwise
  //   buffer_5 drives only 0 and floats otherwise
  //   buffer_6 drives only 0 and floats otherwise
  //   buffer_7 drives only 0 and floats otherwise
  //   buffer_8 drives only 0 and floats otherwise
  //   buffer_9 drives only 0 and floats otherwise
  //   buffer_10 drives only 0 and floats otherwise
  //   buffer_11 drives only 0 and floats otherwise
  //   buffer_12 drives only 0 and floats otherwise
endmodule

module transceiver_inverted_and_non_inverted (
  input  S1,
  input  nS1,
  input  S0,
  input  nS0,
  input  ENC,
  input  ENB,
  input  ENA,
  input  Ain,
  input  Bin,
  input  Cin,
  output Aout,
  output Bout,
  output Cout
);

  wire and_1_out, and_2_out, and_3_out, and_4_out, and_5_out, and_6_out, nor_1_out, nor_2_out, nor_3_out;

  and and_1 (and_1_out, S1, Bin, nS0);
  and and_2 (and_2_out, nS1, Cin, S0);
  and and_3 (and_3_out, nS1, Ain, nS0);
  and and_4 (and_4_out, nS1, ~Cin, S0);  // AND_Gate
  and and_5 (and_5_out, nS1, Ain, nS0);
  and and_6 (and_6_out, S1, ~Bin, nS0);  // AND_Gate
  nor nor_1 (nor_1_out, and_1_out, and_2_out);
  assign Aout = ENA ? nor_1_out : 1'bz;  // Controlled_Buffer controlled_buffer_1
  assign Bout = ENB ? nor_2_out : 1'bz;  // Controlled_Buffer controlled_buffer_2
  nor nor_2 (nor_2_out, and_3_out, and_4_out);
  nor nor_3 (nor_3_out, and_5_out, and_6_out);
  assign Cout = ENC ? nor_3_out : 1'bz;  // Controlled_Buffer controlled_buffer_3
endmodule
