// Logisim project 74LS450.circ as structural Verilog: 1 circuit, main circuit 74LS450
module _74LS450 (
  input  E0,
  input  E1,
  input  E2,
  input  E3,
  input  E4,
  input  E5,
  input  E6,
  input  E7,
  input  E8,
  input  E9,
  input  E10,
  input  E11,
  input  E12,
  input  E13,
  input  E14,
  input  E15,
  input  A,
  input  B,
  input  C,
  input  D,
  output Y,
  output W
);

  Multiplexer #(.select(4), .enable("false")) multiplexer_1 (
    .in0(E0), .in1(E1), .in2(E2), .in3(E3), .in4(E4), .in5(E5), .in6(E6), .in7(E7), .in8(E8), .in9(E9),
    .in10(E10), .in11(E11), .in12(E12), .in13(E13), .in14(E14), .in15(E15), .out(Y), .sel({D, C, B, A}));
  not not_1 (W, Y);

  // Notes on the sheet:
  //   74LS450
endmodule
