// Logisim project 74LS451.circ as structural Verilog: 1 circuit, main circuit 74LS451
module _74LS451 (
  input  _1D0,
  input  _2D0,
  input  _1D1,
  input  _2D1,
  input  _1D2,
  input  _2D2,
  input  _1D3,
  input  _2D3,
  input  _1D4,
  input  _2D4,
  input  _1D5,
  input  _2D5,
  input  _1D6,
  input  _2D6,
  input  _1D7,
  input  _2D7,
  input  A,
  input  B,
  input  C,
  input  S,
  output _1Y,
  output _2Y
);

  wire not_1_out;

  not not_1 (not_1_out, S);
  Multiplexer #(.select(3)) multiplexer_1 (
    .in0(_1D0), .in1(_1D1), .in2(_1D2), .in3(_1D3), .in4(_1D4), .in5(_1D5), .in6(_1D6), .in7(_1D7),
    .out(_1Y), .sel({C, B, A}), .en(not_1_out));
  Pull_Resistor #(.pull(1)) pull_resistor_1 (.node(_1Y));
  Pull_Resistor #(.pull(1)) pull_resistor_2 (.node(_2Y));
  Multiplexer #(.select(3)) multiplexer_2 (
    .in0(_2D0), .in1(_2D1), .in2(_2D2), .in3(_2D3), .in4(_2D4), .in5(_2D5), .in6(_2D6), .in7(_2D7),
    .out(_2Y), .sel({C, B, A}), .en(not_1_out));

  // Notes on the sheet:
  //   74LS451
endmodule
