// Logisim project 74LS453.circ as structural Verilog: 1 circuit, main circuit 74LS453
module _74LS453 (
  input  _1C0,
  input  _2C0,
  input  _3C0,
  input  _4C0,
  input  _1C1,
  input  _2C1,
  input  _3C1,
  input  _4C1,
  input  _1C2,
  input  _2C2,
  input  _3C2,
  input  _4C2,
  input  _1C3,
  input  _2C3,
  input  _3C3,
  input  _4C3,
  input  A,
  input  B,
  output _1Y,
  output _2Y,
  output _3Y,
  output _4Y
);

  Multiplexer #(.select(2), .width(4), .enable("false")) multiplexer_1 (
    .in0({_4C0, _3C0, _2C0, _1C0}), .in1({_4C1, _3C1, _2C1, _1C1}), .in2({_4C2, _3C2, _2C2, _1C2}),
    .in3({_4C3, _3C3, _2C3, _1C3}), .out({_4Y, _3Y, _2Y, _1Y}), .sel({B, A}));

  // Notes on the sheet:
  //   74LS453
endmodule
