// Logisim project 74LS49.circ as structural Verilog: 1 circuit, main circuit 74LS49
module _74LS49 (
  input  INPUT_A,
  input  INPUT_B,
  input  INPUT_C,
  input  INPUT_D,
  input  nBI,
  output a,
  output b,
  output c,
  output d,
  output e,
  output f,
  output g
);

  wire and_1_out, and_2_out, and_3_out, and_4_out, and_5_out, and_6_out, and_7_out, and_8_out, and_9_out,
       and_10_out, and_11_out, and_12_out, and_13_out, and_14_out, and_15_out, and_16_out, and_17_out,
       buffer_1_out, nand_1_out, nand_2_out, nand_3_out, nand_4_out, not_1_out, not_2_out, not_3_out,
       not_4_out, not_5_out, not_6_out;

  Pull_Resistor #(.pull(1)) pull_resistor_1 (.node(nBI));
  not not_1 (not_1_out, INPUT_A);
  not not_2 (not_2_out, INPUT_B);
  not not_3 (not_3_out, INPUT_C);
  not not_4 (not_4_out, INPUT_D);
  not not_5 (not_5_out, not_6_out);
  not not_6 (not_6_out, nBI);
  nand nand_1 (nand_1_out, not_1_out, not_5_out);
  nand nand_2 (nand_2_out, not_2_out, not_5_out);
  nand nand_3 (nand_3_out, not_3_out, not_5_out);
  nand nand_4 (nand_4_out, not_4_out, not_5_out);
  and and_1 (and_1_out, nand_2_out, nand_4_out);
  and and_2 (and_2_out, not_1_out, nand_3_out);
  and and_3 (and_3_out, nand_1_out, not_2_out, not_3_out, not_4_out);
  and and_4 (and_4_out, nand_2_out, nand_4_out);
  and and_5 (and_5_out, nand_1_out, not_2_out, nand_3_out);
  and and_6 (and_6_out, not_1_out, nand_2_out, nand_3_out);
  and and_7 (and_7_out, nand_3_out, nand_4_out);
  and and_8 (and_8_out, not_1_out, nand_2_out, not_3_out);
  and and_9 (and_9_out, nand_1_out, not_2_out, not_3_out);
  and and_10 (and_10_out, not_1_out, not_2_out, nand_3_out);
  and and_11 (and_11_out, nand_1_out, nand_2_out, nand_3_out);
  buf buffer_1 (buffer_1_out, nand_1_out);
  and and_12 (and_12_out, not_2_out, nand_3_out);
  and and_13 (and_13_out, nand_1_out, nand_2_out);
  and and_14 (and_14_out, nand_2_out, not_3_out);
  and and_15 (and_15_out, nand_1_out, not_3_out, not_4_out);
  and and_16 (and_16_out, nand_1_out, nand_2_out, nand_3_out);
  and and_17 (and_17_out, not_2_out, not_3_out, not_4_out);
  and and_18 (a, ~and_1_out, ~and_2_out, ~and_3_out);  // AND_Gate
  and and_19 (b, ~and_4_out, ~and_5_out, ~and_6_out);  // AND_Gate
  and and_20 (c, ~and_7_out, ~and_8_out);  // AND_Gate
  and and_21 (d, ~and_9_out, ~and_10_out, ~and_11_out);  // AND_Gate
  and and_22 (e, ~buffer_1_out, ~and_12_out);  // AND_Gate
  and and_23 (f, ~and_13_out, ~and_14_out, ~and_15_out);  // AND_Gate
  and and_24 (g, ~and_16_out, ~and_17_out);  // AND_Gate
  _7_Segment_Display u_7_segment_display_1 (.g(g), .f(f), .a(a), .b(b), .e(e), .d(d), .c(c));  // open: dp

  // Notes on the sheet:
  //   74LS49
endmodule
