// Logisim project 74LS51.circ as structural Verilog: 1 circuit, main circuit 74LS51
module _74LS51 (
  input  _1A,
  input  _1B,
  input  _1C,
  input  _1D,
  input  _1E,
  input  _1F,
  input  _2A,
  input  _2B,
  input  _2C,
  input  _2D,
  output _1Y,
  output _2Y
);

  wire and_1_out, and_2_out, and_3_out, and_4_out;

  and and_1 (and_1_out, _1A, _1B, _1C);
  and and_2 (and_2_out, _1D, _1E, _1F);
  and and_3 (and_3_out, _2A, _2B);
  and and_4 (and_4_out, _2C, _2D);
  nor nor_1 (_1Y, and_1_out, and_2_out);
  nor nor_2 (_2Y, and_3_out, and_4_out);

  // Notes on the sheet:
  //   74LS51
endmodule
