// Logisim project 74LS67.circ as structural Verilog: 1 circuit, main circuit 74LS67
module _74LS67 (
  input  J1,
  input  J2,
  input  J3,
  input  CLOCK,
  input  K1,
  input  K2,
  input  K3,
  input  nPRESET,
  input  nCLEAR,
  output Q,
  output nQ
);

  wire and_1_out, and_2_out, not_1_out, not_2_out;

  and and_1 (and_1_out, J1, J2, J3);
  and and_2 (and_2_out, K1, K2, K3);
  not not_1 (not_1_out, nCLEAR);
  not not_2 (not_2_out, nPRESET);
  J_K_Flip_Flop j_k_ff_1 (
    .J(and_1_out), .clk(CLOCK), .K(and_2_out), .Q(Q), .Qn(nQ), .preset(not_2_out), .reset(not_1_out));  // open: en

  // Notes on the sheet:
  //   74LS67
endmodule
