// Logisim project 74LS68.circ as structural Verilog: 1 circuit, main circuit 74LS68
module _74LS68 (
  input  _1_CLR,
  input  _2_CLR,
  input  _1CLKA,
  input  _2CLK,
  input  _1CLKB,
  output _1QA,
  output _2QA,
  output _1QB,
  output _2QB,
  output _1QC,
  output _2QC,
  output _1QD,
  output _2QD
);

  wire and_1_out, and_2_out, and_3_out, and_4_out, and_5_out, and_6_out, and_7_out, and_8_out, buffer_1_out,
       buffer_2_out, nor_1_out, nor_2_out, not_1_out, not_2_out, not_3_out, not_4_out, not_5_out, not_6_out,
       not_7_out, not_8_out, not_9_out, not_10_out, not_11_out, not_12_out, not_13_out, not_14_out,
       not_15_out, not_16_out, t_ff_2_qn, t_ff_3_qn, t_ff_4_qn, t_ff_6_qn, t_ff_7_qn, t_ff_8_qn;

  and and_1 (and_1_out, t_ff_2_qn, t_ff_4_qn);
  and and_2 (and_2_out, t_ff_3_qn, t_ff_4_qn);
  buf buffer_1 (buffer_1_out, _1_CLR);
  and and_3 (and_3_out, _1CLKB, t_ff_4_qn);
  and and_4 (and_4_out, _1CLKB, nor_1_out);
  nor nor_1 (nor_1_out, and_1_out, and_2_out);
  T_Flip_Flop t_ff_1 (.clk(not_1_out), .T(1'b1), .Q(_1QA), .reset(not_2_out));  // open: Qn, preset, en
  not not_1 (not_1_out, _1CLKA);
  not not_2 (not_2_out, buffer_1_out);
  T_Flip_Flop t_ff_2 (.clk(not_3_out), .T(1'b1), .Q(_1QB), .Qn(t_ff_2_qn), .reset(not_4_out));  // open: preset, en
  not not_3 (not_3_out, and_3_out);
  not not_4 (not_4_out, buffer_1_out);
  T_Flip_Flop t_ff_3 (.clk(not_5_out), .T(1'b1), .Q(_1QC), .Qn(t_ff_3_qn), .reset(not_6_out));  // open: preset, en
  not not_5 (not_5_out, _1QB);
  not not_6 (not_6_out, buffer_1_out);
  not not_7 (not_7_out, and_4_out);
  T_Flip_Flop t_ff_4 (.clk(not_7_out), .T(1'b1), .Q(_1QD), .Qn(t_ff_4_qn), .reset(not_8_out));  // open: preset, en
  not not_8 (not_8_out, buffer_1_out);
  and and_5 (and_5_out, t_ff_6_qn, t_ff_8_qn);
  and and_6 (and_6_out, t_ff_7_qn, t_ff_8_qn);
  buf buffer_2 (buffer_2_out, _2_CLR);
  and and_7 (and_7_out, _2QA, t_ff_8_qn);
  and and_8 (and_8_out, _2QA, nor_2_out);
  nor nor_2 (nor_2_out, and_5_out, and_6_out);
  not not_9 (not_9_out, _2CLK);
  not not_10 (not_10_out, and_7_out);
  not not_11 (not_11_out, _2QB);
  not not_12 (not_12_out, and_8_out);
  T_Flip_Flop t_ff_5 (.clk(not_9_out), .T(1'b1), .Q(_2QA), .reset(not_13_out));  // open: Qn, preset, en
  not not_13 (not_13_out, buffer_2_out);
  T_Flip_Flop t_ff_6 (.clk(not_10_out), .T(1'b1), .Q(_2QB), .Qn(t_ff_6_qn), .reset(not_14_out));  // open: preset, en
  not not_14 (not_14_out, buffer_2_out);
  T_Flip_Flop t_ff_7 (.clk(not_11_out), .T(1'b1), .Q(_2QC), .Qn(t_ff_7_qn), .reset(not_15_out));  // open: preset, en
  not not_15 (not_15_out, buffer_2_out);
  T_Flip_Flop t_ff_8 (.clk(not_12_out), .T(1'b1), .Q(_2QD), .Qn(t_ff_8_qn), .reset(not_16_out));  // open: preset, en
  not not_16 (not_16_out, buffer_2_out);

  // Notes on the sheet:
  //   74LS68
endmodule
