// Logisim project 74LS69.circ as structural Verilog: 1 circuit, main circuit 74LS69
module _74LS69 (
  input  _1CLKA,
  input  _2CLK,
  input  _1CLKB,
  input  _1_CLR,
  input  _2_CLR,
  output _1QA,
  output _2QA,
  output _1QB,
  output _2QB,
  output _1QC,
  output _2QC,
  output _1QD,
  output _2QD
);

  wire not_1_out, not_2_out, not_3_out, not_4_out, not_5_out, not_6_out, not_7_out, not_8_out, not_9_out,
       not_10_out, not_11_out, not_12_out, not_13_out, not_14_out, not_15_out, not_16_out;

  not not_1 (not_1_out, _1CLKA);
  not not_2 (not_2_out, _1CLKB);
  not not_3 (not_3_out, _1QB);
  not not_4 (not_4_out, _1QC);
  T_Flip_Flop t_ff_1 (.clk(not_1_out), .T(1'b1), .Q(_1QA), .reset(not_5_out));  // open: Qn, preset, en
  not not_5 (not_5_out, _1_CLR);
  T_Flip_Flop t_ff_2 (.clk(not_2_out), .T(1'b1), .Q(_1QB), .reset(not_6_out));  // open: Qn, preset, en
  not not_6 (not_6_out, _1_CLR);
  T_Flip_Flop t_ff_3 (.clk(not_3_out), .T(1'b1), .Q(_1QC), .reset(not_7_out));  // open: Qn, preset, en
  not not_7 (not_7_out, _1_CLR);
  T_Flip_Flop t_ff_4 (.clk(not_4_out), .T(1'b1), .Q(_1QD), .reset(not_8_out));  // open: Qn, preset, en
  not not_8 (not_8_out, _1_CLR);
  T_Flip_Flop t_ff_5 (.clk(not_9_out), .T(1'b1), .Q(_2QA), .reset(not_10_out));  // open: Qn, preset, en
  not not_9 (not_9_out, _2CLK);
  not not_10 (not_10_out, _2_CLR);
  not not_11 (not_11_out, _2QA);
  T_Flip_Flop t_ff_6 (.clk(not_11_out), .T(1'b1), .Q(_2QB), .reset(not_12_out));  // open: Qn, preset, en
  not not_12 (not_12_out, _2_CLR);
  not not_13 (not_13_out, _2QB);
  T_Flip_Flop t_ff_7 (.clk(not_13_out), .T(1'b1), .Q(_2QC), .reset(not_14_out));  // open: Qn, preset, en
  not not_14 (not_14_out, _2_CLR);
  T_Flip_Flop t_ff_8 (.clk(not_15_out), .T(1'b1), .Q(_2QD), .reset(not_16_out));  // open: Qn, preset, en
  not not_15 (not_15_out, _2QC);
  not not_16 (not_16_out, _2_CLR);

  // Notes on the sheet:
  //   74LS69
endmodule
