// Logisim project 74LS75.circ as structural Verilog: 1 circuit, main circuit 74LS75
module _74LS75 (
  input  _1C_2C,
  input  _1D,
  input  _2D,
  input  _3C_4C,
  input  _3D,
  input  _4D,
  output _1Q,
  output _1_Q,
  output _2Q,
  output _2_Q,
  output _3Q,
  output _3_Q,
  output _4Q,
  output _4_Q
);

  D_Flip_Flop #(.trigger("high")) d_ff_1 (.clk(_1C_2C), .D(_1D), .Q(_1Q), .Qn(_1_Q));  // open: preset, en, reset
  D_Flip_Flop #(.trigger("high")) d_ff_2 (.clk(_1C_2C), .D(_2D), .Q(_2Q), .Qn(_2_Q));  // open: preset, en, reset
  D_Flip_Flop #(.trigger("high")) d_ff_3 (.clk(_3C_4C), .D(_3D), .Q(_3Q), .Qn(_3_Q));  // open: preset, en, reset
  D_Flip_Flop #(.trigger("high")) d_ff_4 (.D(_4D), .Q(_4Q), .Qn(_4_Q));  // open: clk, preset, en, reset

  // Notes on the sheet:
  //   74LS75
endmodule
