// Logisim project 74LS78.circ as structural Verilog: 1 circuit, main circuit 74LS78
module _74LS78 (
  input  CLK,
  input  nCLR,
  input  _1J,
  input  _1K,
  input  _1_PRE,
  input  _2J,
  input  _2K,
  input  _2_PRE,
  output _1Q,
  output _1_Q,
  output _2Q,
  output _2_Q
);

  wire not_1_out, not_2_out, not_3_out, not_4_out;

  J_K_Flip_Flop #(.trigger("falling")) Falling_Edge (
    .J(_1J), .clk(CLK), .K(_1K), .Q(_1Q), .Qn(_1_Q), .preset(not_1_out), .reset(not_2_out));  // open: en
  not not_1 (not_1_out, _1_PRE);
  not not_2 (not_2_out, nCLR);
  J_K_Flip_Flop #(.trigger("falling")) Falling_Edge_2 (
    .J(_2J), .clk(CLK), .K(_2K), .Q(_2Q), .Qn(_2_Q), .preset(not_3_out), .reset(not_4_out));  // open: en
  not not_3 (not_3_out, _2_PRE);
  not not_4 (not_4_out, nCLR);

  // Notes on the sheet:
  //   74LS78
endmodule
