// Logisim project 74LS85.circ as structural Verilog: 1 circuit, main circuit 74LS85
module _74LS85 (
  input  A3,
  input  B3,
  input  A2,
  input  B2,
  input  A_B,
  input  A_B_2,
  input  A_B_3,
  input  A1,
  input  B1,
  input  A0,
  input  B0,
  output A_B_4,
  output A_B_5,
  output A_B_6
);

  wire and_1_out, and_2_out, and_3_out, and_4_out, and_5_out, and_6_out, and_7_out, and_8_out, and_9_out,
       and_10_out, and_11_out, and_12_out, and_13_out, and_14_out, and_15_out, and_16_out, and_17_out,
       and_18_out, and_19_out, and_20_out, nand_1_out, nand_2_out, nand_3_out, nand_4_out, nor_1_out,
       nor_2_out, nor_3_out, nor_4_out;

  nand nand_1 (nand_1_out, A3, B3);
  nand nand_2 (nand_2_out, A2, B2);
  nand nand_3 (nand_3_out, A1, B1);
  nand nand_4 (nand_4_out, A0, B0);
  and and_1 (and_1_out, A3, nand_1_out);
  and and_2 (and_2_out, nand_1_out, B3);
  and and_3 (and_3_out, A2, nand_2_out);
  and and_4 (and_4_out, nand_2_out, B2);
  and and_5 (and_5_out, A1, nand_3_out);
  and and_6 (and_6_out, nand_3_out, B1);
  and and_7 (and_7_out, A0, nand_4_out);
  and and_8 (and_8_out, nand_4_out, B0);
  nor nor_1 (nor_1_out, and_1_out, and_2_out);
  nor nor_2 (nor_2_out, and_3_out, and_4_out);
  nor nor_3 (nor_3_out, and_5_out, and_6_out);
  nor nor_4 (nor_4_out, and_7_out, and_8_out);
  and and_9 (and_9_out, B3, nand_1_out);
  and and_10 (and_10_out, B2, nand_2_out, nor_1_out);
  and and_11 (and_11_out, B1, nand_3_out, nor_1_out, nor_2_out);
  and and_12 (and_12_out, B0, nand_4_out, nor_1_out, nor_2_out, nor_3_out);
  and and_13 (and_13_out, nor_1_out, nor_2_out, nor_3_out, nor_4_out, A_B);
  and and_14 (and_14_out, nor_1_out, nor_2_out, nor_3_out, nor_4_out, A_B_2);
  and and_15 (and_15_out, A_B_2, nor_4_out, nor_3_out, nor_2_out, nor_1_out);
  and and_16 (and_16_out, A_B_3, nor_4_out, nor_2_out, nor_3_out, nor_1_out);
  and and_17 (and_17_out, nor_3_out, nor_2_out, nor_1_out, nand_4_out, A0);
  and and_18 (and_18_out, nor_2_out, nor_1_out, nand_3_out, A1);
  and and_19 (and_19_out, nor_1_out, nand_2_out, A2);
  and and_20 (and_20_out, nand_1_out, A3);
  and and_21 (A_B_4, ~and_9_out, ~and_10_out, ~and_11_out, ~and_12_out, ~and_13_out, ~and_14_out);  // AND_Gate
  and and_22 (A_B_5, nor_1_out, nor_2_out, A_B_2, nor_3_out, nor_4_out);
  and and_23 (A_B_6, ~and_15_out, ~and_16_out, ~and_17_out, ~and_18_out, ~and_19_out, ~and_20_out);  // AND_Gate
endmodule
