// Logisim project 74LS87.circ as structural Verilog: 1 circuit, main circuit 74LS87
module _74LS87 (
  input  A1,
  input  A2,
  input  A3,
  input  A4,
  input  B,
  input  C,
  output Y1,
  output Y2,
  output Y3,
  output Y4
);

  wire nand_1_out, nand_2_out, nand_3_out, nand_4_out, not_1_out, not_2_out, not_3_out, not_4_out, not_5_out,
       not_6_out;

  not not_1 (not_1_out, B);
  not not_2 (not_2_out, C);
  nand nand_1 (nand_1_out, A1, not_1_out);
  not not_3 (not_3_out, not_2_out);
  nand nand_2 (nand_2_out, A2, not_1_out);
  not not_4 (not_4_out, not_2_out);
  nand nand_3 (nand_3_out, A3, not_1_out);
  not not_5 (not_5_out, not_2_out);
  nand nand_4 (nand_4_out, A4, not_1_out);
  not not_6 (not_6_out, not_2_out);
  xor xor_1 (Y1, nand_1_out, not_3_out);
  xor xor_2 (Y2, nand_2_out, not_4_out);
  xor xor_3 (Y3, nand_3_out, not_5_out);
  xor xor_4 (Y4, nand_4_out, not_6_out);

  // Notes on the sheet:
  //   74LS87
endmodule
