// Logisim project 74LS90.circ as structural Verilog: 4 circuits, main circuit 74LS90
module _74LS90 (
  input  R9_1,
  input  R9_2,
  input  CKA,
  input  CKB,
  input  R0_1,
  input  R0_2,
  output QA,
  output QB,
  output QC,
  output QD
);

  wire and_1_out, n74ls90_sr_n1n0_1_nq, nand_1_out, nand_2_out, or_1_out, or_2_out;

  nand nand_1 (nand_1_out, R9_1, R9_2);
  nand nand_2 (nand_2_out, R0_1, R0_2);
  and and_1 (and_1_out, QC, QB);
  _74LS90_JK_n1n0 u_74ls90_jk_n1n0_1 (.J(1'b1), .CLK(CKA), .K(1'b1), .Q(QA), .n1(nand_1_out), .n0(nand_2_out));
  _74LS90_JK_0 u_74ls90_jk_0_1 (.J(n74ls90_sr_n1n0_1_nq), .CLK(CKB), .K(1'b1), .Q(QB), ._0(or_1_out));
  or or_1 (or_1_out, ~nand_2_out, ~nand_1_out);  // OR_Gate
  _74LS90_JK_0 u_74ls90_jk_0_2 (.J(1'b1), .CLK(QB), .K(1'b1), .Q(QC), ._0(or_2_out));
  or or_2 (or_2_out, ~nand_2_out, ~nand_1_out);  // OR_Gate
  _74LS90_SR_n1n0 u_74ls90_sr_n1n0_1 (
    .S(and_1_out), .CLK(CKB), .R(QD), .Q(QD), .nQ(n74ls90_sr_n1n0_1_nq), .n1(nand_1_out), .n0(nand_2_out));

  // Notes on the sheet:
  //   74LS90
endmodule

module _74LS90_JK_n1n0 (
  input  J,
  input  CLK,
  input  K,
  input  n1,
  input  n0,
  output Q
);

  wire and_1_out, and_2_out, not_1_out, not_2_out, not_3_out, or_1_out;

  not not_1 (not_1_out, CLK);
  or or_1 (or_1_out, not_2_out, and_1_out);
  and and_1 (and_1_out, not_2_out, not_3_out);
  not not_2 (not_2_out, n1);
  J_K_Flip_Flop j_k_ff_1 (.J(J), .clk(not_1_out), .K(K), .Q(Q), .preset(or_1_out), .reset(and_2_out));  // open: Qn, en
  and and_2 (and_2_out, not_3_out, n1);
  not not_3 (not_3_out, n0);

  // Notes on the sheet:
  //   n1 wins!
endmodule

module _74LS90_JK_0 (
  input  J,
  input  CLK,
  input  K,
  input  _0,
  output Q
);

  wire not_1_out;

  J_K_Flip_Flop j_k_ff_1 (.J(J), .clk(not_1_out), .K(K), .Q(Q), .reset(_0));  // open: Qn, preset, en
  not not_1 (not_1_out, CLK);
endmodule

module _74LS90_SR_n1n0 (
  input  S,
  input  CLK,
  input  R,
  input  n1,
  input  n0,
  output Q,
  output nQ
);

  wire and_1_out, and_2_out, not_1_out, not_2_out, not_3_out, or_1_out;

  not not_1 (not_1_out, CLK);
  S_R_Flip_Flop s_r_ff_1 (
    .S(S), .clk(not_1_out), .R(R), .Q(Q), .Qn(nQ), .preset(or_1_out), .reset(and_2_out));  // open: en
  or or_1 (or_1_out, not_3_out, and_1_out);
  and and_1 (and_1_out, not_3_out, not_2_out);
  and and_2 (and_2_out, not_2_out, n1);
  not not_2 (not_2_out, n0);
  not not_3 (not_3_out, n1);

  // Notes on the sheet:
  //   n1 wins!
endmodule
