// Logisim project 74LS91.circ as structural Verilog: 1 circuit, main circuit 74LS91
module _74LS91 (
  input  A,
  input  B,
  input  CLOCK,
  output QH,
  output nQH
);

  wire nand_1_out, not_1_out, s_r_ff_1_q, s_r_ff_1_qn, s_r_ff_2_q, s_r_ff_2_qn, s_r_ff_3_q, s_r_ff_3_qn,
       s_r_ff_4_q, s_r_ff_4_qn, s_r_ff_5_q, s_r_ff_5_qn, s_r_ff_6_q, s_r_ff_6_qn, s_r_ff_7_q, s_r_ff_7_qn;

  nand nand_1 (nand_1_out, A, B);
  not not_1 (not_1_out, nand_1_out);
  S_R_Flip_Flop s_r_ff_1 (
    .S(not_1_out), .clk(CLOCK), .R(nand_1_out), .Q(s_r_ff_1_q), .Qn(s_r_ff_1_qn));  // open: preset, reset, en
  S_R_Flip_Flop s_r_ff_2 (
    .S(s_r_ff_1_q), .clk(CLOCK), .R(s_r_ff_1_qn), .Q(s_r_ff_2_q), .Qn(s_r_ff_2_qn));  // open: preset, reset, en
  S_R_Flip_Flop s_r_ff_3 (
    .S(s_r_ff_2_q), .clk(CLOCK), .R(s_r_ff_2_qn), .Q(s_r_ff_3_q), .Qn(s_r_ff_3_qn));  // open: preset, reset, en
  S_R_Flip_Flop s_r_ff_4 (
    .S(s_r_ff_3_q), .clk(CLOCK), .R(s_r_ff_3_qn), .Q(s_r_ff_4_q), .Qn(s_r_ff_4_qn));  // open: preset, reset, en
  S_R_Flip_Flop s_r_ff_5 (
    .S(s_r_ff_4_q), .clk(CLOCK), .R(s_r_ff_4_qn), .Q(s_r_ff_5_q), .Qn(s_r_ff_5_qn));  // open: preset, reset, en
  S_R_Flip_Flop s_r_ff_6 (
    .S(s_r_ff_5_q), .clk(CLOCK), .R(s_r_ff_5_qn), .Q(s_r_ff_6_q), .Qn(s_r_ff_6_qn));  // open: preset, reset, en
  S_R_Flip_Flop s_r_ff_7 (
    .S(s_r_ff_6_q), .clk(CLOCK), .R(s_r_ff_6_qn), .Q(s_r_ff_7_q), .Qn(s_r_ff_7_qn));  // open: preset, reset, en
  S_R_Flip_Flop s_r_ff_8 (.S(s_r_ff_7_q), .clk(CLOCK), .R(s_r_ff_7_qn), .Q(QH), .Qn(nQH));  // open: preset, reset, en

  // Notes on the sheet:
  //   74LS91
endmodule
