// Logisim project 74LS94.circ as structural Verilog: 1 circuit, main circuit 74LS94
module _74LS94 (
  input  P1A,
  input  P2A,
  input  P1B,
  input  P2B,
  input  P1C,
  input  P2C,
  input  P1D,
  input  P2D,
  input  PE2,
  input  PE1,
  input  INPUT,
  input  CLOCK,
  input  CLEAR,
  output OUTPUT
);

  wire _1_2_out, _1_3_out, _1_4_out, _1_out, _2_2_out, _2_3_out, _2_4_out, _2_out, A_q, A_qn, B_q, B_qn, C_q,
       C_qn, not_1_out, or_1_out, or_2_out, or_3_out, or_4_out;

  not not_1 (not_1_out, INPUT);
  and _2 (_2_out, PE2, P2A);
  and _1 (_1_out, P1A, PE1);
  or or_1 (or_1_out, _1_out, _2_out);
  and _2_2 (_2_2_out, PE2, P2B);
  and _1_2 (_1_2_out, P1B, PE1);
  or or_2 (or_2_out, _1_2_out, _2_2_out);
  S_R_Flip_Flop A (
    .S(INPUT), .clk(CLOCK), .R(not_1_out), .Q(A_q), .Qn(A_qn), .preset(or_1_out), .reset(CLEAR));  // open: en
  and _1_3 (_1_3_out, P1C, PE1);
  or or_3 (or_3_out, _1_3_out, _2_3_out);
  S_R_Flip_Flop B (.S(A_q), .clk(CLOCK), .R(A_qn), .Q(B_q), .Qn(B_qn), .preset(or_2_out), .reset(CLEAR));  // open: en
  and _1_4 (_1_4_out, P1D, PE1);
  and _2_3 (_2_3_out, PE2, P2C);
  S_R_Flip_Flop C (.S(B_q), .clk(CLOCK), .R(B_qn), .Q(C_q), .Qn(C_qn), .preset(or_3_out), .reset(CLEAR));  // open: en
  and _2_4 (_2_4_out, PE2, P2D);
  or or_4 (or_4_out, _1_4_out, _2_4_out);
  S_R_Flip_Flop D (.S(C_q), .clk(CLOCK), .R(C_qn), .Q(OUTPUT), .preset(or_4_out), .reset(CLEAR));  // open: Qn, en

  // Notes on the sheet:
  //   74LS94
endmodule
