// Logisim project 74LS95.circ as structural Verilog: 1 circuit, main circuit 74LS95
module _74LS95 (
  input  P0,
  input  P1,
  input  P2,
  input  P3,
  input  S,
  input  Ds,
  input  nCP1,
  input  nCP2,
  output Q0,
  output Q1,
  output Q2,
  output Q3
);

  wire and_1_out, and_2_out, and_3_out, and_4_out, and_5_out, and_6_out, and_7_out, and_8_out, and_9_out,
       and_10_out, nor_1_out, nor_2_out, nor_3_out, nor_4_out, not_1_out, not_2_out, not_3_out, not_4_out,
       not_5_out, not_6_out, not_7_out, not_8_out, not_9_out, not_10_out, or_1_out;

  not not_1 (not_1_out, S);
  not not_2 (not_2_out, not_1_out);
  and and_1 (and_1_out, Ds, not_1_out);
  and and_2 (and_2_out, not_1_out, nCP1);
  or or_1 (or_1_out, and_2_out, and_3_out);
  and and_3 (and_3_out, S, nCP2);
  and and_4 (and_4_out, not_2_out, P0);
  nor nor_1 (nor_1_out, and_1_out, and_4_out);
  not not_3 (not_3_out, nor_1_out);
  not not_4 (not_4_out, or_1_out);
  and and_5 (and_5_out, Q0, not_1_out);
  nor nor_2 (nor_2_out, and_5_out, and_6_out);
  S_R_Flip_Flop s_r_ff_1 (.S(not_3_out), .clk(not_4_out), .R(nor_1_out), .Q(Q0));  // open: Qn, preset, reset, en
  and and_6 (and_6_out, not_2_out, P1);
  not not_5 (not_5_out, nor_2_out);
  S_R_Flip_Flop s_r_ff_2 (.S(not_5_out), .clk(not_6_out), .R(nor_2_out), .Q(Q1));  // open: Qn, preset, reset, en
  not not_6 (not_6_out, or_1_out);
  and and_7 (and_7_out, not_2_out, P2);
  and and_8 (and_8_out, Q1, not_1_out);
  nor nor_3 (nor_3_out, and_8_out, and_7_out);
  not not_7 (not_7_out, nor_3_out);
  not not_8 (not_8_out, or_1_out);
  and and_9 (and_9_out, Q2, not_1_out);
  S_R_Flip_Flop s_r_ff_3 (.S(not_7_out), .clk(not_8_out), .R(nor_3_out), .Q(Q2));  // open: Qn, preset, reset, en
  and and_10 (and_10_out, not_2_out, P3);
  nor nor_4 (nor_4_out, and_9_out, and_10_out);
  not not_9 (not_9_out, nor_4_out);
  not not_10 (not_10_out, or_1_out);
  S_R_Flip_Flop s_r_ff_4 (.S(not_9_out), .clk(not_10_out), .R(nor_4_out), .Q(Q3));  // open: Qn, preset, reset, en

  // Notes on the sheet:
  //   74LS95
endmodule
