// Logisim project 74LS96.circ as structural Verilog: 1 circuit, main circuit 74LS96
module _74LS96 (
  input  PRESET_A,
  input  PRESET_B,
  input  PRESET_C,
  input  PRESET_D,
  input  PRESET_E,
  input  PRESET_ENABLE,
  input  SERIAL_INPUT,
  input  nCLEAR,
  input  CLOCK,
  output QA,
  output QB,
  output QC,
  output QD,
  output QE
);

  wire and_1_out, and_2_out, and_3_out, and_4_out, and_5_out, not_1_out, not_2_out, not_3_out, not_4_out,
       not_5_out, not_6_out, s_r_ff_1_qn, s_r_ff_2_qn, s_r_ff_3_qn, s_r_ff_4_qn;

  and and_1 (and_1_out, PRESET_A, PRESET_ENABLE);
  not not_1 (not_1_out, SERIAL_INPUT);
  not not_2 (not_2_out, nCLEAR);
  and and_2 (and_2_out, PRESET_B, PRESET_ENABLE);
  S_R_Flip_Flop s_r_ff_1 (
    .S(SERIAL_INPUT), .clk(CLOCK), .R(not_1_out), .Q(QA), .Qn(s_r_ff_1_qn), .preset(and_1_out),
    .reset(not_2_out));  // open: en
  not not_3 (not_3_out, nCLEAR);
  and and_3 (and_3_out, PRESET_C, PRESET_ENABLE);
  S_R_Flip_Flop s_r_ff_2 (
    .S(QB), .clk(CLOCK), .R(s_r_ff_3_qn), .Q(QC), .Qn(s_r_ff_2_qn), .preset(and_3_out), .reset(not_4_out));  // open: en
  S_R_Flip_Flop s_r_ff_3 (
    .S(QA), .clk(CLOCK), .R(s_r_ff_1_qn), .Q(QB), .Qn(s_r_ff_3_qn), .preset(and_2_out), .reset(not_3_out));  // open: en
  not not_4 (not_4_out, nCLEAR);
  and and_4 (and_4_out, PRESET_D, PRESET_ENABLE);
  S_R_Flip_Flop s_r_ff_4 (
    .S(QC), .clk(CLOCK), .R(s_r_ff_2_qn), .Q(QD), .Qn(s_r_ff_4_qn), .preset(and_4_out), .reset(not_5_out));  // open: en
  not not_5 (not_5_out, nCLEAR);
  and and_5 (and_5_out, PRESET_E, PRESET_ENABLE);
  S_R_Flip_Flop s_r_ff_5 (
    .S(QD), .clk(CLOCK), .R(s_r_ff_4_qn), .Q(QE), .preset(and_5_out), .reset(not_6_out));  // open: Qn, en
  not not_6 (not_6_out, nCLEAR);

  // Notes on the sheet:
  //   74LS96
endmodule
