// Logisim project 74LS97.circ as structural Verilog: 1 circuit, main circuit 74LS97
module _74LS97 (
  input  ENABLE_INPUT,
  input  CLOCK,
  input  CLEAR,
  input  STROBE,
  input  B5,
  input  B4,
  input  B3,
  input  B2,
  input  B1,
  input  B0,
  input  UNITY_CASCADE_INPUT,
  output ENABLE_OUTPUT,
  output Y_OUTPUT,
  output Z_OUTPUT
);

  wire A_out, and_1_out, and_2_out, and_3_out, and_4_out, and_5_out, and_6_out, B_out, C_out, D_out, E_out,
       F_out, not_1_out, t_ff_1_q, t_ff_1_qn, t_ff_2_q, t_ff_2_qn, t_ff_3_q, t_ff_3_qn, t_ff_4_q, t_ff_4_qn,
       t_ff_5_q, t_ff_5_qn, t_ff_6_q, t_ff_6_qn;

  not not_1 (not_1_out, ENABLE_INPUT);
  and and_1 (and_1_out, ~CLOCK, ~STROBE);  // AND_Gate
  T_Flip_Flop t_ff_1 (.clk(CLOCK), .T(not_1_out), .Q(t_ff_1_q), .Qn(t_ff_1_qn), .reset(CLEAR));  // open: preset, en
  and F (F_out, B5, and_1_out, t_ff_1_qn);
  T_Flip_Flop t_ff_2 (.clk(CLOCK), .T(and_2_out), .Q(t_ff_2_q), .Qn(t_ff_2_qn), .reset(CLEAR));  // open: preset, en
  and and_2 (and_2_out, t_ff_1_q, not_1_out);
  and E (E_out, B4, and_1_out, t_ff_1_q, t_ff_2_qn);
  and and_3 (and_3_out, t_ff_2_q, not_1_out, t_ff_1_q);
  and D (D_out, B3, and_1_out, t_ff_1_q, t_ff_2_q, t_ff_3_qn);
  T_Flip_Flop t_ff_3 (.clk(CLOCK), .T(and_3_out), .Q(t_ff_3_q), .Qn(t_ff_3_qn), .reset(CLEAR));  // open: preset, en
  nor nor_1 (Z_OUTPUT, F_out, E_out, D_out, C_out, B_out, A_out);
  T_Flip_Flop t_ff_4 (.clk(CLOCK), .T(and_4_out), .Q(t_ff_4_q), .Qn(t_ff_4_qn), .reset(CLEAR));  // open: preset, en
  and and_4 (and_4_out, not_1_out, t_ff_3_q, t_ff_1_q, t_ff_2_q);
  and C (C_out, B2, and_1_out, t_ff_1_q, t_ff_2_q, t_ff_3_q, t_ff_4_qn);
  or or_1 (Y_OUTPUT, ~Z_OUTPUT, ~UNITY_CASCADE_INPUT);  // OR_Gate
  and and_5 (and_5_out, not_1_out, t_ff_4_q, t_ff_1_q, t_ff_2_q, t_ff_3_q);
  T_Flip_Flop t_ff_5 (.clk(CLOCK), .T(and_5_out), .Q(t_ff_5_q), .Qn(t_ff_5_qn), .reset(CLEAR));  // open: preset, en
  and B (B_out, B1, and_1_out, t_ff_1_q, t_ff_2_q, t_ff_3_q, t_ff_4_q, t_ff_5_qn);
  and and_6 (and_6_out, not_1_out, t_ff_1_q, t_ff_5_q, t_ff_2_q, t_ff_3_q, t_ff_4_q);
  and A (A_out, B0, and_1_out, t_ff_1_q, t_ff_2_q, t_ff_3_q, t_ff_4_q, t_ff_5_q, t_ff_6_qn);
  T_Flip_Flop t_ff_6 (.clk(CLOCK), .T(and_6_out), .Q(t_ff_6_q), .Qn(t_ff_6_qn), .reset(CLEAR));  // open: preset, en
  nand nand_1 (ENABLE_OUTPUT, not_1_out, t_ff_1_q, t_ff_2_q, t_ff_3_q, t_ff_4_q, t_ff_5_q, t_ff_6_q);
endmodule
