// Logisim project 74LS99.circ as structural Verilog: 1 circuit, main circuit 74LS99
module _74LS99 (
  input  J,
  input  nK,
  input  A,
  input  B,
  input  C,
  input  D,
  input  M_MODE,
  input  nCLK1_RS,
  input  nCLK2_LS,
  output QA,
  output QB,
  output QC,
  output QD,
  output nQD
);

  wire and_1_out, and_2_out, and_3_out, and_4_out, and_5_out, and_6_out, and_7_out, and_8_out, and_9_out,
       and_10_out, and_11_out, and_12_out, buffer_1_out, buffer_2_out, nor_1_out, nor_2_out, nor_3_out,
       nor_4_out, nor_5_out, not_1_out, not_2_out, not_3_out, not_4_out, not_5_out, not_6_out, not_7_out,
       not_8_out, not_9_out, not_10_out, not_11_out, or_1_out, s_r_ff_1_qn;

  not not_1 (not_1_out, nK);
  not not_2 (not_2_out, A);
  not not_3 (not_3_out, not_4_out);
  not not_4 (not_4_out, M_MODE);
  and and_1 (and_1_out, s_r_ff_1_qn, J, or_1_out, not_4_out);
  and and_2 (and_2_out, or_1_out, not_3_out, A);
  and and_3 (and_3_out, not_1_out, QA, or_1_out, not_4_out);
  and and_4 (and_4_out, or_1_out, not_3_out, not_2_out);
  and and_5 (and_5_out, QA, not_4_out);
  and and_6 (and_6_out, not_3_out, B);
  and and_7 (and_7_out, QB, not_4_out);
  and and_8 (and_8_out, not_3_out, C);
  and and_9 (and_9_out, QC, not_4_out);
  and and_10 (and_10_out, not_3_out, D);
  and and_11 (and_11_out, not_4_out, nCLK1_RS);
  and and_12 (and_12_out, M_MODE, nCLK2_LS);
  nor nor_1 (nor_1_out, and_1_out, and_2_out, buffer_1_out);
  buf buffer_1 (buffer_1_out, nor_2_out);
  buf buffer_2 (buffer_2_out, nor_1_out);
  nor nor_2 (nor_2_out, buffer_2_out, and_3_out, and_4_out);
  nor nor_3 (nor_3_out, and_5_out, and_6_out);
  nor nor_4 (nor_4_out, and_7_out, and_8_out);
  nor nor_5 (nor_5_out, and_9_out, and_10_out);
  or or_1 (or_1_out, and_11_out, and_12_out);
  S_R_Flip_Flop s_r_ff_1 (
    .S(nor_2_out), .clk(not_5_out), .R(nor_1_out), .Q(QA), .Qn(s_r_ff_1_qn));  // open: preset, reset, en
  not not_5 (not_5_out, or_1_out);
  S_R_Flip_Flop s_r_ff_2 (.S(not_6_out), .clk(not_7_out), .R(nor_3_out), .Q(QB));  // open: Qn, preset, reset, en
  not not_6 (not_6_out, nor_3_out);
  not not_7 (not_7_out, or_1_out);
  S_R_Flip_Flop s_r_ff_3 (.S(not_8_out), .clk(not_9_out), .R(nor_4_out), .Q(QC));  // open: Qn, preset, reset, en
  not not_8 (not_8_out, nor_4_out);
  not not_9 (not_9_out, or_1_out);
  S_R_Flip_Flop s_r_ff_4 (
    .S(not_10_out), .clk(not_11_out), .R(nor_5_out), .Q(QD), .Qn(nQD));  // open: preset, reset, en
  not not_10 (not_10_out, nor_5_out);
  not not_11 (not_11_out, or_1_out);

  // Notes on the sheet:
  //   74LS99
endmodule
