// Logisim project NAND3_OC.circ as structural Verilog: 1 circuit, main circuit NAND3_OC
module NAND3_OC (
  input  in_1,
  input  in_2,
  input  in_3,
  output out_4
);

  nand nand_1 (out_4, in_1, in_2, in_3);

  // Notes on the sheet:
  //   nand_1 drives only 0 and floats otherwise
endmodule
