// Logisim project NAND4_OC.circ as structural Verilog: 1 circuit, main circuit NAND4_OC
module NAND4_OC (
  input  in_1,
  input  in_2,
  input  in_3,
  input  in_4,
  output out_5
);

  nand nand_1 (out_5, in_1, in_2, in_3, in_4);

  // Notes on the sheet:
  //   nand_1 drives only 0 and floats otherwise
endmodule
