// Logisim project NOR2_OC.circ as structural Verilog: 1 circuit, main circuit NOR2_OC
module NOR2_OC (
  input  in_1,
  input  in_2,
  output out_3
);

  nor nor_1 (out_3, in_1, in_2);

  // Notes on the sheet:
  //   nor_1 drives only 0 and floats otherwise
endmodule
