// Logisim project pulse.circ as structural Verilog: 2 circuits, main circuit Pulse
module Pulse (
  output Pulse
);

  wire and_1_out, counter_1_carry, d_ff_1_q, pull_resistor_1_node;

  Pull_Resistor #(.pull(1)) pull_resistor_1 (.node(pull_resistor_1_node));
  D_Flip_Flop #(.trigger("high")) d_ff_1 (
    .clk(pull_resistor_1_node), .D(pull_resistor_1_node), .Q(d_ff_1_q), .reset(and_1_out));  // open: Qn, preset, en
  and and_1 (and_1_out, Pulse, d_ff_1_q);
  Counter #(.width(6), .max('h3f), .ongoal("stay")) counter_1 (
    .carry(counter_1_carry), .clk(d_ff_1_q));  // open: load, D, count, Q, clr
  not not_1 (Pulse, counter_1_carry);

  // Notes on the sheet:
  //   Generate a tiny 0-1-0 pulse after CTRL-R
endmodule

module Test (
  input  J,
  input  K,
  output out_3,
  output out_4
);

  wire or_1_out, pulse_1_pulse;

  Pulse pulse_1 (.Pulse(pulse_1_pulse));
  nand nand_1 (out_3, ~J, out_4);  // NAND_Gate
  nand nand_2 (out_4, out_3, ~or_1_out);  // NAND_Gate
  or or_1 (or_1_out, K, pulse_1_pulse);

  // Notes on the sheet:
  //   Without pulse this starts instable and outputs E
endmodule
